// Logisim project MINIRAM.circ as structural Verilog: 1 circuit, main circuit main
module main (
);

  wire _00_out, _01_out, _10_out, _11_out, and_1_out, and_2_out, and_3_out, and_4_out, and_5_out, and_6_out,
       and_7_out, and_8_out, and_9_out, and_10_out, and_11_out, and_12_out, and_13_out, and_14_out,
       and_15_out, and_16_out, and_17_out, and_18_out, and_19_out, and_20_out, clock_1_out, d_ff_1_q,
       d_ff_2_q, d_ff_3_q, d_ff_5_q, d_ff_8_q, d_ff_9_q, d_ff_10_q, d_ff_11_q, d_ff_12_q, d_ff_13_q,
       d_ff_14_q, d_ff_15_q, d_ff_16_q, d_ff_17_q, d_ff_18_q, d_ff_19_q, d_ff_20_q, d_ff_21_q, d_ff_22_q,
       d_ff_23_q, not_1_out, not_2_out, not_3_out, not_4_out, not_5_out, or_1_out, or_2_out, or_3_out,
       or_4_out, or_5_out, or_6_out, or_7_out, or_8_out, or_9_out, or_10_out, or_11_out, or_12_out,
       or_13_out, or_14_out, or_15_out, or_16_out, or_17_out, or_18_out, or_19_out, or_20_out;

  Clock clock_1 (.out(clock_1_out));
  D_Flip_Flop d_ff_1 (.clk(clock_1_out), .Q(d_ff_1_q));  // open: D, Qn, preset, en, reset
  D_Flip_Flop d_ff_2 (.clk(clock_1_out), .Q(d_ff_2_q));  // open: D, Qn, preset, en, reset
  not not_1 (not_1_out, d_ff_2_q);
  not not_2 (not_2_out, d_ff_1_q);
  not not_3 (not_3_out, d_ff_2_q);
  not not_4 (not_4_out, d_ff_1_q);
  and _00 (_00_out, not_1_out, not_2_out);
  and _10 (_10_out, not_3_out, d_ff_1_q);
  and _01 (_01_out, d_ff_2_q, not_4_out);
  and _11 (_11_out, d_ff_2_q, d_ff_1_q);
  D_Flip_Flop d_ff_3 (.clk(clock_1_out), .Q(d_ff_3_q));  // open: D, Qn, preset, en, reset
  not not_5 (not_5_out, d_ff_3_q);
  D_Flip_Flop d_ff_4 (.clk(clock_1_out), .D(or_20_out), .Q(d_ff_3_q));  // open: Qn, preset, en, reset
  D_Flip_Flop d_ff_5 (.clk(clock_1_out), .D(or_19_out), .Q(d_ff_5_q));  // open: Qn, preset, en, reset
  D_Flip_Flop d_ff_6 (.clk(clock_1_out), .D(or_18_out), .Q(d_ff_3_q));  // open: Qn, preset, en, reset
  D_Flip_Flop d_ff_7 (.clk(clock_1_out), .D(or_17_out), .Q(d_ff_3_q));  // open: Qn, preset, en, reset
  and and_1 (and_1_out, d_ff_3_q, d_ff_3_q, _00_out);
  and and_2 (and_2_out, d_ff_3_q, d_ff_3_q, _00_out);
  and and_3 (and_3_out, d_ff_3_q, d_ff_5_q, _00_out);
  and and_4 (and_4_out, d_ff_3_q, d_ff_3_q, _00_out);
  and and_5 (and_5_out, d_ff_3_q, d_ff_3_q, _10_out);
  and and_6 (and_6_out, d_ff_3_q, d_ff_3_q, _10_out, _10_out);
  and and_7 (and_7_out, d_ff_3_q, d_ff_5_q, _10_out);
  and and_8 (and_8_out, d_ff_3_q, d_ff_3_q, _10_out);
  and and_9 (and_9_out, d_ff_3_q, d_ff_3_q, _01_out);
  and and_10 (and_10_out, d_ff_3_q, d_ff_3_q, _01_out);
  and and_11 (and_11_out, d_ff_3_q, d_ff_5_q, _01_out);
  and and_12 (and_12_out, d_ff_3_q, d_ff_3_q, _01_out);
  and and_13 (and_13_out, d_ff_3_q, d_ff_3_q, _11_out);
  and and_14 (and_14_out, d_ff_3_q, d_ff_3_q, _11_out);
  and and_15 (and_15_out, d_ff_3_q, d_ff_5_q, _11_out);
  and and_16 (and_16_out, d_ff_3_q, d_ff_3_q, _11_out);
  and and_17 (and_17_out, _00_out, not_5_out);
  and and_18 (and_18_out, _10_out, not_5_out);
  and and_19 (and_19_out, _01_out, not_5_out);
  and and_20 (and_20_out, _11_out, not_5_out);
  or or_1 (or_1_out, and_1_out, and_17_out);
  or or_2 (or_2_out, and_2_out, and_17_out);
  or or_3 (or_3_out, and_3_out, and_17_out);
  or or_4 (or_4_out, and_4_out, and_17_out);
  or or_5 (or_5_out, and_5_out, and_18_out);
  or or_6 (or_6_out, and_6_out, and_18_out);
  or or_7 (or_7_out, and_7_out, and_18_out);
  or or_8 (or_8_out, and_8_out, and_18_out);
  or or_9 (or_9_out, and_9_out, and_19_out);
  or or_10 (or_10_out, and_10_out, and_19_out);
  or or_11 (or_11_out, and_11_out, and_19_out);
  or or_12 (or_12_out, and_12_out, and_19_out);
  or or_13 (or_13_out, and_13_out, and_20_out);
  or or_14 (or_14_out, and_14_out, and_20_out);
  or or_15 (or_15_out, and_15_out, and_20_out);
  or or_16 (or_16_out, and_16_out, and_20_out);
  D_Flip_Flop d_ff_8 (.clk(clock_1_out), .D(or_1_out), .Q(d_ff_8_q));  // open: Qn, preset, en, reset
  D_Flip_Flop d_ff_9 (.clk(clock_1_out), .D(or_2_out), .Q(d_ff_9_q));  // open: Qn, preset, en, reset
  D_Flip_Flop d_ff_10 (.clk(clock_1_out), .D(or_3_out), .Q(d_ff_10_q));  // open: Qn, preset, en, reset
  D_Flip_Flop d_ff_11 (.clk(clock_1_out), .D(or_4_out), .Q(d_ff_11_q));  // open: Qn, preset, en, reset
  D_Flip_Flop d_ff_12 (.clk(clock_1_out), .D(or_5_out), .Q(d_ff_12_q));  // open: Qn, preset, en, reset
  D_Flip_Flop d_ff_13 (.clk(clock_1_out), .D(or_6_out), .Q(d_ff_13_q));  // open: Qn, preset, en, reset
  D_Flip_Flop d_ff_14 (.clk(clock_1_out), .D(or_7_out), .Q(d_ff_14_q));  // open: Qn, preset, en, reset
  D_Flip_Flop d_ff_15 (.clk(clock_1_out), .D(or_8_out), .Q(d_ff_15_q));  // open: Qn, preset, en, reset
  D_Flip_Flop d_ff_16 (.clk(clock_1_out), .D(or_9_out), .Q(d_ff_16_q));  // open: Qn, preset, en, reset
  D_Flip_Flop d_ff_17 (.clk(clock_1_out), .D(or_10_out), .Q(d_ff_17_q));  // open: Qn, preset, en, reset
  D_Flip_Flop d_ff_18 (.clk(clock_1_out), .D(or_11_out), .Q(d_ff_18_q));  // open: Qn, preset, en, reset
  D_Flip_Flop d_ff_19 (.clk(clock_1_out), .D(or_12_out), .Q(d_ff_19_q));  // open: Qn, preset, en, reset
  D_Flip_Flop d_ff_20 (.clk(clock_1_out), .D(or_13_out), .Q(d_ff_20_q));  // open: Qn, preset, en, reset
  D_Flip_Flop d_ff_21 (.clk(clock_1_out), .D(or_14_out), .Q(d_ff_21_q));  // open: Qn, preset, en, reset
  D_Flip_Flop d_ff_22 (.clk(clock_1_out), .D(or_15_out), .Q(d_ff_22_q));  // open: Qn, preset, en, reset
  D_Flip_Flop d_ff_23 (.clk(clock_1_out), .D(or_16_out), .Q(d_ff_23_q));  // open: Qn, preset, en, reset
  or or_17 (or_17_out, d_ff_8_q, d_ff_12_q, d_ff_16_q, d_ff_20_q);
  or or_18 (or_18_out, d_ff_9_q, d_ff_13_q, d_ff_17_q, d_ff_21_q);
  or or_19 (or_19_out, d_ff_10_q, d_ff_14_q, d_ff_18_q, d_ff_22_q);
  or or_20 (or_20_out, d_ff_11_q, d_ff_15_q, d_ff_19_q, d_ff_23_q);

  // Notes on the sheet:
  //   AR
  //   R/W R
  //   DR
  //   RAM
endmodule
