// Logisim project Full%203-Bit%20Adder.circ as structural Verilog: 1 circuit, main circuit main
module main (
  input  in_1,
  input  in_2,
  input  in_3,
  input  in_4,
  input  in_5,
  input  in_6,
  output out_7,
  output out_8,
  output out_9,
  output STATUS_REGISTER
);

  wire and_1_out, and_2_out, and_3_out, and_4_out, and_5_out, and_6_out, and_7_out, and_8_out, and_9_out,
       and_10_out, and_11_out, and_12_out, clock_1_out, d_ff_1_q, d_ff_2_q, d_ff_3_q, d_ff_4_q, d_ff_5_q,
       d_ff_6_q, not_1_out, not_2_out, not_3_out, or_1_out, or_2_out, or_3_out, or_4_out, or_5_out, or_6_out,
       or_7_out;

  Clock clock_1 (.out(clock_1_out));
  D_Flip_Flop d_ff_1 (.clk(clock_1_out), .D(in_1), .Q(d_ff_1_q));  // open: Qn, preset, en, reset
  D_Flip_Flop d_ff_2 (.clk(clock_1_out), .D(in_2), .Q(d_ff_2_q));  // open: Qn, preset, en, reset
  D_Flip_Flop d_ff_3 (.clk(clock_1_out), .D(in_3), .Q(d_ff_3_q));  // open: Qn, preset, en, reset
  D_Flip_Flop d_ff_4 (.clk(clock_1_out), .D(in_4), .Q(d_ff_4_q));  // open: Qn, preset, en, reset
  D_Flip_Flop d_ff_5 (.clk(clock_1_out), .D(in_5), .Q(d_ff_5_q));  // open: Qn, preset, en, reset
  D_Flip_Flop d_ff_6 (.clk(clock_1_out), .D(in_6), .Q(d_ff_6_q));  // open: Qn, preset, en, reset
  and and_1 (and_1_out, d_ff_6_q, d_ff_3_q);
  or or_1 (or_1_out, d_ff_3_q, d_ff_6_q);
  not not_1 (not_1_out, and_1_out);
  and and_2 (and_2_out, or_1_out, not_1_out);
  and and_3 (and_3_out, and_1_out, d_ff_5_q, d_ff_2_q);
  or or_2 (or_2_out, and_1_out, d_ff_5_q, d_ff_2_q);
  and and_4 (and_4_out, and_1_out, d_ff_5_q);
  and and_5 (and_5_out, d_ff_5_q, d_ff_2_q);
  and and_6 (and_6_out, d_ff_2_q, and_1_out);
  or or_3 (or_3_out, and_4_out, and_5_out, and_6_out);
  not not_2 (not_2_out, or_3_out);
  and and_7 (and_7_out, or_2_out, not_2_out);
  or or_4 (or_4_out, and_3_out, and_7_out);
  and and_8 (and_8_out, or_3_out, d_ff_4_q, d_ff_1_q);
  or or_5 (or_5_out, or_3_out, d_ff_4_q, d_ff_1_q);
  and and_9 (and_9_out, or_3_out, d_ff_4_q);
  and and_10 (and_10_out, d_ff_4_q, d_ff_1_q);
  and and_11 (and_11_out, or_3_out, d_ff_1_q);
  not not_3 (not_3_out, or_6_out);
  or or_6 (or_6_out, and_9_out, and_10_out, and_11_out);
  and and_12 (and_12_out, or_5_out, not_3_out);
  or or_7 (or_7_out, and_8_out, and_12_out);
  D_Flip_Flop d_ff_7 (.clk(clock_1_out), .D(and_2_out), .Q(out_7));  // open: Qn, preset, en, reset
  D_Flip_Flop d_ff_8 (.clk(clock_1_out), .D(or_4_out), .Q(out_8));  // open: Qn, preset, en, reset
  D_Flip_Flop d_ff_9 (.clk(clock_1_out), .D(or_7_out), .Q(out_9));  // open: Qn, preset, en, reset
  D_Flip_Flop d_ff_10 (.clk(clock_1_out), .D(or_6_out), .Q(STATUS_REGISTER));  // open: Qn, preset, en, reset

  // Notes on the sheet:
  //   LEFT REGISTER
  //   RIGHT REGISTER
  //   FULL ADDER
  //   A REGISTER
  //   turns on when there's an overflow
endmodule
