// Logisim project 0-9-number-keypad.circ as structural Verilog: 1 circuit, main circuit main
module main (
  input  Clk,
  input  _0,
  input  _1,
  input  _2,
  input  _3,
  input  _4,
  input  _5,
  input  _6,
  input  _7,
  input  _8,
  input  _9,
  output out_12,
  output out_13,
  output out_14,
  output out_15,
  output out_16,
  output out_17,
  output out_18,
  output out_19
);

  wire and_1_out, not_1_out, or_1_out, or_2_out, or_3_out, or_4_out;

  not not_1 (not_1_out, _0);
  D_Flip_Flop d_ff_1 (.clk(Clk), .D(and_1_out), .Q(out_12));  // open: Qn, preset, en, reset
  and and_1 (and_1_out, _0, not_1_out);
  D_Flip_Flop d_ff_2 (.clk(Clk), .D(and_1_out), .Q(out_13));  // open: Qn, preset, en, reset
  D_Flip_Flop d_ff_3 (.clk(Clk), .D(and_1_out), .Q(out_14));  // open: Qn, preset, en, reset
  D_Flip_Flop d_ff_4 (.clk(Clk), .D(and_1_out), .Q(out_15));  // open: Qn, preset, en, reset
  or or_1 (or_1_out, _9, _8);
  or or_2 (or_2_out, _7, _6, _5, _4);
  D_Flip_Flop d_ff_5 (.clk(Clk), .D(or_1_out), .Q(out_16));  // open: Qn, preset, en, reset
  D_Flip_Flop d_ff_6 (.clk(Clk), .D(or_2_out), .Q(out_17));  // open: Qn, preset, en, reset
  or or_3 (or_3_out, _7, _6, _3, _2);
  D_Flip_Flop d_ff_7 (.clk(Clk), .D(or_3_out), .Q(out_18));  // open: Qn, preset, en, reset
  or or_4 (or_4_out, _9, _7, _5, _3, _1);
  D_Flip_Flop d_ff_8 (.clk(Clk), .D(or_4_out), .Q(out_19));  // open: Qn, preset, en, reset
endmodule
