// Logisim project 273Proj.circ as structural Verilog: 30 circuits, main circuit main
module main (
  input  in_1,
  input  in_2,
  input  in_3,
  input  in_4,
  input  in_5,
  input  in_6,
  input  in_7,
  input  in_8,
  input  in_9,
  input  in_10,
  input  in_11,
  input  in_12,
  input  in_13,
  input  in_14,
  input  in_15,
  input  in_16,
  input  in_17,
  input  in_18,
  input  in_19,
  input  in_20,
  input  in_21,
  input  in_22,
  input  [7:0] in_23,
  input  [3:0] in_24,
  input  [7:0] in_25,
  input  in_26,
  input  in_27,
  input  in_28,
  input  in_29,
  input  [7:0] in_30,
  input  _0,
  input  in_32,
  input  in_33,
  input  in_34,
  input  in_35,
  input  in_36,
  input  in_37,
  input  in_38,
  input  in_39,
  input  _9,
  input  [7:0] in_41,
  input  [7:0] in_42,
  input  in_43,
  input  in_44,
  input  in_45,
  input  in_46,
  input  in_47,
  input  in_48,
  input  in_49,
  input  in_50,
  input  in_51,
  input  in_52,
  input  in_53,
  input  in_54,
  input  in_55,
  input  in_56,
  input  in_57,
  input  in_58,
  input  in_59,
  input  in_60,
  input  [7:0] in_61,
  input  in_62,
  input  in_63,
  input  in_64,
  input  [7:0] in_65,
  output out_66,
  output out_67,
  output out_68,
  output out_69,
  output out_70,
  output out_71,
  output out_72,
  output out_73,
  output out_74,
  output out_75,
  output out_76,
  output out_77,
  output out_78,
  output out_79,
  output out_80,
  output out_81,
  output out_82,
  output out_83,
  output out_84,
  output out_85,
  output out_86,
  output out_87,
  output out_88,
  output out_89,
  output out_90,
  output out_91,
  output out_92,
  output out_93,
  output out_94,
  output out_95,
  output out_96,
  output out_97,
  output out_98,
  output out_99,
  output out_100,
  output out_101,
  output out_102,
  output out_103,
  output out_104,
  output out_105,
  output out_106,
  output out_107,
  output out_108,
  output out_109,
  output out_110,
  output out_111,
  output out_112,
  output out_113,
  output out_114,
  output out_115,
  output out_116,
  output out_117,
  output out_118,
  output out_119,
  output out_120,
  output out_121,
  output out_122,
  output out_123,
  output out_124,
  output out_125,
  output out_126,
  output out_127,
  output out_128,
  output out_129,
  output out_130,
  output out_131,
  output out_132,
  output out_133,
  output out_134,
  output out_135,
  output out_136,
  output out_137,
  output out_138,
  output out_139,
  output out_140,
  output out_141,
  output out_142,
  output out_143,
  output out_144,
  output out_145,
  output out_146,
  output out_147,
  output out_148,
  output out_149,
  output out_150,
  output out_151,
  output out_152,
  output out_153,
  output out_154,
  output out_155,
  output out_156,
  output out_157,
  output out_158,
  output out_159,
  output out_160,
  output out_161,
  output out_162,
  output out_163,
  output out_164,
  output out_165,
  output out_166,
  output out_167,
  output out_168,
  output out_169,
  output out_170,
  output out_171,
  output out_172,
  output out_173,
  output out_174,
  output out_175,
  output out_176,
  output out_177,
  output out_178,
  output out_179,
  output out_180,
  output out_181,
  output out_182,
  output out_183,
  output out_184,
  output out_185,
  output out_186,
  output out_187,
  output out_188,
  output out_189,
  output out_190,
  output out_191,
  output out_192,
  output out_193,
  output [7:0] out_194,
  output [7:0] out_195,
  output [7:0] out_196,
  output [7:0] out_197,
  output [7:0] out_198,
  output [7:0] out_199,
  output out_200,
  output [7:0] out_201,
  output out_202,
  output out_203,
  output out_204,
  output [15:0] out_205,
  output out_206,
  output [7:0] out_207,
  output overflow
);

  wire addr_reg_1_out_10, addr_reg_1_out_11, addr_reg_1_out_12, addr_reg_1_out_13, addr_reg_1_out_14,
       addr_reg_1_out_15, addr_reg_1_out_16, addr_reg_1_out_17, addr_reg_1_out_18, addr_reg_1_out_19,
       addr_reg_1_out_20, addr_reg_1_out_21, addr_reg_1_out_22, addr_reg_1_out_23, addr_reg_1_out_24,
       addr_reg_1_out_25, and_1_out, and_6_out, and_7_out, button_1_out, button_buffer_1_out_2, clock_1_out,
       clock_2_out, compare_1_out_3, cu_1__1100_mult, cu_1_out_9, cu_1_out_10, cu_1_out_11, cu_1_out_12,
       cu_1_out_13, cu_1_out_14, cu_1_out_15, cu_1_out_16, cu_1_out_17, cu_1_out_18, cu_1_out_19,
       cu_1_out_20, delay_1_out_2, n3_digit_disply_1_out_39, n3_digit_disply_1_out_40,
       n3_digit_disply_1_out_41, n3_digit_disply_1_out_42, n3_digit_disply_1_out_43,
       n3_digit_disply_1_out_44, n3_digit_disply_1_out_45, n3_digit_disply_1_out_46,
       n3_digit_disply_1_out_47, n3_digit_disply_1_out_48, n3_digit_disply_1_out_49,
       n3_digit_disply_1_out_50, n3_digit_disply_1_out_51, n3_digit_disply_1_out_52,
       n3_digit_disply_1_out_53, n3_digit_disply_1_out_54, n3_digit_disply_1_out_55,
       n3_digit_disply_1_out_56, n3_digit_disply_1_out_57, n3_digit_disply_1_out_58,
       n3_digit_disply_1_out_59, not_1_out, not_2_out, not_4_out, or_1_out, or_2_out, or_3_out, or_4_out,
       or_5_out, or_6_out, or_7_out, or_8_out, or_9_out, or_10_out, ram_1_out_27, ram_1_out_28, ram_1_out_29,
       ram_1_out_30, ram_1_out_31, ram_1_out_32, ram_1_out_33, ram_1_out_34;
  wire [0:0] not_3_out;
  wire [7:0] data_reg_1_out_26, instr_reg_1_out_33, instr_reg_1_out_41, keypad_1_out_19, main_1_out_17,
       main_2_out_17, multiplexer_1_out, multiplexer_2_out, multiplexer_4_out, multiplexer_6_out,
       multiplexer_9_out, multiplexer_10_out, multiplexer_11_out, multiplexer_13_out, multiplexer_14_out,
       multiplexer_15_out, multiplexer_16_out, multiplexer_17_out, multiplexer_19_out, multiplexer_20_out,
       multiplexer_22_out, pc_1_out_5, register_3_out_10, register_4_out_10;

  Button button_1 (.out(button_1_out));
  Clock clock_1 (.out(clock_1_out));
  button_buffer button_buffer_1 (.in_1(button_1_out), .out_2(button_buffer_1_out_2));
  not not_1 (not_1_out, cu_1_out_17);
  and and_1 (and_1_out, clock_1_out, not_1_out, button_buffer_1_out_2);
  Multiplexer #(.width(8)) multiplexer_1 (
    .in0(in_25), .in1(out_194), .out(multiplexer_1_out), .sel(cu_1_out_15));  // open: en
  // AND_Gate and_2 is placed but not wired
  // AND_Gate and_3 is placed but not wired
  // AND_Gate and_4 is placed but not wired
  // AND_Gate and_5 is placed but not wired
  _7_Segment_Display u_7_segment_display_1 (
    .g(n3_digit_disply_1_out_39), .f(n3_digit_disply_1_out_40), .a(n3_digit_disply_1_out_41),
    .b(n3_digit_disply_1_out_42), .e(n3_digit_disply_1_out_51), .d(n3_digit_disply_1_out_53),
    .c(n3_digit_disply_1_out_56));  // open: dp
  buffer buffer_1 (.in_1(multiplexer_2_out), .in_2(and_1_out), .out_3(out_199));
  _3_digit_disply u_3_digit_disply_1 (
    .in_1(multiplexer_1_out[7]), .in_2(multiplexer_1_out[6]), .in_3(multiplexer_1_out[5]),
    .in_4(multiplexer_1_out[4]), .in_5(multiplexer_1_out[3]), .in_6(multiplexer_1_out[2]),
    .in_7(multiplexer_1_out[1]), .in_8(multiplexer_1_out[0]), .deflut_zero(in_1), .in_11(in_2), .in_12(in_3),
    .in_13(in_4), .in_15(in_5), .in_16(in_6), .in_17(in_7), .in_19(in_18), .in_20(in_19), .in_21(in_20),
    .in_24(in_21), .in_25(in_22), .in_26(in_8), .in_27(in_9), .in_28(in_10), .in_29(in_11), .in_32(in_12),
    .in_33(in_13), .in_34(in_14), .in_35(in_15), .in_36(in_16), .in_37(in_17), .in_38(and_1_out),
    .out_39(n3_digit_disply_1_out_39), .out_40(n3_digit_disply_1_out_40), .out_41(n3_digit_disply_1_out_41),
    .out_42(n3_digit_disply_1_out_42), .out_43(n3_digit_disply_1_out_43), .out_44(n3_digit_disply_1_out_44),
    .out_45(n3_digit_disply_1_out_45), .out_46(n3_digit_disply_1_out_46), .out_47(n3_digit_disply_1_out_47),
    .out_48(n3_digit_disply_1_out_48), .out_49(n3_digit_disply_1_out_49), .out_50(n3_digit_disply_1_out_50),
    .out_51(n3_digit_disply_1_out_51), .out_52(n3_digit_disply_1_out_52), .out_53(n3_digit_disply_1_out_53),
    .out_54(n3_digit_disply_1_out_54), .out_55(n3_digit_disply_1_out_55), .out_56(n3_digit_disply_1_out_56),
    .out_57(n3_digit_disply_1_out_57), .out_58(n3_digit_disply_1_out_58), .out_59(n3_digit_disply_1_out_59),
    .in_9(in_22), .in_14(in_22), .in_22(in_22), .in_30(in_18), .in_18(in_22), .in_23(in_22), .in_31(in_18));
  _7_Segment_Display u_7_segment_display_2 (
    .g(n3_digit_disply_1_out_43), .f(n3_digit_disply_1_out_46), .a(n3_digit_disply_1_out_47),
    .b(n3_digit_disply_1_out_50), .e(n3_digit_disply_1_out_52), .d(n3_digit_disply_1_out_54),
    .c(n3_digit_disply_1_out_57));  // open: dp
  keypad keypad_1 (
    .Clk(and_1_out), ._0(_0), ._1(in_32), ._2(in_33), ._3(in_34), ._4(in_35), ._5(in_36), ._6(in_37),
    ._7(in_38), ._8(in_39), ._9(_9), .out_12(keypad_1_out_19[7]), .out_13(keypad_1_out_19[6]),
    .out_14(keypad_1_out_19[5]), .out_15(keypad_1_out_19[4]), .out_16(keypad_1_out_19[3]),
    .out_17(keypad_1_out_19[2]), .out_18(keypad_1_out_19[1]), .out_19(keypad_1_out_19[0]));
  Multiplexer #(.width(8)) multiplexer_2 (
    .in0(out_201), .in1(out_207), .out(multiplexer_2_out), .sel(cu_1__1100_mult));  // open: en
  _7_Segment_Display u_7_segment_display_3 (
    .g(n3_digit_disply_1_out_48), .f(n3_digit_disply_1_out_44), .a(n3_digit_disply_1_out_45),
    .b(n3_digit_disply_1_out_49), .e(n3_digit_disply_1_out_55), .d(n3_digit_disply_1_out_58),
    .c(n3_digit_disply_1_out_59));  // open: dp
  Multiplexer #(.width(8)) multiplexer_3 (.in1(keypad_1_out_19), .out(out_194), .sel(cu_1_out_16));  // open: in0, en
  or or_1 (or_1_out, or_8_out, not_2_out);
  not not_2 (not_2_out, or_2_out);
  or or_2 (or_2_out, cu_1_out_18, or_9_out);
  Multiplexer #(.width(8)) multiplexer_4 (.in1(out_196), .out(multiplexer_4_out), .sel(cu_1_out_16));  // open: in0, en
  data_reg data_reg_1 (
    .in_11(ram_1_out_27), .in_12(ram_1_out_28), .in_13(ram_1_out_29), .in_14(ram_1_out_30),
    .in_15(ram_1_out_31), .in_16(ram_1_out_32), .in_17(ram_1_out_33), .in_18(ram_1_out_34),
    .out_19(data_reg_1_out_26[7]), .out_20(data_reg_1_out_26[6]), .out_21(data_reg_1_out_26[5]),
    .out_22(data_reg_1_out_26[4]), .out_23(data_reg_1_out_26[3]), .out_24(data_reg_1_out_26[2]),
    .out_25(data_reg_1_out_26[1]), .out_26(data_reg_1_out_26[0]), .R_W(or_1_out),
    .in_3(multiplexer_6_out[7]), .in_4(multiplexer_6_out[6]), .in_5(multiplexer_6_out[5]),
    .in_6(multiplexer_6_out[4]), .in_7(multiplexer_6_out[3]), .in_8(multiplexer_6_out[2]),
    .in_9(multiplexer_6_out[1]), .in_10(multiplexer_6_out[0]), .Clock(and_1_out));
  Multiplexer #(.width(8)) multiplexer_5 (.in1(out_196), .out(out_199), .sel(cu_1_out_18));  // open: in0, en
  Multiplexer #(.width(8)) multiplexer_6 (
    .in0(in_23), .in1(out_194), .out(multiplexer_6_out), .sel(cu_1_out_10));  // open: en
  Multiplexer #(.width(8)) multiplexer_7 (.in1(out_197), .out(out_196), .sel(cu_1_out_15));  // open: in0, en
  register register_1 (
    .clock(and_1_out), .in_2(out_199[0]), .in_3(out_199[1]), .in_4(out_199[2]), .in_5(out_199[3]),
    .in_6(out_199[4]), .in_7(out_199[5]), .in_8(out_199[6]), .in_9(out_199[7]), .out_10(out_197[0]),
    .out_11(out_197[1]), .out_12(out_197[2]), .out_13(out_197[3]), .out_14(out_197[4]), .out_15(out_197[5]),
    .out_16(out_197[6]), .out_17(out_197[7]));
  register register_2 (
    .clock(and_1_out), .in_2(multiplexer_4_out[0]), .in_3(multiplexer_4_out[1]), .in_4(multiplexer_4_out[2]),
    .in_5(multiplexer_4_out[3]), .in_6(multiplexer_4_out[4]), .in_7(multiplexer_4_out[5]),
    .in_8(multiplexer_4_out[6]), .in_9(multiplexer_4_out[7]), .out_10(out_198[0]), .out_11(out_198[1]),
    .out_12(out_198[2]), .out_13(out_198[3]), .out_14(out_198[4]), .out_15(out_198[5]), .out_16(out_198[6]),
    .out_17(out_198[7]));
  or or_3 (or_3_out, cu_1_out_18, cu_1_out_9);
  Multiplexer #(.width(8)) multiplexer_8 (.in1(data_reg_1_out_26), .out(out_194), .sel(or_3_out));  // open: in0, en
  not not_3 (not_3_out[0], in_48);
  Multiplexer #(.width(8)) multiplexer_9 (
    .in1(multiplexer_19_out), .out(multiplexer_9_out), .sel(cu_1_out_18));  // open: in0, en
  Multiplexer #(.width(8)) multiplexer_10 (.in1(out_194), .out(multiplexer_10_out), .sel(or_4_out));  // open: in0, en
  or or_4 (or_4_out, cu_1_out_18, cu_1_out_9, or_7_out, cu_1_out_16);
  Multiplexer #(.width(8)) multiplexer_11 (
    .in1(out_196), .out(multiplexer_11_out), .sel(cu_1_out_15));  // open: in0, en
  addr_reg addr_reg_1 (
    .in_2(multiplexer_9_out[7]), .in_3(multiplexer_9_out[6]), .in_4(multiplexer_9_out[5]),
    .in_5(multiplexer_9_out[4]), .in_6(multiplexer_9_out[3]), .in_7(multiplexer_9_out[2]),
    .in_8(multiplexer_9_out[1]), .in_9(multiplexer_9_out[0]), .clock(and_1_out), .out_10(addr_reg_1_out_10),
    .out_11(addr_reg_1_out_11), .out_12(addr_reg_1_out_12), .out_13(addr_reg_1_out_13),
    .out_14(addr_reg_1_out_14), .out_15(addr_reg_1_out_15), .out_16(addr_reg_1_out_16),
    .out_17(addr_reg_1_out_17), .out_18(addr_reg_1_out_18), .out_19(addr_reg_1_out_19),
    .out_20(addr_reg_1_out_20), .out_21(addr_reg_1_out_21), .out_22(addr_reg_1_out_22),
    .out_23(addr_reg_1_out_23), .out_24(addr_reg_1_out_24), .out_25(addr_reg_1_out_25));
  Multiplexer #(.width(8)) multiplexer_12 (.in1(main_2_out_17), .out(out_194), .sel(cu_1_out_15));  // open: in0, en
  or or_5 (or_5_out, cu_1_out_12, cu_1_out_15, cu_1_out_10);
  Multiplexer #(.width(8)) multiplexer_13 (
    .in1({in_55, in_54, in_53, in_52, in_51, in_50, in_49, not_3_out[0]}), .out(multiplexer_13_out),
    .sel(or_10_out));  // open: in0, en
  Multiplexer #(.width(8)) multiplexer_14 (
    .in0(multiplexer_10_out), .in1(multiplexer_11_out), .out(multiplexer_14_out), .sel(or_5_out));  // open: en
  Multiplexer #(.width(8)) multiplexer_15 (
    .in0(in_61), .in1(out_197), .out(multiplexer_15_out), .sel(cu_1__1100_mult));  // open: en
  Multiplexer #(.width(8)) multiplexer_16 (
    .in0(in_65), .in1(out_198), .out(multiplexer_16_out), .sel(cu_1__1100_mult));  // open: en
  ram ram_1 (
    ._1for_write_mode(or_1_out), .in_11(addr_reg_1_out_10), .in_12(addr_reg_1_out_11),
    .in_13(addr_reg_1_out_12), .in_14(addr_reg_1_out_13), .in_15(addr_reg_1_out_14),
    .in_16(addr_reg_1_out_15), .in_17(addr_reg_1_out_16), .in_18(addr_reg_1_out_17),
    .in_19(addr_reg_1_out_18), .in_20(addr_reg_1_out_19), .in_21(addr_reg_1_out_20),
    .in_22(addr_reg_1_out_21), .in_23(addr_reg_1_out_22), .in_24(addr_reg_1_out_23),
    .in_25(addr_reg_1_out_24), .in_26(addr_reg_1_out_25), .out_35(out_186), .out_36(out_187),
    .out_37(out_188), .out_38(out_189), .out_39(out_190), .out_40(out_191), .out_41(out_192),
    .out_42(out_193), .out_43(out_178), .out_44(out_179), .out_45(out_180), .out_46(out_181),
    .out_47(out_182), .out_48(out_183), .out_49(out_184), .out_50(out_185), .out_51(out_170),
    .out_52(out_171), .out_53(out_172), .out_54(out_173), .out_55(out_174), .out_56(out_175),
    .out_57(out_176), .out_58(out_177), .out_59(out_162), .out_60(out_163), .out_61(out_164),
    .out_62(out_165), .out_63(out_166), .out_64(out_167), .out_65(out_168), .out_66(out_169),
    .out_67(out_154), .out_68(out_155), .out_69(out_156), .out_70(out_157), .out_71(out_158),
    .out_72(out_159), .out_73(out_160), .out_74(out_161), .out_75(out_146), .out_76(out_147),
    .out_77(out_148), .out_78(out_149), .out_79(out_150), .out_80(out_151), .out_81(out_152),
    .out_82(out_153), .out_83(out_138), .out_84(out_139), .out_85(out_140), .out_86(out_141),
    .out_87(out_142), .out_88(out_143), .out_89(out_144), .out_90(out_145), .out_91(out_130),
    .out_92(out_131), .out_93(out_132), .out_94(out_133), .out_95(out_134), .out_96(out_135),
    .out_97(out_136), .out_98(out_137), .out_99(out_122), .out_100(out_123), .out_101(out_124),
    .out_102(out_125), .out_103(out_126), .out_104(out_127), .out_105(out_128), .out_106(out_129),
    .out_107(out_114), .out_108(out_115), .out_109(out_116), .out_110(out_117), .out_111(out_118),
    .out_112(out_119), .out_113(out_120), .out_114(out_121), .out_115(out_106), .out_116(out_107),
    .out_117(out_108), .out_118(out_109), .out_119(out_110), .out_120(out_111), .out_121(out_112),
    .out_122(out_113), .out_123(out_98), .out_124(out_99), .out_125(out_100), .out_126(out_101),
    .out_127(out_102), .out_128(out_103), .out_129(out_104), .out_130(out_105), .out_131(out_90),
    .out_132(out_91), .out_133(out_92), .out_134(out_93), .out_135(out_94), .out_136(out_95),
    .out_137(out_96), .out_138(out_97), .out_139(out_82), .out_140(out_83), .out_141(out_84),
    .out_142(out_85), .out_143(out_86), .out_144(out_87), .out_145(out_88), .out_146(out_89),
    .out_147(out_74), .out_148(out_75), .out_149(out_76), .out_150(out_77), .out_151(out_78),
    .out_152(out_79), .out_153(out_80), .out_154(out_81), .out_155(out_66), .out_156(out_67),
    .out_157(out_68), .out_158(out_69), .out_159(out_70), .out_160(out_71), .out_161(out_72),
    .out_162(out_73), .in_3(multiplexer_6_out[7]), .in_4(multiplexer_6_out[6]), .in_5(multiplexer_6_out[5]),
    .in_6(multiplexer_6_out[4]), .in_7(multiplexer_6_out[3]), .in_8(multiplexer_6_out[2]),
    .in_9(multiplexer_6_out[1]), .in_10(multiplexer_6_out[0]), .in_1(and_1_out), .out_27(ram_1_out_27),
    .out_28(ram_1_out_28), .out_29(ram_1_out_29), .out_30(ram_1_out_30), .out_31(ram_1_out_31),
    .out_32(ram_1_out_32), .out_33(ram_1_out_33), .out_34(ram_1_out_34));
  Multiplexer #(.width(8)) multiplexer_17 (
    .in0(in_41), .in1(out_197), .out(multiplexer_17_out), .sel(cu_1_out_11));  // open: en
  Multiplexer #(.width(8)) multiplexer_18 (
    .in0(in_42), .in1(out_198), .out(multiplexer_13_out), .sel(cu_1_out_11));  // open: en
  mult mult_1 (
    .in_1(multiplexer_15_out), .in_2(multiplexer_16_out), .out_3(out_205), .out_4(out_207),
    .overflow(overflow));
  delay delay_1 (.in_1(and_1_out), .out_2(delay_1_out_2));
  Multiplexer #(.width(8)) multiplexer_19 (
    .in1(main_1_out_17), .out(multiplexer_19_out), .sel(cu_1_out_18));  // open: in0, en
  pc pc_1 (
    .Clk(delay_1_out_2), .out_6(pc_1_out_5[7]), .out_7(pc_1_out_5[6]), .out_8(pc_1_out_5[5]),
    .out_9(pc_1_out_5[4]), .out_2(pc_1_out_5[3]), .out_3(pc_1_out_5[2]), .out_4(pc_1_out_5[1]),
    .out_5(pc_1_out_5[0]));
  Multiplexer #(.width(8)) multiplexer_20 (
    .in0(instr_reg_1_out_41), .in1(pc_1_out_5), .out(multiplexer_20_out), .sel(cu_1_out_18));  // open: en
  MAR_main main_1 (
    .clock(and_1_out), .in_2(multiplexer_20_out[7]), .in_3(multiplexer_20_out[6]),
    .in_4(multiplexer_20_out[5]), .in_5(multiplexer_20_out[4]), .in_6(multiplexer_20_out[3]),
    .in_7(multiplexer_20_out[2]), .in_8(multiplexer_20_out[1]), .in_9(multiplexer_20_out[0]),
    .out_10(main_1_out_17[7]), .out_11(main_1_out_17[6]), .out_12(main_1_out_17[5]),
    .out_13(main_1_out_17[4]), .out_14(main_1_out_17[3]), .out_15(main_1_out_17[2]),
    .out_16(main_1_out_17[1]), .out_17(main_1_out_17[0]));
  MBR_main main_2 (
    .clock(and_1_out), .in_2(multiplexer_14_out[7]), .in_3(multiplexer_14_out[6]),
    .in_4(multiplexer_14_out[5]), .in_5(multiplexer_14_out[4]), .in_6(multiplexer_14_out[3]),
    .in_7(multiplexer_14_out[2]), .in_8(multiplexer_14_out[1]), .in_9(multiplexer_14_out[0]),
    .out_10(main_2_out_17[7]), .out_11(main_2_out_17[6]), .out_12(main_2_out_17[5]),
    .out_13(main_2_out_17[4]), .out_14(main_2_out_17[3]), .out_15(main_2_out_17[2]),
    .out_16(main_2_out_17[1]), .out_17(main_2_out_17[0]));
  Multiplexer #(.width(8)) multiplexer_21 (.in1(main_2_out_17), .out(out_196), .sel(or_7_out));  // open: in0, en
  or or_6 (or_6_out, cu_1_out_11, cu_1_out_19);
  alu alu_1 (
    .Clk(and_1_out), .cOR(in_43), .cAND(in_44), .cADD(or_6_out), .A0(multiplexer_17_out[0]),
    .A1(multiplexer_17_out[1]), .A2(multiplexer_17_out[2]), .A3(multiplexer_17_out[3]),
    .A4(multiplexer_17_out[4]), .A5(multiplexer_17_out[5]), .A6(multiplexer_17_out[6]),
    .A7(multiplexer_17_out[7]), .B0(multiplexer_13_out[0]), .B1(multiplexer_13_out[1]),
    .B2(multiplexer_13_out[2]), .B3(multiplexer_13_out[3]), .B4(multiplexer_13_out[4]),
    .B5(multiplexer_13_out[5]), .B6(multiplexer_13_out[6]), .B7(multiplexer_13_out[7]), .cSUB(or_10_out),
    .cBEQ(in_45), .cBNE(in_46), .in_24(in_47), .R0_to_R7(out_201[0]), .out_26(out_201[1]),
    .out_27(out_201[2]), .out_28(out_201[3]), .Zero(out_200), .out_30(out_201[4]), .out_31(out_201[5]),
    .out_32(out_201[6]), .out_33(out_201[7]), .Overflow(out_202), .Negative(out_203));
  Multiplexer #(.width(8)) multiplexer_22 (
    .in1(main_2_out_17), .out(multiplexer_22_out), .sel(cu_1_out_18));  // open: in0, en
  or or_7 (or_7_out, cu_1_out_9, cu_1_out_16, cu_1_out_18);
  and and_6 (and_6_out, or_6_out, clock_2_out);
  instr_reg instr_reg_1 (
    .in_2(in_24[0]), .in_3(in_24[1]), .in_4(in_24[2]), .in_5(in_24[3]), .out_26(instr_reg_1_out_33[7]),
    .out_27(instr_reg_1_out_33[6]), .out_28(instr_reg_1_out_33[5]), .out_29(instr_reg_1_out_33[4]),
    .Clk(and_1_out), .out_30(instr_reg_1_out_33[3]), .out_31(instr_reg_1_out_33[2]),
    .out_32(instr_reg_1_out_33[1]), .out_33(instr_reg_1_out_33[0]), .in_6(multiplexer_22_out[7]),
    .in_7(multiplexer_22_out[6]), .in_8(multiplexer_22_out[5]), .in_9(multiplexer_22_out[4]),
    .out_34(instr_reg_1_out_41[7]), .out_35(instr_reg_1_out_41[6]), .out_36(instr_reg_1_out_41[5]),
    .out_37(instr_reg_1_out_41[4]), .in_10(in_26), .in_11(in_27), .in_12(in_28), .in_13(in_29),
    .out_38(instr_reg_1_out_41[3]), .out_39(instr_reg_1_out_41[2]), .out_40(instr_reg_1_out_41[1]),
    .out_41(instr_reg_1_out_41[0]), .in_14(multiplexer_22_out[3]), .in_15(multiplexer_22_out[2]),
    .in_16(multiplexer_22_out[1]), .in_17(multiplexer_22_out[0]));  // open: out_42, out_43, out_44, out_45, out_46, out_47, out_48, out_49, in_18, in_19, in_20, in_21, in_22, in_23, in_24, in_25
  register register_3 (
    .clock(and_6_out), .in_2(out_201[0]), .in_3(out_201[1]), .in_4(out_201[2]), .in_5(out_201[3]),
    .in_6(out_201[4]), .in_7(out_201[5]), .in_8(out_201[6]), .in_9(out_201[7]),
    .out_10(register_3_out_10[0]), .out_11(register_3_out_10[1]), .out_12(register_3_out_10[2]),
    .out_13(register_3_out_10[3]), .out_14(register_3_out_10[4]), .out_15(register_3_out_10[5]),
    .out_16(register_3_out_10[6]), .out_17(register_3_out_10[7]));
  register register_4 (
    .clock(and_7_out), .in_2(out_201[0]), .in_3(out_201[1]), .in_4(out_201[2]), .in_5(out_201[3]),
    .in_6(out_201[4]), .in_7(out_201[5]), .in_8(out_201[6]), .in_9(out_201[7]),
    .out_10(register_4_out_10[0]), .out_11(register_4_out_10[1]), .out_12(register_4_out_10[2]),
    .out_13(register_4_out_10[3]), .out_14(register_4_out_10[4]), .out_15(register_4_out_10[5]),
    .out_16(register_4_out_10[6]), .out_17(register_4_out_10[7]));
  buf or_8 (or_8_out, cu_1_out_10);  // OR_Gate
  Clock clock_2 (.out(clock_2_out));
  or or_9 (or_9_out, cu_1_out_9, cu_1_out_12, cu_1_out_11);
  cu cu_1 (
    .Zero(in_30[7]), .Overflow(in_30[6]), .Negative(in_30[5]), .Clock(in_30[4]), .in_5(in_30[0]),
    .in_6(in_30[1]), .in_7(in_30[2]), .in_8(in_30[3]), .out_9(cu_1_out_9), .out_10(cu_1_out_10),
    .out_11(cu_1_out_11), .out_12(cu_1_out_12), .out_13(cu_1_out_13), .out_14(cu_1_out_14),
    .out_15(cu_1_out_15), .out_16(cu_1_out_16), .out_17(cu_1_out_17), .out_18(cu_1_out_18),
    .out_19(cu_1_out_19), .out_20(cu_1_out_20), ._1100_mult(cu_1__1100_mult));
  Multiplexer #(.width(8)) multiplexer_23 (
    .in1(register_3_out_10), .out(multiplexer_17_out), .sel(cu_1_out_19));  // open: in0, en
  Multiplexer #(.width(8)) multiplexer_24 (
    .in1(register_4_out_10), .out(multiplexer_17_out), .sel(cu_1_out_20));  // open: in0, en
  and and_7 (and_7_out, clock_2_out, or_10_out);
  compare compare_1 (
    .in_1(register_4_out_10), .in_2({in_64, in_63, in_62, in_60, in_59, in_58, in_57, in_56}),
    .out_3(compare_1_out_3));
  or or_10 (or_10_out, cu_1_out_20, cu_1_out_12);
  Multiplexer multiplexer_25 (.in1(compare_1_out_3), .out(out_204), .sel(cu_1_out_13));  // open: in0, en
  Multiplexer multiplexer_26 (.in1(not_4_out), .out(out_206), .sel(cu_1_out_14));  // open: in0, en
  not not_4 (not_4_out, compare_1_out_3);

  assign out_195 = out_194;

  // Other names for the same wires on the sheet: BNE = out_206

  // Notes on the sheet:
  //   Power
  //   Add MUX for Print
  //   to load into MBR from Bus
  //   to load into MBR from CPU Bus
  //   Address Choice
  //   only take in if operation needs 
  //   only take in if operation needs 
  //   $one
  //   CPU Bus
  //   mux for choosing what bus to load into mbr
  //   Delay
  //   need second clock cuz data + clock arriving at same time?
  //   mult
  //   MAR
  //   MBR
  //   IR
  //   write
  //   $zero
  //   BNE $zero, sub sum, address in RAM
  //   read
  //   BEQ
  //   BNE
  //   Sum of 0+5
  //   Sum of 5+5
  //   Sum of 10+5
endmodule

module keypad (
  input  Clk,
  input  _0,
  input  _1,
  input  _2,
  input  _3,
  input  _4,
  input  _5,
  input  _6,
  input  _7,
  input  _8,
  input  _9,
  output out_12,
  output out_13,
  output out_14,
  output out_15,
  output out_16,
  output out_17,
  output out_18,
  output out_19
);

  wire and_1_out, not_1_out, or_1_out, or_2_out, or_3_out, or_4_out;

  not not_1 (not_1_out, _0);
  D_Flip_Flop d_ff_1 (.clk(Clk), .D(and_1_out), .Q(out_12));  // open: Qn, preset, en, reset
  and and_1 (and_1_out, _0, not_1_out);
  D_Flip_Flop d_ff_2 (.clk(Clk), .D(and_1_out), .Q(out_13));  // open: Qn, preset, en, reset
  D_Flip_Flop d_ff_3 (.clk(Clk), .D(and_1_out), .Q(out_14));  // open: Qn, preset, en, reset
  D_Flip_Flop d_ff_4 (.clk(Clk), .D(and_1_out), .Q(out_15));  // open: Qn, preset, en, reset
  or or_1 (or_1_out, _9, _8);
  or or_2 (or_2_out, _7, _6, _5, _4);
  D_Flip_Flop d_ff_5 (.clk(Clk), .D(or_1_out), .Q(out_16));  // open: Qn, preset, en, reset
  D_Flip_Flop d_ff_6 (.clk(Clk), .D(or_2_out), .Q(out_17));  // open: Qn, preset, en, reset
  or or_3 (or_3_out, _7, _6, _3, _2);
  D_Flip_Flop d_ff_7 (.clk(Clk), .D(or_3_out), .Q(out_18));  // open: Qn, preset, en, reset
  or or_4 (or_4_out, _9, _7, _5, _3, _1);
  D_Flip_Flop d_ff_8 (.clk(Clk), .D(or_4_out), .Q(out_19));  // open: Qn, preset, en, reset
endmodule

module cu (
  input  Zero,
  input  Overflow,
  input  Negative,
  input  Clock,
  input  in_5,
  input  in_6,
  input  in_7,
  input  in_8,
  output out_9,
  output out_10,
  output out_11,
  output out_12,
  output out_13,
  output out_14,
  output out_15,
  output out_16,
  output out_17,
  output out_18,
  output out_19,
  output out_20,
  output _1100_mult
);

  wire not_1_out, not_2_out, not_3_out, not_4_out, not_5_out, not_6_out, not_7_out, not_8_out, not_9_out,
       not_10_out, not_11_out, not_12_out, not_13_out, not_14_out, not_15_out, not_16_out, not_17_out,
       not_18_out, not_19_out, not_20_out, not_21_out, not_22_out, not_23_out, not_24_out, not_25_out,
       not_26_out, not_27_out, not_28_out, not_29_out, not_30_out;

  not not_1 (not_1_out, in_5);
  not not_2 (not_2_out, in_8);
  not not_3 (not_3_out, in_6);
  not not_4 (not_4_out, in_7);
  not not_5 (not_5_out, in_7);
  not not_6 (not_6_out, in_5);
  not not_7 (not_7_out, in_7);
  not not_8 (not_8_out, in_7);
  not not_9 (not_9_out, in_5);
  not not_10 (not_10_out, in_8);
  not not_11 (not_11_out, in_5);
  not not_12 (not_12_out, in_8);
  not not_13 (not_13_out, in_5);
  not not_14 (not_14_out, in_7);
  not not_15 (not_15_out, in_6);
  not not_16 (not_16_out, in_5);
  not not_17 (not_17_out, in_7);
  not not_18 (not_18_out, in_7);
  not not_19 (not_19_out, in_5);
  not not_20 (not_20_out, in_6);
  and and_1 (out_9, in_5, not_3_out, not_4_out, in_8);
  not not_21 (not_21_out, in_6);
  and and_2 (out_10, in_5, not_21_out, not_5_out, not_22_out);
  not not_22 (not_22_out, in_8);
  and and_3 (out_11, not_6_out, in_6, not_7_out, not_23_out);
  not not_23 (not_23_out, in_8);
  not not_24 (not_24_out, in_8);
  not not_25 (not_25_out, in_6);
  not not_26 (not_26_out, in_8);
  not not_27 (not_27_out, in_6);
  not not_28 (not_28_out, in_8);
  not not_29 (not_29_out, in_6);
  not not_30 (not_30_out, in_7);
  and and_4 (out_12, in_5, in_6, not_8_out, not_24_out);
  and and_5 (out_13, not_9_out, not_25_out, in_7, not_26_out);
  and and_6 (out_14, in_5, not_27_out, in_7, not_10_out);
  and and_7 (out_15, not_11_out, in_6, in_7, not_28_out);
  and and_8 (out_16, in_5, in_6, in_7, not_12_out);
  and and_9 (out_17, not_13_out, not_29_out, not_14_out, in_8);
  and and_10 (out_18, not_1_out, not_15_out, not_30_out, not_2_out);
  and and_11 (out_19, not_16_out, in_6, not_17_out, in_8);
  and and_12 (out_20, in_5, in_6, not_18_out, in_8);
  and and_13 (_1100_mult, not_19_out, not_20_out, in_7, in_8);

  // Notes on the sheet:
  //   Op1
  //   Op2
  //   Op3
  //   Op4
  //   1001 fech
  //   0001 store
  //   0010 add
  //   0011 subtract
  //   0100 beq
  //   0101 bne
  //   0110 print
  //   0111 input
  //   1000 stop
  //   0000 load
  //   1010 add2
  //   1011 sub2
endmodule

module addr_reg (
  input  clock,
  input  in_2,
  input  in_3,
  input  in_4,
  input  in_5,
  input  in_6,
  input  in_7,
  input  in_8,
  input  in_9,
  output out_10,
  output out_11,
  output out_12,
  output out_13,
  output out_14,
  output out_15,
  output out_16,
  output out_17,
  output out_18,
  output out_19,
  output out_20,
  output out_21,
  output out_22,
  output out_23,
  output out_24,
  output out_25
);

  wire d_ff_1_q, d_ff_2_q, d_ff_3_q, d_ff_4_q, d_ff_5_q, d_ff_6_q, d_ff_7_q, d_ff_8_q, not_1_out, not_2_out,
       not_3_out, not_4_out, not_5_out, not_6_out, not_7_out, not_8_out, not_9_out, not_10_out, not_11_out,
       not_12_out, not_13_out, not_14_out, not_15_out, not_16_out, not_17_out, not_18_out, not_19_out,
       not_20_out, not_21_out, not_22_out, not_23_out, not_24_out, not_25_out, not_26_out, not_27_out,
       not_28_out, not_29_out, not_30_out, not_31_out, not_32_out, not_33_out, not_34_out, not_35_out,
       not_36_out;

  D_Flip_Flop d_ff_1 (.clk(clock), .D(in_2), .Q(d_ff_1_q));  // open: Qn, preset, en, reset
  not not_1 (not_1_out, d_ff_1_q);
  D_Flip_Flop d_ff_2 (.clk(clock), .D(in_3), .Q(d_ff_2_q));  // open: Qn, preset, en, reset
  not not_2 (not_2_out, d_ff_2_q);
  D_Flip_Flop d_ff_3 (.clk(clock), .D(in_4), .Q(d_ff_3_q));  // open: Qn, preset, en, reset
  not not_3 (not_3_out, d_ff_3_q);
  D_Flip_Flop d_ff_4 (.clk(clock), .D(in_5), .Q(d_ff_4_q));  // open: Qn, preset, en, reset
  not not_4 (not_4_out, d_ff_4_q);
  D_Flip_Flop d_ff_5 (.clk(clock), .D(in_6), .Q(d_ff_5_q));  // open: Qn, preset, en, reset
  D_Flip_Flop d_ff_6 (.clk(clock), .D(in_7), .Q(d_ff_6_q));  // open: Qn, preset, en, reset
  not not_5 (not_5_out, d_ff_5_q);
  not not_6 (not_6_out, d_ff_5_q);
  not not_7 (not_7_out, d_ff_5_q);
  not not_8 (not_8_out, d_ff_5_q);
  not not_9 (not_9_out, d_ff_5_q);
  not not_10 (not_10_out, d_ff_5_q);
  not not_11 (not_11_out, d_ff_5_q);
  not not_12 (not_12_out, d_ff_5_q);
  not not_13 (not_13_out, d_ff_6_q);
  not not_14 (not_14_out, d_ff_6_q);
  not not_15 (not_15_out, d_ff_6_q);
  not not_16 (not_16_out, d_ff_6_q);
  not not_17 (not_17_out, d_ff_6_q);
  not not_18 (not_18_out, d_ff_6_q);
  not not_19 (not_19_out, d_ff_6_q);
  not not_20 (not_20_out, d_ff_6_q);
  D_Flip_Flop d_ff_7 (.clk(clock), .D(in_8), .Q(d_ff_7_q));  // open: Qn, preset, en, reset
  not not_21 (not_21_out, d_ff_7_q);
  not not_22 (not_22_out, d_ff_7_q);
  not not_23 (not_23_out, d_ff_7_q);
  not not_24 (not_24_out, d_ff_7_q);
  not not_25 (not_25_out, d_ff_7_q);
  not not_26 (not_26_out, d_ff_7_q);
  not not_27 (not_27_out, d_ff_7_q);
  not not_28 (not_28_out, d_ff_7_q);
  D_Flip_Flop d_ff_8 (.clk(clock), .D(in_9), .Q(d_ff_8_q));  // open: Qn, preset, en, reset
  not not_29 (not_29_out, d_ff_8_q);
  not not_30 (not_30_out, d_ff_8_q);
  not not_31 (not_31_out, d_ff_8_q);
  not not_32 (not_32_out, d_ff_8_q);
  not not_33 (not_33_out, d_ff_8_q);
  not not_34 (not_34_out, d_ff_8_q);
  not not_35 (not_35_out, d_ff_8_q);
  not not_36 (not_36_out, d_ff_8_q);
  and and_1 (out_10, not_29_out, not_21_out, not_13_out, not_5_out, not_1_out, not_2_out, not_3_out, not_4_out);
  and and_2 (out_11, d_ff_8_q, not_22_out, not_14_out, not_6_out, not_1_out, not_2_out, not_3_out, not_4_out);
  and and_3 (out_12, not_30_out, d_ff_7_q, not_15_out, not_7_out, not_1_out, not_2_out, not_3_out, not_4_out);
  and and_4 (out_13, d_ff_8_q, d_ff_7_q, not_16_out, not_8_out, not_1_out, not_2_out, not_3_out, not_4_out);
  and and_5 (out_14, not_31_out, not_23_out, d_ff_6_q, not_9_out, not_1_out, not_2_out, not_3_out, not_4_out);
  and and_6 (out_15, d_ff_8_q, not_24_out, d_ff_6_q, not_10_out, not_1_out, not_2_out, not_3_out, not_4_out);
  and and_7 (out_16, not_32_out, d_ff_7_q, d_ff_6_q, not_11_out, not_1_out, not_2_out, not_3_out, not_4_out);
  and and_8 (out_17, d_ff_8_q, d_ff_7_q, d_ff_6_q, not_12_out, not_1_out, not_2_out, not_3_out, not_4_out);
  and and_9 (out_18, not_33_out, not_25_out, not_17_out, d_ff_5_q, not_1_out, not_2_out, not_3_out, not_4_out);
  and and_10 (out_19, d_ff_8_q, not_26_out, not_18_out, d_ff_5_q, not_1_out, not_2_out, not_3_out, not_4_out);
  and and_11 (out_20, not_34_out, d_ff_7_q, not_19_out, d_ff_5_q, not_1_out, not_2_out, not_3_out, not_4_out);
  and and_12 (out_21, d_ff_8_q, d_ff_7_q, not_20_out, d_ff_5_q, not_1_out, not_2_out, not_3_out, not_4_out);
  and and_13 (out_22, not_35_out, not_27_out, d_ff_6_q, d_ff_5_q, not_1_out, not_2_out, not_3_out, not_4_out);
  and and_14 (out_23, d_ff_8_q, not_28_out, d_ff_6_q, d_ff_5_q, not_1_out, not_2_out, not_3_out, not_4_out);
  and and_15 (out_24, not_36_out, d_ff_7_q, d_ff_6_q, d_ff_5_q, not_1_out, not_2_out, not_3_out, not_4_out);
  and and_16 (out_25, d_ff_8_q, d_ff_7_q, d_ff_6_q, d_ff_5_q, not_1_out, not_2_out, not_3_out, not_4_out);

  // Notes on the sheet:
  //   adress register
endmodule

module instr_reg (
  input  Clk,
  input  in_2,
  input  in_3,
  input  in_4,
  input  in_5,
  input  in_6,
  input  in_7,
  input  in_8,
  input  in_9,
  input  in_10,
  input  in_11,
  input  in_12,
  input  in_13,
  input  in_14,
  input  in_15,
  input  in_16,
  input  in_17,
  input  in_18,
  input  in_19,
  input  in_20,
  input  in_21,
  input  in_22,
  input  in_23,
  input  in_24,
  input  in_25,
  output out_26,
  output out_27,
  output out_28,
  output out_29,
  output out_30,
  output out_31,
  output out_32,
  output out_33,
  output out_34,
  output out_35,
  output out_36,
  output out_37,
  output out_38,
  output out_39,
  output out_40,
  output out_41,
  output out_42,
  output out_43,
  output out_44,
  output out_45,
  output out_46,
  output out_47,
  output out_48,
  output out_49
);

  D_Flip_Flop d_ff_1 (.clk(Clk), .D(in_2), .Q(out_26));  // open: Qn, preset, en, reset
  D_Flip_Flop d_ff_2 (.clk(Clk), .D(in_3), .Q(out_27));  // open: Qn, preset, en, reset
  D_Flip_Flop d_ff_3 (.clk(Clk), .D(in_4), .Q(out_28));  // open: Qn, preset, en, reset
  D_Flip_Flop d_ff_4 (.clk(Clk), .D(in_5), .Q(out_29));  // open: Qn, preset, en, reset
  D_Flip_Flop d_ff_5 (.clk(Clk), .D(in_6), .Q(out_30));  // open: Qn, preset, en, reset
  D_Flip_Flop d_ff_6 (.clk(Clk), .D(in_7), .Q(out_31));  // open: Qn, preset, en, reset
  D_Flip_Flop d_ff_7 (.clk(Clk), .D(in_8), .Q(out_32));  // open: Qn, preset, en, reset
  D_Flip_Flop d_ff_8 (.clk(Clk), .D(in_9), .Q(out_33));  // open: Qn, preset, en, reset
  D_Flip_Flop d_ff_9 (.clk(Clk), .D(in_10), .Q(out_34));  // open: Qn, preset, en, reset
  D_Flip_Flop d_ff_10 (.clk(Clk), .D(in_11), .Q(out_35));  // open: Qn, preset, en, reset
  D_Flip_Flop d_ff_11 (.clk(Clk), .D(in_12), .Q(out_36));  // open: Qn, preset, en, reset
  D_Flip_Flop d_ff_12 (.clk(Clk), .D(in_13), .Q(out_37));  // open: Qn, preset, en, reset
  D_Flip_Flop d_ff_13 (.clk(Clk), .D(in_14), .Q(out_38));  // open: Qn, preset, en, reset
  D_Flip_Flop d_ff_14 (.clk(Clk), .D(in_15), .Q(out_39));  // open: Qn, preset, en, reset
  D_Flip_Flop d_ff_15 (.clk(Clk), .D(in_16), .Q(out_40));  // open: Qn, preset, en, reset
  D_Flip_Flop d_ff_16 (.clk(Clk), .D(in_17), .Q(out_41));  // open: Qn, preset, en, reset
  D_Flip_Flop d_ff_17 (.clk(Clk), .D(in_18), .Q(out_42));  // open: Qn, preset, en, reset
  D_Flip_Flop d_ff_18 (.clk(Clk), .D(in_19), .Q(out_43));  // open: Qn, preset, en, reset
  D_Flip_Flop d_ff_19 (.clk(Clk), .D(in_20), .Q(out_44));  // open: Qn, preset, en, reset
  D_Flip_Flop d_ff_20 (.clk(Clk), .D(in_21), .Q(out_45));  // open: Qn, preset, en, reset
  D_Flip_Flop d_ff_21 (.clk(Clk), .D(in_22), .Q(out_46));  // open: Qn, preset, en, reset
  D_Flip_Flop d_ff_22 (.clk(Clk), .D(in_23), .Q(out_47));  // open: Qn, preset, en, reset
  D_Flip_Flop d_ff_23 (.clk(Clk), .D(in_24), .Q(out_48));  // open: Qn, preset, en, reset
  D_Flip_Flop d_ff_24 (.clk(Clk), .D(in_25), .Q(out_49));  // open: Qn, preset, en, reset

  // Notes on the sheet:
  //   NOT Load
  //   (we only load another instruction if the previous instruction is  not load)
endmodule

module pc (
  input  Clk,
  output out_2,
  output out_3,
  output out_4,
  output out_5,
  output out_6,
  output out_7,
  output out_8,
  output out_9
);

  wire j_k_ff_1_q, j_k_ff_1_qn, j_k_ff_2_q, j_k_ff_2_qn, j_k_ff_3_q, j_k_ff_3_qn, j_k_ff_4_q, j_k_ff_4_qn,
       j_k_ff_5_q, j_k_ff_5_qn, j_k_ff_6_q, j_k_ff_6_qn, j_k_ff_7_q, j_k_ff_7_qn, j_k_ff_8_q, j_k_ff_8_qn;

  not not_1 (out_6, j_k_ff_1_q);
  J_K_Flip_Flop j_k_ff_1 (
    .J(j_k_ff_1_qn), .clk(Clk), .K(j_k_ff_1_q), .Q(j_k_ff_1_q), .Qn(j_k_ff_1_qn));  // open: preset, en, reset
  J_K_Flip_Flop j_k_ff_2 (
    .J(j_k_ff_2_qn), .clk(j_k_ff_1_q), .K(j_k_ff_2_q), .Q(j_k_ff_2_q), .Qn(j_k_ff_2_qn));  // open: preset, en, reset
  not not_2 (out_7, j_k_ff_2_q);
  J_K_Flip_Flop j_k_ff_3 (
    .J(j_k_ff_3_qn), .clk(j_k_ff_2_q), .K(j_k_ff_3_q), .Q(j_k_ff_3_q), .Qn(j_k_ff_3_qn));  // open: preset, en, reset
  not not_3 (out_8, j_k_ff_3_q);
  not not_4 (out_9, j_k_ff_4_q);
  J_K_Flip_Flop j_k_ff_4 (
    .J(j_k_ff_4_qn), .clk(j_k_ff_3_q), .K(j_k_ff_4_q), .Q(j_k_ff_4_q), .Qn(j_k_ff_4_qn));  // open: preset, en, reset
  J_K_Flip_Flop j_k_ff_5 (
    .J(j_k_ff_5_qn), .clk(j_k_ff_4_q), .K(j_k_ff_5_q), .Q(j_k_ff_5_q), .Qn(j_k_ff_5_qn));  // open: preset, en, reset
  not not_5 (out_2, j_k_ff_5_q);
  J_K_Flip_Flop j_k_ff_6 (
    .J(j_k_ff_6_qn), .clk(j_k_ff_5_q), .K(j_k_ff_6_q), .Q(j_k_ff_6_q), .Qn(j_k_ff_6_qn));  // open: preset, en, reset
  not not_6 (out_3, j_k_ff_6_q);
  J_K_Flip_Flop j_k_ff_7 (
    .J(j_k_ff_7_qn), .clk(j_k_ff_6_q), .K(j_k_ff_7_q), .Q(j_k_ff_7_q), .Qn(j_k_ff_7_qn));  // open: preset, en, reset
  not not_7 (out_4, j_k_ff_7_q);
  not not_8 (out_5, j_k_ff_8_q);
  J_K_Flip_Flop j_k_ff_8 (
    .J(j_k_ff_8_qn), .clk(j_k_ff_7_q), .K(j_k_ff_8_q), .Q(j_k_ff_8_q), .Qn(j_k_ff_8_qn));  // open: preset, en, reset
endmodule

module _3_digit_disply (
  input  in_1,
  input  in_2,
  input  in_3,
  input  in_4,
  input  in_5,
  input  in_6,
  input  in_7,
  input  in_8,
  input  in_9,
  input  deflut_zero,
  input  in_11,
  input  in_12,
  input  in_13,
  input  in_14,
  input  in_15,
  input  in_16,
  input  in_17,
  input  in_18,
  input  in_19,
  input  in_20,
  input  in_21,
  input  in_22,
  input  in_23,
  input  in_24,
  input  in_25,
  input  in_26,
  input  in_27,
  input  in_28,
  input  in_29,
  input  in_30,
  input  in_31,
  input  in_32,
  input  in_33,
  input  in_34,
  input  in_35,
  input  in_36,
  input  in_37,
  input  in_38,
  output out_39,
  output out_40,
  output out_41,
  output out_42,
  output out_43,
  output out_44,
  output out_45,
  output out_46,
  output out_47,
  output out_48,
  output out_49,
  output out_50,
  output out_51,
  output out_52,
  output out_53,
  output out_54,
  output out_55,
  output out_56,
  output out_57,
  output out_58,
  output out_59
);

  wire c_for_display_1_out_9, c_for_display_1_out_10, c_for_display_1_out_11, c_for_display_1_out_12,
       c_for_display_2_out_9, c_for_display_2_out_10, c_for_display_2_out_11, c_for_display_2_out_12,
       c_for_display_3_out_9, c_for_display_3_out_10, c_for_display_3_out_11, c_for_display_3_out_12,
       c_for_display_4_out_9, c_for_display_4_out_10, c_for_display_4_out_11, c_for_display_4_out_12,
       c_for_display_5_out_9, c_for_display_5_out_10, c_for_display_5_out_11, c_for_display_5_out_12,
       c_for_display_6_out_9, c_for_display_6_out_10, c_for_display_6_out_11, c_for_display_6_out_12,
       c_for_display_7_out_9, c_for_display_7_out_10, c_for_display_7_out_11, c_for_display_7_out_12;

  c_for_display c_for_display_1 (
    .in_5(deflut_zero), .in_6(c_for_display_3_out_9), .in_7(c_for_display_4_out_9),
    .in_8(c_for_display_5_out_9), .in_2(in_24), .in_3(in_26), .in_4(in_28), .out_9(c_for_display_1_out_9),
    .out_10(c_for_display_1_out_10), .out_11(c_for_display_1_out_11), .out_12(c_for_display_1_out_12),
    .in_1(in_23));
  c_for_display c_for_display_2 (
    .in_5(c_for_display_1_out_10), .in_6(c_for_display_1_out_11), .in_7(c_for_display_1_out_12),
    .in_8(c_for_display_6_out_9), .in_2(in_32), .in_3(in_34), .in_4(in_36), .out_9(c_for_display_2_out_9),
    .out_10(c_for_display_2_out_10), .out_11(c_for_display_2_out_11), .out_12(c_for_display_2_out_12),
    .in_1(in_31));
  c_for_display c_for_display_3 (
    .in_5(deflut_zero), .in_6(in_1), .in_7(in_2), .in_8(in_3), .in_2(in_11), .in_3(in_12), .in_4(in_13),
    .out_9(c_for_display_3_out_9), .out_10(c_for_display_3_out_10), .out_11(c_for_display_3_out_11),
    .out_12(c_for_display_3_out_12), .in_1(in_9));
  c_for_display c_for_display_4 (
    .in_5(c_for_display_3_out_10), .in_6(c_for_display_3_out_11), .in_7(c_for_display_3_out_12), .in_8(in_4),
    .in_2(in_15), .in_3(in_16), .in_4(in_17), .out_9(c_for_display_4_out_9), .out_10(c_for_display_4_out_10),
    .out_11(c_for_display_4_out_11), .out_12(c_for_display_4_out_12), .in_1(in_14));
  _1_display u_1_display_1 (
    .in_1(in_38), .in_2(deflut_zero), .in_3(deflut_zero), .in_4(c_for_display_1_out_9),
    .in_5(c_for_display_2_out_9), .out_6(out_40), .out_7(out_41), .out_8(out_42), .out_9(out_39),
    .out_10(out_51), .out_11(out_53), .out_12(out_56));
  c_for_display c_for_display_5 (
    .in_5(c_for_display_4_out_10), .in_6(c_for_display_4_out_11), .in_7(c_for_display_4_out_12), .in_8(in_5),
    .in_2(in_19), .in_3(in_20), .in_4(in_21), .out_9(c_for_display_5_out_9), .out_10(c_for_display_5_out_10),
    .out_11(c_for_display_5_out_11), .out_12(c_for_display_5_out_12), .in_1(in_18));
  c_for_display c_for_display_6 (
    .in_5(c_for_display_5_out_10), .in_6(c_for_display_5_out_11), .in_7(c_for_display_5_out_12), .in_8(in_6),
    .in_2(in_25), .in_3(in_27), .in_4(in_29), .out_9(c_for_display_6_out_9), .out_10(c_for_display_6_out_10),
    .out_11(c_for_display_6_out_11), .out_12(c_for_display_6_out_12), .in_1(in_22));
  c_for_display c_for_display_7 (
    .in_5(c_for_display_6_out_10), .in_6(c_for_display_6_out_11), .in_7(c_for_display_6_out_12), .in_8(in_7),
    .in_2(in_33), .in_3(in_35), .in_4(in_37), .out_9(c_for_display_7_out_9), .out_10(c_for_display_7_out_10),
    .out_11(c_for_display_7_out_11), .out_12(c_for_display_7_out_12), .in_1(in_30));
  _1_display u_1_display_2 (
    .in_1(in_38), .in_2(c_for_display_2_out_10), .in_3(c_for_display_2_out_11),
    .in_4(c_for_display_2_out_12), .in_5(c_for_display_7_out_9), .out_6(out_46), .out_7(out_47),
    .out_8(out_50), .out_9(out_43), .out_10(out_52), .out_11(out_54), .out_12(out_57));
  _1_display u_1_display_3 (
    .in_1(in_38), .in_2(c_for_display_7_out_10), .in_3(c_for_display_7_out_11),
    .in_4(c_for_display_7_out_12), .in_5(in_8), .out_6(out_44), .out_7(out_45), .out_8(out_49),
    .out_9(out_48), .out_10(out_55), .out_11(out_58), .out_12(out_59));

  // Notes on the sheet:
  //   clock
endmodule

module _1_display (
  input  in_1,
  input  in_2,
  input  in_3,
  input  in_4,
  input  in_5,
  output out_6,
  output out_7,
  output out_8,
  output out_9,
  output out_10,
  output out_11,
  output out_12
);

  wire _0_out, _1_out, _2_out, _3_out, _4_out, _5_out, _6_out, _7_out, _8_out, _9_out, d_ff_1_q, d_ff_2_q,
       d_ff_3_q, d_ff_4_q, not_1_out, not_2_out, not_3_out, not_4_out, not_5_out, not_6_out, not_7_out,
       not_8_out, not_9_out, not_10_out, not_11_out, not_12_out, not_13_out, not_14_out, not_15_out,
       not_16_out, not_17_out, not_18_out, not_19_out, not_20_out, not_21_out, not_22_out, not_23_out,
       not_24_out, not_25_out;

  D_Flip_Flop d_ff_1 (.clk(in_1), .D(in_2), .Q(d_ff_1_q));  // open: Qn, preset, en, reset
  D_Flip_Flop d_ff_2 (.clk(in_1), .D(in_3), .Q(d_ff_2_q));  // open: Qn, preset, en, reset
  D_Flip_Flop d_ff_3 (.clk(in_1), .D(in_4), .Q(d_ff_3_q));  // open: Qn, preset, en, reset
  D_Flip_Flop d_ff_4 (.clk(in_1), .D(in_5), .Q(d_ff_4_q));  // open: Qn, preset, en, reset
  not not_1 (not_1_out, d_ff_4_q);
  not not_2 (not_2_out, d_ff_3_q);
  not not_3 (not_3_out, d_ff_2_q);
  not not_4 (not_4_out, d_ff_1_q);
  not not_5 (not_5_out, d_ff_3_q);
  not not_6 (not_6_out, d_ff_2_q);
  not not_7 (not_7_out, d_ff_1_q);
  not not_8 (not_8_out, d_ff_4_q);
  not not_9 (not_9_out, d_ff_2_q);
  not not_10 (not_10_out, d_ff_1_q);
  not not_11 (not_11_out, d_ff_2_q);
  not not_12 (not_12_out, d_ff_1_q);
  not not_13 (not_13_out, d_ff_4_q);
  not not_14 (not_14_out, d_ff_3_q);
  not not_15 (not_15_out, d_ff_1_q);
  not not_16 (not_16_out, d_ff_3_q);
  not not_17 (not_17_out, d_ff_1_q);
  not not_18 (not_18_out, d_ff_4_q);
  not not_19 (not_19_out, d_ff_1_q);
  not not_20 (not_20_out, d_ff_1_q);
  not not_21 (not_21_out, d_ff_4_q);
  not not_22 (not_22_out, d_ff_3_q);
  not not_23 (not_23_out, d_ff_2_q);
  not not_24 (not_24_out, d_ff_3_q);
  not not_25 (not_25_out, d_ff_2_q);
  and _0 (_0_out, not_1_out, not_2_out, not_3_out, not_4_out);
  and _1 (_1_out, d_ff_4_q, not_5_out, not_6_out, not_7_out);
  and _2 (_2_out, not_8_out, d_ff_3_q, not_9_out, not_10_out);
  and _3 (_3_out, d_ff_4_q, d_ff_3_q, not_11_out, not_12_out);
  and _4 (_4_out, not_13_out, not_14_out, d_ff_2_q, not_15_out);
  and _5 (_5_out, d_ff_4_q, not_16_out, d_ff_2_q, not_17_out);
  and _6 (_6_out, not_18_out, d_ff_3_q, d_ff_2_q, not_19_out);
  and _7 (_7_out, d_ff_4_q, d_ff_3_q, d_ff_2_q, not_20_out);
  and _8 (_8_out, not_21_out, not_22_out, not_23_out, d_ff_1_q);
  and _9 (_9_out, d_ff_4_q, not_24_out, not_25_out, d_ff_1_q);
  or or_1 (out_6, _0_out, _4_out, _5_out, _6_out, _8_out, _9_out);
  or or_2 (out_7, _0_out, _2_out, _3_out, _5_out, _7_out, _8_out, _9_out);
  or or_3 (out_8, _0_out, _1_out, _2_out, _3_out, _4_out, _7_out, _8_out, _9_out);
  or or_4 (out_9, _2_out, _3_out, _4_out, _5_out, _6_out, _8_out, _9_out);
  or or_5 (out_10, _0_out, _2_out, _6_out, _8_out);
  or or_6 (out_11, _0_out, _2_out, _3_out, _5_out, _6_out, _8_out);
  or or_7 (out_12, _0_out, _5_out, _1_out, _3_out, _9_out, _6_out, _4_out, _7_out, _8_out);
endmodule

module c_for_display (
  input  in_1,
  input  in_2,
  input  in_3,
  input  in_4,
  input  in_5,
  input  in_6,
  input  in_7,
  input  in_8,
  output out_9,
  output out_10,
  output out_11,
  output out_12
);

  wire and_1_out, not_1_out, not_2_out, or_1_out, or_2_out;
  wire [1:0] and_3_out;

  and and_1 (and_1_out, in_6, or_2_out);
  or or_1 (or_1_out, in_5, and_1_out);
  or or_2 (or_2_out, in_7, in_8);
  and and_2 (and_3_out[1], or_1_out, not_1_out);
  not not_1 (not_1_out, in_3);
  not not_2 (not_2_out, in_4);
  and and_3 (and_3_out[0], or_1_out, not_2_out);
  _4_bit_adder u_4_bit_adder_1 (
    .in_1({in_1, in_2, and_3_out}), .in_2({in_5, in_6, in_7, in_8}), .out_3({out_9, out_10, out_11, out_12}));  // open: C
endmodule

module _3_bit_adder (
  input  in_1,
  input  in_2,
  input  right_register,
  input  in_4,
  input  in_5,
  input  left_register,
  output out_7,
  output out_8,
  output out_9,
  output out_10
);

  wire and_1_out, and_2_out, and_3_out, and_4_out, and_5_out, and_6_out, and_7_out, and_8_out, and_9_out,
       and_10_out, and_11_out, and_12_out, and_13_out, and_14_out, and_15_out, not_1_out, not_2_out,
       not_3_out, not_4_out, not_5_out, not_6_out, not_7_out, not_8_out, not_9_out, not_10_out, or_1_out,
       or_2_out, or_6_out;

  not not_1 (not_1_out, in_1);
  and and_1 (and_1_out, right_register, not_1_out);
  not not_2 (not_2_out, left_register);
  or or_1 (or_1_out, and_1_out, and_8_out);
  not not_3 (not_3_out, in_2);
  and and_2 (and_2_out, in_4, not_2_out);
  or or_2 (or_2_out, and_2_out, and_10_out);
  not not_4 (not_4_out, or_1_out);
  and and_3 (and_3_out, in_5, not_3_out);
  or or_3 (out_10, and_3_out, and_13_out);
  not not_5 (not_5_out, or_2_out);
  and and_4 (and_4_out, or_6_out, not_4_out);
  and and_5 (and_5_out, in_2, in_5);
  and and_6 (and_6_out, and_5_out, not_5_out);
  or or_4 (out_9, and_6_out, and_11_out);
  and and_7 (and_7_out, or_2_out, and_5_out);
  not not_6 (not_6_out, right_register);
  or or_5 (out_8, and_15_out, and_4_out);
  not not_7 (not_7_out, in_4);
  not not_8 (not_8_out, and_5_out);
  and and_8 (and_8_out, in_1, not_6_out);
  and and_9 (and_9_out, or_6_out, or_1_out);
  not not_9 (not_9_out, in_5);
  and and_10 (and_10_out, left_register, not_7_out);
  and and_11 (and_11_out, or_2_out, not_8_out);
  or or_6 (or_6_out, and_12_out, and_7_out);
  and and_12 (and_12_out, left_register, in_4);
  and and_13 (and_13_out, in_2, not_9_out);
  not not_10 (not_10_out, or_6_out);
  and and_14 (and_14_out, in_1, right_register);
  and and_15 (and_15_out, or_1_out, not_10_out);
  or or_7 (out_7, and_14_out, and_9_out);

  // Notes on the sheet:
  //   A-register
  //   sum1
  //   sum2
  //   carry1
  //   sum3
  //   carry2
  //   Adder
  //   carry3
  //   reporter
endmodule

module register (
  input  clock,
  input  in_2,
  input  in_3,
  input  in_4,
  input  in_5,
  input  in_6,
  input  in_7,
  input  in_8,
  input  in_9,
  output out_10,
  output out_11,
  output out_12,
  output out_13,
  output out_14,
  output out_15,
  output out_16,
  output out_17
);

  D_Flip_Flop d_ff_1 (.clk(clock), .D(in_2), .Q(out_10));  // open: Qn, preset, en, reset
  D_Flip_Flop d_ff_2 (.clk(clock), .D(in_3), .Q(out_11));  // open: Qn, preset, en, reset
  D_Flip_Flop d_ff_3 (.clk(clock), .D(in_4), .Q(out_12));  // open: Qn, preset, en, reset
  D_Flip_Flop d_ff_4 (.clk(clock), .D(in_5), .Q(out_13));  // open: Qn, preset, en, reset
  D_Flip_Flop d_ff_5 (.clk(clock), .D(in_6), .Q(out_14));  // open: Qn, preset, en, reset
  D_Flip_Flop d_ff_6 (.clk(clock), .D(in_7), .Q(out_15));  // open: Qn, preset, en, reset
  D_Flip_Flop d_ff_7 (.clk(clock), .D(in_8), .Q(out_16));  // open: Qn, preset, en, reset
  D_Flip_Flop d_ff_8 (.clk(clock), .D(in_9), .Q(out_17));  // open: Qn, preset, en, reset
endmodule

module status (
  input  Add,
  input  Sub,
  input  in_3,
  input  BNE,
  input  in_5,
  input  in_6,
  input  in_7,
  input  in_8,
  input  in_9,
  input  in_10,
  input  in_11,
  input  in_12,
  input  in_13,
  input  in_14,
  input  Negative
);

  wire and_1_out, and_2_out, not_1_out;

  and and_1 (and_1_out, in_3, in_13);
  not not_1 (not_1_out, in_13);
  and and_2 (and_2_out, BNE, not_1_out);

  // Notes on the sheet:
  //   R0 to R7
  //   Zero
  //   Overflow
  //   BEQ
  //   send MAR to PC
  //   send MAR to PC
endmodule

module button_buffer (
  input  in_1,
  output out_2
);

  wire not_1_out;

  D_Flip_Flop d_ff_1 (.clk(in_1), .D(not_1_out), .Q(out_2), .en(in_1));  // open: Qn, preset, reset
  not not_1 (not_1_out, out_2);
endmodule

module alu (
  input  Clk,
  input  cOR,
  input  cAND,
  input  cADD,
  input  A0,
  input  A1,
  input  A2,
  input  A3,
  input  A4,
  input  A5,
  input  A6,
  input  A7,
  input  B0,
  input  B1,
  input  B2,
  input  B3,
  input  B4,
  input  B5,
  input  B6,
  input  B7,
  input  cSUB,
  input  cBEQ,
  input  cBNE,
  input  in_24,
  output R0_to_R7,
  output out_26,
  output out_27,
  output out_28,
  output Zero,
  output out_30,
  output out_31,
  output out_32,
  output out_33,
  output Overflow,
  output Negative
);

  wire and_1_out, and_2_out, and_3_out, and_4_out, n8bitadd_1_r0, n8bitadd_1_r1, n8bitadd_1_r2,
       n8bitadd_1_r3, n8bitadd_1_r4, n8bitadd_1_r5, n8bitadd_1_r6, n8bitadd_1_r7, n8bitand_1_r0,
       n8bitand_1_r1, n8bitand_1_r2, n8bitand_1_r3, n8bitand_1_r4, n8bitand_1_r5, n8bitand_1_r6,
       n8bitand_1_r7, n8bitor_1_r0, n8bitor_1_r1, n8bitor_1_r2, n8bitor_1_r3, n8bitor_1_r4, n8bitor_1_r5,
       n8bitor_1_r6, n8bitor_1_r7, n8bitsub_1_negative, n8bitsub_1_r0, n8bitsub_1_r1, n8bitsub_1_r2,
       n8bitsub_1_r3, n8bitsub_1_r4, n8bitsub_1_r5, n8bitsub_1_r6, n8bitsub_1_r7, not_1_out, not_3_out,
       not_4_out, not_5_out, not_6_out, not_7_out, not_8_out, not_9_out, not_10_out, or_1_out;

  not not_1 (not_1_out, Clk);
  or or_1 (or_1_out, cSUB, cBEQ, cBNE);
  and and_1 (and_1_out, not_1_out, or_1_out);
  and and_2 (and_2_out, not_1_out, cAND);
  and and_3 (and_3_out, not_1_out, cADD);
  and and_4 (and_4_out, not_1_out, cOR);
  _8bitOR u_8bitor_1 (
    .C(and_4_out), .A0(A0), .A1(A1), .A2(A2), .A3(A3), .A4(A4), .A5(A5), .A6(A6), .A7(A7), .B0(B0), .B1(B1),
    .B2(B2), .B3(B3), .B4(B4), .B5(B5), .B6(B6), .B7(B7), .R0(n8bitor_1_r0), .R1(n8bitor_1_r1),
    .R2(n8bitor_1_r2), .R3(n8bitor_1_r3), .R4(n8bitor_1_r4), .R5(n8bitor_1_r5), .R6(n8bitor_1_r6),
    .R7(n8bitor_1_r7));
  _8bitAND u_8bitand_1 (
    .C(and_2_out), .A0(A0), .A1(A1), .A2(A2), .A3(A3), .A4(A4), .A5(A5), .A6(A6), .A7(A7), .B0(B0), .B1(B1),
    .B2(B2), .B3(B3), .B4(B4), .B5(B5), .B6(B6), .B7(B7), .R0(n8bitand_1_r0), .R1(n8bitand_1_r1),
    .R2(n8bitand_1_r2), .R3(n8bitand_1_r3), .R4(n8bitand_1_r4), .R5(n8bitand_1_r5), .R6(n8bitand_1_r6),
    .R7(n8bitand_1_r7));
  _8bitADD u_8bitadd_1 (
    .C(and_3_out), .A0(A0), .A1(A1), .A2(A2), .A3(A3), .A4(A4), .A5(A5), .A6(A6), .A7(A7), .B0(B0), .B1(B1),
    .B2(B2), .B3(B3), .B4(B4), .B5(B5), .B6(B6), .B7(B7), .R0(n8bitadd_1_r0), .R1(n8bitadd_1_r1),
    .R2(n8bitadd_1_r2), .R3(n8bitadd_1_r3), .R4(n8bitadd_1_r4), .R5(n8bitadd_1_r5), .R6(n8bitadd_1_r6),
    .R7(n8bitadd_1_r7), .Overflow(Overflow));
  _8bitSUB u_8bitsub_1 (
    .C(and_1_out), .A0(A0), .A1(A1), .A2(A2), .A3(A3), .A4(A4), .A5(A5), .A6(A6), .A7(A7), .B0(B0), .B1(B1),
    .B2(B2), .B3(B3), .B4(B4), .B5(B5), .B6(B6), .B7(B7), .useless_shitter(in_24), .R0(n8bitsub_1_r0),
    .R1(n8bitsub_1_r1), .R2(n8bitsub_1_r2), .R3(n8bitsub_1_r3), .R4(n8bitsub_1_r4), .R5(n8bitsub_1_r5),
    .R6(n8bitsub_1_r6), .R7(n8bitsub_1_r7), .Negative(n8bitsub_1_negative));
  not not_2 (Negative, n8bitsub_1_negative);
  or or_2 (R0_to_R7, n8bitor_1_r0, n8bitand_1_r0, n8bitadd_1_r0, n8bitsub_1_r0);
  or or_3 (out_26, n8bitor_1_r1, n8bitand_1_r1, n8bitadd_1_r1, n8bitsub_1_r1);
  or or_4 (out_27, n8bitor_1_r2, n8bitand_1_r2, n8bitadd_1_r2, n8bitsub_1_r2);
  or or_5 (out_28, n8bitor_1_r3, n8bitand_1_r3, n8bitadd_1_r3, n8bitsub_1_r3);
  or or_6 (out_30, n8bitor_1_r4, n8bitand_1_r4, n8bitadd_1_r4, n8bitsub_1_r4);
  or or_7 (out_31, n8bitor_1_r5, n8bitand_1_r5, n8bitadd_1_r5, n8bitsub_1_r5);
  or or_8 (out_32, n8bitor_1_r6, n8bitand_1_r6, n8bitadd_1_r6, n8bitsub_1_r6);
  or or_9 (out_33, n8bitor_1_r7, n8bitand_1_r7, n8bitadd_1_r7, n8bitsub_1_r7);
  not not_3 (not_3_out, R0_to_R7);
  not not_4 (not_4_out, out_26);
  not not_5 (not_5_out, out_27);
  not not_6 (not_6_out, out_28);
  not not_7 (not_7_out, out_30);
  not not_8 (not_8_out, out_31);
  not not_9 (not_9_out, out_32);
  not not_10 (not_10_out, out_33);
  and and_5 (Zero, not_3_out, not_4_out, not_5_out, not_6_out, not_7_out, not_8_out, not_9_out, not_10_out);

  // Notes on the sheet:
  //   useless shit for subtraction
endmodule
module ram (
  input  in_1,
  input  _1for_write_mode,
  input  in_3,
  input  in_4,
  input  in_5,
  input  in_6,
  input  in_7,
  input  in_8,
  input  in_9,
  input  in_10,
  input  in_11,
  input  in_12,
  input  in_13,
  input  in_14,
  input  in_15,
  input  in_16,
  input  in_17,
  input  in_18,
  input  in_19,
  input  in_20,
  input  in_21,
  input  in_22,
  input  in_23,
  input  in_24,
  input  in_25,
  input  in_26,
  output out_27,
  output out_28,
  output out_29,
  output out_30,
  output out_31,
  output out_32,
  output out_33,
  output out_34,
  output out_35,
  output out_36,
  output out_37,
  output out_38,
  output out_39,
  output out_40,
  output out_41,
  output out_42,
  output out_43,
  output out_44,
  output out_45,
  output out_46,
  output out_47,
  output out_48,
  output out_49,
  output out_50,
  output out_51,
  output out_52,
  output out_53,
  output out_54,
  output out_55,
  output out_56,
  output out_57,
  output out_58,
  output out_59,
  output out_60,
  output out_61,
  output out_62,
  output out_63,
  output out_64,
  output out_65,
  output out_66,
  output out_67,
  output out_68,
  output out_69,
  output out_70,
  output out_71,
  output out_72,
  output out_73,
  output out_74,
  output out_75,
  output out_76,
  output out_77,
  output out_78,
  output out_79,
  output out_80,
  output out_81,
  output out_82,
  output out_83,
  output out_84,
  output out_85,
  output out_86,
  output out_87,
  output out_88,
  output out_89,
  output out_90,
  output out_91,
  output out_92,
  output out_93,
  output out_94,
  output out_95,
  output out_96,
  output out_97,
  output out_98,
  output out_99,
  output out_100,
  output out_101,
  output out_102,
  output out_103,
  output out_104,
  output out_105,
  output out_106,
  output out_107,
  output out_108,
  output out_109,
  output out_110,
  output out_111,
  output out_112,
  output out_113,
  output out_114,
  output out_115,
  output out_116,
  output out_117,
  output out_118,
  output out_119,
  output out_120,
  output out_121,
  output out_122,
  output out_123,
  output out_124,
  output out_125,
  output out_126,
  output out_127,
  output out_128,
  output out_129,
  output out_130,
  output out_131,
  output out_132,
  output out_133,
  output out_134,
  output out_135,
  output out_136,
  output out_137,
  output out_138,
  output out_139,
  output out_140,
  output out_141,
  output out_142,
  output out_143,
  output out_144,
  output out_145,
  output out_146,
  output out_147,
  output out_148,
  output out_149,
  output out_150,
  output out_151,
  output out_152,
  output out_153,
  output out_154,
  output out_155,
  output out_156,
  output out_157,
  output out_158,
  output out_159,
  output out_160,
  output out_161,
  output out_162
);

  wire and_1_out, and_2_out, and_3_out, and_4_out, and_5_out, and_6_out, and_7_out, and_8_out, and_9_out,
       and_10_out, and_11_out, and_12_out, and_13_out, and_14_out, and_15_out, and_16_out, and_17_out,
       and_18_out, and_19_out, and_20_out, and_21_out, and_22_out, and_23_out, and_24_out, and_25_out,
       and_26_out, and_27_out, and_28_out, and_29_out, and_30_out, and_31_out, and_32_out, byte_1_out_11,
       byte_1_out_13, byte_1_out_15, byte_1_out_17, byte_1_out_19, byte_1_out_21, byte_1_out_23,
       byte_1_out_25, byte_2_out_11, byte_2_out_13, byte_2_out_15, byte_2_out_17, byte_2_out_19,
       byte_2_out_21, byte_2_out_23, byte_2_out_25, byte_3_out_11, byte_3_out_13, byte_3_out_15,
       byte_3_out_17, byte_3_out_19, byte_3_out_21, byte_3_out_23, byte_3_out_25, byte_4_out_11,
       byte_4_out_13, byte_4_out_15, byte_4_out_17, byte_4_out_19, byte_4_out_21, byte_4_out_23,
       byte_4_out_25, byte_5_out_11, byte_5_out_13, byte_5_out_15, byte_5_out_17, byte_5_out_19,
       byte_5_out_21, byte_5_out_23, byte_5_out_25, byte_6_out_11, byte_6_out_13, byte_6_out_15,
       byte_6_out_17, byte_6_out_19, byte_6_out_21, byte_6_out_23, byte_6_out_25, byte_7_out_11,
       byte_7_out_13, byte_7_out_15, byte_7_out_17, byte_7_out_19, byte_7_out_21, byte_7_out_23,
       byte_7_out_25, byte_8_out_11, byte_8_out_13, byte_8_out_15, byte_8_out_17, byte_8_out_19,
       byte_8_out_21, byte_8_out_23, byte_8_out_25, byte_9_out_11, byte_9_out_13, byte_9_out_15,
       byte_9_out_17, byte_9_out_19, byte_9_out_21, byte_9_out_23, byte_9_out_25, byte_10_out_11,
       byte_10_out_13, byte_10_out_15, byte_10_out_17, byte_10_out_19, byte_10_out_21, byte_10_out_23,
       byte_10_out_25, byte_11_out_11, byte_11_out_13, byte_11_out_15, byte_11_out_17, byte_11_out_19,
       byte_11_out_21, byte_11_out_23, byte_11_out_25, byte_12_out_11, byte_12_out_13, byte_12_out_15,
       byte_12_out_17, byte_12_out_19, byte_12_out_21, byte_12_out_23, byte_12_out_25, byte_13_out_11,
       byte_13_out_13, byte_13_out_15, byte_13_out_17, byte_13_out_19, byte_13_out_21, byte_13_out_23,
       byte_13_out_25, byte_14_out_11, byte_14_out_13, byte_14_out_15, byte_14_out_17, byte_14_out_19,
       byte_14_out_21, byte_14_out_23, byte_14_out_25, byte_15_out_11, byte_15_out_13, byte_15_out_15,
       byte_15_out_17, byte_15_out_19, byte_15_out_21, byte_15_out_23, byte_15_out_25, byte_16_out_11,
       byte_16_out_13, byte_16_out_15, byte_16_out_17, byte_16_out_19, byte_16_out_21, byte_16_out_23,
       byte_16_out_25, n8_bit_condition_gate_1_out_10, n8_bit_condition_gate_1_out_11,
       n8_bit_condition_gate_1_out_12, n8_bit_condition_gate_1_out_13, n8_bit_condition_gate_1_out_14,
       n8_bit_condition_gate_1_out_15, n8_bit_condition_gate_1_out_16, n8_bit_condition_gate_1_out_17,
       n8_bit_condition_gate_2_out_10, n8_bit_condition_gate_2_out_11, n8_bit_condition_gate_2_out_12,
       n8_bit_condition_gate_2_out_13, n8_bit_condition_gate_2_out_14, n8_bit_condition_gate_2_out_15,
       n8_bit_condition_gate_2_out_16, n8_bit_condition_gate_2_out_17, n8_bit_condition_gate_3_out_10,
       n8_bit_condition_gate_3_out_11, n8_bit_condition_gate_3_out_12, n8_bit_condition_gate_3_out_13,
       n8_bit_condition_gate_3_out_14, n8_bit_condition_gate_3_out_15, n8_bit_condition_gate_3_out_16,
       n8_bit_condition_gate_3_out_17, n8_bit_condition_gate_4_out_10, n8_bit_condition_gate_4_out_11,
       n8_bit_condition_gate_4_out_12, n8_bit_condition_gate_4_out_13, n8_bit_condition_gate_4_out_14,
       n8_bit_condition_gate_4_out_15, n8_bit_condition_gate_4_out_16, n8_bit_condition_gate_4_out_17,
       n8_bit_condition_gate_5_out_10, n8_bit_condition_gate_5_out_11, n8_bit_condition_gate_5_out_12,
       n8_bit_condition_gate_5_out_13, n8_bit_condition_gate_5_out_14, n8_bit_condition_gate_5_out_15,
       n8_bit_condition_gate_5_out_16, n8_bit_condition_gate_5_out_17, n8_bit_condition_gate_6_out_10,
       n8_bit_condition_gate_6_out_11, n8_bit_condition_gate_6_out_12, n8_bit_condition_gate_6_out_13,
       n8_bit_condition_gate_6_out_14, n8_bit_condition_gate_6_out_15, n8_bit_condition_gate_6_out_16,
       n8_bit_condition_gate_6_out_17, n8_bit_condition_gate_7_out_10, n8_bit_condition_gate_7_out_11,
       n8_bit_condition_gate_7_out_12, n8_bit_condition_gate_7_out_13, n8_bit_condition_gate_7_out_14,
       n8_bit_condition_gate_7_out_15, n8_bit_condition_gate_7_out_16, n8_bit_condition_gate_7_out_17,
       n8_bit_condition_gate_8_out_10, n8_bit_condition_gate_8_out_11, n8_bit_condition_gate_8_out_12,
       n8_bit_condition_gate_8_out_13, n8_bit_condition_gate_8_out_14, n8_bit_condition_gate_8_out_15,
       n8_bit_condition_gate_8_out_16, n8_bit_condition_gate_8_out_17, n8_bit_condition_gate_9_out_10,
       n8_bit_condition_gate_9_out_11, n8_bit_condition_gate_9_out_12, n8_bit_condition_gate_9_out_13,
       n8_bit_condition_gate_9_out_14, n8_bit_condition_gate_9_out_15, n8_bit_condition_gate_9_out_16,
       n8_bit_condition_gate_9_out_17, n8_bit_condition_gate_10_out_10, n8_bit_condition_gate_10_out_11,
       n8_bit_condition_gate_10_out_12, n8_bit_condition_gate_10_out_13, n8_bit_condition_gate_10_out_14,
       n8_bit_condition_gate_10_out_15, n8_bit_condition_gate_10_out_16, n8_bit_condition_gate_10_out_17,
       n8_bit_condition_gate_11_out_10, n8_bit_condition_gate_11_out_11, n8_bit_condition_gate_11_out_12,
       n8_bit_condition_gate_11_out_13, n8_bit_condition_gate_11_out_14, n8_bit_condition_gate_11_out_15,
       n8_bit_condition_gate_11_out_16, n8_bit_condition_gate_11_out_17, n8_bit_condition_gate_12_out_10,
       n8_bit_condition_gate_12_out_11, n8_bit_condition_gate_12_out_12, n8_bit_condition_gate_12_out_13,
       n8_bit_condition_gate_12_out_14, n8_bit_condition_gate_12_out_15, n8_bit_condition_gate_12_out_16,
       n8_bit_condition_gate_12_out_17, n8_bit_condition_gate_13_out_10, n8_bit_condition_gate_13_out_11,
       n8_bit_condition_gate_13_out_12, n8_bit_condition_gate_13_out_13, n8_bit_condition_gate_13_out_14,
       n8_bit_condition_gate_13_out_15, n8_bit_condition_gate_13_out_16, n8_bit_condition_gate_13_out_17,
       n8_bit_condition_gate_14_out_10, n8_bit_condition_gate_14_out_11, n8_bit_condition_gate_14_out_12,
       n8_bit_condition_gate_14_out_13, n8_bit_condition_gate_14_out_14, n8_bit_condition_gate_14_out_15,
       n8_bit_condition_gate_14_out_16, n8_bit_condition_gate_14_out_17, n8_bit_condition_gate_15_out_10,
       n8_bit_condition_gate_15_out_11, n8_bit_condition_gate_15_out_12, n8_bit_condition_gate_15_out_13,
       n8_bit_condition_gate_15_out_14, n8_bit_condition_gate_15_out_15, n8_bit_condition_gate_15_out_16,
       n8_bit_condition_gate_15_out_17, n8_bit_condition_gate_16_out_10, n8_bit_condition_gate_16_out_11,
       n8_bit_condition_gate_16_out_12, n8_bit_condition_gate_16_out_13, n8_bit_condition_gate_16_out_14,
       n8_bit_condition_gate_16_out_15, n8_bit_condition_gate_16_out_16, n8_bit_condition_gate_16_out_17,
       n8_bit_condition_gate_17_out_10, n8_bit_condition_gate_17_out_11, n8_bit_condition_gate_17_out_12,
       n8_bit_condition_gate_17_out_13, n8_bit_condition_gate_17_out_14, n8_bit_condition_gate_17_out_15,
       n8_bit_condition_gate_17_out_16, n8_bit_condition_gate_17_out_17, n8_bit_condition_gate_18_out_10,
       n8_bit_condition_gate_18_out_11, n8_bit_condition_gate_18_out_12, n8_bit_condition_gate_18_out_13,
       n8_bit_condition_gate_18_out_14, n8_bit_condition_gate_18_out_15, n8_bit_condition_gate_18_out_16,
       n8_bit_condition_gate_18_out_17, n8_bit_condition_gate_19_out_10, n8_bit_condition_gate_19_out_11,
       n8_bit_condition_gate_19_out_12, n8_bit_condition_gate_19_out_13, n8_bit_condition_gate_19_out_14,
       n8_bit_condition_gate_19_out_15, n8_bit_condition_gate_19_out_16, n8_bit_condition_gate_19_out_17,
       n8_bit_condition_gate_20_out_10, n8_bit_condition_gate_20_out_11, n8_bit_condition_gate_20_out_12,
       n8_bit_condition_gate_20_out_13, n8_bit_condition_gate_20_out_14, n8_bit_condition_gate_20_out_15,
       n8_bit_condition_gate_20_out_16, n8_bit_condition_gate_20_out_17, n8_bit_condition_gate_21_out_10,
       n8_bit_condition_gate_21_out_11, n8_bit_condition_gate_21_out_12, n8_bit_condition_gate_21_out_13,
       n8_bit_condition_gate_21_out_14, n8_bit_condition_gate_21_out_15, n8_bit_condition_gate_21_out_16,
       n8_bit_condition_gate_21_out_17, n8_bit_condition_gate_22_out_10, n8_bit_condition_gate_22_out_11,
       n8_bit_condition_gate_22_out_12, n8_bit_condition_gate_22_out_13, n8_bit_condition_gate_22_out_14,
       n8_bit_condition_gate_22_out_15, n8_bit_condition_gate_22_out_16, n8_bit_condition_gate_22_out_17,
       n8_bit_condition_gate_23_out_10, n8_bit_condition_gate_23_out_11, n8_bit_condition_gate_23_out_12,
       n8_bit_condition_gate_23_out_13, n8_bit_condition_gate_23_out_14, n8_bit_condition_gate_23_out_15,
       n8_bit_condition_gate_23_out_16, n8_bit_condition_gate_23_out_17, n8_bit_condition_gate_24_out_10,
       n8_bit_condition_gate_24_out_11, n8_bit_condition_gate_24_out_12, n8_bit_condition_gate_24_out_13,
       n8_bit_condition_gate_24_out_14, n8_bit_condition_gate_24_out_15, n8_bit_condition_gate_24_out_16,
       n8_bit_condition_gate_24_out_17, n8_bit_condition_gate_25_out_10, n8_bit_condition_gate_25_out_11,
       n8_bit_condition_gate_25_out_12, n8_bit_condition_gate_25_out_13, n8_bit_condition_gate_25_out_14,
       n8_bit_condition_gate_25_out_15, n8_bit_condition_gate_25_out_16, n8_bit_condition_gate_25_out_17,
       n8_bit_condition_gate_26_out_10, n8_bit_condition_gate_26_out_11, n8_bit_condition_gate_26_out_12,
       n8_bit_condition_gate_26_out_13, n8_bit_condition_gate_26_out_14, n8_bit_condition_gate_26_out_15,
       n8_bit_condition_gate_26_out_16, n8_bit_condition_gate_26_out_17, n8_bit_condition_gate_27_out_10,
       n8_bit_condition_gate_27_out_11, n8_bit_condition_gate_27_out_12, n8_bit_condition_gate_27_out_13,
       n8_bit_condition_gate_27_out_14, n8_bit_condition_gate_27_out_15, n8_bit_condition_gate_27_out_16,
       n8_bit_condition_gate_27_out_17, n8_bit_condition_gate_28_out_10, n8_bit_condition_gate_28_out_11,
       n8_bit_condition_gate_28_out_12, n8_bit_condition_gate_28_out_13, n8_bit_condition_gate_28_out_14,
       n8_bit_condition_gate_28_out_15, n8_bit_condition_gate_28_out_16, n8_bit_condition_gate_28_out_17,
       n8_bit_condition_gate_29_out_10, n8_bit_condition_gate_29_out_11, n8_bit_condition_gate_29_out_12,
       n8_bit_condition_gate_29_out_13, n8_bit_condition_gate_29_out_14, n8_bit_condition_gate_29_out_15,
       n8_bit_condition_gate_29_out_16, n8_bit_condition_gate_29_out_17, n8_bit_condition_gate_30_out_10,
       n8_bit_condition_gate_30_out_11, n8_bit_condition_gate_30_out_12, n8_bit_condition_gate_30_out_13,
       n8_bit_condition_gate_30_out_14, n8_bit_condition_gate_30_out_15, n8_bit_condition_gate_30_out_16,
       n8_bit_condition_gate_30_out_17, n8_bit_condition_gate_31_out_10, n8_bit_condition_gate_31_out_11,
       n8_bit_condition_gate_31_out_12, n8_bit_condition_gate_31_out_13, n8_bit_condition_gate_31_out_14,
       n8_bit_condition_gate_31_out_15, n8_bit_condition_gate_31_out_16, n8_bit_condition_gate_31_out_17,
       n8_bit_condition_gate_32_out_10, n8_bit_condition_gate_32_out_11, n8_bit_condition_gate_32_out_12,
       n8_bit_condition_gate_32_out_13, n8_bit_condition_gate_32_out_14, n8_bit_condition_gate_32_out_15,
       n8_bit_condition_gate_32_out_16, n8_bit_condition_gate_32_out_17, not_1_out, not_2_out, not_3_out,
       not_4_out, not_5_out, not_6_out, not_7_out, not_8_out, not_9_out, not_10_out, not_11_out, not_12_out,
       not_13_out, not_14_out, not_15_out, not_16_out, or_2_out, or_3_out, or_4_out, or_5_out, or_6_out,
       or_7_out, or_8_out, or_9_out, or_10_out, or_11_out, or_12_out, or_13_out, or_14_out, or_15_out,
       or_16_out, or_19_out, or_20_out, or_21_out, or_22_out, or_23_out, or_24_out, or_25_out, or_26_out,
       or_27_out, or_28_out, or_29_out, or_30_out, or_31_out, or_32_out, or_34_out, or_35_out, or_36_out,
       or_37_out, or_38_out, or_39_out, or_40_out, or_41_out, or_42_out, or_43_out, or_44_out, or_45_out,
       or_46_out, or_47_out, or_48_out, or_51_out, or_52_out, or_53_out, or_54_out, or_55_out, or_56_out,
       or_57_out, or_58_out, or_59_out, or_60_out, or_61_out, or_62_out, or_63_out, or_64_out, or_65_out,
       or_66_out, or_67_out, or_68_out, or_69_out, or_70_out, or_71_out, or_72_out, or_73_out, or_74_out,
       or_75_out, or_76_out, or_77_out, or_78_out, or_79_out, or_80_out, or_83_out, or_84_out, or_85_out,
       or_86_out, or_87_out, or_88_out, or_89_out, or_90_out, or_91_out, or_92_out, or_93_out, or_94_out,
       or_95_out, or_96_out, or_97_out, or_98_out, or_99_out, or_100_out, or_101_out, or_102_out, or_103_out,
       or_104_out, or_105_out, or_106_out, or_107_out, or_108_out, or_109_out, or_110_out, or_111_out,
       or_112_out, or_114_out, or_115_out, or_116_out, or_117_out, or_118_out, or_119_out, or_120_out,
       or_121_out, or_122_out, or_123_out, or_124_out, or_125_out, or_126_out, or_127_out, or_128_out;

  not not_1 (not_1_out, _1for_write_mode);
  and and_1 (and_1_out, not_1_out, in_11);
  and and_2 (and_2_out, in_11, _1for_write_mode);
  not not_2 (not_2_out, _1for_write_mode);
  and and_3 (and_3_out, not_2_out, in_12);
  and and_4 (and_4_out, in_12, _1for_write_mode);
  not not_3 (not_3_out, _1for_write_mode);
  and and_5 (and_5_out, not_3_out, in_13);
  and and_6 (and_6_out, in_13, _1for_write_mode);
  not not_4 (not_4_out, _1for_write_mode);
  and and_7 (and_7_out, not_4_out, in_14);
  and and_8 (and_8_out, in_14, _1for_write_mode);
  not not_5 (not_5_out, _1for_write_mode);
  and and_9 (and_9_out, not_5_out, in_15);
  and and_10 (and_10_out, in_15, _1for_write_mode);
  not not_6 (not_6_out, _1for_write_mode);
  and and_11 (and_11_out, not_6_out, in_16);
  and and_12 (and_12_out, in_16, _1for_write_mode);
  not not_7 (not_7_out, _1for_write_mode);
  and and_13 (and_13_out, not_7_out, in_17);
  and and_14 (and_14_out, in_17, _1for_write_mode);
  not not_8 (not_8_out, _1for_write_mode);
  and and_15 (and_15_out, not_8_out, in_18);
  and and_16 (and_16_out, in_18, _1for_write_mode);
  not not_9 (not_9_out, _1for_write_mode);
  and and_17 (and_17_out, not_9_out, in_19);
  and and_18 (and_18_out, in_19, _1for_write_mode);
  not not_10 (not_10_out, _1for_write_mode);
  and and_19 (and_19_out, not_10_out, in_20);
  and and_20 (and_20_out, in_20, _1for_write_mode);
  not not_11 (not_11_out, _1for_write_mode);
  and and_21 (and_21_out, not_11_out, in_21);
  and and_22 (and_22_out, in_21, _1for_write_mode);
  not not_12 (not_12_out, _1for_write_mode);
  and and_23 (and_23_out, not_12_out, in_22);
  and and_24 (and_24_out, in_22, _1for_write_mode);
  not not_13 (not_13_out, _1for_write_mode);
  and and_25 (and_25_out, not_13_out, in_23);
  and and_26 (and_26_out, in_23, _1for_write_mode);
  not not_14 (not_14_out, _1for_write_mode);
  and and_27 (and_27_out, not_14_out, in_24);
  and and_28 (and_28_out, in_24, _1for_write_mode);
  not not_15 (not_15_out, _1for_write_mode);
  and and_29 (and_29_out, not_15_out, in_25);
  and and_30 (and_30_out, in_25, _1for_write_mode);
  not not_16 (not_16_out, _1for_write_mode);
  and and_31 (and_31_out, not_16_out, in_26);
  and and_32 (and_32_out, in_26, _1for_write_mode);
  \byte  byte_1 (
    .in_3(n8_bit_condition_gate_1_out_10), .in_4(n8_bit_condition_gate_1_out_11),
    .in_5(n8_bit_condition_gate_1_out_12), .in_6(n8_bit_condition_gate_1_out_13),
    .in_7(n8_bit_condition_gate_1_out_14), .in_8(n8_bit_condition_gate_1_out_15),
    .in_9(n8_bit_condition_gate_1_out_16), .in_10(n8_bit_condition_gate_1_out_17), .out_11(byte_1_out_11),
    .out_13(byte_1_out_13), .out_15(byte_1_out_15), .out_17(byte_1_out_17), .out_19(byte_1_out_19),
    .out_21(byte_1_out_21), .out_23(byte_1_out_23), .out_25(byte_1_out_25), .R_W(and_2_out), .Clock(in_1),
    .out_12(out_35), .out_14(out_36), .out_16(out_37), .out_18(out_38), .out_20(out_39), .out_22(out_40),
    .out_24(out_41), .out_26(out_42));
  _8_bit_condition_gate u_8_bit_condition_gate_1 (
    .Bit_7(in_3), .Bit_6(in_4), .Bit_5(in_5), .Bit_4(in_6), .Bit_3(in_7), .Bit_2(in_8), .Bit_1(in_9),
    .Bit_0(in_10), .out_10(n8_bit_condition_gate_1_out_10), .out_11(n8_bit_condition_gate_1_out_11),
    .out_12(n8_bit_condition_gate_1_out_12), .out_13(n8_bit_condition_gate_1_out_13),
    .out_14(n8_bit_condition_gate_1_out_14), .out_15(n8_bit_condition_gate_1_out_15),
    .out_16(n8_bit_condition_gate_1_out_16), .out_17(n8_bit_condition_gate_1_out_17), .Condition(and_2_out));
  _8_bit_condition_gate u_8_bit_condition_gate_2 (
    .Bit_7(in_3), .Bit_6(in_4), .Bit_5(in_5), .Bit_4(in_6), .Bit_3(in_7), .Bit_2(in_8), .Bit_1(in_9),
    .Bit_0(in_10), .out_10(n8_bit_condition_gate_2_out_10), .out_11(n8_bit_condition_gate_2_out_11),
    .out_12(n8_bit_condition_gate_2_out_12), .out_13(n8_bit_condition_gate_2_out_13),
    .out_14(n8_bit_condition_gate_2_out_14), .out_15(n8_bit_condition_gate_2_out_15),
    .out_16(n8_bit_condition_gate_2_out_16), .out_17(n8_bit_condition_gate_2_out_17), .Condition(and_4_out));
  \byte  byte_2 (
    .in_3(n8_bit_condition_gate_2_out_10), .in_4(n8_bit_condition_gate_2_out_11),
    .in_5(n8_bit_condition_gate_2_out_12), .in_6(n8_bit_condition_gate_2_out_13),
    .in_7(n8_bit_condition_gate_2_out_14), .in_8(n8_bit_condition_gate_2_out_15),
    .in_9(n8_bit_condition_gate_2_out_16), .in_10(n8_bit_condition_gate_2_out_17), .out_11(byte_2_out_11),
    .out_13(byte_2_out_13), .out_15(byte_2_out_15), .out_17(byte_2_out_17), .out_19(byte_2_out_19),
    .out_21(byte_2_out_21), .out_23(byte_2_out_23), .out_25(byte_2_out_25), .R_W(and_4_out), .Clock(in_1),
    .out_12(out_43), .out_14(out_44), .out_16(out_45), .out_18(out_46), .out_20(out_47), .out_22(out_48),
    .out_24(out_49), .out_26(out_50));
  _8_bit_condition_gate u_8_bit_condition_gate_3 (
    .Bit_7(in_3), .Bit_6(in_4), .Bit_5(in_5), .Bit_4(in_6), .Bit_3(in_7), .Bit_2(in_8), .Bit_1(in_9),
    .Bit_0(in_10), .out_10(n8_bit_condition_gate_3_out_10), .out_11(n8_bit_condition_gate_3_out_11),
    .out_12(n8_bit_condition_gate_3_out_12), .out_13(n8_bit_condition_gate_3_out_13),
    .out_14(n8_bit_condition_gate_3_out_14), .out_15(n8_bit_condition_gate_3_out_15),
    .out_16(n8_bit_condition_gate_3_out_16), .out_17(n8_bit_condition_gate_3_out_17), .Condition(and_6_out));
  \byte  byte_3 (
    .in_3(n8_bit_condition_gate_3_out_10), .in_4(n8_bit_condition_gate_3_out_11),
    .in_5(n8_bit_condition_gate_3_out_12), .in_6(n8_bit_condition_gate_3_out_13),
    .in_7(n8_bit_condition_gate_3_out_14), .in_8(n8_bit_condition_gate_3_out_15),
    .in_9(n8_bit_condition_gate_3_out_16), .in_10(n8_bit_condition_gate_3_out_17), .out_11(byte_3_out_11),
    .out_13(byte_3_out_13), .out_15(byte_3_out_15), .out_17(byte_3_out_17), .out_19(byte_3_out_19),
    .out_21(byte_3_out_21), .out_23(byte_3_out_23), .out_25(byte_3_out_25), .R_W(and_6_out), .Clock(in_1),
    .out_12(out_51), .out_14(out_52), .out_16(out_53), .out_18(out_54), .out_20(out_55), .out_22(out_56),
    .out_24(out_57), .out_26(out_58));
  \byte  byte_4 (
    .in_3(n8_bit_condition_gate_4_out_10), .in_4(n8_bit_condition_gate_4_out_11),
    .in_5(n8_bit_condition_gate_4_out_12), .in_6(n8_bit_condition_gate_4_out_13),
    .in_7(n8_bit_condition_gate_4_out_14), .in_8(n8_bit_condition_gate_4_out_15),
    .in_9(n8_bit_condition_gate_4_out_16), .in_10(n8_bit_condition_gate_4_out_17), .out_11(byte_4_out_11),
    .out_13(byte_4_out_13), .out_15(byte_4_out_15), .out_17(byte_4_out_17), .out_19(byte_4_out_19),
    .out_21(byte_4_out_21), .out_23(byte_4_out_23), .out_25(byte_4_out_25), .R_W(and_8_out), .Clock(in_1),
    .out_12(out_59), .out_14(out_60), .out_16(out_61), .out_18(out_62), .out_20(out_63), .out_22(out_64),
    .out_24(out_65), .out_26(out_66));
  _8_bit_condition_gate u_8_bit_condition_gate_4 (
    .Bit_7(in_3), .Bit_6(in_4), .Bit_5(in_5), .Bit_4(in_6), .Bit_3(in_7), .Bit_2(in_8), .Bit_1(in_9),
    .Bit_0(in_10), .out_10(n8_bit_condition_gate_4_out_10), .out_11(n8_bit_condition_gate_4_out_11),
    .out_12(n8_bit_condition_gate_4_out_12), .out_13(n8_bit_condition_gate_4_out_13),
    .out_14(n8_bit_condition_gate_4_out_14), .out_15(n8_bit_condition_gate_4_out_15),
    .out_16(n8_bit_condition_gate_4_out_16), .out_17(n8_bit_condition_gate_4_out_17), .Condition(and_8_out));
  \byte  byte_5 (
    .in_3(n8_bit_condition_gate_5_out_10), .in_4(n8_bit_condition_gate_5_out_11),
    .in_5(n8_bit_condition_gate_5_out_12), .in_6(n8_bit_condition_gate_5_out_13),
    .in_7(n8_bit_condition_gate_5_out_14), .in_8(n8_bit_condition_gate_5_out_15),
    .in_9(n8_bit_condition_gate_5_out_16), .in_10(n8_bit_condition_gate_5_out_17), .out_11(byte_5_out_11),
    .out_13(byte_5_out_13), .out_15(byte_5_out_15), .out_17(byte_5_out_17), .out_19(byte_5_out_19),
    .out_21(byte_5_out_21), .out_23(byte_5_out_23), .out_25(byte_5_out_25), .R_W(and_10_out), .Clock(in_1),
    .out_12(out_67), .out_14(out_68), .out_16(out_69), .out_18(out_70), .out_20(out_71), .out_22(out_72),
    .out_24(out_73), .out_26(out_74));
  _8_bit_condition_gate u_8_bit_condition_gate_5 (
    .Bit_7(in_3), .Bit_6(in_4), .Bit_5(in_5), .Bit_4(in_6), .Bit_3(in_7), .Bit_2(in_8), .Bit_1(in_9),
    .Bit_0(in_10), .out_10(n8_bit_condition_gate_5_out_10), .out_11(n8_bit_condition_gate_5_out_11),
    .out_12(n8_bit_condition_gate_5_out_12), .out_13(n8_bit_condition_gate_5_out_13),
    .out_14(n8_bit_condition_gate_5_out_14), .out_15(n8_bit_condition_gate_5_out_15),
    .out_16(n8_bit_condition_gate_5_out_16), .out_17(n8_bit_condition_gate_5_out_17), .Condition(and_10_out));
  \byte  byte_6 (
    .in_3(n8_bit_condition_gate_6_out_10), .in_4(n8_bit_condition_gate_6_out_11),
    .in_5(n8_bit_condition_gate_6_out_12), .in_6(n8_bit_condition_gate_6_out_13),
    .in_7(n8_bit_condition_gate_6_out_14), .in_8(n8_bit_condition_gate_6_out_15),
    .in_9(n8_bit_condition_gate_6_out_16), .in_10(n8_bit_condition_gate_6_out_17), .out_11(byte_6_out_11),
    .out_13(byte_6_out_13), .out_15(byte_6_out_15), .out_17(byte_6_out_17), .out_19(byte_6_out_19),
    .out_21(byte_6_out_21), .out_23(byte_6_out_23), .out_25(byte_6_out_25), .R_W(and_12_out), .Clock(in_1),
    .out_12(out_75), .out_14(out_76), .out_16(out_77), .out_18(out_78), .out_20(out_79), .out_22(out_80),
    .out_24(out_81), .out_26(out_82));
  _8_bit_condition_gate u_8_bit_condition_gate_6 (
    .Bit_7(in_3), .Bit_6(in_4), .Bit_5(in_5), .Bit_4(in_6), .Bit_3(in_7), .Bit_2(in_8), .Bit_1(in_9),
    .Bit_0(in_10), .out_10(n8_bit_condition_gate_6_out_10), .out_11(n8_bit_condition_gate_6_out_11),
    .out_12(n8_bit_condition_gate_6_out_12), .out_13(n8_bit_condition_gate_6_out_13),
    .out_14(n8_bit_condition_gate_6_out_14), .out_15(n8_bit_condition_gate_6_out_15),
    .out_16(n8_bit_condition_gate_6_out_16), .out_17(n8_bit_condition_gate_6_out_17), .Condition(and_12_out));
  \byte  byte_7 (
    .in_3(n8_bit_condition_gate_7_out_10), .in_4(n8_bit_condition_gate_7_out_11),
    .in_5(n8_bit_condition_gate_7_out_12), .in_6(n8_bit_condition_gate_7_out_13),
    .in_7(n8_bit_condition_gate_7_out_14), .in_8(n8_bit_condition_gate_7_out_15),
    .in_9(n8_bit_condition_gate_7_out_16), .in_10(n8_bit_condition_gate_7_out_17), .out_11(byte_7_out_11),
    .out_13(byte_7_out_13), .out_15(byte_7_out_15), .out_17(byte_7_out_17), .out_19(byte_7_out_19),
    .out_21(byte_7_out_21), .out_23(byte_7_out_23), .out_25(byte_7_out_25), .R_W(and_14_out), .Clock(in_1),
    .out_12(out_83), .out_14(out_84), .out_16(out_85), .out_18(out_86), .out_20(out_87), .out_22(out_88),
    .out_24(out_89), .out_26(out_90));
  _8_bit_condition_gate u_8_bit_condition_gate_7 (
    .Bit_7(in_3), .Bit_6(in_4), .Bit_5(in_5), .Bit_4(in_6), .Bit_3(in_7), .Bit_2(in_8), .Bit_1(in_9),
    .Bit_0(in_10), .out_10(n8_bit_condition_gate_7_out_10), .out_11(n8_bit_condition_gate_7_out_11),
    .out_12(n8_bit_condition_gate_7_out_12), .out_13(n8_bit_condition_gate_7_out_13),
    .out_14(n8_bit_condition_gate_7_out_14), .out_15(n8_bit_condition_gate_7_out_15),
    .out_16(n8_bit_condition_gate_7_out_16), .out_17(n8_bit_condition_gate_7_out_17), .Condition(and_14_out));
  \byte  byte_8 (
    .in_3(n8_bit_condition_gate_8_out_10), .in_4(n8_bit_condition_gate_8_out_11),
    .in_5(n8_bit_condition_gate_8_out_12), .in_6(n8_bit_condition_gate_8_out_13),
    .in_7(n8_bit_condition_gate_8_out_14), .in_8(n8_bit_condition_gate_8_out_15),
    .in_9(n8_bit_condition_gate_8_out_16), .in_10(n8_bit_condition_gate_8_out_17), .out_11(byte_8_out_11),
    .out_13(byte_8_out_13), .out_15(byte_8_out_15), .out_17(byte_8_out_17), .out_19(byte_8_out_19),
    .out_21(byte_8_out_21), .out_23(byte_8_out_23), .out_25(byte_8_out_25), .R_W(and_16_out), .Clock(in_1),
    .out_12(out_91), .out_14(out_92), .out_16(out_93), .out_18(out_94), .out_20(out_95), .out_22(out_96),
    .out_24(out_97), .out_26(out_98));
  _8_bit_condition_gate u_8_bit_condition_gate_8 (
    .Bit_7(in_3), .Bit_6(in_4), .Bit_5(in_5), .Bit_4(in_6), .Bit_3(in_7), .Bit_2(in_8), .Bit_1(in_9),
    .Bit_0(in_10), .out_10(n8_bit_condition_gate_8_out_10), .out_11(n8_bit_condition_gate_8_out_11),
    .out_12(n8_bit_condition_gate_8_out_12), .out_13(n8_bit_condition_gate_8_out_13),
    .out_14(n8_bit_condition_gate_8_out_14), .out_15(n8_bit_condition_gate_8_out_15),
    .out_16(n8_bit_condition_gate_8_out_16), .out_17(n8_bit_condition_gate_8_out_17), .Condition(and_16_out));
  \byte  byte_9 (
    .in_3(n8_bit_condition_gate_9_out_10), .in_4(n8_bit_condition_gate_9_out_11),
    .in_5(n8_bit_condition_gate_9_out_12), .in_6(n8_bit_condition_gate_9_out_13),
    .in_7(n8_bit_condition_gate_9_out_14), .in_8(n8_bit_condition_gate_9_out_15),
    .in_9(n8_bit_condition_gate_9_out_16), .in_10(n8_bit_condition_gate_9_out_17), .out_11(byte_9_out_11),
    .out_13(byte_9_out_13), .out_15(byte_9_out_15), .out_17(byte_9_out_17), .out_19(byte_9_out_19),
    .out_21(byte_9_out_21), .out_23(byte_9_out_23), .out_25(byte_9_out_25), .R_W(and_18_out), .Clock(in_1),
    .out_12(out_99), .out_14(out_100), .out_16(out_101), .out_18(out_102), .out_20(out_103),
    .out_22(out_104), .out_24(out_105), .out_26(out_106));
  _8_bit_condition_gate u_8_bit_condition_gate_9 (
    .Bit_7(in_3), .Bit_6(in_4), .Bit_5(in_5), .Bit_4(in_6), .Bit_3(in_7), .Bit_2(in_8), .Bit_1(in_9),
    .Bit_0(in_10), .out_10(n8_bit_condition_gate_9_out_10), .out_11(n8_bit_condition_gate_9_out_11),
    .out_12(n8_bit_condition_gate_9_out_12), .out_13(n8_bit_condition_gate_9_out_13),
    .out_14(n8_bit_condition_gate_9_out_14), .out_15(n8_bit_condition_gate_9_out_15),
    .out_16(n8_bit_condition_gate_9_out_16), .out_17(n8_bit_condition_gate_9_out_17), .Condition(and_18_out));
  _8_bit_condition_gate u_8_bit_condition_gate_10 (
    .Bit_7(in_3), .Bit_6(in_4), .Bit_5(in_5), .Bit_4(in_6), .Bit_3(in_7), .Bit_2(in_8), .Bit_1(in_9),
    .Bit_0(in_10), .out_10(n8_bit_condition_gate_10_out_10), .out_11(n8_bit_condition_gate_10_out_11),
    .out_12(n8_bit_condition_gate_10_out_12), .out_13(n8_bit_condition_gate_10_out_13),
    .out_14(n8_bit_condition_gate_10_out_14), .out_15(n8_bit_condition_gate_10_out_15),
    .out_16(n8_bit_condition_gate_10_out_16), .out_17(n8_bit_condition_gate_10_out_17), .Condition(and_20_out));
  \byte  byte_10 (
    .in_3(n8_bit_condition_gate_10_out_10), .in_4(n8_bit_condition_gate_10_out_11),
    .in_5(n8_bit_condition_gate_10_out_12), .in_6(n8_bit_condition_gate_10_out_13),
    .in_7(n8_bit_condition_gate_10_out_14), .in_8(n8_bit_condition_gate_10_out_15),
    .in_9(n8_bit_condition_gate_10_out_16), .in_10(n8_bit_condition_gate_10_out_17), .out_11(byte_10_out_11),
    .out_13(byte_10_out_13), .out_15(byte_10_out_15), .out_17(byte_10_out_17), .out_19(byte_10_out_19),
    .out_21(byte_10_out_21), .out_23(byte_10_out_23), .out_25(byte_10_out_25), .R_W(and_20_out),
    .Clock(in_1), .out_12(out_107), .out_14(out_108), .out_16(out_109), .out_18(out_110), .out_20(out_111),
    .out_22(out_112), .out_24(out_113), .out_26(out_114));
  _8_bit_condition_gate u_8_bit_condition_gate_11 (
    .Bit_7(in_3), .Bit_6(in_4), .Bit_5(in_5), .Bit_4(in_6), .Bit_3(in_7), .Bit_2(in_8), .Bit_1(in_9),
    .Bit_0(in_10), .out_10(n8_bit_condition_gate_11_out_10), .out_11(n8_bit_condition_gate_11_out_11),
    .out_12(n8_bit_condition_gate_11_out_12), .out_13(n8_bit_condition_gate_11_out_13),
    .out_14(n8_bit_condition_gate_11_out_14), .out_15(n8_bit_condition_gate_11_out_15),
    .out_16(n8_bit_condition_gate_11_out_16), .out_17(n8_bit_condition_gate_11_out_17), .Condition(and_22_out));
  \byte  byte_11 (
    .in_3(n8_bit_condition_gate_11_out_10), .in_4(n8_bit_condition_gate_11_out_11),
    .in_5(n8_bit_condition_gate_11_out_12), .in_6(n8_bit_condition_gate_11_out_13),
    .in_7(n8_bit_condition_gate_11_out_14), .in_8(n8_bit_condition_gate_11_out_15),
    .in_9(n8_bit_condition_gate_11_out_16), .in_10(n8_bit_condition_gate_11_out_17), .out_11(byte_11_out_11),
    .out_13(byte_11_out_13), .out_15(byte_11_out_15), .out_17(byte_11_out_17), .out_19(byte_11_out_19),
    .out_21(byte_11_out_21), .out_23(byte_11_out_23), .out_25(byte_11_out_25), .R_W(and_22_out),
    .Clock(in_1), .out_12(out_115), .out_14(out_116), .out_16(out_117), .out_18(out_118), .out_20(out_119),
    .out_22(out_120), .out_24(out_121), .out_26(out_122));
  \byte  byte_12 (
    .in_3(n8_bit_condition_gate_12_out_10), .in_4(n8_bit_condition_gate_12_out_11),
    .in_5(n8_bit_condition_gate_12_out_12), .in_6(n8_bit_condition_gate_12_out_13),
    .in_7(n8_bit_condition_gate_12_out_14), .in_8(n8_bit_condition_gate_12_out_15),
    .in_9(n8_bit_condition_gate_12_out_16), .in_10(n8_bit_condition_gate_12_out_17), .out_11(byte_12_out_11),
    .out_13(byte_12_out_13), .out_15(byte_12_out_15), .out_17(byte_12_out_17), .out_19(byte_12_out_19),
    .out_21(byte_12_out_21), .out_23(byte_12_out_23), .out_25(byte_12_out_25), .R_W(and_24_out),
    .Clock(in_1), .out_12(out_123), .out_14(out_124), .out_16(out_125), .out_18(out_126), .out_20(out_127),
    .out_22(out_128), .out_24(out_129), .out_26(out_130));
  _8_bit_condition_gate u_8_bit_condition_gate_12 (
    .Bit_7(in_3), .Bit_6(in_4), .Bit_5(in_5), .Bit_4(in_6), .Bit_3(in_7), .Bit_2(in_8), .Bit_1(in_9),
    .Bit_0(in_10), .out_10(n8_bit_condition_gate_12_out_10), .out_11(n8_bit_condition_gate_12_out_11),
    .out_12(n8_bit_condition_gate_12_out_12), .out_13(n8_bit_condition_gate_12_out_13),
    .out_14(n8_bit_condition_gate_12_out_14), .out_15(n8_bit_condition_gate_12_out_15),
    .out_16(n8_bit_condition_gate_12_out_16), .out_17(n8_bit_condition_gate_12_out_17), .Condition(and_24_out));
  \byte  byte_13 (
    .in_3(n8_bit_condition_gate_13_out_10), .in_4(n8_bit_condition_gate_13_out_11),
    .in_5(n8_bit_condition_gate_13_out_12), .in_6(n8_bit_condition_gate_13_out_13),
    .in_7(n8_bit_condition_gate_13_out_14), .in_8(n8_bit_condition_gate_13_out_15),
    .in_9(n8_bit_condition_gate_13_out_16), .in_10(n8_bit_condition_gate_13_out_17), .out_11(byte_13_out_11),
    .out_13(byte_13_out_13), .out_15(byte_13_out_15), .out_17(byte_13_out_17), .out_19(byte_13_out_19),
    .out_21(byte_13_out_21), .out_23(byte_13_out_23), .out_25(byte_13_out_25), .R_W(and_26_out),
    .Clock(in_1), .out_12(out_131), .out_14(out_132), .out_16(out_133), .out_18(out_134), .out_20(out_135),
    .out_22(out_136), .out_24(out_137), .out_26(out_138));
  _8_bit_condition_gate u_8_bit_condition_gate_13 (
    .Bit_7(in_3), .Bit_6(in_4), .Bit_5(in_5), .Bit_4(in_6), .Bit_3(in_7), .Bit_2(in_8), .Bit_1(in_9),
    .Bit_0(in_10), .out_10(n8_bit_condition_gate_13_out_10), .out_11(n8_bit_condition_gate_13_out_11),
    .out_12(n8_bit_condition_gate_13_out_12), .out_13(n8_bit_condition_gate_13_out_13),
    .out_14(n8_bit_condition_gate_13_out_14), .out_15(n8_bit_condition_gate_13_out_15),
    .out_16(n8_bit_condition_gate_13_out_16), .out_17(n8_bit_condition_gate_13_out_17), .Condition(and_26_out));
  _8_bit_condition_gate u_8_bit_condition_gate_14 (
    .Bit_7(in_3), .Bit_6(in_4), .Bit_5(in_5), .Bit_4(in_6), .Bit_3(in_7), .Bit_2(in_8), .Bit_1(in_9),
    .Bit_0(in_10), .out_10(n8_bit_condition_gate_14_out_10), .out_11(n8_bit_condition_gate_14_out_11),
    .out_12(n8_bit_condition_gate_14_out_12), .out_13(n8_bit_condition_gate_14_out_13),
    .out_14(n8_bit_condition_gate_14_out_14), .out_15(n8_bit_condition_gate_14_out_15),
    .out_16(n8_bit_condition_gate_14_out_16), .out_17(n8_bit_condition_gate_14_out_17), .Condition(and_28_out));
  \byte  byte_14 (
    .in_3(n8_bit_condition_gate_14_out_10), .in_4(n8_bit_condition_gate_14_out_11),
    .in_5(n8_bit_condition_gate_14_out_12), .in_6(n8_bit_condition_gate_14_out_13),
    .in_7(n8_bit_condition_gate_14_out_14), .in_8(n8_bit_condition_gate_14_out_15),
    .in_9(n8_bit_condition_gate_14_out_16), .in_10(n8_bit_condition_gate_14_out_17), .out_11(byte_14_out_11),
    .out_13(byte_14_out_13), .out_15(byte_14_out_15), .out_17(byte_14_out_17), .out_19(byte_14_out_19),
    .out_21(byte_14_out_21), .out_23(byte_14_out_23), .out_25(byte_14_out_25), .R_W(and_28_out),
    .Clock(in_1), .out_12(out_139), .out_14(out_140), .out_16(out_141), .out_18(out_142), .out_20(out_143),
    .out_22(out_144), .out_24(out_145), .out_26(out_146));
  \byte  byte_15 (
    .in_3(n8_bit_condition_gate_15_out_10), .in_4(n8_bit_condition_gate_15_out_11),
    .in_5(n8_bit_condition_gate_15_out_12), .in_6(n8_bit_condition_gate_15_out_13),
    .in_7(n8_bit_condition_gate_15_out_14), .in_8(n8_bit_condition_gate_15_out_15),
    .in_9(n8_bit_condition_gate_15_out_16), .in_10(n8_bit_condition_gate_15_out_17), .out_11(byte_15_out_11),
    .out_13(byte_15_out_13), .out_15(byte_15_out_15), .out_17(byte_15_out_17), .out_19(byte_15_out_19),
    .out_21(byte_15_out_21), .out_23(byte_15_out_23), .out_25(byte_15_out_25), .R_W(and_30_out),
    .Clock(in_1), .out_12(out_147), .out_14(out_148), .out_16(out_149), .out_18(out_150), .out_20(out_151),
    .out_22(out_152), .out_24(out_153), .out_26(out_154));
  _8_bit_condition_gate u_8_bit_condition_gate_15 (
    .Bit_7(in_3), .Bit_6(in_4), .Bit_5(in_5), .Bit_4(in_6), .Bit_3(in_7), .Bit_2(in_8), .Bit_1(in_9),
    .Bit_0(in_10), .out_10(n8_bit_condition_gate_15_out_10), .out_11(n8_bit_condition_gate_15_out_11),
    .out_12(n8_bit_condition_gate_15_out_12), .out_13(n8_bit_condition_gate_15_out_13),
    .out_14(n8_bit_condition_gate_15_out_14), .out_15(n8_bit_condition_gate_15_out_15),
    .out_16(n8_bit_condition_gate_15_out_16), .out_17(n8_bit_condition_gate_15_out_17), .Condition(and_30_out));
  \byte  byte_16 (
    .in_3(n8_bit_condition_gate_16_out_10), .in_4(n8_bit_condition_gate_16_out_11),
    .in_5(n8_bit_condition_gate_16_out_12), .in_6(n8_bit_condition_gate_16_out_13),
    .in_7(n8_bit_condition_gate_16_out_14), .in_8(n8_bit_condition_gate_16_out_15),
    .in_9(n8_bit_condition_gate_16_out_16), .in_10(n8_bit_condition_gate_16_out_17), .out_11(byte_16_out_11),
    .out_13(byte_16_out_13), .out_15(byte_16_out_15), .out_17(byte_16_out_17), .out_19(byte_16_out_19),
    .out_21(byte_16_out_21), .out_23(byte_16_out_23), .out_25(byte_16_out_25), .R_W(and_32_out),
    .Clock(in_1), .out_12(out_155), .out_14(out_156), .out_16(out_157), .out_18(out_158), .out_20(out_159),
    .out_22(out_160), .out_24(out_161), .out_26(out_162));
  _8_bit_condition_gate u_8_bit_condition_gate_16 (
    .Bit_7(in_3), .Bit_6(in_4), .Bit_5(in_5), .Bit_4(in_6), .Bit_3(in_7), .Bit_2(in_8), .Bit_1(in_9),
    .Bit_0(in_10), .out_10(n8_bit_condition_gate_16_out_10), .out_11(n8_bit_condition_gate_16_out_11),
    .out_12(n8_bit_condition_gate_16_out_12), .out_13(n8_bit_condition_gate_16_out_13),
    .out_14(n8_bit_condition_gate_16_out_14), .out_15(n8_bit_condition_gate_16_out_15),
    .out_16(n8_bit_condition_gate_16_out_16), .out_17(n8_bit_condition_gate_16_out_17), .Condition(and_32_out));
  or or_1 (out_27, n8_bit_condition_gate_17_out_10, or_2_out);
  _8_bit_condition_gate u_8_bit_condition_gate_17 (
    .Bit_7(byte_1_out_11), .Bit_6(byte_1_out_13), .Bit_5(byte_1_out_15), .Bit_4(byte_1_out_17),
    .Bit_3(byte_1_out_19), .Bit_2(byte_1_out_21), .Bit_1(byte_1_out_23), .Bit_0(byte_1_out_25),
    .out_10(n8_bit_condition_gate_17_out_10), .out_11(n8_bit_condition_gate_17_out_11),
    .out_12(n8_bit_condition_gate_17_out_12), .out_13(n8_bit_condition_gate_17_out_13),
    .out_14(n8_bit_condition_gate_17_out_14), .out_15(n8_bit_condition_gate_17_out_15),
    .out_16(n8_bit_condition_gate_17_out_16), .out_17(n8_bit_condition_gate_17_out_17), .Condition(and_1_out));
  or or_2 (or_2_out, n8_bit_condition_gate_18_out_10, or_3_out);
  _8_bit_condition_gate u_8_bit_condition_gate_18 (
    .Bit_7(byte_2_out_11), .Bit_6(byte_2_out_13), .Bit_5(byte_2_out_15), .Bit_4(byte_2_out_17),
    .Bit_3(byte_2_out_19), .Bit_2(byte_2_out_21), .Bit_1(byte_2_out_23), .Bit_0(byte_2_out_25),
    .out_10(n8_bit_condition_gate_18_out_10), .out_11(n8_bit_condition_gate_18_out_11),
    .out_12(n8_bit_condition_gate_18_out_12), .out_13(n8_bit_condition_gate_18_out_13),
    .out_14(n8_bit_condition_gate_18_out_14), .out_15(n8_bit_condition_gate_18_out_15),
    .out_16(n8_bit_condition_gate_18_out_16), .out_17(n8_bit_condition_gate_18_out_17), .Condition(and_3_out));
  or or_3 (or_3_out, n8_bit_condition_gate_19_out_10, or_4_out);
  _8_bit_condition_gate u_8_bit_condition_gate_19 (
    .Bit_7(byte_3_out_11), .Bit_6(byte_3_out_13), .Bit_5(byte_3_out_15), .Bit_4(byte_3_out_17),
    .Bit_3(byte_3_out_19), .Bit_2(byte_3_out_21), .Bit_1(byte_3_out_23), .Bit_0(byte_3_out_25),
    .out_10(n8_bit_condition_gate_19_out_10), .out_11(n8_bit_condition_gate_19_out_11),
    .out_12(n8_bit_condition_gate_19_out_12), .out_13(n8_bit_condition_gate_19_out_13),
    .out_14(n8_bit_condition_gate_19_out_14), .out_15(n8_bit_condition_gate_19_out_15),
    .out_16(n8_bit_condition_gate_19_out_16), .out_17(n8_bit_condition_gate_19_out_17), .Condition(and_5_out));
  or or_4 (or_4_out, n8_bit_condition_gate_20_out_10, or_5_out);
  _8_bit_condition_gate u_8_bit_condition_gate_20 (
    .Bit_7(byte_4_out_11), .Bit_6(byte_4_out_13), .Bit_5(byte_4_out_15), .Bit_4(byte_4_out_17),
    .Bit_3(byte_4_out_19), .Bit_2(byte_4_out_21), .Bit_1(byte_4_out_23), .Bit_0(byte_4_out_25),
    .out_10(n8_bit_condition_gate_20_out_10), .out_11(n8_bit_condition_gate_20_out_11),
    .out_12(n8_bit_condition_gate_20_out_12), .out_13(n8_bit_condition_gate_20_out_13),
    .out_14(n8_bit_condition_gate_20_out_14), .out_15(n8_bit_condition_gate_20_out_15),
    .out_16(n8_bit_condition_gate_20_out_16), .out_17(n8_bit_condition_gate_20_out_17), .Condition(and_7_out));
  or or_5 (or_5_out, n8_bit_condition_gate_21_out_10, or_6_out);
  _8_bit_condition_gate u_8_bit_condition_gate_21 (
    .Bit_7(byte_5_out_11), .Bit_6(byte_5_out_13), .Bit_5(byte_5_out_15), .Bit_4(byte_5_out_17),
    .Bit_3(byte_5_out_19), .Bit_2(byte_5_out_21), .Bit_1(byte_5_out_23), .Bit_0(byte_5_out_25),
    .out_10(n8_bit_condition_gate_21_out_10), .out_11(n8_bit_condition_gate_21_out_11),
    .out_12(n8_bit_condition_gate_21_out_12), .out_13(n8_bit_condition_gate_21_out_13),
    .out_14(n8_bit_condition_gate_21_out_14), .out_15(n8_bit_condition_gate_21_out_15),
    .out_16(n8_bit_condition_gate_21_out_16), .out_17(n8_bit_condition_gate_21_out_17), .Condition(and_9_out));
  or or_6 (or_6_out, n8_bit_condition_gate_22_out_10, or_7_out);
  _8_bit_condition_gate u_8_bit_condition_gate_22 (
    .Bit_7(byte_6_out_11), .Bit_6(byte_6_out_13), .Bit_5(byte_6_out_15), .Bit_4(byte_6_out_17),
    .Bit_3(byte_6_out_19), .Bit_2(byte_6_out_21), .Bit_1(byte_6_out_23), .Bit_0(byte_6_out_25),
    .out_10(n8_bit_condition_gate_22_out_10), .out_11(n8_bit_condition_gate_22_out_11),
    .out_12(n8_bit_condition_gate_22_out_12), .out_13(n8_bit_condition_gate_22_out_13),
    .out_14(n8_bit_condition_gate_22_out_14), .out_15(n8_bit_condition_gate_22_out_15),
    .out_16(n8_bit_condition_gate_22_out_16), .out_17(n8_bit_condition_gate_22_out_17), .Condition(and_11_out));
  or or_7 (or_7_out, n8_bit_condition_gate_23_out_10, or_8_out);
  _8_bit_condition_gate u_8_bit_condition_gate_23 (
    .Bit_7(byte_7_out_11), .Bit_6(byte_7_out_13), .Bit_5(byte_7_out_15), .Bit_4(byte_7_out_17),
    .Bit_3(byte_7_out_19), .Bit_2(byte_7_out_21), .Bit_1(byte_7_out_23), .Bit_0(byte_7_out_25),
    .out_10(n8_bit_condition_gate_23_out_10), .out_11(n8_bit_condition_gate_23_out_11),
    .out_12(n8_bit_condition_gate_23_out_12), .out_13(n8_bit_condition_gate_23_out_13),
    .out_14(n8_bit_condition_gate_23_out_14), .out_15(n8_bit_condition_gate_23_out_15),
    .out_16(n8_bit_condition_gate_23_out_16), .out_17(n8_bit_condition_gate_23_out_17), .Condition(and_13_out));
  or or_8 (or_8_out, n8_bit_condition_gate_24_out_10, or_9_out);
  _8_bit_condition_gate u_8_bit_condition_gate_24 (
    .Bit_7(byte_8_out_11), .Bit_6(byte_8_out_13), .Bit_5(byte_8_out_15), .Bit_4(byte_8_out_17),
    .Bit_3(byte_8_out_19), .Bit_2(byte_8_out_21), .Bit_1(byte_8_out_23), .Bit_0(byte_8_out_25),
    .out_10(n8_bit_condition_gate_24_out_10), .out_11(n8_bit_condition_gate_24_out_11),
    .out_12(n8_bit_condition_gate_24_out_12), .out_13(n8_bit_condition_gate_24_out_13),
    .out_14(n8_bit_condition_gate_24_out_14), .out_15(n8_bit_condition_gate_24_out_15),
    .out_16(n8_bit_condition_gate_24_out_16), .out_17(n8_bit_condition_gate_24_out_17), .Condition(and_15_out));
  or or_9 (or_9_out, n8_bit_condition_gate_25_out_10, or_10_out);
  _8_bit_condition_gate u_8_bit_condition_gate_25 (
    .Bit_7(byte_9_out_11), .Bit_6(byte_9_out_13), .Bit_5(byte_9_out_15), .Bit_4(byte_9_out_17),
    .Bit_3(byte_9_out_19), .Bit_2(byte_9_out_21), .Bit_1(byte_9_out_23), .Bit_0(byte_9_out_25),
    .out_10(n8_bit_condition_gate_25_out_10), .out_11(n8_bit_condition_gate_25_out_11),
    .out_12(n8_bit_condition_gate_25_out_12), .out_13(n8_bit_condition_gate_25_out_13),
    .out_14(n8_bit_condition_gate_25_out_14), .out_15(n8_bit_condition_gate_25_out_15),
    .out_16(n8_bit_condition_gate_25_out_16), .out_17(n8_bit_condition_gate_25_out_17), .Condition(and_17_out));
  or or_10 (or_10_out, n8_bit_condition_gate_26_out_10, or_11_out);
  _8_bit_condition_gate u_8_bit_condition_gate_26 (
    .Bit_7(byte_10_out_11), .Bit_6(byte_10_out_13), .Bit_5(byte_10_out_15), .Bit_4(byte_10_out_17),
    .Bit_3(byte_10_out_19), .Bit_2(byte_10_out_21), .Bit_1(byte_10_out_23), .Bit_0(byte_10_out_25),
    .out_10(n8_bit_condition_gate_26_out_10), .out_11(n8_bit_condition_gate_26_out_11),
    .out_12(n8_bit_condition_gate_26_out_12), .out_13(n8_bit_condition_gate_26_out_13),
    .out_14(n8_bit_condition_gate_26_out_14), .out_15(n8_bit_condition_gate_26_out_15),
    .out_16(n8_bit_condition_gate_26_out_16), .out_17(n8_bit_condition_gate_26_out_17), .Condition(and_19_out));
  or or_11 (or_11_out, n8_bit_condition_gate_27_out_10, or_12_out);
  _8_bit_condition_gate u_8_bit_condition_gate_27 (
    .Bit_7(byte_11_out_11), .Bit_6(byte_11_out_13), .Bit_5(byte_11_out_15), .Bit_4(byte_11_out_17),
    .Bit_3(byte_11_out_19), .Bit_2(byte_11_out_21), .Bit_1(byte_11_out_23), .Bit_0(byte_11_out_25),
    .out_10(n8_bit_condition_gate_27_out_10), .out_11(n8_bit_condition_gate_27_out_11),
    .out_12(n8_bit_condition_gate_27_out_12), .out_13(n8_bit_condition_gate_27_out_13),
    .out_14(n8_bit_condition_gate_27_out_14), .out_15(n8_bit_condition_gate_27_out_15),
    .out_16(n8_bit_condition_gate_27_out_16), .out_17(n8_bit_condition_gate_27_out_17), .Condition(and_21_out));
  or or_12 (or_12_out, n8_bit_condition_gate_28_out_10, or_13_out);
  _8_bit_condition_gate u_8_bit_condition_gate_28 (
    .Bit_7(byte_12_out_11), .Bit_6(byte_12_out_13), .Bit_5(byte_12_out_15), .Bit_4(byte_12_out_17),
    .Bit_3(byte_12_out_19), .Bit_2(byte_12_out_21), .Bit_1(byte_12_out_23), .Bit_0(byte_12_out_25),
    .out_10(n8_bit_condition_gate_28_out_10), .out_11(n8_bit_condition_gate_28_out_11),
    .out_12(n8_bit_condition_gate_28_out_12), .out_13(n8_bit_condition_gate_28_out_13),
    .out_14(n8_bit_condition_gate_28_out_14), .out_15(n8_bit_condition_gate_28_out_15),
    .out_16(n8_bit_condition_gate_28_out_16), .out_17(n8_bit_condition_gate_28_out_17), .Condition(and_23_out));
  or or_13 (or_13_out, n8_bit_condition_gate_29_out_10, or_14_out);
  _8_bit_condition_gate u_8_bit_condition_gate_29 (
    .Bit_7(byte_13_out_11), .Bit_6(byte_13_out_13), .Bit_5(byte_13_out_15), .Bit_4(byte_13_out_17),
    .Bit_3(byte_13_out_19), .Bit_2(byte_13_out_21), .Bit_1(byte_13_out_23), .Bit_0(byte_13_out_25),
    .out_10(n8_bit_condition_gate_29_out_10), .out_11(n8_bit_condition_gate_29_out_11),
    .out_12(n8_bit_condition_gate_29_out_12), .out_13(n8_bit_condition_gate_29_out_13),
    .out_14(n8_bit_condition_gate_29_out_14), .out_15(n8_bit_condition_gate_29_out_15),
    .out_16(n8_bit_condition_gate_29_out_16), .out_17(n8_bit_condition_gate_29_out_17), .Condition(and_25_out));
  or or_14 (or_14_out, n8_bit_condition_gate_30_out_10, or_15_out);
  _8_bit_condition_gate u_8_bit_condition_gate_30 (
    .Bit_7(byte_14_out_11), .Bit_6(byte_14_out_13), .Bit_5(byte_14_out_15), .Bit_4(byte_14_out_17),
    .Bit_3(byte_14_out_19), .Bit_2(byte_14_out_21), .Bit_1(byte_14_out_23), .Bit_0(byte_14_out_25),
    .out_10(n8_bit_condition_gate_30_out_10), .out_11(n8_bit_condition_gate_30_out_11),
    .out_12(n8_bit_condition_gate_30_out_12), .out_13(n8_bit_condition_gate_30_out_13),
    .out_14(n8_bit_condition_gate_30_out_14), .out_15(n8_bit_condition_gate_30_out_15),
    .out_16(n8_bit_condition_gate_30_out_16), .out_17(n8_bit_condition_gate_30_out_17), .Condition(and_27_out));
  or or_15 (or_15_out, n8_bit_condition_gate_31_out_10, or_16_out);
  _8_bit_condition_gate u_8_bit_condition_gate_31 (
    .Bit_7(byte_15_out_11), .Bit_6(byte_15_out_13), .Bit_5(byte_15_out_15), .Bit_4(byte_15_out_17),
    .Bit_3(byte_15_out_19), .Bit_2(byte_15_out_21), .Bit_1(byte_15_out_23), .Bit_0(byte_15_out_25),
    .out_10(n8_bit_condition_gate_31_out_10), .out_11(n8_bit_condition_gate_31_out_11),
    .out_12(n8_bit_condition_gate_31_out_12), .out_13(n8_bit_condition_gate_31_out_13),
    .out_14(n8_bit_condition_gate_31_out_14), .out_15(n8_bit_condition_gate_31_out_15),
    .out_16(n8_bit_condition_gate_31_out_16), .out_17(n8_bit_condition_gate_31_out_17), .Condition(and_29_out));
  buf or_16 (or_16_out, n8_bit_condition_gate_32_out_10);  // OR_Gate
  _8_bit_condition_gate u_8_bit_condition_gate_32 (
    .Bit_7(byte_16_out_11), .Bit_6(byte_16_out_13), .Bit_5(byte_16_out_15), .Bit_4(byte_16_out_17),
    .Bit_3(byte_16_out_19), .Bit_2(byte_16_out_21), .Bit_1(byte_16_out_23), .Bit_0(byte_16_out_25),
    .out_10(n8_bit_condition_gate_32_out_10), .out_11(n8_bit_condition_gate_32_out_11),
    .out_12(n8_bit_condition_gate_32_out_12), .out_13(n8_bit_condition_gate_32_out_13),
    .out_14(n8_bit_condition_gate_32_out_14), .out_15(n8_bit_condition_gate_32_out_15),
    .out_16(n8_bit_condition_gate_32_out_16), .out_17(n8_bit_condition_gate_32_out_17), .Condition(and_31_out));
  or or_17 (out_28, n8_bit_condition_gate_17_out_11, or_19_out);
  or or_18 (out_29, n8_bit_condition_gate_17_out_12, or_20_out);
  or or_19 (or_19_out, n8_bit_condition_gate_18_out_11, or_21_out);
  or or_20 (or_20_out, n8_bit_condition_gate_18_out_12, or_22_out);
  or or_21 (or_21_out, n8_bit_condition_gate_19_out_11, or_23_out);
  or or_22 (or_22_out, n8_bit_condition_gate_19_out_12, or_24_out);
  or or_23 (or_23_out, n8_bit_condition_gate_20_out_11, or_25_out);
  or or_24 (or_24_out, n8_bit_condition_gate_20_out_12, or_26_out);
  or or_25 (or_25_out, n8_bit_condition_gate_21_out_11, or_27_out);
  or or_26 (or_26_out, n8_bit_condition_gate_21_out_12, or_28_out);
  or or_27 (or_27_out, n8_bit_condition_gate_22_out_11, or_29_out);
  or or_28 (or_28_out, n8_bit_condition_gate_22_out_12, or_30_out);
  or or_29 (or_29_out, n8_bit_condition_gate_23_out_11, or_31_out);
  or or_30 (or_30_out, n8_bit_condition_gate_23_out_12, or_32_out);
  or or_31 (or_31_out, n8_bit_condition_gate_24_out_11, n8_bit_condition_gate_24_out_13);
  or or_32 (or_32_out, n8_bit_condition_gate_24_out_12, or_34_out);
  or or_33 (n8_bit_condition_gate_24_out_13, n8_bit_condition_gate_25_out_11, or_35_out);
  or or_34 (or_34_out, n8_bit_condition_gate_25_out_12, or_36_out);
  or or_35 (or_35_out, n8_bit_condition_gate_26_out_11, or_37_out);
  or or_36 (or_36_out, n8_bit_condition_gate_26_out_12, or_38_out);
  or or_37 (or_37_out, n8_bit_condition_gate_27_out_11, or_39_out);
  or or_38 (or_38_out, n8_bit_condition_gate_27_out_12, or_40_out);
  or or_39 (or_39_out, n8_bit_condition_gate_28_out_11, or_41_out);
  or or_40 (or_40_out, n8_bit_condition_gate_28_out_12, or_42_out);
  or or_41 (or_41_out, n8_bit_condition_gate_29_out_11, or_43_out);
  or or_42 (or_42_out, n8_bit_condition_gate_29_out_12, or_44_out);
  or or_43 (or_43_out, n8_bit_condition_gate_30_out_11, or_45_out);
  or or_44 (or_44_out, n8_bit_condition_gate_30_out_12, or_46_out);
  or or_45 (or_45_out, n8_bit_condition_gate_31_out_11, or_47_out);
  or or_46 (or_46_out, n8_bit_condition_gate_31_out_12, or_48_out);
  buf or_47 (or_47_out, n8_bit_condition_gate_32_out_11);  // OR_Gate
  buf or_48 (or_48_out, n8_bit_condition_gate_32_out_12);  // OR_Gate
  or or_49 (out_30, n8_bit_condition_gate_17_out_13, or_51_out);
  or or_50 (out_31, n8_bit_condition_gate_17_out_14, or_52_out);
  or or_51 (or_51_out, n8_bit_condition_gate_18_out_13, or_53_out);
  or or_52 (or_52_out, n8_bit_condition_gate_18_out_14, or_54_out);
  or or_53 (or_53_out, n8_bit_condition_gate_19_out_13, or_55_out);
  or or_54 (or_54_out, n8_bit_condition_gate_19_out_14, or_56_out);
  or or_55 (or_55_out, n8_bit_condition_gate_20_out_13, or_57_out);
  or or_56 (or_56_out, n8_bit_condition_gate_20_out_14, or_58_out);
  or or_57 (or_57_out, n8_bit_condition_gate_21_out_13, or_59_out);
  or or_58 (or_58_out, n8_bit_condition_gate_21_out_14, or_60_out);
  or or_59 (or_59_out, n8_bit_condition_gate_22_out_13, or_61_out);
  or or_60 (or_60_out, n8_bit_condition_gate_22_out_14, or_62_out);
  or or_61 (or_61_out, n8_bit_condition_gate_23_out_13, or_63_out);
  or or_62 (or_62_out, n8_bit_condition_gate_23_out_14, or_64_out);
  or or_63 (or_63_out, n8_bit_condition_gate_24_out_13, or_65_out);
  or or_64 (or_64_out, n8_bit_condition_gate_24_out_14, or_66_out);
  or or_65 (or_65_out, n8_bit_condition_gate_25_out_13, or_67_out);
  or or_66 (or_66_out, n8_bit_condition_gate_25_out_14, or_68_out);
  or or_67 (or_67_out, n8_bit_condition_gate_26_out_13, or_69_out);
  or or_68 (or_68_out, n8_bit_condition_gate_26_out_14, or_70_out);
  or or_69 (or_69_out, n8_bit_condition_gate_27_out_13, or_71_out);
  or or_70 (or_70_out, n8_bit_condition_gate_27_out_14, or_72_out);
  or or_71 (or_71_out, n8_bit_condition_gate_28_out_13, or_73_out);
  or or_72 (or_72_out, n8_bit_condition_gate_28_out_14, or_74_out);
  or or_73 (or_73_out, n8_bit_condition_gate_29_out_13, or_75_out);
  or or_74 (or_74_out, n8_bit_condition_gate_29_out_14, or_76_out);
  or or_75 (or_75_out, n8_bit_condition_gate_30_out_13, or_77_out);
  or or_76 (or_76_out, n8_bit_condition_gate_30_out_14, or_78_out);
  or or_77 (or_77_out, n8_bit_condition_gate_31_out_13, or_79_out);
  or or_78 (or_78_out, n8_bit_condition_gate_31_out_14, or_80_out);
  buf or_79 (or_79_out, n8_bit_condition_gate_32_out_13);  // OR_Gate
  buf or_80 (or_80_out, n8_bit_condition_gate_32_out_14);  // OR_Gate
  or or_81 (out_32, n8_bit_condition_gate_17_out_15, or_83_out);
  or or_82 (out_33, n8_bit_condition_gate_17_out_16, or_84_out);
  or or_83 (or_83_out, n8_bit_condition_gate_18_out_15, or_85_out);
  or or_84 (or_84_out, n8_bit_condition_gate_18_out_16, or_86_out);
  or or_85 (or_85_out, n8_bit_condition_gate_19_out_15, or_87_out);
  or or_86 (or_86_out, n8_bit_condition_gate_19_out_16, or_88_out);
  or or_87 (or_87_out, n8_bit_condition_gate_20_out_15, or_89_out);
  or or_88 (or_88_out, n8_bit_condition_gate_20_out_16, or_90_out);
  or or_89 (or_89_out, n8_bit_condition_gate_21_out_15, or_91_out);
  or or_90 (or_90_out, n8_bit_condition_gate_21_out_16, or_92_out);
  or or_91 (or_91_out, n8_bit_condition_gate_22_out_15, or_93_out);
  or or_92 (or_92_out, n8_bit_condition_gate_22_out_16, or_94_out);
  or or_93 (or_93_out, n8_bit_condition_gate_23_out_15, or_95_out);
  or or_94 (or_94_out, n8_bit_condition_gate_23_out_16, or_96_out);
  or or_95 (or_95_out, n8_bit_condition_gate_24_out_15, or_97_out);
  or or_96 (or_96_out, n8_bit_condition_gate_24_out_16, or_98_out);
  or or_97 (or_97_out, n8_bit_condition_gate_25_out_15, or_99_out);
  or or_98 (or_98_out, n8_bit_condition_gate_25_out_16, or_100_out);
  or or_99 (or_99_out, n8_bit_condition_gate_26_out_15, or_101_out);
  or or_100 (or_100_out, n8_bit_condition_gate_26_out_16, or_102_out);
  or or_101 (or_101_out, n8_bit_condition_gate_27_out_15, or_103_out);
  or or_102 (or_102_out, n8_bit_condition_gate_27_out_16, or_104_out);
  or or_103 (or_103_out, n8_bit_condition_gate_28_out_15, or_105_out);
  or or_104 (or_104_out, n8_bit_condition_gate_28_out_16, or_106_out);
  or or_105 (or_105_out, n8_bit_condition_gate_29_out_15, or_107_out);
  or or_106 (or_106_out, n8_bit_condition_gate_29_out_16, or_108_out);
  or or_107 (or_107_out, n8_bit_condition_gate_30_out_15, or_109_out);
  or or_108 (or_108_out, n8_bit_condition_gate_30_out_16, or_110_out);
  or or_109 (or_109_out, n8_bit_condition_gate_31_out_15, or_111_out);
  or or_110 (or_110_out, n8_bit_condition_gate_31_out_16, or_112_out);
  buf or_111 (or_111_out, n8_bit_condition_gate_32_out_15);  // OR_Gate
  buf or_112 (or_112_out, n8_bit_condition_gate_32_out_16);  // OR_Gate
  or or_113 (out_34, n8_bit_condition_gate_17_out_17, or_114_out);
  or or_114 (or_114_out, n8_bit_condition_gate_18_out_17, or_115_out);
  or or_115 (or_115_out, n8_bit_condition_gate_19_out_17, or_116_out);
  or or_116 (or_116_out, n8_bit_condition_gate_20_out_17, or_117_out);
  or or_117 (or_117_out, n8_bit_condition_gate_21_out_17, or_118_out);
  or or_118 (or_118_out, n8_bit_condition_gate_22_out_17, or_119_out);
  or or_119 (or_119_out, n8_bit_condition_gate_23_out_17, or_120_out);
  or or_120 (or_120_out, n8_bit_condition_gate_24_out_17, or_121_out);
  or or_121 (or_121_out, n8_bit_condition_gate_25_out_17, or_122_out);
  or or_122 (or_122_out, n8_bit_condition_gate_26_out_17, or_123_out);
  or or_123 (or_123_out, n8_bit_condition_gate_27_out_17, or_124_out);
  or or_124 (or_124_out, n8_bit_condition_gate_28_out_17, or_125_out);
  or or_125 (or_125_out, n8_bit_condition_gate_29_out_17, or_126_out);
  or or_126 (or_126_out, n8_bit_condition_gate_30_out_17, or_127_out);
  or or_127 (or_127_out, n8_bit_condition_gate_31_out_17, or_128_out);
  buf or_128 (or_128_out, n8_bit_condition_gate_32_out_17);  // OR_Gate
endmodule

module \byte  (
  input  R_W,
  input  Clock,
  input  in_3,
  input  in_4,
  input  in_5,
  input  in_6,
  input  in_7,
  input  in_8,
  input  in_9,
  input  in_10,
  output out_11,
  output out_12,
  output out_13,
  output out_14,
  output out_15,
  output out_16,
  output out_17,
  output out_18,
  output out_19,
  output out_20,
  output out_21,
  output out_22,
  output out_23,
  output out_24,
  output out_25,
  output out_26
);

  wire and_1_out, and_2_out, and_3_out, and_4_out, and_5_out, and_6_out, and_7_out, and_8_out, and_9_out,
       and_10_out, and_11_out, and_12_out, and_13_out, and_14_out, and_15_out, and_16_out, not_1_out,
       or_1_out, or_2_out, or_3_out, or_4_out, or_5_out, or_6_out, or_7_out, or_8_out;

  not not_1 (not_1_out, R_W);
  and and_1 (and_1_out, out_12, not_1_out);
  or or_1 (or_1_out, and_1_out, and_2_out);
  and and_2 (and_2_out, R_W, in_3);
  and and_3 (and_3_out, out_14, not_1_out);
  or or_2 (or_2_out, and_3_out, and_4_out);
  and and_4 (and_4_out, R_W, in_4);
  and and_5 (and_5_out, out_16, not_1_out);
  or or_3 (or_3_out, and_5_out, and_6_out);
  and and_6 (and_6_out, R_W, in_5);
  and and_7 (and_7_out, out_18, not_1_out);
  or or_4 (or_4_out, and_7_out, and_8_out);
  and and_8 (and_8_out, R_W, in_6);
  and and_9 (and_9_out, out_20, not_1_out);
  or or_5 (or_5_out, and_9_out, and_10_out);
  and and_10 (and_10_out, R_W, in_7);
  and and_11 (and_11_out, out_22, not_1_out);
  or or_6 (or_6_out, and_11_out, and_12_out);
  and and_12 (and_12_out, R_W, in_8);
  and and_13 (and_13_out, out_24, not_1_out);
  or or_7 (or_7_out, and_13_out, and_14_out);
  and and_14 (and_14_out, R_W, in_9);
  and and_15 (and_15_out, out_26, not_1_out);
  or or_8 (or_8_out, and_15_out, and_16_out);
  and and_16 (and_16_out, R_W, in_10);
  D_Flip_Flop d_ff_1 (.clk(Clock), .D(or_1_out), .Q(out_12));  // open: Qn, preset, en, reset
  D_Flip_Flop d_ff_2 (.clk(Clock), .D(or_2_out), .Q(out_14));  // open: Qn, preset, en, reset
  D_Flip_Flop d_ff_3 (.clk(Clock), .D(or_3_out), .Q(out_16));  // open: Qn, preset, en, reset
  D_Flip_Flop d_ff_4 (.clk(Clock), .D(or_4_out), .Q(out_18));  // open: Qn, preset, en, reset
  D_Flip_Flop d_ff_5 (.clk(Clock), .D(or_5_out), .Q(out_20));  // open: Qn, preset, en, reset
  D_Flip_Flop d_ff_6 (.clk(Clock), .D(or_6_out), .Q(out_22));  // open: Qn, preset, en, reset
  D_Flip_Flop d_ff_7 (.clk(Clock), .D(or_7_out), .Q(out_24));  // open: Qn, preset, en, reset
  D_Flip_Flop d_ff_8 (.clk(Clock), .D(or_8_out), .Q(out_26));  // open: Qn, preset, en, reset
  and and_17 (out_11, not_1_out, out_12);
  and and_18 (out_13, not_1_out, out_14);
  and and_19 (out_15, not_1_out, out_16);
  and and_20 (out_17, not_1_out, out_18);
  and and_21 (out_19, not_1_out, out_20);
  and and_22 (out_21, not_1_out, out_22);
  and and_23 (out_23, not_1_out, out_24);
  and and_24 (out_25, not_1_out, out_26);
endmodule

module _8_bit_condition_gate (
  input  Condition,
  input  Bit_7,
  input  Bit_6,
  input  Bit_5,
  input  Bit_4,
  input  Bit_3,
  input  Bit_2,
  input  Bit_1,
  input  Bit_0,
  output out_10,
  output out_11,
  output out_12,
  output out_13,
  output out_14,
  output out_15,
  output out_16,
  output out_17
);

  and and_1 (out_10, Condition, Bit_7);
  and and_2 (out_11, Condition, Bit_6);
  and and_3 (out_12, Condition, Bit_5);
  and and_4 (out_13, Condition, Bit_4);
  and and_5 (out_14, Condition, Bit_3);
  and and_6 (out_15, Condition, Bit_2);
  and and_7 (out_16, Condition, Bit_1);
  and and_8 (out_17, Condition, Bit_0);
endmodule

module data_reg (
  input  Clock,
  input  R_W,
  input  in_3,
  input  in_4,
  input  in_5,
  input  in_6,
  input  in_7,
  input  in_8,
  input  in_9,
  input  in_10,
  input  in_11,
  input  in_12,
  input  in_13,
  input  in_14,
  input  in_15,
  input  in_16,
  input  in_17,
  input  in_18,
  output out_19,
  output out_20,
  output out_21,
  output out_22,
  output out_23,
  output out_24,
  output out_25,
  output out_26
);

  wire and_1_out, and_2_out, and_3_out, and_4_out, and_5_out, and_6_out, and_7_out, and_8_out, and_9_out,
       and_10_out, and_11_out, and_12_out, and_13_out, and_14_out, and_15_out, and_16_out, not_1_out,
       or_1_out, or_2_out, or_3_out, or_4_out, or_5_out, or_6_out, or_7_out, or_8_out;

  not not_1 (not_1_out, R_W);
  and and_1 (and_1_out, not_1_out, in_11);
  and and_2 (and_2_out, in_3, R_W);
  or or_1 (or_1_out, and_2_out, and_1_out);
  D_Flip_Flop d_ff_1 (.clk(Clock), .D(or_1_out), .Q(out_19));  // open: Qn, preset, en, reset
  and and_3 (and_3_out, not_1_out, in_12);
  and and_4 (and_4_out, in_4, R_W);
  or or_2 (or_2_out, and_4_out, and_3_out);
  and and_5 (and_5_out, not_1_out, in_13);
  and and_6 (and_6_out, in_5, R_W);
  or or_3 (or_3_out, and_6_out, and_5_out);
  D_Flip_Flop d_ff_2 (.clk(Clock), .D(or_2_out), .Q(out_20));  // open: Qn, preset, en, reset
  and and_7 (and_7_out, not_1_out, in_14);
  and and_8 (and_8_out, in_6, R_W);
  or or_4 (or_4_out, and_8_out, and_7_out);
  D_Flip_Flop d_ff_3 (.clk(Clock), .D(or_3_out), .Q(out_21));  // open: Qn, preset, en, reset
  and and_9 (and_9_out, in_7, R_W);
  or or_5 (or_5_out, and_9_out, and_11_out);
  D_Flip_Flop d_ff_4 (.clk(Clock), .D(or_4_out), .Q(out_22));  // open: Qn, preset, en, reset
  and and_10 (and_10_out, in_8, R_W);
  and and_11 (and_11_out, not_1_out, in_15);
  or or_6 (or_6_out, and_10_out, and_13_out);
  D_Flip_Flop d_ff_5 (.clk(Clock), .D(or_5_out), .Q(out_23));  // open: Qn, preset, en, reset
  and and_12 (and_12_out, in_9, R_W);
  and and_13 (and_13_out, not_1_out, in_16);
  D_Flip_Flop d_ff_6 (.clk(Clock), .D(or_6_out), .Q(out_24));  // open: Qn, preset, en, reset
  and and_14 (and_14_out, in_10, R_W);
  and and_15 (and_15_out, not_1_out, in_17);
  or or_7 (or_7_out, and_12_out, and_15_out);
  D_Flip_Flop d_ff_7 (.clk(Clock), .D(or_7_out), .Q(out_25));  // open: Qn, preset, en, reset
  and and_16 (and_16_out, not_1_out, in_18);
  or or_8 (or_8_out, and_14_out, and_16_out);
  D_Flip_Flop d_ff_8 (.clk(Clock), .D(or_8_out), .Q(out_26));  // open: Qn, preset, en, reset

  // Notes on the sheet:
  //   Manual input
endmodule

module rom (
  input  in_1,
  input  [7:0] in_2,
  input  [7:0] in_3,
  input  [7:0] in_4,
  input  [7:0] in_5,
  input  [7:0] in_6,
  input  [7:0] in_7,
  input  [7:0] in_8,
  input  [7:0] in_9,
  input  [7:0] in_10,
  input  [7:0] in_11,
  input  [7:0] in_12,
  input  [7:0] in_13,
  input  [7:0] in_14,
  input  [7:0] in_15,
  input  [7:0] in_16,
  input  [7:0] in_17,
  output [7:0] out_18,
  output [7:0] out_19,
  output [7:0] out_20,
  output [7:0] out_21,
  output [7:0] out_22,
  output [7:0] out_23,
  output [7:0] out_24,
  output [7:0] out_25,
  output [7:0] out_26,
  output [7:0] out_27,
  output [7:0] out_28,
  output [7:0] out_29,
  output [7:0] out_30,
  output [7:0] out_31,
  output [7:0] out_32,
  output [7:0] out_33
);

  byte_for_rom byte_for_rom_1 (.in_1(in_1), .in_2(in_2), .out_3(out_18));
  byte_for_rom byte_for_rom_2 (.in_1(in_1), .in_2(in_3), .out_3(out_19));
  byte_for_rom byte_for_rom_3 (.in_1(in_1), .in_2(in_4), .out_3(out_20));
  byte_for_rom byte_for_rom_4 (.in_1(in_1), .in_2(in_5), .out_3(out_21));
  byte_for_rom byte_for_rom_5 (.in_1(in_1), .in_2(in_6), .out_3(out_22));
  byte_for_rom byte_for_rom_6 (.in_1(in_1), .in_2(in_7), .out_3(out_23));
  byte_for_rom byte_for_rom_7 (.in_1(in_1), .in_2(in_8), .out_3(out_24));
  byte_for_rom byte_for_rom_8 (.in_1(in_1), .in_2(in_9), .out_3(out_25));
  byte_for_rom byte_for_rom_9 (.in_1(in_1), .in_2(in_10), .out_3(out_26));
  byte_for_rom byte_for_rom_10 (.in_1(in_1), .in_2(in_11), .out_3(out_27));
  byte_for_rom byte_for_rom_11 (.in_1(in_1), .in_2(in_12), .out_3(out_28));
  byte_for_rom byte_for_rom_12 (.in_1(in_1), .in_2(in_13), .out_3(out_29));
  byte_for_rom byte_for_rom_13 (.in_1(in_1), .in_2(in_14), .out_3(out_30));
  byte_for_rom byte_for_rom_14 (.in_1(in_1), .in_2(in_15), .out_3(out_31));
  byte_for_rom byte_for_rom_15 (.in_1(in_1), .in_2(in_16), .out_3(out_32));
  byte_for_rom byte_for_rom_16 (.in_1(in_1), .in_2(in_17), .out_3(out_33));

  // Notes on the sheet:
  //   Load Program Here
endmodule

module byte_for_rom (
  input  in_1,
  input  [7:0] in_2,
  output [7:0] out_3
);

  D_Flip_Flop d_ff_1 (.clk(in_1), .D(in_2[7]), .Q(out_3[7]));  // open: Qn, preset, en, reset
  D_Flip_Flop d_ff_2 (.clk(in_1), .D(in_2[6]), .Q(out_3[6]));  // open: Qn, preset, en, reset
  D_Flip_Flop d_ff_3 (.clk(in_1), .D(in_2[5]), .Q(out_3[5]));  // open: Qn, preset, en, reset
  D_Flip_Flop d_ff_4 (.clk(in_1), .D(in_2[4]), .Q(out_3[4]));  // open: Qn, preset, en, reset
  D_Flip_Flop d_ff_5 (.clk(in_1), .D(in_2[3]), .Q(out_3[3]));  // open: Qn, preset, en, reset
  D_Flip_Flop d_ff_6 (.clk(in_1), .D(in_2[1]), .Q(out_3[1]));  // open: Qn, preset, en, reset
  D_Flip_Flop d_ff_7 (.clk(in_1), .D(in_2[2]), .Q(out_3[2]));  // open: Qn, preset, en, reset
  D_Flip_Flop d_ff_8 (.clk(in_1), .D(in_2[0]), .Q(out_3[0]));  // open: Qn, preset, en, reset
endmodule

module compare (
  input  [7:0] in_1,
  input  [7:0] in_2,
  output out_3
);

  wire and_1_out, and_2_out, and_3_out, and_4_out, and_5_out, and_6_out, and_7_out, and_8_out;
  wire [7:0] not_1_out, not_2_out;

  assign not_1_out = ~in_1;  // NOT_Gate not_1, 8 bits wide
  assign not_2_out = ~in_2;  // NOT_Gate not_2, 8 bits wide
  and and_1 (and_1_out, not_1_out[0], not_2_out[0]);
  and and_2 (and_2_out, not_1_out[1], not_2_out[1]);
  and and_3 (and_3_out, not_1_out[2], not_2_out[2]);
  and and_4 (and_4_out, not_1_out[3], not_2_out[3]);
  and and_5 (and_5_out, not_2_out[4], not_1_out[4]);
  and and_6 (and_6_out, not_1_out[5], not_2_out[5]);
  and and_7 (and_7_out, not_1_out[6], not_2_out[6]);
  and and_8 (and_8_out, not_1_out[7], not_2_out[7]);
  and and_9 (out_3, and_1_out, and_2_out, and_3_out, and_5_out, and_6_out, and_7_out, and_8_out);
endmodule

module twoPC (
  input  Clk,
  output out_2,
  output out_3,
  output out_4,
  output out_5
);

  wire j_k_ff_1_q, j_k_ff_1_qn, j_k_ff_2_q, j_k_ff_2_qn, j_k_ff_3_q, j_k_ff_3_qn, j_k_ff_4_q, j_k_ff_4_qn;

  not not_1 (out_2, j_k_ff_1_q);
  J_K_Flip_Flop j_k_ff_1 (
    .J(j_k_ff_1_qn), .clk(Clk), .K(j_k_ff_1_q), .Q(j_k_ff_1_q), .Qn(j_k_ff_1_qn));  // open: preset, en, reset
  J_K_Flip_Flop j_k_ff_2 (
    .J(j_k_ff_2_qn), .clk(j_k_ff_1_q), .K(j_k_ff_2_q), .Q(j_k_ff_2_q), .Qn(j_k_ff_2_qn));  // open: preset, en, reset
  not not_2 (out_3, j_k_ff_2_q);
  J_K_Flip_Flop j_k_ff_3 (
    .J(j_k_ff_3_qn), .clk(j_k_ff_2_q), .K(j_k_ff_3_q), .Q(j_k_ff_3_q), .Qn(j_k_ff_3_qn));  // open: preset, en, reset
  not not_3 (out_4, j_k_ff_3_q);
  not not_4 (out_5, j_k_ff_4_q);
  J_K_Flip_Flop j_k_ff_4 (
    .J(j_k_ff_4_qn), .clk(j_k_ff_3_q), .K(j_k_ff_4_q), .Q(j_k_ff_4_q), .Qn(j_k_ff_4_qn));  // open: preset, en, reset
endmodule

module delay (
  input  in_1,
  output out_2
);

  wire d_ff_1_q, not_1_out, not_2_out;

  not not_1 (not_1_out, d_ff_1_q);
  D_Flip_Flop d_ff_1 (.clk(in_1), .D(not_1_out), .Q(d_ff_1_q), .en(in_1));  // open: Qn, preset, reset
  not not_2 (not_2_out, d_ff_1_q);
  S_R_Flip_Flop s_r_ff_1 (.S(d_ff_1_q), .clk(in_1), .R(not_2_out), .Q(out_2));  // open: Qn, preset, reset, en
endmodule

module _2_bit_adder (
  input  [1:0] in_1,
  input  [1:0] in_2,
  output [1:0] out_3,
  output out_4
);

  wire and_1_out, and_2_out, and_3_out, xor_2_out;

  xor xor_1 (out_3[0], in_1[0], in_2[0]);
  and and_1 (and_1_out, in_1[0], in_2[0]);
  xor xor_2 (xor_2_out, in_1[1], in_2[1]);
  and and_2 (and_2_out, in_1[1], in_2[1]);
  or or_1 (out_4, and_3_out, and_2_out);
  xor xor_3 (out_3[1], and_1_out, xor_2_out);
  and and_3 (and_3_out, and_1_out, xor_2_out);
endmodule

module _4_bit_adder (
  input  [3:0] in_1,
  input  [3:0] in_2,
  output [3:0] out_3,
  output C
);

  wire n2_bit_adder_2_out_4, n2_bit_adder_3_out_4;
  wire [1:0] n2_bit_adder_1_out_4, n2_bit_adder_2_out_3;

  _2_bit_adder u_2_bit_adder_1 (
    .in_1(in_1[1:0]), .in_2(in_2[1:0]), .out_3(out_3[1:0]), .out_4(n2_bit_adder_1_out_4[0]));
  _2_bit_adder u_2_bit_adder_2 (
    .in_1(in_1[3:2]), .in_2(in_2[3:2]), .out_3(n2_bit_adder_2_out_3), .out_4(n2_bit_adder_2_out_4));
  not not_1 (n2_bit_adder_1_out_4[1], 1'b1);
  _2_bit_adder u_2_bit_adder_3 (
    .in_1(n2_bit_adder_1_out_4), .in_2(n2_bit_adder_2_out_3), .out_3(out_3[3:2]), .out_4(n2_bit_adder_3_out_4));
  or or_1 (C, n2_bit_adder_3_out_4, n2_bit_adder_2_out_4);
endmodule

module _8_bit_adder (
  input  [7:0] in_1,
  input  [7:0] in_2,
  output [7:0] out_3,
  output out_4
);

  wire n4_bit_adder_2_c, n4_bit_adder_3_c;
  wire [3:0] n4_bit_adder_1_c, n4_bit_adder_2_out_3;

  _4_bit_adder u_4_bit_adder_1 (.in_1(in_1[3:0]), .in_2(in_2[3:0]), .out_3(out_3[3:0]), .C(n4_bit_adder_1_c[0]));
  _4_bit_adder u_4_bit_adder_2 (.in_1(in_1[7:4]), .in_2(in_2[7:4]), .out_3(n4_bit_adder_2_out_3), .C(n4_bit_adder_2_c));
  not not_1 (n4_bit_adder_1_c[3], 1'b1);
  _4_bit_adder u_4_bit_adder_3 (
    .in_1(n4_bit_adder_2_out_3), .in_2({{3{n4_bit_adder_1_c[3]}}, n4_bit_adder_1_c[0]}), .out_3(out_3[7:4]),
    .C(n4_bit_adder_3_c));
  or or_1 (out_4, n4_bit_adder_3_c, n4_bit_adder_2_c);
endmodule

module _16_bit_adder (
  input  [15:0] in_1,
  input  [15:0] in_2,
  output [15:0] out_3,
  output out_4
);

  wire n8_bit_adder_2_out_4, n8_bit_adder_3_out_4;
  wire [7:0] n8_bit_adder_1_out_4, n8_bit_adder_2_out_3;

  _8_bit_adder u_8_bit_adder_1 (
    .in_1(in_1[7:0]), .in_2(in_2[7:0]), .out_3(out_3[7:0]), .out_4(n8_bit_adder_1_out_4[0]));
  _8_bit_adder u_8_bit_adder_2 (
    .in_1(in_1[15:8]), .in_2(in_2[15:8]), .out_3(n8_bit_adder_2_out_3), .out_4(n8_bit_adder_2_out_4));
  not not_1 (n8_bit_adder_1_out_4[7], 1'b1);
  _8_bit_adder u_8_bit_adder_3 (
    .in_1({{7{n8_bit_adder_1_out_4[7]}}, n8_bit_adder_1_out_4[0]}), .in_2(n8_bit_adder_2_out_3),
    .out_3(out_3[15:8]), .out_4(n8_bit_adder_3_out_4));
  or or_1 (out_4, n8_bit_adder_3_out_4, n8_bit_adder_2_out_4);
endmodule

module _1x8_mult (
  input  in_1,
  input  [7:0] in_2,
  output [7:0] out_3
);

  and and_1 (out_3[0], in_1, in_2[0]);
  and and_2 (out_3[1], in_1, in_2[1]);
  and and_3 (out_3[2], in_1, in_2[2]);
  and and_4 (out_3[3], in_1, in_2[3]);
  and and_5 (out_3[4], in_1, in_2[4]);
  and and_6 (out_3[5], in_1, in_2[5]);
  and and_7 (out_3[6], in_1, in_2[6]);
  and and_8 (out_3[7], in_1, in_2[7]);
endmodule

module mult (
  input  [7:0] in_1,
  input  [7:0] in_2,
  output [15:0] out_3,
  output [7:0] out_4,
  output overflow
);

  wire [7:0] n1x8_mult_1_out_3, n1x8_mult_2_out_3, n1x8_mult_3_out_3, n1x8_mult_4_out_3, n1x8_mult_5_out_3,
       n1x8_mult_6_out_3, n1x8_mult_7_out_3, n1x8_mult_8_out_3;
  wire [15:0] n16_bit_adder_1_out_3, n16_bit_adder_2_out_3, n16_bit_adder_3_out_3, n16_bit_adder_4_out_3,
       n16_bit_adder_5_out_3, n16_bit_adder_6_out_3;
  wire [15:15] not_1_out, not_2_out, not_3_out, not_4_out, not_5_out, not_6_out, not_7_out, not_8_out;

  _1x8_mult u_1x8_mult_1 (.in_1(in_1[0]), .in_2(in_2), .out_3(n1x8_mult_1_out_3));
  _1x8_mult u_1x8_mult_2 (.in_1(in_1[1]), .in_2(in_2), .out_3(n1x8_mult_2_out_3));
  _1x8_mult u_1x8_mult_3 (.in_1(in_1[2]), .in_2(in_2), .out_3(n1x8_mult_3_out_3));
  _1x8_mult u_1x8_mult_4 (.in_1(in_1[3]), .in_2(in_2), .out_3(n1x8_mult_4_out_3));
  _1x8_mult u_1x8_mult_5 (.in_1(in_1[4]), .in_2(in_2), .out_3(n1x8_mult_5_out_3));
  _1x8_mult u_1x8_mult_6 (.in_1(in_1[5]), .in_2(in_2), .out_3(n1x8_mult_6_out_3));
  _1x8_mult u_1x8_mult_7 (.in_1(in_1[6]), .in_2(in_2), .out_3(n1x8_mult_7_out_3));
  _1x8_mult u_1x8_mult_8 (.in_1(in_1[7]), .in_2(in_2), .out_3(n1x8_mult_8_out_3));
  not not_1 (not_1_out[15], 1'b1);
  not not_2 (not_2_out[15], 1'b1);
  not not_3 (not_3_out[15], 1'b1);
  not not_4 (not_4_out[15], 1'b1);
  not not_5 (not_5_out[15], 1'b1);
  not not_6 (not_6_out[15], 1'b1);
  not not_7 (not_7_out[15], 1'b1);
  not not_8 (not_8_out[15], 1'b1);
  _16_bit_adder u_16_bit_adder_1 (
    .in_1({{8{not_1_out[15]}}, n1x8_mult_1_out_3}),
    .in_2({{7{not_2_out[15]}}, n1x8_mult_2_out_3, not_2_out[15]}), .out_3(n16_bit_adder_1_out_3));  // open: out_4
  _16_bit_adder u_16_bit_adder_2 (
    .in_1({{4{not_5_out[15]}}, n1x8_mult_5_out_3, {4{not_5_out[15]}}}),
    .in_2({{3{not_6_out[15]}}, n1x8_mult_6_out_3, {5{not_6_out[15]}}}), .out_3(n16_bit_adder_2_out_3));  // open: out_4
  _16_bit_adder u_16_bit_adder_3 (
    .in_1({{6{not_3_out[15]}}, n1x8_mult_3_out_3, {2{not_3_out[15]}}}),
    .in_2({{5{not_4_out[15]}}, n1x8_mult_4_out_3, {3{not_4_out[15]}}}), .out_3(n16_bit_adder_3_out_3));  // open: out_4
  _16_bit_adder u_16_bit_adder_4 (
    .in_1({{2{not_7_out[15]}}, n1x8_mult_7_out_3, {6{not_7_out[15]}}}),
    .in_2({not_8_out[15], n1x8_mult_8_out_3, {7{not_8_out[15]}}}), .out_3(n16_bit_adder_4_out_3));  // open: out_4
  _16_bit_adder u_16_bit_adder_5 (
    .in_1(n16_bit_adder_1_out_3), .in_2(n16_bit_adder_3_out_3), .out_3(n16_bit_adder_5_out_3));  // open: out_4
  _16_bit_adder u_16_bit_adder_6 (
    .in_1(n16_bit_adder_2_out_3), .in_2(n16_bit_adder_4_out_3), .out_3(n16_bit_adder_6_out_3));  // open: out_4
  _16_bit_adder u_16_bit_adder_7 (
    .in_1(n16_bit_adder_5_out_3), .in_2(n16_bit_adder_6_out_3), .out_3(out_3));  // open: out_4
  or or_1 (overflow, out_3[8], out_3[9], out_3[10], out_3[11], out_3[12], out_3[13], out_3[14], out_3[15]);

  assign out_4 = out_3[7:0];

  // Notes on the sheet:
  //   Input 1
  //   Input 2
  //   Output
endmodule

module buffer (
  input  [7:0] in_1,
  input  in_2,
  output [7:0] out_3
);

  wire not_1_out;

  not not_1 (not_1_out, in_2);
  and and_1 (out_3[7], not_1_out, in_1[7]);
  and and_2 (out_3[6], not_1_out, in_1[6]);
  and and_3 (out_3[5], not_1_out, in_1[5]);
  and and_4 (out_3[4], in_1[4], not_1_out);
  and and_5 (out_3[3], in_1[3], not_1_out);
  and and_6 (out_3[2], in_1[2], not_1_out);
  and and_7 (out_3[1], not_1_out, in_1[1]);
  and and_8 (out_3[0], not_1_out, in_1[0]);
endmodule
