// Logisim project 3-digit-display-2.circ as structural Verilog: 2 circuits, main circuit display
module _1_display (
  input  in_1,
  input  in_2,
  input  in_3,
  input  in_4,
  input  in_5,
  output out_6,
  output out_7,
  output out_8,
  output out_9,
  output out_10,
  output out_11,
  output out_12
);

  wire _0_out, _1_out, _2_out, _3_out, _4_out, _5_out, _6_out, _7_out, _8_out, _9_out, d_ff_1_q, d_ff_2_q,
       d_ff_3_q, d_ff_4_q, not_1_out, not_2_out, not_3_out, not_4_out, not_5_out, not_6_out, not_7_out,
       not_8_out, not_9_out, not_10_out, not_11_out, not_12_out, not_13_out, not_14_out, not_15_out,
       not_16_out, not_17_out, not_18_out, not_19_out, not_20_out, not_21_out, not_22_out, not_23_out,
       not_24_out, not_25_out;

  D_Flip_Flop d_ff_1 (.clk(in_1), .D(in_2), .Q(d_ff_1_q));  // open: Qn, preset, en, reset
  D_Flip_Flop d_ff_2 (.clk(in_1), .D(in_3), .Q(d_ff_2_q));  // open: Qn, preset, en, reset
  D_Flip_Flop d_ff_3 (.clk(in_1), .D(in_4), .Q(d_ff_3_q));  // open: Qn, preset, en, reset
  D_Flip_Flop d_ff_4 (.clk(in_1), .D(in_5), .Q(d_ff_4_q));  // open: Qn, preset, en, reset
  not not_1 (not_1_out, d_ff_4_q);
  not not_2 (not_2_out, d_ff_3_q);
  not not_3 (not_3_out, d_ff_2_q);
  not not_4 (not_4_out, d_ff_1_q);
  not not_5 (not_5_out, d_ff_3_q);
  not not_6 (not_6_out, d_ff_2_q);
  not not_7 (not_7_out, d_ff_1_q);
  not not_8 (not_8_out, d_ff_4_q);
  not not_9 (not_9_out, d_ff_2_q);
  not not_10 (not_10_out, d_ff_1_q);
  not not_11 (not_11_out, d_ff_2_q);
  not not_12 (not_12_out, d_ff_1_q);
  not not_13 (not_13_out, d_ff_4_q);
  not not_14 (not_14_out, d_ff_3_q);
  not not_15 (not_15_out, d_ff_1_q);
  not not_16 (not_16_out, d_ff_3_q);
  not not_17 (not_17_out, d_ff_1_q);
  not not_18 (not_18_out, d_ff_4_q);
  not not_19 (not_19_out, d_ff_1_q);
  not not_20 (not_20_out, d_ff_1_q);
  not not_21 (not_21_out, d_ff_4_q);
  not not_22 (not_22_out, d_ff_3_q);
  not not_23 (not_23_out, d_ff_2_q);
  not not_24 (not_24_out, d_ff_3_q);
  not not_25 (not_25_out, d_ff_2_q);
  and _0 (_0_out, not_1_out, not_2_out, not_3_out, not_4_out);
  and _1 (_1_out, d_ff_4_q, not_5_out, not_6_out, not_7_out);
  and _2 (_2_out, not_8_out, d_ff_3_q, not_9_out, not_10_out);
  and _3 (_3_out, d_ff_4_q, d_ff_3_q, not_11_out, not_12_out);
  and _4 (_4_out, not_13_out, not_14_out, d_ff_2_q, not_15_out);
  and _5 (_5_out, d_ff_4_q, not_16_out, d_ff_2_q, not_17_out);
  and _6 (_6_out, not_18_out, d_ff_3_q, d_ff_2_q, not_19_out);
  and _7 (_7_out, d_ff_4_q, d_ff_3_q, d_ff_2_q, not_20_out);
  and _8 (_8_out, not_21_out, not_22_out, not_23_out, d_ff_1_q);
  and _9 (_9_out, d_ff_4_q, not_24_out, not_25_out, d_ff_1_q);
  or or_1 (out_6, _0_out, _4_out, _5_out, _6_out, _8_out, _9_out);
  or or_2 (out_7, _0_out, _2_out, _3_out, _5_out, _7_out, _8_out, _9_out);
  or or_3 (out_8, _0_out, _1_out, _2_out, _3_out, _4_out, _7_out, _8_out, _9_out);
  or or_4 (out_9, _2_out, _3_out, _4_out, _5_out, _6_out, _8_out, _9_out);
  or or_5 (out_10, _0_out, _2_out, _6_out, _8_out);
  or or_6 (out_11, _0_out, _2_out, _3_out, _5_out, _6_out, _8_out);
  or or_7 (out_12, _0_out, _5_out, _1_out, _3_out, _9_out, _6_out, _4_out, _7_out, _8_out);
endmodule

module display (
  input  in_1,
  input  in_2,
  input  in_3,
  input  in_4,
  input  in_5,
  input  in_6,
  input  in_7,
  input  in_8,
  input  in_9,
  input  in_10,
  input  in_11,
  input  in_12
);

  wire clock_1_out, n1_display_1_out_6, n1_display_1_out_8, n1_display_1_out_9, n1_display_1_out_10,
       n1_display_1_out_11, n1_display_1_out_12, n1_display_2_out_6, n1_display_2_out_7, n1_display_2_out_8,
       n1_display_2_out_9, n1_display_2_out_10, n1_display_2_out_11, n1_display_2_out_12, n1_display_3_out_6,
       n1_display_3_out_7, n1_display_3_out_8, n1_display_3_out_9, n1_display_3_out_10, n1_display_3_out_11,
       n1_display_3_out_12;

  Clock clock_1 (.out(clock_1_out));
  _1_display u_1_display_1 (
    .in_2(in_1), .in_3(in_4), .in_4(in_7), .in_5(in_10), .out_6(n1_display_1_out_6),
    .out_7(n1_display_1_out_6), .out_8(n1_display_1_out_8), .out_9(n1_display_1_out_9),
    .out_10(n1_display_1_out_10), .out_11(n1_display_1_out_11), .out_12(n1_display_1_out_12),
    .in_1(clock_1_out));
  _7_Segment_Display u_7_segment_display_1 (
    .g(n1_display_1_out_9), .f(n1_display_1_out_6), .a(n1_display_1_out_6), .b(n1_display_1_out_8),
    .e(n1_display_1_out_10), .d(n1_display_1_out_11), .c(n1_display_1_out_12));  // open: dp
  _1_display u_1_display_2 (
    .in_2(in_2), .in_3(in_5), .in_4(in_8), .in_5(in_11), .out_6(n1_display_2_out_6),
    .out_7(n1_display_2_out_7), .out_8(n1_display_2_out_8), .out_9(n1_display_2_out_9),
    .out_10(n1_display_2_out_10), .out_11(n1_display_2_out_11), .out_12(n1_display_2_out_12),
    .in_1(clock_1_out));
  _7_Segment_Display u_7_segment_display_2 (
    .g(n1_display_2_out_9), .f(n1_display_2_out_6), .a(n1_display_2_out_7), .b(n1_display_2_out_8),
    .e(n1_display_2_out_10), .d(n1_display_2_out_11), .c(n1_display_2_out_12));  // open: dp
  _1_display u_1_display_3 (
    .in_2(in_3), .in_3(in_6), .in_4(in_9), .in_5(in_12), .out_6(n1_display_3_out_6),
    .out_7(n1_display_3_out_7), .out_8(n1_display_3_out_8), .out_9(n1_display_3_out_9),
    .out_10(n1_display_3_out_10), .out_11(n1_display_3_out_11), .out_12(n1_display_3_out_12),
    .in_1(clock_1_out));
  _7_Segment_Display u_7_segment_display_3 (
    .g(n1_display_3_out_9), .f(n1_display_3_out_6), .a(n1_display_3_out_7), .b(n1_display_3_out_8),
    .e(n1_display_3_out_10), .d(n1_display_3_out_11), .c(n1_display_3_out_12));  // open: dp
endmodule
