// Logisim project 3-digit-display.circ as structural Verilog: 4 circuits, main circuit display
module _1_display (
  input  in_1,
  input  in_2,
  input  in_3,
  input  in_4,
  input  in_5,
  output out_6,
  output out_7,
  output out_8,
  output out_9,
  output out_10,
  output out_11,
  output out_12
);

  wire _0_out, _1_out, _2_out, _3_out, _4_out, _5_out, _6_out, _7_out, _8_out, _9_out, d_ff_1_q, d_ff_2_q,
       d_ff_3_q, d_ff_4_q, not_1_out, not_2_out, not_3_out, not_4_out, not_5_out, not_6_out, not_7_out,
       not_8_out, not_9_out, not_10_out, not_11_out, not_12_out, not_13_out, not_14_out, not_15_out,
       not_16_out, not_17_out, not_18_out, not_19_out, not_20_out, not_21_out, not_22_out, not_23_out,
       not_24_out, not_25_out;

  D_Flip_Flop d_ff_1 (.clk(in_1), .D(in_2), .Q(d_ff_1_q));  // open: Qn, preset, en, reset
  D_Flip_Flop d_ff_2 (.clk(in_1), .D(in_3), .Q(d_ff_2_q));  // open: Qn, preset, en, reset
  D_Flip_Flop d_ff_3 (.clk(in_1), .D(in_4), .Q(d_ff_3_q));  // open: Qn, preset, en, reset
  D_Flip_Flop d_ff_4 (.clk(in_1), .D(in_5), .Q(d_ff_4_q));  // open: Qn, preset, en, reset
  not not_1 (not_1_out, d_ff_4_q);
  not not_2 (not_2_out, d_ff_3_q);
  not not_3 (not_3_out, d_ff_2_q);
  not not_4 (not_4_out, d_ff_1_q);
  not not_5 (not_5_out, d_ff_3_q);
  not not_6 (not_6_out, d_ff_2_q);
  not not_7 (not_7_out, d_ff_1_q);
  not not_8 (not_8_out, d_ff_4_q);
  not not_9 (not_9_out, d_ff_2_q);
  not not_10 (not_10_out, d_ff_1_q);
  not not_11 (not_11_out, d_ff_2_q);
  not not_12 (not_12_out, d_ff_1_q);
  not not_13 (not_13_out, d_ff_4_q);
  not not_14 (not_14_out, d_ff_3_q);
  not not_15 (not_15_out, d_ff_1_q);
  not not_16 (not_16_out, d_ff_3_q);
  not not_17 (not_17_out, d_ff_1_q);
  not not_18 (not_18_out, d_ff_4_q);
  not not_19 (not_19_out, d_ff_1_q);
  not not_20 (not_20_out, d_ff_1_q);
  not not_21 (not_21_out, d_ff_4_q);
  not not_22 (not_22_out, d_ff_3_q);
  not not_23 (not_23_out, d_ff_2_q);
  not not_24 (not_24_out, d_ff_3_q);
  not not_25 (not_25_out, d_ff_2_q);
  and _0 (_0_out, not_1_out, not_2_out, not_3_out, not_4_out);
  and _1 (_1_out, d_ff_4_q, not_5_out, not_6_out, not_7_out);
  and _2 (_2_out, not_8_out, d_ff_3_q, not_9_out, not_10_out);
  and _3 (_3_out, d_ff_4_q, d_ff_3_q, not_11_out, not_12_out);
  and _4 (_4_out, not_13_out, not_14_out, d_ff_2_q, not_15_out);
  and _5 (_5_out, d_ff_4_q, not_16_out, d_ff_2_q, not_17_out);
  and _6 (_6_out, not_18_out, d_ff_3_q, d_ff_2_q, not_19_out);
  and _7 (_7_out, d_ff_4_q, d_ff_3_q, d_ff_2_q, not_20_out);
  and _8 (_8_out, not_21_out, not_22_out, not_23_out, d_ff_1_q);
  and _9 (_9_out, d_ff_4_q, not_24_out, not_25_out, d_ff_1_q);
  or or_1 (out_6, _0_out, _4_out, _5_out, _6_out, _8_out, _9_out);
  or or_2 (out_7, _0_out, _2_out, _3_out, _5_out, _7_out, _8_out, _9_out);
  or or_3 (out_8, _0_out, _1_out, _2_out, _3_out, _4_out, _7_out, _8_out, _9_out);
  or or_4 (out_9, _2_out, _3_out, _4_out, _5_out, _6_out, _8_out, _9_out);
  or or_5 (out_10, _0_out, _2_out, _6_out, _8_out);
  or or_6 (out_11, _0_out, _2_out, _3_out, _5_out, _6_out, _8_out);
  or or_7 (out_12, _0_out, _5_out, _1_out, _3_out, _9_out, _6_out, _4_out, _7_out, _8_out);
endmodule

module display (
  input  in_1,
  input  in_2,
  input  in_3,
  input  in_4,
  input  in_5,
  input  in_6,
  input  in_7,
  input  in_8,
  input  deflut_zero,
  input  in_10,
  input  in_11,
  input  in_12,
  input  in_13,
  input  in_14,
  input  in_15,
  input  in_16,
  input  in_17,
  input  in_18,
  input  in_19,
  input  in_20,
  input  in_21,
  input  in_22,
  input  in_23,
  input  in_24,
  input  in_25,
  input  in_26,
  input  in_27,
  input  in_28,
  input  in_29,
  input  in_30,
  input  in_31,
  output out_32,
  output out_33,
  output out_34,
  output out_35,
  output out_36,
  output out_37,
  output out_38,
  output out_39,
  output out_40,
  output out_41,
  output out_42,
  output out_43,
  output out_44,
  output out_45,
  output out_46,
  output out_47,
  output out_48,
  output out_49,
  output out_50,
  output out_51,
  output out_52
);

  wire c_1_out_8, c_1_out_9, c_1_out_10, c_1_out_11, c_2_out_8, c_2_out_9, c_2_out_10, c_2_out_11, c_3_out_8,
       c_3_out_9, c_3_out_10, c_3_out_11, c_4_out_8, c_4_out_9, c_4_out_10, c_4_out_11, c_5_out_8, c_5_out_9,
       c_5_out_10, c_5_out_11, c_6_out_8, c_6_out_9, c_6_out_10, c_6_out_11, c_7_out_8, c_7_out_9,
       c_7_out_10, c_7_out_11;

  c c_1 (
    .in_1(deflut_zero), .in_2(in_1), .in_3(in_2), .in_4(in_3), .in_5(in_10), .in_6(in_11), .in_7(in_12),
    .out_8(c_1_out_8), .out_9(c_1_out_9), .out_10(c_1_out_10), .out_11(c_1_out_11));
  c c_2 (
    .in_1(deflut_zero), .in_2(c_1_out_8), .in_3(c_4_out_8), .in_4(c_5_out_8), .in_5(in_19), .in_6(in_21),
    .in_7(in_23), .out_8(c_2_out_8), .out_9(c_2_out_9), .out_10(c_2_out_10), .out_11(c_2_out_11));
  c c_3 (
    .in_1(c_2_out_9), .in_2(c_2_out_10), .in_3(c_2_out_11), .in_4(c_6_out_8), .in_5(in_25), .in_6(in_27),
    .in_7(in_29), .out_8(c_3_out_8), .out_9(c_3_out_9), .out_10(c_3_out_10), .out_11(c_3_out_11));
  c c_4 (
    .in_1(c_1_out_9), .in_2(c_1_out_10), .in_3(c_1_out_11), .in_4(in_4), .in_5(in_13), .in_6(in_14),
    .in_7(in_15), .out_8(c_4_out_8), .out_9(c_4_out_9), .out_10(c_4_out_10), .out_11(c_4_out_11));
  _1_display u_1_display_1 (
    .in_2(deflut_zero), .in_3(deflut_zero), .in_4(c_2_out_8), .in_5(c_3_out_8), .out_6(out_33),
    .out_7(out_34), .out_8(out_35), .out_9(out_32), .out_10(out_44), .out_11(out_46), .out_12(out_49),
    .in_1(in_31));
  c c_5 (
    .in_1(c_4_out_9), .in_2(c_4_out_10), .in_3(c_4_out_11), .in_4(in_5), .in_5(in_16), .in_6(in_17),
    .in_7(in_18), .out_8(c_5_out_8), .out_9(c_5_out_9), .out_10(c_5_out_10), .out_11(c_5_out_11));
  c c_6 (
    .in_1(c_5_out_9), .in_2(c_5_out_10), .in_3(c_5_out_11), .in_4(in_6), .in_5(in_20), .in_6(in_22),
    .in_7(in_24), .out_8(c_6_out_8), .out_9(c_6_out_9), .out_10(c_6_out_10), .out_11(c_6_out_11));
  c c_7 (
    .in_1(c_6_out_9), .in_2(c_6_out_10), .in_3(c_6_out_11), .in_4(in_7), .in_5(in_26), .in_6(in_28),
    .in_7(in_30), .out_8(c_7_out_8), .out_9(c_7_out_9), .out_10(c_7_out_10), .out_11(c_7_out_11));
  _1_display u_1_display_2 (
    .in_2(c_3_out_9), .in_3(c_3_out_10), .in_4(c_3_out_11), .in_5(c_7_out_8), .out_6(out_39), .out_7(out_40),
    .out_8(out_43), .out_9(out_36), .out_10(out_45), .out_11(out_47), .out_12(out_50), .in_1(in_31));
  _1_display u_1_display_3 (
    .in_2(c_7_out_9), .in_3(c_7_out_10), .in_4(c_7_out_11), .in_5(in_8), .out_6(out_37), .out_7(out_38),
    .out_8(out_42), .out_9(out_41), .out_10(out_48), .out_11(out_51), .out_12(out_52), .in_1(in_31));

  // Notes on the sheet:
  //   clock
endmodule

module c (
  input  in_1,
  input  in_2,
  input  in_3,
  input  in_4,
  input  in_5,
  input  in_6,
  input  in_7,
  output out_8,
  output out_9,
  output out_10,
  output out_11
);

  wire and_1_out, and_2_out, and_3_out, not_1_out, not_2_out, or_1_out, or_2_out;

  and and_1 (and_1_out, in_2, or_2_out);
  or or_1 (or_1_out, in_1, and_1_out);
  or or_2 (or_2_out, in_3, in_4);
  and and_2 (and_2_out, or_1_out, not_2_out);
  not not_1 (not_1_out, in_7);
  not not_2 (not_2_out, in_6);
  and and_3 (and_3_out, or_1_out, not_1_out);
  _3_bit_adding u_3_bit_adding_1 (
    .in_1(in_2), .left_register(in_3), .in_2(in_4), .right_register(in_5), .in_4(and_2_out),
    .in_5(and_3_out), .out_8(out_9), .out_9(out_10), .out_10(out_11), .out_7(out_8));
endmodule

module _3_bit_adding (
  input  in_1,
  input  in_2,
  input  right_register,
  input  in_4,
  input  in_5,
  input  left_register,
  output out_7,
  output out_8,
  output out_9,
  output out_10
);

  wire and_1_out, and_2_out, and_3_out, and_4_out, and_5_out, and_6_out, and_7_out, and_8_out, and_9_out,
       and_10_out, and_11_out, and_12_out, and_13_out, and_14_out, and_15_out, not_1_out, not_2_out,
       not_3_out, not_4_out, not_5_out, not_6_out, not_7_out, not_8_out, not_9_out, not_10_out, or_1_out,
       or_2_out, or_6_out;

  not not_1 (not_1_out, in_1);
  and and_1 (and_1_out, right_register, not_1_out);
  not not_2 (not_2_out, left_register);
  or or_1 (or_1_out, and_1_out, and_8_out);
  not not_3 (not_3_out, in_2);
  and and_2 (and_2_out, in_4, not_2_out);
  or or_2 (or_2_out, and_2_out, and_10_out);
  not not_4 (not_4_out, or_1_out);
  and and_3 (and_3_out, in_5, not_3_out);
  or or_3 (out_10, and_3_out, and_13_out);
  not not_5 (not_5_out, or_2_out);
  and and_4 (and_4_out, or_6_out, not_4_out);
  and and_5 (and_5_out, in_2, in_5);
  and and_6 (and_6_out, and_5_out, not_5_out);
  or or_4 (out_9, and_6_out, and_11_out);
  and and_7 (and_7_out, or_2_out, and_5_out);
  not not_6 (not_6_out, right_register);
  or or_5 (out_8, and_15_out, and_4_out);
  not not_7 (not_7_out, in_4);
  not not_8 (not_8_out, and_5_out);
  and and_8 (and_8_out, in_1, not_6_out);
  and and_9 (and_9_out, or_6_out, or_1_out);
  not not_9 (not_9_out, in_5);
  and and_10 (and_10_out, left_register, not_7_out);
  and and_11 (and_11_out, or_2_out, not_8_out);
  or or_6 (or_6_out, and_12_out, and_7_out);
  and and_12 (and_12_out, left_register, in_4);
  and and_13 (and_13_out, in_2, not_9_out);
  not not_10 (not_10_out, or_6_out);
  and and_14 (and_14_out, in_1, right_register);
  and and_15 (and_15_out, or_1_out, not_10_out);
  or or_7 (out_7, and_14_out, and_9_out);

  // Notes on the sheet:
  //   A-register
  //   sum1
  //   sum2
  //   carry1
  //   sum3
  //   carry2
  //   Adder
  //   carry3
  //   reporter
endmodule
