// Logisim project Adder-2.circ as structural Verilog: 1 circuit, main circuit main
module main (
  input  in_1,
  input  in_2,
  output out_3,
  output Carry
);

  xor xor_1 (out_3, in_1, in_2);
  and and_1 (Carry, in_1, in_2);

  // Notes on the sheet:
  //   1bit Adder
  //   Digit
endmodule
