// Logisim project CPUSTATE1.circ as structural Verilog: 26 circuits, main circuit Control Unit
module main (
  input  in_1,
  input  in_2,
  input  in_3,
  input  in_4,
  input  in_5,
  input  in_6,
  input  in_7,
  input  in_8,
  input  in_9,
  input  in_10,
  input  in_11
);

  wire ALU_3_out, ALU_4_out, ALU_5_out, ALU_6_out, ALU_7_out, ALU_8_out, ALU_out, and_1_out, and_2_out,
       and_3_out, and_4_out, and_5_out, and_6_out, and_7_out, and_8_out, and_9_out, BNZ_2_out, BNZ_out,
       branch_1_out_3, buffer_count_1_out_2, button_1_out, clock_1_out, clock_2_out, control_unit_1_add_d0,
       control_unit_1_add_d1, control_unit_1_bz_d0, control_unit_1_bz_d1, control_unit_1_inp_d0,
       control_unit_1_inp_d1, control_unit_1_lw_d0, control_unit_1_lw_d1, control_unit_1_prt_d0,
       control_unit_1_prt_d1, control_unit_1_stop, control_unit_1_sub_d0, control_unit_1_sub_d1,
       control_unit_1_sw_d0, control_unit_1_sw_d1, controlled_buffer_6_out, d_ff_1_q, d_ff_2_q, d_ff_3_q,
       d_ff_3_qn, d_ff_4_q, d_ff_4_qn, d_ff_5_q, d_ff_5_qn, d_ff_6_q, d_ff_6_qn, hex_digit_convert_1_middle,
       hex_digit_convert_1_out_2, hex_digit_convert_1_out_3, hex_digit_convert_1_out_5,
       hex_digit_convert_1_out_6, hex_digit_convert_1_out_7, hex_digit_convert_1_out_8,
       hex_digit_convert_2_middle, hex_digit_convert_2_out_2, hex_digit_convert_2_out_3,
       hex_digit_convert_2_out_5, hex_digit_convert_2_out_6, hex_digit_convert_2_out_7,
       hex_digit_convert_2_out_8, INP_out, instruction_register_1_out_10, instruction_register_1_out_11,
       instruction_register_1_out_12, instruction_register_1_out_17, keyboard_input_1_out_13, logic3_1_out_2,
       logic_1_out_3, logic_1_out_4, logic_1_out_5, LW_out, multiplexer_19_out, nand_1_out, not_1_out,
       not_2_out, not_3_out, not_4_out, not_5_out, not_6_out, not_7_out, not_8_out, not_9_out, not_10_out,
       or_1_out, or_2_out, or_3_out, or_4_out, or_5_out, or_6_out, PRT_2_out, PRT_3_out, PRT_out, SUB_out,
       SW_2_out, SW_3_out, SW_out;
  wire [3:0] adder_1_out, controlled_buffer_4_out, controlled_buffer_4_out_2, instruction_register_1_out_16,
       mar_1_out_6, multiplexer_13_out, multiplexer_20_out, pc_1_out_6;
  wire [7:0] alu_2_out_4, alu_register_1_out_3, alu_register_2_out_3, bigram_1_out_6,
       controlled_buffer_1_out, controlled_buffer_2_out, controlled_buffer_3_out, data_1_out_10,
       data_2_out_10, keyboard_input_1_out_14, mbr_1_out_10, mbr_1_out_11, multiplexer_1_out,
       multiplexer_2_out, multiplexer_3_out, multiplexer_4_out, multiplexer_7_out, multiplexer_10_out,
       multiplexer_12_out, multiplexer_15_out, multiplexer_17_out, multiplexer_18_out;

  Hex_Digit_convert hex_digit_convert_1 (
    .in_1(controlled_buffer_4_out_2), .out_2(hex_digit_convert_1_out_2), .out_3(hex_digit_convert_1_out_3),
    .Middle(hex_digit_convert_1_middle), .out_5(hex_digit_convert_1_out_5),
    .out_6(hex_digit_convert_1_out_6), .out_7(hex_digit_convert_1_out_7), .out_8(hex_digit_convert_1_out_8));
  _7_Segment_Display u_7_segment_display_1 (
    .g(hex_digit_convert_1_middle), .f(hex_digit_convert_1_out_2), .a(hex_digit_convert_1_out_3),
    .b(hex_digit_convert_1_out_5), .e(hex_digit_convert_1_out_6), .d(hex_digit_convert_1_out_7),
    .c(hex_digit_convert_1_out_8));  // open: dp
  Clock clock_1 (.out(clock_1_out));
  BIGRAM bigram_1 (
    .Clock(clock_1_out), .Read_Write_Bit(and_1_out), .in_4(mar_1_out_6), .Write(controlled_buffer_2_out),
    .out_6(bigram_1_out_6), .in_1(in_1));
  _7_Segment_Display u_7_segment_display_2 (
    .g(hex_digit_convert_2_middle), .f(hex_digit_convert_2_out_2), .a(hex_digit_convert_2_out_3),
    .b(hex_digit_convert_2_out_5), .e(hex_digit_convert_2_out_6), .d(hex_digit_convert_2_out_7),
    .c(hex_digit_convert_2_out_8));  // open: dp
  Hex_Digit_convert hex_digit_convert_2 (
    .in_1(controlled_buffer_4_out), .out_2(hex_digit_convert_2_out_2), .out_3(hex_digit_convert_2_out_3),
    .Middle(hex_digit_convert_2_middle), .out_5(hex_digit_convert_2_out_5),
    .out_6(hex_digit_convert_2_out_6), .out_7(hex_digit_convert_2_out_7), .out_8(hex_digit_convert_2_out_8));
  not not_1 (not_1_out, and_1_out);
  assign controlled_buffer_1_out = not_1_out ? bigram_1_out_6 : 8'bz;  // Controlled_Buffer controlled_buffer_1
  not not_2 (not_2_out, not_9_out);
  and and_1 (and_1_out, SW_3_out, not_2_out);
  assign controlled_buffer_2_out = and_1_out ? mbr_1_out_10 : 8'bz;  // Controlled_Buffer controlled_buffer_2
  D_Flip_Flop d_ff_1 (.clk(and_5_out), .D(keyboard_input_1_out_13), .Q(d_ff_1_q));  // open: Qn, preset, en, reset
  Keyboard_Input keyboard_input_1 (
    .in_1(and_5_out), .out_14(keyboard_input_1_out_14), .in_2(controlled_buffer_6_out), ._0(in_2), ._1(in_3),
    ._2(in_4), ._3(in_5), ._4(in_6), ._5(in_7), ._6(in_8), ._7(in_9), ._8(in_10), ._9(in_11),
    .out_13(keyboard_input_1_out_13));
  assign controlled_buffer_3_out = not_3_out ? controlled_buffer_1_out : 8'bz;  // Controlled_Buffer controlled_buffer_3
  not not_3 (not_3_out, and_3_out);
  and and_2 (and_2_out, and_4_out, d_ff_2_q);
  assign {controlled_buffer_4_out_2, controlled_buffer_4_out} = and_2_out ? mbr_1_out_10 : 8'bz;  // Controlled_Buffer controlled_buffer_4
  not not_4 (not_4_out, not_9_out);
  and and_3 (and_3_out, not_4_out, d_ff_1_q, INP_out);
  assign controlled_buffer_3_out = and_3_out ? keyboard_input_1_out_14 : 8'bz;  // Controlled_Buffer controlled_buffer_5
  assign controlled_buffer_6_out = INP_out ? not_9_out : 1'bz;  // Controlled_Buffer controlled_buffer_6
  not not_5 (not_5_out, not_9_out);
  and and_4 (and_4_out, not_5_out, PRT_out);
  D_Flip_Flop d_ff_2 (.clk(and_5_out), .D(PRT_out), .Q(d_ff_2_q), .en(not_7_out));  // open: Qn, preset, reset
  or or_1 (or_1_out, control_unit_1_inp_d0, control_unit_1_lw_d0);
  or or_2 (or_2_out, control_unit_1_lw_d1, control_unit_1_inp_d1);
  or PRT (PRT_out, control_unit_1_prt_d0, control_unit_1_prt_d1);
  Multiplexer #(.width(8)) multiplexer_1 (
    .in1(multiplexer_3_out), .out(multiplexer_1_out), .sel(or_1_out));  // open: in0, en
  Multiplexer #(.width(8)) multiplexer_2 (
    .in1(multiplexer_3_out), .out(multiplexer_2_out), .sel(or_2_out));  // open: in0, en
  buffer_count buffer_count_1 (.in_1(button_1_out), .out_2(buffer_count_1_out_2));
  Button button_1 (.out(button_1_out));
  or INP (INP_out, control_unit_1_inp_d1, control_unit_1_inp_d0);
  Multiplexer #(.width(8)) multiplexer_3 (
    .in1(multiplexer_4_out), .out(multiplexer_3_out), .sel(PRT_out));  // open: in0, en
  Multiplexer #(.width(8)) multiplexer_4 (
    .in0(data_1_out_10), .in1(data_2_out_10), .out(multiplexer_4_out), .sel(PRT_3_out));  // open: en
  Clock clock_2 (.out(clock_2_out));
  and PRT_2 (PRT_2_out, PRT_out, not_7_out);
  and SW (SW_out, control_unit_1_sw_d1, not_6_out);
  not not_6 (not_6_out, control_unit_1_sw_d0);
  Multiplexer #(.width(8)) multiplexer_5 (
    .in1(multiplexer_3_out), .out(multiplexer_1_out), .sel(ALU_out));  // open: in0, en
  Multiplexer #(.width(8)) multiplexer_6 (
    .in1(multiplexer_3_out), .out(multiplexer_2_out), .sel(ALU_3_out));  // open: in0, en
  and and_5 (and_5_out, clock_2_out, buffer_count_1_out_2);
  Multiplexer #(.width(8)) multiplexer_7 (
    .in0(controlled_buffer_3_out), .in1(multiplexer_3_out), .out(multiplexer_7_out), .sel(or_3_out));  // open: en
  or or_3 (or_3_out, SW_2_out, PRT_2_out);
  and SW_2 (SW_2_out, SW_3_out, not_7_out);
  or or_4 (or_4_out, LW_out, INP_out);
  DATA data_1 (
    .out_3(data_1_out_10[7]), .out_4(data_1_out_10[6]), .out_5(data_1_out_10[5]), .out_6(data_1_out_10[4]),
    .out_7(data_1_out_10[3]), .out_8(data_1_out_10[2]), .out_9(data_1_out_10[1]), .out_10(data_1_out_10[0]),
    .in_1(not_9_out), .in_2(multiplexer_1_out));
  DATA data_2 (
    .out_3(data_2_out_10[7]), .out_4(data_2_out_10[6]), .out_5(data_2_out_10[5]), .out_6(data_2_out_10[4]),
    .out_7(data_2_out_10[3]), .out_8(data_2_out_10[2]), .out_9(data_2_out_10[1]), .out_10(data_2_out_10[0]),
    .in_1(not_9_out), .in_2(multiplexer_2_out));
  Multiplexer #(.width(8)) multiplexer_8 (
    .in1(mbr_1_out_10), .out(multiplexer_3_out), .sel(or_4_out));  // open: in0, en
  Multiplexer #(.width(8)) multiplexer_9 (
    .in1(multiplexer_10_out), .out(multiplexer_3_out), .sel(SW_3_out));  // open: in0, en
  Multiplexer #(.width(8)) multiplexer_10 (
    .in0(data_1_out_10), .in1(data_2_out_10), .out(multiplexer_10_out), .sel(SW_out));  // open: en
  MAR mar_1 (
    .in_1(and_5_out), .in_2(multiplexer_13_out[0]), .in_3(multiplexer_13_out[1]),
    .in_4(multiplexer_13_out[2]), .in_5(multiplexer_13_out[3]), .out_6(mar_1_out_6[0]),
    .out_7(mar_1_out_6[1]), .out_8(mar_1_out_6[2]), .out_9(mar_1_out_6[3]));
  MBR mbr_1 (
    .in_1(and_5_out), .in_2(multiplexer_7_out[0]), .in_3(multiplexer_7_out[1]), .in_4(multiplexer_7_out[2]),
    .in_5(multiplexer_7_out[3]), .in_6(multiplexer_7_out[4]), .in_7(multiplexer_7_out[5]),
    .in_8(multiplexer_7_out[6]), .in_9(multiplexer_7_out[7]), .out_10(mbr_1_out_10), .out_11(mbr_1_out_11));
  D_Flip_Flop d_ff_3 (
    .clk(and_5_out), .D(d_ff_3_qn), .Q(d_ff_3_q), .Qn(d_ff_3_qn), .en(not_9_out));  // open: preset, reset
  D_Flip_Flop d_ff_4 (
    .clk(d_ff_3_qn), .D(d_ff_4_qn), .Q(d_ff_4_q), .Qn(d_ff_4_qn), .en(not_9_out));  // open: preset, reset
  Multiplexer #(.width(8)) multiplexer_11 (
    .in1(multiplexer_12_out), .out(multiplexer_3_out), .sel(BNZ_out));  // open: in0, en
  Multiplexer #(.width(8)) multiplexer_12 (
    .in0(data_1_out_10), .in1(data_2_out_10), .out(multiplexer_12_out), .sel(BNZ_2_out));  // open: en
  and ALU (ALU_out, ALU_8_out, and_8_out);
  Multiplexer #(.width(4)) multiplexer_13 (
    .in0(pc_1_out_6), .in1(instruction_register_1_out_16), .out(multiplexer_13_out), .sel(and_6_out));  // open: en
  nand nand_1 (nand_1_out, d_ff_3_q, d_ff_4_q);
  or or_5 (or_5_out, SW_3_out, LW_out);
  Multiplexer #(.width(8)) multiplexer_14 (
    .in1(multiplexer_15_out), .out(multiplexer_3_out), .sel(ALU_4_out));  // open: in0, en
  Multiplexer #(.width(8)) multiplexer_15 (
    .in0(data_1_out_10), .in1(data_2_out_10), .out(multiplexer_15_out), .sel(ALU_7_out));  // open: en
  Multiplexer #(.width(8)) multiplexer_16 (
    .in1(multiplexer_17_out), .out(multiplexer_3_out), .sel(ALU_5_out));  // open: in0, en
  Multiplexer #(.width(8)) multiplexer_17 (
    .in0(data_1_out_10), .in1(data_2_out_10), .out(multiplexer_17_out), .sel(ALU_8_out));  // open: en
  and and_6 (and_6_out, or_5_out, not_7_out);
  ALU_Register alu_register_1 (
    .in_1(ALU_4_out), .in_2(multiplexer_3_out), .out_3(alu_register_1_out_3[0]),
    .out_4(alu_register_1_out_3[1]), .out_5(alu_register_1_out_3[2]), .out_6(alu_register_1_out_3[3]),
    .out_7(alu_register_1_out_3[4]), .out_8(alu_register_1_out_3[5]), .out_9(alu_register_1_out_3[6]),
    .out_10(alu_register_1_out_3[7]));
  ALU_Register alu_register_2 (
    .in_1(ALU_5_out), .in_2(multiplexer_3_out), .out_3(alu_register_2_out_3[0]),
    .out_4(alu_register_2_out_3[1]), .out_5(alu_register_2_out_3[2]), .out_6(alu_register_2_out_3[3]),
    .out_7(alu_register_2_out_3[4]), .out_8(alu_register_2_out_3[5]), .out_9(alu_register_2_out_3[6]),
    .out_10(alu_register_2_out_3[7]));
  Multiplexer #(.width(8)) multiplexer_18 (
    .in0(mbr_1_out_11), .out(multiplexer_18_out), .sel(multiplexer_19_out));  // open: in1, en
  Multiplexer multiplexer_19 (
    .in0(and_7_out), .in1(nand_1_out), .out(multiplexer_19_out), .sel(not_9_out));  // open: en
  and and_7 (and_7_out, or_6_out, not_7_out);
  or or_6 (or_6_out, PRT_out, LW_out, SW_3_out, INP_out);
  not not_7 (not_7_out, not_9_out);
  Branch branch_1 (.in_1(multiplexer_3_out), .in_2(BNZ_out), .out_3(branch_1_out_3));
  or SUB (SUB_out, control_unit_1_sub_d1, control_unit_1_sub_d0);
  Adder #(.width(4)) adder_1 (.a(pc_1_out_6), .b(4'b0001), .out(adder_1_out));  // open: cin, cout
  PC pc_1 (
    .in_1(not_9_out), .in_2(multiplexer_20_out[0]), .in_3(multiplexer_20_out[1]),
    .in_4(multiplexer_20_out[2]), .in_5(multiplexer_20_out[3]), .out_6(pc_1_out_6[0]), .out_7(pc_1_out_6[1]),
    .out_8(pc_1_out_6[2]), .out_9(pc_1_out_6[3]));
  ALU alu_2 (
    .in_1(alu_register_1_out_3), .Input_2(alu_register_2_out_3), .sub_enable(SUB_out), .out_4(alu_2_out_4));  // open: Overflow, Zero, Negative
  Multiplexer #(.width(4)) multiplexer_20 (
    .in0(adder_1_out), .in1(instruction_register_1_out_16), .out(multiplexer_20_out), .sel(branch_1_out_3));  // open: en
  Multiplexer #(.width(8)) multiplexer_21 (
    .in1(alu_2_out_4), .out(multiplexer_3_out), .sel(and_8_out));  // open: in0, en
  and ALU_3 (ALU_3_out, and_8_out, ALU_7_out);
  D_Flip_Flop d_ff_5 (.clk(and_5_out), .D(d_ff_5_qn), .Q(d_ff_5_q), .Qn(d_ff_5_qn));  // open: preset, en, reset
  D_Flip_Flop d_ff_6 (.clk(d_ff_5_qn), .D(d_ff_6_qn), .Q(d_ff_6_q), .Qn(d_ff_6_qn));  // open: preset, en, reset
  and PRT_3 (PRT_3_out, control_unit_1_prt_d1, not_8_out);
  and ALU_4 (ALU_4_out, ALU_6_out, logic_1_out_3);
  Logic logic_1 (.in_1(d_ff_5_q), .in_2(d_ff_6_q), .out_3(logic_1_out_3), .out_4(logic_1_out_4), .out_5(logic_1_out_5));
  and and_8 (and_8_out, logic_1_out_4, ALU_6_out);
  not not_8 (not_8_out, control_unit_1_prt_d0);
  not not_9 (not_9_out, and_9_out);
  and ALU_5 (ALU_5_out, logic_1_out_5, ALU_6_out);
  or ALU_6 (ALU_6_out, ALU_7_out, ALU_8_out);
  and and_9 (and_9_out, buffer_count_1_out_2, logic3_1_out_2);
  Instruction_Register instruction_register_1 (
    .in_1(and_5_out), .in_2(multiplexer_18_out[0]), .in_3(multiplexer_18_out[1]),
    .in_4(multiplexer_18_out[2]), .in_5(multiplexer_18_out[3]), .in_6(multiplexer_18_out[4]),
    .in_7(multiplexer_18_out[5]), .in_8(multiplexer_18_out[6]), .in_9(multiplexer_18_out[7]),
    .out_10(instruction_register_1_out_10), .out_11(instruction_register_1_out_11),
    .out_12(instruction_register_1_out_12), .out_13(instruction_register_1_out_16[3]),
    .out_14(instruction_register_1_out_16[2]), .out_15(instruction_register_1_out_16[1]),
    .out_16(instruction_register_1_out_16[0]), .out_17(instruction_register_1_out_17));
  Control_Unit control_unit_1 (
    .in_1(instruction_register_1_out_10), .in_2(instruction_register_1_out_11),
    .in_3(instruction_register_1_out_12), .in_4(instruction_register_1_out_17),
    .Add_D1(control_unit_1_add_d1), .Sub_D1(control_unit_1_sub_d1), .SW_D1(control_unit_1_sw_d1),
    .LW_D1(control_unit_1_lw_d1), .BZ_D1(control_unit_1_bz_d1), .Add_D0(control_unit_1_add_d0),
    .Sub_D0(control_unit_1_sub_d0), .SW_D0(control_unit_1_sw_d0), .LW_D0(control_unit_1_lw_d0),
    .BZ_D0(control_unit_1_bz_d0), .PRT_D1(control_unit_1_prt_d1), .INP_D1(control_unit_1_inp_d1),
    .PRT_D0(control_unit_1_prt_d0), .INP_D0(control_unit_1_inp_d0), .STOP(control_unit_1_stop));
  or LW (LW_out, control_unit_1_lw_d1, control_unit_1_lw_d0);
  or SW_3 (SW_3_out, control_unit_1_sw_d1, control_unit_1_sw_d0);
  or ALU_7 (ALU_7_out, control_unit_1_add_d1, control_unit_1_sub_d1);
  or ALU_8 (ALU_8_out, control_unit_1_add_d0, control_unit_1_sub_d0);
  or BNZ (BNZ_out, control_unit_1_bz_d1, control_unit_1_bz_d0);
  and BNZ_2 (BNZ_2_out, control_unit_1_bz_d1, not_10_out);
  Logic3 logic3_1 (.in_1(and_5_out), .out_2(logic3_1_out_2));
  not not_10 (not_10_out, control_unit_1_bz_d0);

  // Notes on the sheet:
  //   Read
  //   Write
  //   Address
  //   Power
endmodule

// CU
module Control_Unit (
  input  in_1,
  input  in_2,
  input  in_3,
  input  in_4,
  output Add_D1,
  output Sub_D1,
  output SW_D1,
  output LW_D1,
  output BZ_D1,
  output Add_D0,
  output Sub_D0,
  output SW_D0,
  output LW_D0,
  output BZ_D0,
  output PRT_D1,
  output INP_D1,
  output PRT_D0,
  output INP_D0,
  output STOP
);

  wire not_1_out, not_2_out, not_3_out, not_4_out, not_5_out, not_6_out, not_7_out, not_8_out, not_9_out,
       not_10_out, not_11_out, not_12_out, not_13_out, not_14_out, not_15_out, not_16_out, not_17_out,
       not_18_out, not_19_out, not_20_out, not_21_out, not_22_out, not_23_out, not_24_out, not_25_out,
       not_26_out, not_27_out, not_28_out, not_29_out, not_30_out, not_31_out;

  not not_1 (not_1_out, in_3);
  not not_2 (not_2_out, in_2);
  not not_3 (not_3_out, in_1);
  not not_4 (not_4_out, in_2);
  not not_5 (not_5_out, in_1);
  not not_6 (not_6_out, in_3);
  not not_7 (not_7_out, in_1);
  not not_8 (not_8_out, in_1);
  not not_9 (not_9_out, in_3);
  not not_10 (not_10_out, in_2);
  not not_11 (not_11_out, in_4);
  not not_12 (not_12_out, in_3);
  not not_13 (not_13_out, in_2);
  not not_14 (not_14_out, in_1);
  not not_15 (not_15_out, in_4);
  not not_16 (not_16_out, in_2);
  not not_17 (not_17_out, in_1);
  not not_18 (not_18_out, in_4);
  not not_19 (not_19_out, in_3);
  not not_20 (not_20_out, in_1);
  not not_21 (not_21_out, in_4);
  not not_22 (not_22_out, in_1);
  not not_23 (not_23_out, in_4);
  not not_24 (not_24_out, in_3);
  not not_25 (not_25_out, in_2);
  not not_26 (not_26_out, in_2);
  not not_27 (not_27_out, in_3);
  not not_28 (not_28_out, in_4);
  not not_29 (not_29_out, in_2);
  not not_30 (not_30_out, in_4);
  not not_31 (not_31_out, in_3);
  and and_1 (Add_D1, in_4, not_1_out, not_2_out, not_3_out);
  and and_2 (Sub_D1, in_4, in_3, not_4_out, not_5_out);
  and and_3 (SW_D1, in_4, not_6_out, in_2, not_7_out);
  and and_4 (LW_D1, in_4, in_3, in_2, not_8_out);
  and and_5 (BZ_D1, in_4, not_9_out, not_10_out, in_1);
  and and_6 (Add_D0, not_11_out, not_12_out, not_13_out, not_14_out);
  and and_7 (Sub_D0, not_15_out, in_3, not_16_out, not_17_out);
  and and_8 (SW_D0, not_18_out, not_19_out, in_2, not_20_out);
  and and_9 (LW_D0, not_21_out, in_3, in_2, not_22_out);
  and and_10 (BZ_D0, not_23_out, not_24_out, not_25_out, in_1);
  and and_11 (PRT_D1, in_4, in_3, not_26_out, in_1);
  and and_12 (INP_D1, in_4, not_27_out, in_2, in_1);
  and and_13 (PRT_D0, not_28_out, in_3, not_29_out, in_1);
  and and_14 (INP_D0, not_30_out, not_31_out, in_2, in_1);
  and and_15 (STOP, in_3, in_2, in_1);
endmodule

// IR
module Instruction_Register (
  input  in_1,
  input  in_2,
  input  in_3,
  input  in_4,
  input  in_5,
  input  in_6,
  input  in_7,
  input  in_8,
  input  in_9,
  output out_10,
  output out_11,
  output out_12,
  output out_13,
  output out_14,
  output out_15,
  output out_16,
  output out_17
);

  D_Flip_Flop d_ff_1 (.clk(in_1), .D(in_2), .Q(out_10));  // open: Qn, preset, en, reset
  D_Flip_Flop d_ff_2 (.clk(in_1), .D(in_3), .Q(out_11));  // open: Qn, preset, en, reset
  D_Flip_Flop d_ff_3 (.clk(in_1), .D(in_4), .Q(out_12));  // open: Qn, preset, en, reset
  D_Flip_Flop d_ff_4 (.clk(in_1), .D(in_5), .Q(out_13));  // open: Qn, preset, en, reset
  D_Flip_Flop d_ff_5 (.clk(in_1), .D(in_6), .Q(out_14));  // open: Qn, preset, en, reset
  D_Flip_Flop d_ff_6 (.clk(in_1), .D(in_7), .Q(out_15));  // open: Qn, preset, en, reset
  D_Flip_Flop d_ff_7 (.clk(in_1), .D(in_8), .Q(out_16));  // open: Qn, preset, en, reset
  D_Flip_Flop d_ff_8 (.clk(in_1), .D(in_9), .Q(out_17));  // open: Qn, preset, en, reset
endmodule

module MBR (
  input  in_1,
  input  in_2,
  input  in_3,
  input  in_4,
  input  in_5,
  input  in_6,
  input  in_7,
  input  in_8,
  input  in_9,
  output [7:0] out_10,
  output [7:0] out_11
);

  D_Flip_Flop d_ff_1 (.clk(in_1), .D(in_2), .Q(out_10[0]));  // open: Qn, preset, en, reset
  D_Flip_Flop d_ff_2 (.clk(in_1), .D(in_3), .Q(out_10[1]));  // open: Qn, preset, en, reset
  D_Flip_Flop d_ff_3 (.clk(in_1), .D(in_4), .Q(out_10[2]));  // open: Qn, preset, en, reset
  D_Flip_Flop d_ff_4 (.clk(in_1), .D(in_5), .Q(out_10[3]));  // open: Qn, preset, en, reset
  D_Flip_Flop d_ff_5 (.clk(in_1), .D(in_6), .Q(out_10[4]));  // open: Qn, preset, en, reset
  D_Flip_Flop d_ff_6 (.clk(in_1), .D(in_7), .Q(out_10[5]));  // open: Qn, preset, en, reset
  D_Flip_Flop d_ff_7 (.clk(in_1), .D(in_8), .Q(out_10[6]));  // open: Qn, preset, en, reset
  D_Flip_Flop d_ff_8 (.clk(in_1), .D(in_9), .Q(out_10[7]));  // open: Qn, preset, en, reset

  assign out_11 = out_10;
endmodule

module MAR (
  input  in_1,
  input  in_2,
  input  in_3,
  input  in_4,
  input  in_5,
  output out_6,
  output out_7,
  output out_8,
  output out_9
);

  D_Flip_Flop d_ff_1 (.clk(in_1), .D(in_2), .Q(out_6));  // open: Qn, preset, en, reset
  D_Flip_Flop d_ff_2 (.clk(in_1), .D(in_3), .Q(out_7));  // open: Qn, preset, en, reset
  D_Flip_Flop d_ff_3 (.clk(in_1), .D(in_4), .Q(out_8));  // open: Qn, preset, en, reset
  D_Flip_Flop d_ff_4 (.clk(in_1), .D(in_5), .Q(out_9));  // open: Qn, preset, en, reset
endmodule

module ALU (
  input  [7:0] in_1,
  input  [7:0] Input_2,
  input  sub_enable,
  output [7:0] out_4,
  output Overflow,
  output Zero,
  output Negative
);

  wire multiplexer_1_out, multiplexer_2_out, multiplexer_3_out, multiplexer_4_out, multiplexer_5_out,
       multiplexer_6_out, multiplexer_7_out, multiplexer_8_out, multiplexer_9_out, nand_1_out, nand_2_out,
       nand_3_out, nand_4_out, nand_5_out, nand_6_out, nand_7_out, nand_8_out, nand_9_out, nand_10_out,
       nand_11_out, nand_12_out, nand_13_out, nand_14_out, nand_15_out, nand_16_out, nand_17_out,
       nand_18_out, nand_19_out, nand_20_out, nand_21_out, nand_22_out, nand_23_out, nand_24_out, not_1_out,
       not_2_out, not_3_out, not_4_out, not_5_out, not_6_out, not_7_out, not_8_out, not_9_out, not_10_out,
       xor_1_out, xor_2_out, xor_3_out, xor_4_out, xor_5_out, xor_6_out, xor_7_out, xor_8_out;

  not not_1 (not_1_out, 1'b1);
  Multiplexer #(.enable("false")) multiplexer_1 (
    .in0(not_1_out), .in1(1'b1), .out(multiplexer_1_out), .sel(sub_enable));
  not not_2 (not_2_out, Input_2[0]);
  not not_3 (not_3_out, Input_2[1]);
  not not_4 (not_4_out, Input_2[2]);
  not not_5 (not_5_out, Input_2[3]);
  not not_6 (not_6_out, Input_2[4]);
  not not_7 (not_7_out, Input_2[5]);
  not not_8 (not_8_out, Input_2[6]);
  not not_9 (not_9_out, Input_2[7]);
  Multiplexer #(.enable("false")) multiplexer_2 (
    .in0(Input_2[0]), .in1(not_2_out), .out(multiplexer_2_out), .sel(sub_enable));
  Multiplexer #(.enable("false")) multiplexer_3 (
    .in0(Input_2[1]), .in1(not_3_out), .out(multiplexer_3_out), .sel(sub_enable));
  Multiplexer #(.enable("false")) multiplexer_4 (
    .in0(Input_2[2]), .in1(not_4_out), .out(multiplexer_4_out), .sel(sub_enable));
  Multiplexer #(.enable("false")) multiplexer_5 (
    .in0(Input_2[3]), .in1(not_5_out), .out(multiplexer_5_out), .sel(sub_enable));
  Multiplexer #(.enable("false")) multiplexer_6 (
    .in0(Input_2[4]), .in1(not_6_out), .out(multiplexer_6_out), .sel(sub_enable));
  Multiplexer #(.enable("false")) multiplexer_7 (
    .in0(Input_2[5]), .in1(not_7_out), .out(multiplexer_7_out), .sel(sub_enable));
  Multiplexer #(.enable("false")) multiplexer_8 (
    .in0(Input_2[6]), .in1(not_8_out), .out(multiplexer_8_out), .sel(sub_enable));
  Multiplexer #(.enable("false")) multiplexer_9 (
    .in0(Input_2[7]), .in1(not_9_out), .out(multiplexer_9_out), .sel(sub_enable));
  nand nand_1 (nand_1_out, in_1[0], multiplexer_2_out);
  nand nand_2 (nand_2_out, in_1[2], multiplexer_4_out);
  nand nand_3 (nand_3_out, in_1[4], multiplexer_6_out);
  nand nand_4 (nand_4_out, in_1[6], multiplexer_8_out);
  xor xor_1 (xor_1_out, in_1[0], multiplexer_2_out);
  xor xor_2 (xor_2_out, in_1[1], multiplexer_3_out);
  nand nand_5 (nand_5_out, in_1[1], multiplexer_3_out);
  xor xor_3 (xor_3_out, in_1[2], multiplexer_4_out);
  xor xor_4 (xor_4_out, in_1[3], multiplexer_5_out);
  nand nand_6 (nand_6_out, in_1[3], multiplexer_5_out);
  xor xor_5 (xor_5_out, in_1[4], multiplexer_6_out);
  xor xor_6 (xor_6_out, in_1[5], multiplexer_7_out);
  nand nand_7 (nand_7_out, in_1[5], multiplexer_7_out);
  xor xor_7 (xor_7_out, in_1[6], multiplexer_8_out);
  xor xor_8 (xor_8_out, in_1[7], multiplexer_9_out);
  nand nand_8 (nand_8_out, in_1[7], multiplexer_9_out);
  xor xor_9 (out_4[0], xor_1_out, multiplexer_1_out);
  nand nand_9 (nand_9_out, multiplexer_1_out, xor_1_out);
  nand nand_10 (nand_10_out, nand_17_out, xor_2_out);
  xor xor_10 (out_4[2], xor_3_out, nand_23_out);
  nand nand_11 (nand_11_out, nand_23_out, xor_3_out);
  nand nand_12 (nand_12_out, nand_18_out, xor_4_out);
  xor xor_11 (out_4[4], xor_5_out, nand_24_out);
  nand nand_13 (nand_13_out, nand_24_out, xor_5_out);
  nand nand_14 (nand_14_out, nand_19_out, xor_6_out);
  xor xor_12 (out_4[6], xor_7_out, nand_20_out);
  nand nand_15 (nand_15_out, nand_20_out, xor_7_out);
  nand nand_16 (nand_16_out, nand_21_out, xor_8_out);
  nand nand_17 (nand_17_out, nand_1_out, nand_9_out);
  xor xor_13 (out_4[1], xor_2_out, nand_17_out);
  nand nand_18 (nand_18_out, nand_2_out, nand_11_out);
  xor xor_14 (out_4[3], xor_4_out, nand_18_out);
  nand nand_19 (nand_19_out, nand_3_out, nand_13_out);
  xor xor_15 (out_4[5], xor_6_out, nand_19_out);
  nand nand_20 (nand_20_out, nand_7_out, nand_14_out);
  nand nand_21 (nand_21_out, nand_4_out, nand_15_out);
  xor xor_16 (out_4[7], xor_8_out, nand_21_out);
  nand nand_22 (nand_22_out, nand_8_out, nand_16_out);
  not not_10 (not_10_out, sub_enable);
  nand nand_23 (nand_23_out, nand_5_out, nand_10_out);
  nand nand_24 (nand_24_out, nand_6_out, nand_12_out);
  and and_1 (Overflow, nand_22_out, not_10_out);
  and and_2 (Negative, out_4[7], sub_enable);
  and and_3 (Zero, ~out_4[0], ~out_4[1], ~out_4[2], ~out_4[3], ~out_4[4], ~out_4[5], ~out_4[6], ~out_4[7], ~Overflow);  // AND_Gate

  // Notes on the sheet:
  //   Input 1
  //   Sum
endmodule

// Data Register
module DATA (
  input  in_1,
  input  [7:0] in_2,
  output out_3,
  output out_4,
  output out_5,
  output out_6,
  output out_7,
  output out_8,
  output out_9,
  output out_10
);

  D_Flip_Flop d_ff_1 (.clk(in_1), .D(in_2[0]), .Q(out_10));  // open: Qn, preset, en, reset
  D_Flip_Flop d_ff_2 (.clk(in_1), .D(in_2[1]), .Q(out_9));  // open: Qn, preset, en, reset
  D_Flip_Flop d_ff_3 (.clk(in_1), .D(in_2[2]), .Q(out_8));  // open: Qn, preset, en, reset
  D_Flip_Flop d_ff_4 (.clk(in_1), .D(in_2[3]), .Q(out_7));  // open: Qn, preset, en, reset
  D_Flip_Flop d_ff_5 (.clk(in_1), .D(in_2[4]), .Q(out_6));  // open: Qn, preset, en, reset
  D_Flip_Flop d_ff_6 (.clk(in_1), .D(in_2[5]), .Q(out_5));  // open: Qn, preset, en, reset
  D_Flip_Flop d_ff_7 (.clk(in_1), .D(in_2[6]), .Q(out_4));  // open: Qn, preset, en, reset
  D_Flip_Flop d_ff_8 (.clk(in_1), .D(in_2[7]), .Q(out_3));  // open: Qn, preset, en, reset
endmodule

module PC (
  input  in_1,
  input  in_2,
  input  in_3,
  input  in_4,
  input  in_5,
  output out_6,
  output out_7,
  output out_8,
  output out_9
);

  D_Flip_Flop d_ff_1 (.clk(in_1), .D(in_2), .Q(out_6));  // open: Qn, preset, en, reset
  D_Flip_Flop d_ff_2 (.clk(in_1), .D(in_3), .Q(out_7));  // open: Qn, preset, en, reset
  D_Flip_Flop d_ff_3 (.clk(in_1), .D(in_4), .Q(out_8));  // open: Qn, preset, en, reset
  D_Flip_Flop d_ff_4 (.clk(in_1), .D(in_5), .Q(out_9));  // open: Qn, preset, en, reset
endmodule

module BIGRAM (
  input  in_1,
  input  Clock,
  input  Read_Write_Bit,
  input  [3:0] in_4,
  input  [7:0] Write,
  output [7:0] out_6
);

  wire and_1_out, and_2_out, and_3_out, and_4_out, and_5_out, and_6_out, and_7_out, and_8_out, and_9_out,
       and_10_out, and_11_out, and_12_out, and_13_out, and_14_out, and_15_out, and_16_out, and_17_out,
       and_18_out, and_19_out, and_20_out, and_21_out, and_22_out, and_23_out, and_24_out, and_25_out,
       and_26_out, and_27_out, and_28_out, and_29_out, and_30_out, and_31_out, and_32_out, d_ff_1_q,
       d_ff_1_qn, d_ff_2_q, d_ff_2_qn, d_ff_3_q, d_ff_3_qn, d_ff_4_q, d_ff_4_qn, d_ff_5_q, not_1_out,
       not_2_out, not_3_out, not_4_out, not_5_out, not_6_out, not_7_out, not_8_out, not_9_out, not_10_out,
       not_11_out, not_12_out, not_13_out, not_14_out, not_15_out, not_16_out, not_17_out, ram_1_out_12,
       ram_1_out_13, ram_1_out_14, ram_1_out_15, ram_1_out_16, ram_1_out_17, ram_1_out_18, ram_1_out_19,
       ram_2_out_12, ram_2_out_13, ram_2_out_14, ram_2_out_15, ram_2_out_16, ram_2_out_17, ram_2_out_18,
       ram_2_out_19, ram_3_out_12, ram_3_out_13, ram_3_out_14, ram_3_out_15, ram_3_out_16, ram_3_out_17,
       ram_3_out_18, ram_3_out_19, ram_4_out_12, ram_4_out_13, ram_4_out_14, ram_4_out_15, ram_4_out_16,
       ram_4_out_17, ram_4_out_18, ram_4_out_19, ram_5_out_12, ram_5_out_13, ram_5_out_14, ram_5_out_15,
       ram_5_out_16, ram_5_out_17, ram_5_out_18, ram_5_out_19, ram_6_out_12, ram_6_out_13, ram_6_out_14,
       ram_6_out_15, ram_6_out_16, ram_6_out_17, ram_6_out_18, ram_6_out_19, ram_7_out_12, ram_7_out_13,
       ram_7_out_14, ram_7_out_15, ram_7_out_16, ram_7_out_17, ram_7_out_18, ram_7_out_19, ram_8_out_12,
       ram_8_out_13, ram_8_out_14, ram_8_out_15, ram_8_out_16, ram_8_out_17, ram_8_out_18, ram_8_out_19,
       ram_9_out_12, ram_9_out_13, ram_9_out_14, ram_9_out_15, ram_9_out_16, ram_9_out_17, ram_9_out_18,
       ram_9_out_19, ram_10_out_12, ram_10_out_13, ram_10_out_14, ram_10_out_15, ram_10_out_16,
       ram_10_out_17, ram_10_out_18, ram_10_out_19, ram_11_out_12, ram_11_out_13, ram_11_out_14,
       ram_11_out_15, ram_11_out_16, ram_11_out_17, ram_11_out_18, ram_11_out_19, ram_12_out_12,
       ram_12_out_13, ram_12_out_14, ram_12_out_15, ram_12_out_16, ram_12_out_17, ram_12_out_18,
       ram_12_out_19, ram_13_out_12, ram_13_out_13, ram_13_out_14, ram_13_out_15, ram_13_out_16,
       ram_13_out_17, ram_13_out_18, ram_13_out_19, ram_14_out_12, ram_14_out_13, ram_14_out_14,
       ram_14_out_15, ram_14_out_16, ram_14_out_17, ram_14_out_18, ram_14_out_19, ram_15_out_12,
       ram_15_out_13, ram_15_out_14, ram_15_out_15, ram_15_out_16, ram_15_out_17, ram_15_out_18,
       ram_15_out_19, ram_16_out_12, ram_16_out_13, ram_16_out_14, ram_16_out_15, ram_16_out_16,
       ram_16_out_17, ram_16_out_18, ram_16_out_19, write_combine_1_out_3, write_combine_1_out_4,
       write_combine_1_out_5, write_combine_1_out_6, write_combine_1_out_7, write_combine_1_out_8,
       write_combine_1_out_9, write_combine_1_out_10, write_combine_1_out_11, write_combine_1_out_12,
       write_combine_1_out_13, write_combine_1_out_14, write_combine_1_out_15, write_combine_1_out_16,
       write_combine_1_out_17, write_combine_1_out_18;
  wire [7:0] controlled_buffer_1_out, d_ff_6_q;
  wire [15:0] reads_1_out_12, reads_2_out_12, reads_3_out_12, reads_4_out_12, reads_5_out_12, reads_6_out_12,
       reads_7_out_12, reads_8_out_12, reads_9_out_12, reads_10_out_12, reads_11_out_12, reads_12_out_12,
       reads_13_out_12, reads_14_out_12, reads_15_out_12, reads_16_out_12, writes_1_out_9, writes_2_out_9;

  assign controlled_buffer_1_out = d_ff_5_q ? Write : 8'bz;  // Controlled_Buffer controlled_buffer_1
  assign out_6 = not_1_out ? d_ff_6_q : 8'bz;  // Controlled_Buffer controlled_buffer_2
  not not_1 (not_1_out, d_ff_5_q);
  D_Flip_Flop d_ff_1 (.clk(Clock), .D(in_4[0]), .Q(d_ff_1_q), .Qn(d_ff_1_qn), .en(Clock));  // open: preset, reset
  D_Flip_Flop d_ff_2 (.clk(Clock), .D(in_4[1]), .Q(d_ff_2_q), .Qn(d_ff_2_qn), .en(Clock));  // open: preset, reset
  D_Flip_Flop d_ff_3 (.clk(Clock), .D(in_4[2]), .Q(d_ff_3_q), .Qn(d_ff_3_qn), .en(Clock));  // open: preset, reset
  D_Flip_Flop d_ff_4 (.clk(Clock), .D(in_4[3]), .Q(d_ff_4_q), .Qn(d_ff_4_qn), .en(Clock));  // open: preset, reset
  D_Flip_Flop d_ff_5 (.clk(Clock), .D(Read_Write_Bit), .Q(d_ff_5_q), .en(Clock));  // open: Qn, preset, reset
  D_Flip_Flop d_ff_6 (
    .clk(Clock), .D(controlled_buffer_1_out[0]), .Q(d_ff_6_q[0]), .preset(write_combine_1_out_18),
    .en(Clock), .reset(write_combine_1_out_17));  // open: Qn
  D_Flip_Flop d_ff_7 (
    .clk(Clock), .D(controlled_buffer_1_out[1]), .Q(d_ff_6_q[1]), .preset(write_combine_1_out_16),
    .en(Clock), .reset(write_combine_1_out_15));  // open: Qn
  D_Flip_Flop d_ff_8 (
    .clk(Clock), .D(controlled_buffer_1_out[2]), .Q(d_ff_6_q[2]), .preset(write_combine_1_out_14),
    .en(Clock), .reset(write_combine_1_out_13));  // open: Qn
  D_Flip_Flop d_ff_9 (
    .clk(Clock), .D(controlled_buffer_1_out[3]), .Q(d_ff_6_q[3]), .preset(write_combine_1_out_12),
    .en(Clock), .reset(write_combine_1_out_11));  // open: Qn
  D_Flip_Flop d_ff_10 (
    .clk(Clock), .D(controlled_buffer_1_out[4]), .Q(d_ff_6_q[4]), .preset(write_combine_1_out_10),
    .en(Clock), .reset(write_combine_1_out_9));  // open: Qn
  D_Flip_Flop d_ff_11 (
    .clk(Clock), .D(controlled_buffer_1_out[5]), .Q(d_ff_6_q[5]), .preset(write_combine_1_out_8), .en(Clock),
    .reset(write_combine_1_out_7));  // open: Qn
  D_Flip_Flop d_ff_12 (
    .clk(Clock), .D(controlled_buffer_1_out[6]), .Q(d_ff_6_q[6]), .preset(write_combine_1_out_6), .en(Clock),
    .reset(write_combine_1_out_5));  // open: Qn
  D_Flip_Flop d_ff_13 (
    .clk(Clock), .D(controlled_buffer_1_out[7]), .Q(d_ff_6_q[7]), .preset(write_combine_1_out_4), .en(Clock),
    .reset(write_combine_1_out_3));  // open: Qn
  and and_1 (and_1_out, d_ff_4_qn, d_ff_3_qn, d_ff_2_qn, d_ff_1_qn);
  and and_2 (and_2_out, d_ff_4_qn, d_ff_3_qn, d_ff_2_qn, d_ff_1_q);
  and and_3 (and_3_out, d_ff_4_qn, d_ff_3_qn, d_ff_2_q, d_ff_1_qn);
  and and_4 (and_4_out, d_ff_4_qn, d_ff_3_qn, d_ff_2_q, d_ff_1_q);
  and and_5 (and_5_out, d_ff_4_qn, d_ff_3_q, d_ff_2_qn, d_ff_1_qn);
  and and_6 (and_6_out, d_ff_4_qn, d_ff_3_q, d_ff_2_qn, d_ff_1_q);
  and and_7 (and_7_out, d_ff_4_qn, d_ff_3_q, d_ff_2_q, d_ff_1_qn);
  and and_8 (and_8_out, d_ff_4_qn, d_ff_3_q, d_ff_2_q, d_ff_1_q);
  and and_9 (and_9_out, d_ff_4_q, d_ff_3_qn, d_ff_2_qn, d_ff_1_qn);
  and and_10 (and_10_out, d_ff_4_q, d_ff_3_qn, d_ff_2_qn, d_ff_1_q);
  and and_11 (and_11_out, d_ff_4_q, d_ff_3_qn, d_ff_2_q, d_ff_1_qn);
  and and_12 (and_12_out, d_ff_4_q, d_ff_3_qn, d_ff_2_q, d_ff_1_q);
  and and_13 (and_13_out, d_ff_4_q, d_ff_3_q, d_ff_2_qn, d_ff_1_qn);
  and and_14 (and_14_out, d_ff_4_q, d_ff_3_q, d_ff_2_qn, d_ff_1_q);
  and and_15 (and_15_out, d_ff_4_q, d_ff_3_q, d_ff_2_q, d_ff_1_qn);
  and and_16 (and_16_out, d_ff_4_q, d_ff_3_q, d_ff_2_q, d_ff_1_q);
  not not_2 (not_2_out, d_ff_5_q);
  and and_17 (and_17_out, d_ff_5_q, and_1_out);
  not not_3 (not_3_out, d_ff_5_q);
  Write_Gates writes_1 (
    .out_9(writes_1_out_9), .in_1(reads_1_out_12), .in_2(reads_3_out_12), .in_3(reads_5_out_12),
    .in_4(reads_7_out_12), .in_5(reads_9_out_12), .in_6(reads_11_out_12), .in_7(reads_13_out_12),
    .in_8(reads_15_out_12));
  ram ram_1 (
    .out_12(ram_1_out_12), .out_13(ram_1_out_13), .out_14(ram_1_out_14), .out_15(ram_1_out_15),
    .out_16(ram_1_out_16), .out_17(ram_1_out_17), .out_18(ram_1_out_18), .out_19(ram_1_out_19),
    .in_1(d_ff_6_q[7]), .in_2(d_ff_6_q[6]), .in_3(d_ff_6_q[5]), .in_4(d_ff_6_q[4]), .in_5(d_ff_6_q[3]),
    .in_6(d_ff_6_q[2]), .in_7(d_ff_6_q[1]), .in_8(d_ff_6_q[0]), .Clock(Clock), .Address(and_18_out),
    .in_11({1'b0, {5{in_1}}, 1'b0, in_1}));
  and and_18 (and_18_out, and_9_out, d_ff_5_q);
  Read_Gates reads_1 (
    .Read(not_2_out), .Clock(Clock), .Address(and_1_out), .out_12(reads_1_out_12), .in_4(ram_2_out_12),
    .in_5(ram_2_out_13), .in_6(ram_2_out_14), .in_7(ram_2_out_15), .in_8(ram_2_out_16), .in_9(ram_2_out_17),
    .in_10(ram_2_out_18), .in_11(ram_2_out_19));
  ram ram_2 (
    .out_12(ram_2_out_12), .out_13(ram_2_out_13), .out_14(ram_2_out_14), .out_15(ram_2_out_15),
    .out_16(ram_2_out_16), .out_17(ram_2_out_17), .out_18(ram_2_out_18), .out_19(ram_2_out_19),
    .in_1(d_ff_6_q[7]), .in_2(d_ff_6_q[6]), .in_3(d_ff_6_q[5]), .in_4(d_ff_6_q[4]), .in_5(d_ff_6_q[3]),
    .in_6(d_ff_6_q[2]), .in_7(d_ff_6_q[1]), .in_8(d_ff_6_q[0]), .Clock(Clock), .Address(and_17_out),
    .in_11({{2{in_1}}, {6{1'b0}}}));
  Read_Gates reads_2 (
    .Read(not_3_out), .Clock(Clock), .Address(and_9_out), .out_12(reads_2_out_12), .in_4(ram_1_out_12),
    .in_5(ram_1_out_13), .in_6(ram_1_out_14), .in_7(ram_1_out_15), .in_8(ram_1_out_16), .in_9(ram_1_out_17),
    .in_10(ram_1_out_18), .in_11(ram_1_out_19));
  Write_Combine write_combine_1 (
    .out_3(write_combine_1_out_3), .out_4(write_combine_1_out_4), .out_5(write_combine_1_out_5),
    .out_6(write_combine_1_out_6), .out_7(write_combine_1_out_7), .out_8(write_combine_1_out_8),
    .out_9(write_combine_1_out_9), .out_10(write_combine_1_out_10), .out_11(write_combine_1_out_11),
    .out_12(write_combine_1_out_12), .out_13(write_combine_1_out_13), .out_14(write_combine_1_out_14),
    .out_15(write_combine_1_out_15), .out_16(write_combine_1_out_16), .out_17(write_combine_1_out_17),
    .out_18(write_combine_1_out_18), .in_1(writes_2_out_9), .in_2(writes_1_out_9));
  not not_4 (not_4_out, d_ff_5_q);
  not not_5 (not_5_out, d_ff_5_q);
  and and_19 (and_19_out, d_ff_5_q, and_2_out);
  ram ram_3 (
    .out_12(ram_3_out_12), .out_13(ram_3_out_13), .out_14(ram_3_out_14), .out_15(ram_3_out_15),
    .out_16(ram_3_out_16), .out_17(ram_3_out_17), .out_18(ram_3_out_18), .out_19(ram_3_out_19),
    .in_1(d_ff_6_q[7]), .in_2(d_ff_6_q[6]), .in_3(d_ff_6_q[5]), .in_4(d_ff_6_q[4]), .in_5(d_ff_6_q[3]),
    .in_6(d_ff_6_q[2]), .in_7(d_ff_6_q[1]), .in_8(d_ff_6_q[0]), .Clock(Clock), .Address(and_20_out),
    .in_11({2'b00, in_1, {5{1'b0}}}));
  and and_20 (and_20_out, and_10_out, d_ff_5_q);
  Read_Gates reads_3 (
    .Read(not_5_out), .Clock(Clock), .Address(and_2_out), .out_12(reads_3_out_12), .in_4(ram_4_out_12),
    .in_5(ram_4_out_13), .in_6(ram_4_out_14), .in_7(ram_4_out_15), .in_8(ram_4_out_16), .in_9(ram_4_out_17),
    .in_10(ram_4_out_18), .in_11(ram_4_out_19));
  ram ram_4 (
    .out_12(ram_4_out_12), .out_13(ram_4_out_13), .out_14(ram_4_out_14), .out_15(ram_4_out_15),
    .out_16(ram_4_out_16), .out_17(ram_4_out_17), .out_18(ram_4_out_18), .out_19(ram_4_out_19),
    .in_1(d_ff_6_q[7]), .in_2(d_ff_6_q[6]), .in_3(d_ff_6_q[5]), .in_4(d_ff_6_q[4]), .in_5(d_ff_6_q[3]),
    .in_6(d_ff_6_q[2]), .in_7(d_ff_6_q[1]), .in_8(d_ff_6_q[0]), .Clock(Clock), .Address(and_19_out),
    .in_11({{2{in_1}}, {5{1'b0}}, in_1}));
  Read_Gates reads_4 (
    .Read(not_4_out), .Clock(Clock), .Address(and_10_out), .out_12(reads_4_out_12), .in_4(ram_3_out_12),
    .in_5(ram_3_out_13), .in_6(ram_3_out_14), .in_7(ram_3_out_15), .in_8(ram_3_out_16), .in_9(ram_3_out_17),
    .in_10(ram_3_out_18), .in_11(ram_3_out_19));
  not not_6 (not_6_out, d_ff_5_q);
  not not_7 (not_7_out, d_ff_5_q);
  and and_21 (and_21_out, and_11_out, d_ff_5_q);
  Read_Gates reads_5 (
    .Read(not_6_out), .Clock(Clock), .Address(and_3_out), .out_12(reads_5_out_12), .in_4(ram_5_out_12),
    .in_5(ram_5_out_13), .in_6(ram_5_out_14), .in_7(ram_5_out_15), .in_8(ram_5_out_16), .in_9(ram_5_out_17),
    .in_10(ram_5_out_18), .in_11(ram_5_out_19));
  ram ram_5 (
    .out_12(ram_5_out_12), .out_13(ram_5_out_13), .out_14(ram_5_out_14), .out_15(ram_5_out_15),
    .out_16(ram_5_out_16), .out_17(ram_5_out_17), .out_18(ram_5_out_18), .out_19(ram_5_out_19),
    .in_1(d_ff_6_q[7]), .in_2(d_ff_6_q[6]), .in_3(d_ff_6_q[5]), .in_4(d_ff_6_q[4]), .in_5(d_ff_6_q[3]),
    .in_6(d_ff_6_q[2]), .in_7(d_ff_6_q[1]), .in_8(d_ff_6_q[0]), .Clock(Clock), .Address(and_22_out),
    .in_11({{7{1'b0}}, in_1}));
  and and_22 (and_22_out, and_3_out, d_ff_5_q);
  Read_Gates reads_6 (
    .Read(not_7_out), .Clock(Clock), .Address(and_11_out), .out_12(reads_6_out_12), .in_4(ram_6_out_12),
    .in_5(ram_6_out_13), .in_6(ram_6_out_14), .in_7(ram_6_out_15), .in_8(ram_6_out_16), .in_9(ram_6_out_17),
    .in_10(ram_6_out_18), .in_11(ram_6_out_19));
  ram ram_6 (
    .out_12(ram_6_out_12), .out_13(ram_6_out_13), .out_14(ram_6_out_14), .out_15(ram_6_out_15),
    .out_16(ram_6_out_16), .out_17(ram_6_out_17), .out_18(ram_6_out_18), .out_19(ram_6_out_19),
    .in_1(d_ff_6_q[7]), .in_2(d_ff_6_q[6]), .in_3(d_ff_6_q[5]), .in_4(d_ff_6_q[4]), .in_5(d_ff_6_q[3]),
    .in_6(d_ff_6_q[2]), .in_7(d_ff_6_q[1]), .in_8(d_ff_6_q[0]), .Clock(Clock), .Address(and_21_out),
    .in_11({1'b0, in_1, 1'b0, {4{in_1}}, 1'b0}));
  not not_8 (not_8_out, d_ff_5_q);
  not not_9 (not_9_out, d_ff_5_q);
  ram ram_7 (
    .out_12(ram_7_out_12), .out_13(ram_7_out_13), .out_14(ram_7_out_14), .out_15(ram_7_out_15),
    .out_16(ram_7_out_16), .out_17(ram_7_out_17), .out_18(ram_7_out_18), .out_19(ram_7_out_19),
    .in_1(d_ff_6_q[7]), .in_2(d_ff_6_q[6]), .in_3(d_ff_6_q[5]), .in_4(d_ff_6_q[4]), .in_5(d_ff_6_q[3]),
    .in_6(d_ff_6_q[2]), .in_7(d_ff_6_q[1]), .in_8(d_ff_6_q[0]), .Clock(Clock), .Address(and_23_out),
    .in_11({1'b0, {2{in_1}}, 2'b00, in_1, 1'b0, in_1}));
  and and_23 (and_23_out, and_12_out, d_ff_5_q);
  Read_Gates reads_7 (
    .Read(not_8_out), .Clock(Clock), .Address(and_4_out), .out_12(reads_7_out_12), .in_4(ram_8_out_12),
    .in_5(ram_8_out_13), .in_6(ram_8_out_14), .in_7(ram_8_out_15), .in_8(ram_8_out_16), .in_9(ram_8_out_17),
    .in_10(ram_8_out_18), .in_11(ram_8_out_19));
  ram ram_8 (
    .out_12(ram_8_out_12), .out_13(ram_8_out_13), .out_14(ram_8_out_14), .out_15(ram_8_out_15),
    .out_16(ram_8_out_16), .out_17(ram_8_out_17), .out_18(ram_8_out_18), .out_19(ram_8_out_19),
    .in_1(d_ff_6_q[7]), .in_2(d_ff_6_q[6]), .in_3(d_ff_6_q[5]), .in_4(d_ff_6_q[4]), .in_5(d_ff_6_q[3]),
    .in_6(d_ff_6_q[2]), .in_7(d_ff_6_q[1]), .in_8(d_ff_6_q[0]), .Clock(Clock), .Address(and_24_out),
    .in_11({1'b0, in_1, 4'b0000, {2{in_1}}}));
  and and_24 (and_24_out, and_4_out, d_ff_5_q);
  Read_Gates reads_8 (
    .Read(not_9_out), .Clock(Clock), .Address(and_12_out), .out_12(reads_8_out_12), .in_4(ram_7_out_12),
    .in_5(ram_7_out_13), .in_6(ram_7_out_14), .in_7(ram_7_out_15), .in_8(ram_7_out_16), .in_9(ram_7_out_17),
    .in_10(ram_7_out_18), .in_11(ram_7_out_19));
  not not_10 (not_10_out, d_ff_5_q);
  not not_11 (not_11_out, d_ff_5_q);
  and and_25 (and_25_out, and_5_out, d_ff_5_q);
  ram ram_9 (
    .out_12(ram_9_out_12), .out_13(ram_9_out_13), .out_14(ram_9_out_14), .out_15(ram_9_out_15),
    .out_16(ram_9_out_16), .out_17(ram_9_out_17), .out_18(ram_9_out_18), .out_19(ram_9_out_19),
    .in_1(d_ff_6_q[7]), .in_2(d_ff_6_q[6]), .in_3(d_ff_6_q[5]), .in_4(d_ff_6_q[4]), .in_5(d_ff_6_q[3]),
    .in_6(d_ff_6_q[2]), .in_7(d_ff_6_q[1]), .in_8(d_ff_6_q[0]), .Clock(Clock), .Address(and_26_out),
    .in_11({in_1, 3'b000, in_1, 3'b000}));
  and and_26 (and_26_out, and_13_out, d_ff_5_q);
  Read_Gates reads_9 (
    .Read(not_11_out), .Clock(Clock), .Address(and_5_out), .out_12(reads_9_out_12), .in_4(ram_10_out_12),
    .in_5(ram_10_out_13), .in_6(ram_10_out_14), .in_7(ram_10_out_15), .in_8(ram_10_out_16),
    .in_9(ram_10_out_17), .in_10(ram_10_out_18), .in_11(ram_10_out_19));
  ram ram_10 (
    .out_12(ram_10_out_12), .out_13(ram_10_out_13), .out_14(ram_10_out_14), .out_15(ram_10_out_15),
    .out_16(ram_10_out_16), .out_17(ram_10_out_17), .out_18(ram_10_out_18), .out_19(ram_10_out_19),
    .in_1(d_ff_6_q[7]), .in_2(d_ff_6_q[6]), .in_3(d_ff_6_q[5]), .in_4(d_ff_6_q[4]), .in_5(d_ff_6_q[3]),
    .in_6(d_ff_6_q[2]), .in_7(d_ff_6_q[1]), .in_8(d_ff_6_q[0]), .Clock(Clock), .Address(and_25_out),
    .in_11({1'b0, {2{in_1}}, 3'b000, in_1, 1'b0}));
  Read_Gates reads_10 (
    .Read(not_10_out), .Clock(Clock), .Address(and_13_out), .out_12(reads_10_out_12), .in_4(ram_9_out_12),
    .in_5(ram_9_out_13), .in_6(ram_9_out_14), .in_7(ram_9_out_15), .in_8(ram_9_out_16), .in_9(ram_9_out_17),
    .in_10(ram_9_out_18), .in_11(ram_9_out_19));
  not not_12 (not_12_out, d_ff_5_q);
  and and_27 (and_27_out, and_6_out, d_ff_5_q);
  not not_13 (not_13_out, d_ff_5_q);
  ram ram_11 (
    .out_12(ram_11_out_12), .out_13(ram_11_out_13), .out_14(ram_11_out_14), .out_15(ram_11_out_15),
    .out_16(ram_11_out_16), .out_17(ram_11_out_17), .out_18(ram_11_out_18), .out_19(ram_11_out_19),
    .in_1(d_ff_6_q[7]), .in_2(d_ff_6_q[6]), .in_3(d_ff_6_q[5]), .in_4(d_ff_6_q[4]), .in_5(d_ff_6_q[3]),
    .in_6(d_ff_6_q[2]), .in_7(d_ff_6_q[1]), .in_8(d_ff_6_q[0]), .Clock(Clock), .Address(and_28_out),
    .in_11({in_1, 1'b0, in_1, 4'b0000, in_1}));
  and and_28 (and_28_out, and_14_out, d_ff_5_q);
  Read_Gates reads_11 (
    .Read(not_12_out), .Clock(Clock), .Address(and_6_out), .out_12(reads_11_out_12), .in_4(ram_12_out_12),
    .in_5(ram_12_out_13), .in_6(ram_12_out_14), .in_7(ram_12_out_15), .in_8(ram_12_out_16),
    .in_9(ram_12_out_17), .in_10(ram_12_out_18), .in_11(ram_12_out_19));
  ram ram_12 (
    .out_12(ram_12_out_12), .out_13(ram_12_out_13), .out_14(ram_12_out_14), .out_15(ram_12_out_15),
    .out_16(ram_12_out_16), .out_17(ram_12_out_17), .out_18(ram_12_out_18), .out_19(ram_12_out_19),
    .in_1(d_ff_6_q[7]), .in_2(d_ff_6_q[6]), .in_3(d_ff_6_q[5]), .in_4(d_ff_6_q[4]), .in_5(d_ff_6_q[3]),
    .in_6(d_ff_6_q[2]), .in_7(d_ff_6_q[1]), .in_8(d_ff_6_q[0]), .Clock(Clock), .Address(and_27_out),
    .in_11({8{1'b0}}));
  Read_Gates reads_12 (
    .Read(not_13_out), .Clock(Clock), .Address(and_14_out), .out_12(reads_12_out_12), .in_4(ram_11_out_12),
    .in_5(ram_11_out_13), .in_6(ram_11_out_14), .in_7(ram_11_out_15), .in_8(ram_11_out_16),
    .in_9(ram_11_out_17), .in_10(ram_11_out_18), .in_11(ram_11_out_19));
  not not_14 (not_14_out, d_ff_5_q);
  not not_15 (not_15_out, d_ff_5_q);
  and and_29 (and_29_out, and_15_out, d_ff_5_q);
  Read_Gates reads_13 (
    .Read(not_14_out), .Clock(Clock), .Address(and_7_out), .out_12(reads_13_out_12), .in_4(ram_13_out_12),
    .in_5(ram_13_out_13), .in_6(ram_13_out_14), .in_7(ram_13_out_15), .in_8(ram_13_out_16),
    .in_9(ram_13_out_17), .in_10(ram_13_out_18), .in_11(ram_13_out_19));
  ram ram_13 (
    .out_12(ram_13_out_12), .out_13(ram_13_out_13), .out_14(ram_13_out_14), .out_15(ram_13_out_15),
    .out_16(ram_13_out_16), .out_17(ram_13_out_17), .out_18(ram_13_out_18), .out_19(ram_13_out_19),
    .in_1(d_ff_6_q[7]), .in_2(d_ff_6_q[6]), .in_3(d_ff_6_q[5]), .in_4(d_ff_6_q[4]), .in_5(d_ff_6_q[3]),
    .in_6(d_ff_6_q[2]), .in_7(d_ff_6_q[1]), .in_8(d_ff_6_q[0]), .Clock(Clock), .Address(and_30_out),
    .in_11({1'b0, in_1, 3'b000, in_1, 2'b00}));
  and and_30 (and_30_out, and_7_out, d_ff_5_q);
  Read_Gates reads_14 (
    .Read(not_15_out), .Clock(Clock), .Address(and_15_out), .out_12(reads_14_out_12), .in_4(ram_14_out_12),
    .in_5(ram_14_out_13), .in_6(ram_14_out_14), .in_7(ram_14_out_15), .in_8(ram_14_out_16),
    .in_9(ram_14_out_17), .in_10(ram_14_out_18), .in_11(ram_14_out_19));
  ram ram_14 (
    .out_12(ram_14_out_12), .out_13(ram_14_out_13), .out_14(ram_14_out_14), .out_15(ram_14_out_15),
    .out_16(ram_14_out_16), .out_17(ram_14_out_17), .out_18(ram_14_out_18), .out_19(ram_14_out_19),
    .in_1(d_ff_6_q[7]), .in_2(d_ff_6_q[6]), .in_3(d_ff_6_q[5]), .in_4(d_ff_6_q[4]), .in_5(d_ff_6_q[3]),
    .in_6(d_ff_6_q[2]), .in_7(d_ff_6_q[1]), .in_8(d_ff_6_q[0]), .Clock(Clock), .Address(and_29_out),
    .in_11({in_1, {7{1'b0}}}));
  not not_16 (not_16_out, d_ff_5_q);
  not not_17 (not_17_out, d_ff_5_q);
  ram ram_15 (
    .out_12(ram_15_out_12), .out_13(ram_15_out_13), .out_14(ram_15_out_14), .out_15(ram_15_out_15),
    .out_16(ram_15_out_16), .out_17(ram_15_out_17), .out_18(ram_15_out_18), .out_19(ram_15_out_19),
    .in_1(d_ff_6_q[7]), .in_2(d_ff_6_q[6]), .in_3(d_ff_6_q[5]), .in_4(d_ff_6_q[4]), .in_5(d_ff_6_q[3]),
    .in_6(d_ff_6_q[2]), .in_7(d_ff_6_q[1]), .in_8(d_ff_6_q[0]), .Clock(Clock), .Address(and_31_out),
    .in_11({1'b0, in_1, {6{1'b0}}}));
  and and_31 (and_31_out, and_16_out, d_ff_5_q);
  Read_Gates reads_15 (
    .Read(not_16_out), .Clock(Clock), .Address(and_8_out), .out_12(reads_15_out_12), .in_4(ram_16_out_12),
    .in_5(ram_16_out_13), .in_6(ram_16_out_14), .in_7(ram_16_out_15), .in_8(ram_16_out_16),
    .in_9(ram_16_out_17), .in_10(ram_16_out_18), .in_11(ram_16_out_19));
  ram ram_16 (
    .out_12(ram_16_out_12), .out_13(ram_16_out_13), .out_14(ram_16_out_14), .out_15(ram_16_out_15),
    .out_16(ram_16_out_16), .out_17(ram_16_out_17), .out_18(ram_16_out_18), .out_19(ram_16_out_19),
    .in_1(d_ff_6_q[7]), .in_2(d_ff_6_q[6]), .in_3(d_ff_6_q[5]), .in_4(d_ff_6_q[4]), .in_5(d_ff_6_q[3]),
    .in_6(d_ff_6_q[2]), .in_7(d_ff_6_q[1]), .in_8(d_ff_6_q[0]), .Clock(Clock), .Address(and_32_out),
    .in_11({1'b0, {6{in_1}}, 1'b0}));
  and and_32 (and_32_out, and_8_out, d_ff_5_q);
  Write_Gates writes_2 (
    .out_9(writes_2_out_9), .in_1(reads_16_out_12), .in_2(reads_14_out_12), .in_3(reads_12_out_12),
    .in_4(reads_10_out_12), .in_5(reads_8_out_12), .in_6(reads_6_out_12), .in_7(reads_4_out_12),
    .in_8(reads_2_out_12));
  Read_Gates reads_16 (
    .Read(not_17_out), .Clock(Clock), .Address(and_16_out), .out_12(reads_16_out_12), .in_4(ram_15_out_12),
    .in_5(ram_15_out_13), .in_6(ram_15_out_14), .in_7(ram_15_out_15), .in_8(ram_15_out_16),
    .in_9(ram_15_out_17), .in_10(ram_15_out_18), .in_11(ram_15_out_19));

  // Notes on the sheet:
  //   Address register
  //   Data Register
  //   AutoSet
  //   1
  //   0
  //   1
  //   0
  //   0
  //   1
  //   0
  //   1
endmodule

module ram (
  input  in_1,
  input  in_2,
  input  in_3,
  input  in_4,
  input  in_5,
  input  in_6,
  input  in_7,
  input  in_8,
  input  Clock,
  input  Address,
  input  [7:0] in_11,
  output out_12,
  output out_13,
  output out_14,
  output out_15,
  output out_16,
  output out_17,
  output out_18,
  output out_19
);

  wire and_1_out, and_2_out, and_3_out, and_4_out, and_5_out, and_6_out, and_7_out, and_8_out, and_9_out,
       and_10_out, and_11_out, and_12_out, and_13_out, and_14_out, and_15_out, and_16_out, not_1_out,
       not_2_out, not_3_out, not_4_out, not_5_out, not_6_out, not_7_out, not_8_out;

  and and_1 (and_1_out, in_1, Address);
  and and_2 (and_2_out, in_2, Address);
  and and_3 (and_3_out, in_3, Address);
  and and_4 (and_4_out, in_4, Address);
  and and_5 (and_5_out, in_5, Address);
  and and_6 (and_6_out, in_6, Address);
  and and_7 (and_7_out, in_7, Address);
  and and_8 (and_8_out, in_8, Address);
  not not_1 (not_1_out, and_8_out);
  not not_2 (not_2_out, and_7_out);
  not not_3 (not_3_out, and_5_out);
  not not_4 (not_4_out, and_6_out);
  not not_5 (not_5_out, and_4_out);
  not not_6 (not_6_out, and_3_out);
  not not_7 (not_7_out, and_1_out);
  not not_8 (not_8_out, and_2_out);
  and and_9 (and_9_out, not_1_out, Address);
  and and_10 (and_10_out, not_2_out, Address);
  and and_11 (and_11_out, not_4_out, Address);
  and and_12 (and_12_out, not_3_out, Address);
  and and_13 (and_13_out, not_5_out, Address);
  and and_14 (and_14_out, not_6_out, Address);
  and and_15 (and_15_out, not_8_out, Address);
  and and_16 (and_16_out, not_7_out, Address);
  S_R_Flip_Flop s_r_ff_1 (
    .S(and_8_out), .clk(Clock), .R(and_9_out), .Q(out_12), .preset(in_11[7]), .en(Clock));  // open: Qn, reset
  S_R_Flip_Flop s_r_ff_2 (
    .S(and_7_out), .clk(Clock), .R(and_10_out), .Q(out_13), .preset(in_11[6]), .en(Clock));  // open: Qn, reset
  S_R_Flip_Flop s_r_ff_3 (
    .S(and_6_out), .clk(Clock), .R(and_11_out), .Q(out_14), .preset(in_11[5]), .en(Clock));  // open: Qn, reset
  S_R_Flip_Flop s_r_ff_4 (
    .S(and_5_out), .clk(Clock), .R(and_12_out), .Q(out_15), .preset(in_11[4]), .en(Clock));  // open: Qn, reset
  S_R_Flip_Flop s_r_ff_5 (
    .S(and_4_out), .clk(Clock), .R(and_13_out), .Q(out_16), .preset(in_11[3]), .en(Clock));  // open: Qn, reset
  S_R_Flip_Flop s_r_ff_6 (
    .S(and_3_out), .clk(Clock), .R(and_14_out), .Q(out_17), .preset(in_11[2]), .en(Clock));  // open: Qn, reset
  S_R_Flip_Flop s_r_ff_7 (
    .S(and_2_out), .clk(Clock), .R(and_15_out), .Q(out_18), .preset(in_11[1]), .en(Clock));  // open: Qn, reset
  S_R_Flip_Flop s_r_ff_8 (
    .S(and_1_out), .clk(Clock), .R(and_16_out), .Q(out_19), .preset(in_11[0]), .en(Clock));  // open: Qn, reset

  // Notes on the sheet:
  //   Data
  //   Input
  //   Output
endmodule

module Read_Gates (
  input  Read,
  input  Clock,
  input  Address,
  input  in_4,
  input  in_5,
  input  in_6,
  input  in_7,
  input  in_8,
  input  in_9,
  input  in_10,
  input  in_11,
  output [15:0] out_12
);

  wire not_1_out, not_2_out, not_3_out, not_4_out, not_5_out, not_6_out, not_7_out, not_8_out;

  and and_1 (out_12[15], Read, Clock, Address, in_4);
  and and_2 (out_12[14], Read, Clock, Address, not_1_out);
  not not_1 (not_1_out, in_4);
  and and_3 (out_12[13], Read, Clock, Address, in_5);
  and and_4 (out_12[12], Read, Clock, Address, not_2_out);
  not not_2 (not_2_out, in_5);
  and and_5 (out_12[11], Read, Clock, Address, in_6);
  and and_6 (out_12[10], Read, Clock, Address, not_3_out);
  not not_3 (not_3_out, in_6);
  and and_7 (out_12[9], Read, Clock, Address, in_7);
  and and_8 (out_12[8], Read, Clock, Address, not_4_out);
  not not_4 (not_4_out, in_7);
  and and_9 (out_12[7], Read, Clock, Address, in_8);
  and and_10 (out_12[6], Read, Clock, Address, not_5_out);
  not not_5 (not_5_out, in_8);
  and and_11 (out_12[5], Read, Clock, Address, in_9);
  and and_12 (out_12[4], Read, Clock, Address, not_6_out);
  not not_6 (not_6_out, in_9);
  and and_13 (out_12[3], Read, Clock, Address, in_10);
  and and_14 (out_12[2], Read, Clock, Address, not_7_out);
  not not_7 (not_7_out, in_10);
  and and_15 (out_12[1], Read, Clock, Address, in_11);
  and and_16 (out_12[0], Read, Clock, Address, not_8_out);
  not not_8 (not_8_out, in_11);
endmodule

module Write_Gates (
  input  [15:0] in_1,
  input  [15:0] in_2,
  input  [15:0] in_3,
  input  [15:0] in_4,
  input  [15:0] in_5,
  input  [15:0] in_6,
  input  [15:0] in_7,
  input  [15:0] in_8,
  output [15:0] out_9
);

  or or_1 (out_9[0], in_1[0], in_2[0], in_3[0], in_4[0], in_5[0], in_6[0], in_7[0], in_8[0]);
  or or_2 (out_9[1], in_1[1], in_2[1], in_3[1], in_4[1], in_5[1], in_6[1], in_7[1], in_8[1]);
  or or_3 (out_9[2], in_1[2], in_2[2], in_3[2], in_4[2], in_5[2], in_6[2], in_7[2], in_8[2]);
  or or_4 (out_9[3], in_1[3], in_2[3], in_3[3], in_4[3], in_5[3], in_6[3], in_7[3], in_8[3]);
  or or_5 (out_9[4], in_1[4], in_2[4], in_3[4], in_4[4], in_5[4], in_6[4], in_7[4], in_8[4]);
  or or_6 (out_9[5], in_1[5], in_2[5], in_3[5], in_4[5], in_5[5], in_6[5], in_7[5], in_8[5]);
  or or_7 (out_9[6], in_1[6], in_2[6], in_3[6], in_4[6], in_5[6], in_6[6], in_7[6], in_8[6]);
  or or_8 (out_9[7], in_1[7], in_2[7], in_3[7], in_4[7], in_5[7], in_6[7], in_7[7], in_8[7]);
  or or_9 (out_9[8], in_1[8], in_2[8], in_3[8], in_4[8], in_5[8], in_6[8], in_7[8], in_8[8]);
  or or_10 (out_9[9], in_1[9], in_2[9], in_3[9], in_4[9], in_5[9], in_6[9], in_7[9], in_8[9]);
  or or_11 (out_9[10], in_1[10], in_2[10], in_3[10], in_4[10], in_5[10], in_6[10], in_7[10], in_8[10]);
  or or_12 (out_9[11], in_1[11], in_2[11], in_3[11], in_4[11], in_5[11], in_6[11], in_7[11], in_8[11]);
  or or_13 (out_9[12], in_1[12], in_2[12], in_3[12], in_4[12], in_5[12], in_6[12], in_7[12], in_8[12]);
  or or_14 (out_9[13], in_1[13], in_2[13], in_3[13], in_4[13], in_5[13], in_6[13], in_7[13], in_8[13]);
  or or_15 (out_9[14], in_1[14], in_2[14], in_3[14], in_4[14], in_5[14], in_6[14], in_7[14], in_8[14]);
  or or_16 (out_9[15], in_1[15], in_2[15], in_3[15], in_4[15], in_5[15], in_6[15], in_7[15], in_8[15]);
endmodule

module Write_Combine (
  input  [15:0] in_1,
  input  [15:0] in_2,
  output out_3,
  output out_4,
  output out_5,
  output out_6,
  output out_7,
  output out_8,
  output out_9,
  output out_10,
  output out_11,
  output out_12,
  output out_13,
  output out_14,
  output out_15,
  output out_16,
  output out_17,
  output out_18
);

  or or_1 (out_3, in_1[0], in_2[0]);
  or or_2 (out_4, in_1[1], in_2[1]);
  or or_3 (out_5, in_1[2], in_2[2]);
  or or_4 (out_6, in_1[3], in_2[3]);
  or or_5 (out_7, in_1[4], in_2[4]);
  or or_6 (out_8, in_1[5], in_2[5]);
  or or_7 (out_9, in_1[6], in_2[6]);
  or or_8 (out_10, in_1[7], in_2[7]);
  or or_9 (out_11, in_1[8], in_2[8]);
  or or_10 (out_12, in_1[9], in_2[9]);
  or or_11 (out_13, in_1[10], in_2[10]);
  or or_12 (out_14, in_1[11], in_2[11]);
  or or_13 (out_15, in_1[12], in_2[12]);
  or or_14 (out_16, in_1[13], in_2[13]);
  or or_15 (out_17, in_1[14], in_2[14]);
  or or_16 (out_18, in_1[15], in_2[15]);
endmodule

module Bus (
  input  [7:0] in_1,
  input  Read,
  input  Write,
  input  in_4
);

  wire clock_1_out, hex_digit_convert_1_middle, hex_digit_convert_1_out_2, hex_digit_convert_1_out_3,
       hex_digit_convert_1_out_5, hex_digit_convert_1_out_6, hex_digit_convert_1_out_7,
       hex_digit_convert_1_out_8, hex_digit_convert_2_middle, hex_digit_convert_2_out_2,
       hex_digit_convert_2_out_3, hex_digit_convert_2_out_5, hex_digit_convert_2_out_6,
       hex_digit_convert_2_out_7, hex_digit_convert_2_out_8, undriven, undriven_3;
  wire [3:0] controlled_buffer_3_out, controlled_buffer_3_out_2;
  wire [7:0] controlled_buffer_1_out, controlled_buffer_2_out, undriven_2;

  BIGRAM bigram_1 (
    .Clock(undriven), .Read_Write_Bit(undriven_3), .in_4(controlled_buffer_2_out[3:0]), .Write(undriven_2),
    .in_1(clock_1_out));  // open: out_6
  Hex_Digit_convert hex_digit_convert_1 (
    .in_1(controlled_buffer_3_out), .out_2(hex_digit_convert_1_out_2), .out_3(hex_digit_convert_1_out_3),
    .Middle(hex_digit_convert_1_middle), .out_5(hex_digit_convert_1_out_5),
    .out_6(hex_digit_convert_1_out_6), .out_7(hex_digit_convert_1_out_7), .out_8(hex_digit_convert_1_out_8));
  Clock clock_1 (.out(clock_1_out));
  _7_Segment_Display u_7_segment_display_1 (
    .g(hex_digit_convert_1_middle), .f(hex_digit_convert_1_out_2), .a(hex_digit_convert_1_out_3),
    .b(hex_digit_convert_1_out_5), .e(hex_digit_convert_1_out_6), .d(hex_digit_convert_1_out_7),
    .c(hex_digit_convert_1_out_8));  // open: dp
  assign controlled_buffer_1_out = Read ? undriven_2 : 8'bz;  // Controlled_Buffer controlled_buffer_1
  assign controlled_buffer_2_out = Write ? in_1 : 8'bz;  // Controlled_Buffer controlled_buffer_2
  Hex_Digit_convert hex_digit_convert_2 (
    .in_1(controlled_buffer_3_out_2), .out_2(hex_digit_convert_2_out_2), .out_3(hex_digit_convert_2_out_3),
    .Middle(hex_digit_convert_2_middle), .out_5(hex_digit_convert_2_out_5),
    .out_6(hex_digit_convert_2_out_6), .out_7(hex_digit_convert_2_out_7), .out_8(hex_digit_convert_2_out_8));
  _7_Segment_Display u_7_segment_display_2 (
    .g(hex_digit_convert_2_middle), .f(hex_digit_convert_2_out_2), .a(hex_digit_convert_2_out_3),
    .b(hex_digit_convert_2_out_5), .e(hex_digit_convert_2_out_6), .d(hex_digit_convert_2_out_7),
    .c(hex_digit_convert_2_out_8));  // open: dp
  assign {controlled_buffer_3_out_2, controlled_buffer_3_out} = in_4 ? in_1 : 8'bz;  // Controlled_Buffer controlled_buffer_3
  // Pins of 4 and 8 bits meet at controlled_buffer_2_out

  // Notes on the sheet:
  //   Address
endmodule

module input_buffer (
  input  in_1,
  input  [7:0] in_2,
  output [7:0] out_3
);

  D_Flip_Flop d_ff_1 (.clk(in_1), .D(in_2[0]), .Q(out_3[0]));  // open: Qn, preset, en, reset
  D_Flip_Flop d_ff_2 (.clk(in_1), .D(in_2[1]), .Q(out_3[1]));  // open: Qn, preset, en, reset
  D_Flip_Flop d_ff_3 (.clk(in_1), .D(in_2[2]), .Q(out_3[2]));  // open: Qn, preset, en, reset
  D_Flip_Flop d_ff_4 (.clk(in_1), .D(in_2[3]), .Q(out_3[3]));  // open: Qn, preset, en, reset
  D_Flip_Flop d_ff_5 (.clk(in_1), .D(in_2[4]), .Q(out_3[4]));  // open: Qn, preset, en, reset
  D_Flip_Flop d_ff_6 (.clk(in_1), .D(in_2[5]), .Q(out_3[5]));  // open: Qn, preset, en, reset
  D_Flip_Flop d_ff_7 (.clk(in_1), .D(in_2[6]), .Q(out_3[6]));  // open: Qn, preset, en, reset
  D_Flip_Flop d_ff_8 (.clk(in_1), .D(in_2[7]), .Q(out_3[7]));  // open: Qn, preset, en, reset
endmodule

module Hex_Digit_convert (
  input  [3:0] in_1,
  output out_2,
  output out_3,
  output Middle,
  output out_5,
  output out_6,
  output out_7,
  output out_8
);

  wire and_1_out, and_2_out, and_3_out, and_4_out, and_5_out, and_6_out, and_7_out, and_8_out, and_9_out,
       and_10_out, and_11_out, and_12_out, and_13_out, and_14_out, and_15_out, and_16_out, and_17_out,
       and_18_out, and_19_out, and_20_out, and_21_out, and_22_out, and_23_out, and_24_out, and_25_out,
       and_26_out, and_27_out, and_28_out, and_29_out, and_30_out, and_31_out, and_32_out, and_33_out,
       and_34_out, and_35_out, not_1_out, not_2_out, not_3_out, not_4_out, not_5_out, not_6_out, not_7_out,
       not_8_out, not_9_out, not_10_out, not_11_out, not_12_out, not_13_out, not_14_out, not_15_out,
       not_16_out, not_17_out, not_18_out, not_19_out, not_20_out, not_21_out, not_22_out, not_23_out,
       not_24_out, not_25_out, not_26_out, not_27_out, not_28_out, not_29_out, not_30_out, not_31_out,
       not_32_out, not_33_out, not_34_out, not_35_out, not_36_out, not_37_out, not_38_out, not_39_out,
       not_40_out, not_41_out, not_42_out, not_43_out;

  not not_1 (not_1_out, in_1[1]);
  not not_2 (not_2_out, in_1[0]);
  not not_3 (not_3_out, in_1[3]);
  not not_4 (not_4_out, in_1[1]);
  not not_5 (not_5_out, in_1[0]);
  not not_6 (not_6_out, in_1[2]);
  not not_7 (not_7_out, in_1[2]);
  not not_8 (not_8_out, in_1[0]);
  not not_9 (not_9_out, in_1[3]);
  not not_10 (not_10_out, in_1[3]);
  not not_11 (not_11_out, in_1[2]);
  not not_12 (not_12_out, in_1[1]);
  not not_13 (not_13_out, in_1[0]);
  not not_14 (not_14_out, in_1[2]);
  not not_15 (not_15_out, in_1[0]);
  not not_16 (not_16_out, in_1[3]);
  not not_17 (not_17_out, in_1[1]);
  not not_18 (not_18_out, in_1[2]);
  not not_19 (not_19_out, in_1[3]);
  not not_20 (not_20_out, in_1[2]);
  not not_21 (not_21_out, in_1[3]);
  not not_22 (not_22_out, in_1[1]);
  not not_23 (not_23_out, in_1[0]);
  not not_24 (not_24_out, in_1[2]);
  not not_25 (not_25_out, in_1[0]);
  not not_26 (not_26_out, in_1[3]);
  not not_27 (not_27_out, in_1[1]);
  not not_28 (not_28_out, in_1[2]);
  not not_29 (not_29_out, in_1[0]);
  not not_30 (not_30_out, in_1[0]);
  not not_31 (not_31_out, in_1[3]);
  not not_32 (not_32_out, in_1[2]);
  not not_33 (not_33_out, in_1[0]);
  not not_34 (not_34_out, in_1[2]);
  not not_35 (not_35_out, in_1[1]);
  not not_36 (not_36_out, in_1[0]);
  not not_37 (not_37_out, in_1[1]);
  not not_38 (not_38_out, in_1[3]);
  not not_39 (not_39_out, in_1[1]);
  not not_40 (not_40_out, in_1[3]);
  not not_41 (not_41_out, in_1[1]);
  not not_42 (not_42_out, in_1[3]);
  not not_43 (not_43_out, in_1[2]);
  and and_1 (and_1_out, not_1_out, not_2_out);
  and and_2 (and_2_out, not_3_out, in_1[2], not_4_out);
  and and_3 (and_3_out, in_1[2], not_5_out);
  and and_4 (and_4_out, in_1[3], not_6_out);
  and and_5 (and_5_out, in_1[3], in_1[1]);
  and and_6 (and_6_out, not_7_out, not_8_out);
  and and_7 (and_7_out, not_9_out, in_1[1]);
  and and_8 (and_8_out, not_10_out, in_1[2], in_1[0]);
  and and_9 (and_9_out, in_1[2], in_1[1]);
  and and_10 (and_10_out, in_1[3], not_11_out, not_12_out);
  and and_11 (and_11_out, in_1[3], not_13_out);
  and and_12 (and_12_out, not_14_out, in_1[1]);
  and and_13 (and_13_out, in_1[1], not_15_out);
  and and_14 (and_14_out, not_16_out, in_1[2], not_17_out);
  and and_15 (and_15_out, in_1[3], not_18_out);
  and and_16 (and_16_out, in_1[3], in_1[0]);
  and and_17 (and_17_out, not_19_out, not_20_out);
  and and_18 (and_18_out, not_21_out, not_22_out, not_23_out);
  and and_19 (and_19_out, not_24_out, not_25_out);
  and and_20 (and_20_out, not_26_out, in_1[1], in_1[0]);
  and and_21 (and_21_out, in_1[3], not_27_out, in_1[0]);
  and and_22 (and_22_out, not_28_out, not_29_out);
  and and_23 (and_23_out, in_1[1], not_30_out);
  and and_24 (and_24_out, in_1[3], in_1[1]);
  and and_25 (and_25_out, in_1[3], in_1[2]);
  and and_26 (and_26_out, not_31_out, not_32_out, not_33_out);
  and and_27 (and_27_out, not_34_out, in_1[1], in_1[0]);
  and and_28 (and_28_out, in_1[2], not_35_out, in_1[0]);
  and and_29 (and_29_out, in_1[2], in_1[1], not_36_out);
  and and_30 (and_30_out, in_1[3], not_37_out);
  and and_31 (and_31_out, not_38_out, not_39_out);
  and and_32 (and_32_out, not_40_out, in_1[0]);
  and and_33 (and_33_out, not_41_out, in_1[0]);
  and and_34 (and_34_out, not_42_out, in_1[2]);
  and and_35 (and_35_out, in_1[3], not_43_out);
  or or_1 (out_2, and_1_out, and_2_out, and_3_out, and_4_out, and_5_out);
  or or_2 (out_3, and_6_out, and_7_out, and_8_out, and_9_out, and_10_out, and_11_out);
  or or_3 (Middle, and_12_out, and_13_out, and_14_out, and_15_out, and_16_out);
  or or_4 (out_5, and_17_out, and_18_out, and_19_out, and_20_out, and_21_out);
  or or_5 (out_6, and_22_out, and_23_out, and_24_out, and_25_out);
  or or_6 (out_7, and_26_out, and_27_out, and_28_out, and_29_out, and_30_out);
  or or_7 (out_8, and_31_out, and_32_out, and_33_out, and_34_out, and_35_out);
endmodule

module binary_convert (
  input  in_1,
  input  in_2,
  input  in_3,
  input  in_4,
  input  in_5,
  input  in_6,
  input  in_7,
  input  in_8,
  input  in_9,
  input  in_10,
  output [7:0] out_11
);

  wire and_1_out, and_11_out, and_12_out, and_13_out, and_14_out, and_15_out, and_16_out, and_17_out,
       and_18_out, and_19_out, and_20_out, xor_1_out;
  wire [7:0] and_2_out, controlled_buffer_5_out;
  wire [7:1] and_3_out, and_4_out;
  wire [7:2] and_5_out, and_6_out, and_7_out, and_8_out;
  wire [7:3] and_9_out, and_10_out;
  wire [7:4] controlled_buffer_1_out, controlled_buffer_2_out, controlled_buffer_3_out,
       controlled_buffer_4_out, controlled_buffer_6_out, controlled_buffer_7_out, controlled_buffer_8_out,
       controlled_buffer_9_out, controlled_buffer_10_out;
  wire [7:7] not_1_out;

  ExactlyOne xor_1 (
    .out(xor_1_out), .in0(in_1), .in1(in_2), .in2(in_3), .in3(in_4), .in4(in_5), .in5(in_6), .in6(in_7),
    .in7(in_8), .in8(in_9), .in9(in_10));
  and and_1 (and_1_out, xor_1_out, in_1);
  and and_2 (and_2_out[0], xor_1_out, in_2);
  and and_3 (and_3_out[1], xor_1_out, in_3);
  and and_4 (and_4_out[1], xor_1_out, in_4);
  and and_5 (and_5_out[2], xor_1_out, in_5);
  and and_6 (and_6_out[2], xor_1_out, in_6);
  and and_7 (and_7_out[2], xor_1_out, in_7);
  and and_8 (and_8_out[2], xor_1_out, in_8);
  and and_9 (and_9_out[3], xor_1_out, in_9);
  and and_10 (and_10_out[3], xor_1_out, in_10);
  and and_11 (and_11_out, in_1, xor_1_out);
  and and_12 (and_12_out, xor_1_out, in_2);
  and and_13 (and_13_out, xor_1_out, in_3);
  and and_14 (and_14_out, xor_1_out, in_4);
  and and_15 (and_15_out, xor_1_out, in_5);
  and and_16 (and_16_out, xor_1_out, in_6);
  and and_17 (and_17_out, xor_1_out, in_7);
  and and_18 (and_18_out, xor_1_out, in_8);
  and and_19 (and_19_out, xor_1_out, in_9);
  and and_20 (and_20_out, xor_1_out, in_10);
  not not_1 (not_1_out[7], and_1_out);
  not not_2 (and_2_out[7], and_2_out[0]);
  not not_3 (and_3_out[7], and_3_out[1]);
  not not_4 (and_5_out[7], and_5_out[2]);
  not not_5 (and_7_out[7], and_7_out[2]);
  not not_6 (and_8_out[7], and_8_out[2]);
  not not_7 (and_10_out[7], and_10_out[3]);
  not not_8 (and_4_out[7], and_4_out[1]);
  not not_9 (and_6_out[7], and_6_out[2]);
  not not_10 (and_9_out[7], and_9_out[3]);
  assign {controlled_buffer_1_out, controlled_buffer_5_out[3:0]} = and_11_out ? {8{not_1_out[7]}} : 8'bz;  // Controlled_Buffer controlled_buffer_1
  assign {controlled_buffer_2_out, controlled_buffer_5_out[3:0]} = and_12_out ? {{7{and_2_out[7]}}, and_2_out[0]} : 8'bz;  // Controlled_Buffer controlled_buffer_2
  assign {controlled_buffer_3_out, controlled_buffer_5_out[3:0]} = and_13_out ? {{6{and_3_out[7]}}, and_3_out[1], and_3_out[7]} : 8'bz;  // Controlled_Buffer controlled_buffer_3
  assign {controlled_buffer_4_out, controlled_buffer_5_out[3:0]} = and_14_out ? {{6{and_4_out[7]}}, {2{and_4_out[1]}}} : 8'bz;  // Controlled_Buffer controlled_buffer_4
  assign controlled_buffer_5_out = and_15_out ? {{5{and_5_out[7]}}, and_5_out[2], {2{and_5_out[7]}}} : 8'bz;  // Controlled_Buffer controlled_buffer_5
  assign {controlled_buffer_6_out, controlled_buffer_5_out[3:0]} = and_16_out ? {{5{and_6_out[7]}}, and_6_out[2], and_6_out[7], and_6_out[2]} : 8'bz;  // Controlled_Buffer controlled_buffer_6
  assign {controlled_buffer_7_out, controlled_buffer_5_out[3:0]} = and_17_out ? {{5{and_7_out[7]}}, {2{and_7_out[2]}}, and_7_out[7]} : 8'bz;  // Controlled_Buffer controlled_buffer_7
  assign {controlled_buffer_8_out, controlled_buffer_5_out[3:0]} = and_18_out ? {{5{and_8_out[7]}}, {3{and_8_out[2]}}} : 8'bz;  // Controlled_Buffer controlled_buffer_8
  assign {controlled_buffer_9_out, controlled_buffer_5_out[3:0]} = and_19_out ? {{4{and_9_out[7]}}, and_9_out[3], {3{and_9_out[7]}}} : 8'bz;  // Controlled_Buffer controlled_buffer_9
  assign {controlled_buffer_10_out, controlled_buffer_5_out[3:0]} = and_20_out ? {{4{and_10_out[7]}}, and_10_out[3], {2{and_10_out[7]}}, and_10_out[3]} : 8'bz;  // Controlled_Buffer controlled_buffer_10
  Multiplexer #(.select(4), .width(8)) multiplexer_1 (
    .in0({8{not_1_out[7]}}), .in1({{7{and_2_out[7]}}, and_2_out[0]}),
    .in2({{6{and_3_out[7]}}, and_3_out[1], and_3_out[7]}), .in3({{6{and_4_out[7]}}, {2{and_4_out[1]}}}),
    .in4({{5{and_5_out[7]}}, and_5_out[2], {2{and_5_out[7]}}}),
    .in5({{5{and_6_out[7]}}, and_6_out[2], and_6_out[7], and_6_out[2]}),
    .in6({{5{and_7_out[7]}}, {2{and_7_out[2]}}, and_7_out[7]}), .in7({{5{and_8_out[7]}}, {3{and_8_out[2]}}}),
    .in8({{4{and_9_out[7]}}, and_9_out[3], {3{and_9_out[7]}}}),
    .in9({{4{and_10_out[7]}}, and_10_out[3], {2{and_10_out[7]}}, and_10_out[3]}), .out(out_11),
    .sel(controlled_buffer_5_out[3:0]));  // open: in10, in11, in12, in13, in14, in15, en
endmodule

module buffer_count (
  input  in_1,
  output out_2
);

  wire not_1_out;

  D_Flip_Flop d_ff_1 (.clk(in_1), .D(not_1_out), .Q(out_2), .en(in_1));  // open: Qn, preset, reset
  not not_1 (not_1_out, out_2);
endmodule

module counter (
  input  in_1,
  output out_2
);

  D_Flip_Flop d_ff_1 (.clk(in_1), .D(out_2), .Qn(out_2));  // open: Q, preset, en, reset
endmodule

module Keyboard_Input (
  input  in_1,
  input  in_2,
  input  _0,
  input  _1,
  input  _2,
  input  _3,
  input  _4,
  input  _5,
  input  _6,
  input  _7,
  input  _8,
  input  _9,
  output out_13,
  output [7:0] out_14
);

  wire buffer_count_1_out_2, controlled_buffer_6_out, controlled_buffer_7_out, counter_1_out_2,
       counter_2_out_2, counter_3_out_2, counter_4_out_2, d_ff_1_q, d_ff_1_qn, not_1_out, not_2_out,
       not_3_out, not_4_out, not_5_out, or_1_out;
  wire [7:0] binary_convert_1_out_11, controlled_buffer_1_out, controlled_buffer_2_out,
       controlled_buffer_3_out, input_buffer_1_out_3, input_buffer_2_out_3, tens_convert_1_out_3;

  binary_convert binary_convert_1 (
    .in_1(_0), .in_2(_1), .in_3(_2), .in_4(_3), .in_5(_4), .in_6(_5), .in_7(_6), .in_8(_7), .in_9(_8),
    .in_10(_9), .out_11(binary_convert_1_out_11));
  or or_1 (or_1_out, _0, _1, _2, _3, _4, _5, _6, _7, _8, _9);
  tens_convert tens_convert_1 (
    .in_1(controlled_buffer_1_out), .out_3(tens_convert_1_out_3), .in_2(buffer_count_1_out_2));
  assign controlled_buffer_1_out = buffer_count_1_out_2 ? binary_convert_1_out_11 : 8'bz;  // Controlled_Buffer controlled_buffer_1
  assign controlled_buffer_2_out = not_1_out ? binary_convert_1_out_11 : 8'bz;  // Controlled_Buffer controlled_buffer_2
  not not_1 (not_1_out, buffer_count_1_out_2);
  buffer_count buffer_count_1 (.in_1(or_1_out), .out_2(buffer_count_1_out_2));
  assign controlled_buffer_3_out = or_1_out ? tens_convert_1_out_3 : 8'bz;  // Controlled_Buffer controlled_buffer_3
  assign out_14 = not_2_out ? input_buffer_1_out_3 : 8'bz;  // Controlled_Buffer controlled_buffer_4
  input_buffer input_buffer_1 (.in_1(in_1), .in_2(controlled_buffer_3_out), .out_3(input_buffer_1_out_3));
  input_buffer input_buffer_2 (.in_1(in_1), .in_2(controlled_buffer_2_out), .out_3(input_buffer_2_out_3));
  not not_2 (not_2_out, d_ff_1_q);
  D_Flip_Flop d_ff_1 (.clk(in_2), .D(d_ff_1_qn), .Q(d_ff_1_q), .Qn(d_ff_1_qn));  // open: preset, en, reset
  assign out_14 = not_3_out ? input_buffer_2_out_3 : 8'bz;  // Controlled_Buffer controlled_buffer_5
  not not_3 (not_3_out, not_2_out);
  counter counter_1 (.in_1(counter_2_out_2), .out_2(counter_1_out_2));
  counter counter_2 (.in_1(or_1_out), .out_2(counter_2_out_2));
  not not_4 (not_4_out, counter_1_out_2);
  assign controlled_buffer_6_out = or_1_out ? not_4_out : 1'bz;  // Controlled_Buffer controlled_buffer_6
  counter counter_3 (.in_1(in_2), .out_2(counter_3_out_2));
  D_Flip_Flop d_ff_2 (
    .Q(out_13), .preset(controlled_buffer_6_out), .reset(controlled_buffer_7_out));  // open: clk, D, Qn, en
  assign controlled_buffer_7_out = in_2 ? not_5_out : 1'bz;  // Controlled_Buffer controlled_buffer_7
  not not_5 (not_5_out, counter_4_out_2);
  counter counter_4 (.in_1(counter_3_out_2), .out_2(counter_4_out_2));
endmodule

module ALU_Register (
  input  in_1,
  input  [7:0] in_2,
  output out_3,
  output out_4,
  output out_5,
  output out_6,
  output out_7,
  output out_8,
  output out_9,
  output out_10
);

  D_Flip_Flop #(.trigger("high")) d_ff_1 (.clk(in_1), .D(in_2[0]), .Q(out_3));  // open: Qn, preset, en, reset
  D_Flip_Flop #(.trigger("high")) d_ff_2 (.clk(in_1), .D(in_2[1]), .Q(out_4));  // open: Qn, preset, en, reset
  D_Flip_Flop #(.trigger("high")) d_ff_3 (.clk(in_1), .D(in_2[2]), .Q(out_5));  // open: Qn, preset, en, reset
  D_Flip_Flop #(.trigger("high")) d_ff_4 (.clk(in_1), .D(in_2[3]), .Q(out_6));  // open: Qn, preset, en, reset
  D_Flip_Flop #(.trigger("high")) d_ff_5 (.clk(in_1), .D(in_2[4]), .Q(out_7));  // open: Qn, preset, en, reset
  D_Flip_Flop #(.trigger("high")) d_ff_6 (.clk(in_1), .D(in_2[5]), .Q(out_8));  // open: Qn, preset, en, reset
  D_Flip_Flop #(.trigger("high")) d_ff_7 (.clk(in_1), .D(in_2[6]), .Q(out_9));  // open: Qn, preset, en, reset
  D_Flip_Flop #(.trigger("high")) d_ff_8 (.clk(in_1), .D(in_2[7]), .Q(out_10));  // open: Qn, preset, en, reset
endmodule

module Logic (
  input  in_1,
  input  in_2,
  output out_3,
  output out_4,
  output out_5
);

  wire and_1_out, and_4_out, not_1_out, not_2_out, not_3_out, not_4_out;

  not not_1 (not_1_out, in_2);
  not not_2 (not_2_out, in_1);
  not not_3 (not_3_out, in_1);
  not not_4 (not_4_out, in_2);
  and and_1 (and_1_out, in_1, in_2);
  and and_2 (out_3, not_1_out, in_1);
  and and_3 (out_5, not_2_out, in_2);
  and and_4 (and_4_out, not_3_out, not_4_out);
  or or_1 (out_4, and_1_out, and_4_out);
endmodule

// BNZ
module Branch (
  input  [7:0] in_1,
  input  in_2,
  output out_3
);

  wire or_1_out;

  or or_1 (or_1_out, in_1[0], in_1[1], in_1[2], in_1[3], in_1[4], in_1[5], in_1[6], in_1[7]);
  and and_1 (out_3, or_1_out, in_2);
endmodule

module Logic2 (
  input  in_1,
  output out_2
);

  wire d_ff_1_q, d_ff_1_qn, d_ff_2_q, d_ff_2_qn, d_ff_3_q, d_ff_3_qn, not_1_out;

  D_Flip_Flop d_ff_1 (.clk(in_1), .D(d_ff_1_qn), .Q(d_ff_1_q), .Qn(d_ff_1_qn));  // open: preset, en, reset
  D_Flip_Flop d_ff_2 (.clk(d_ff_1_qn), .D(d_ff_2_qn), .Q(d_ff_2_q), .Qn(d_ff_2_qn));  // open: preset, en, reset
  D_Flip_Flop d_ff_3 (.clk(d_ff_2_qn), .D(d_ff_3_qn), .Q(d_ff_3_q), .Qn(d_ff_3_qn));  // open: preset, en, reset
  not not_1 (not_1_out, d_ff_2_q);
  or or_1 (out_2, d_ff_1_q, not_1_out, d_ff_3_q);
endmodule

module tens_convert (
  input  [7:0] in_1,
  input  in_2,
  output [7:0] out_3
);

  wire and_1_out, and_2_out, and_3_out, and_4_out, and_5_out, and_6_out, and_7_out, and_8_out, and_9_out,
       and_10_out, not_2_out, not_3_out, not_4_out, not_5_out, not_6_out, not_7_out, not_8_out, not_9_out,
       not_10_out, not_11_out, not_12_out, not_13_out, not_14_out, not_15_out, not_16_out, not_17_out,
       not_18_out, not_19_out, not_20_out, not_21_out, not_22_out, not_23_out, not_24_out, not_25_out,
       not_26_out, not_27_out, not_28_out, not_29_out, not_30_out, not_31_out, not_32_out, not_33_out,
       not_34_out, not_35_out, not_36_out, not_37_out, not_38_out, not_39_out, not_40_out, not_41_out,
       not_42_out, not_43_out, not_44_out, not_45_out, not_46_out, not_47_out, not_48_out, not_49_out,
       not_50_out, not_51_out, not_52_out, not_53_out, not_54_out, not_55_out, not_56_out, not_57_out,
       not_58_out;
  wire [7:0] controlled_buffer_1_out, not_1_out;

  assign not_1_out = ~in_1;  // NOT_Gate not_1, 8 bits wide
  and and_1 (and_1_out, not_1_out[0], not_1_out[1], not_1_out[2], not_1_out[3], not_1_out[4], not_1_out[5], not_1_out[6], not_1_out[7]);
  not not_2 (not_2_out, in_1[1]);
  not not_3 (not_3_out, in_1[2]);
  not not_4 (not_4_out, in_1[3]);
  not not_5 (not_5_out, in_1[4]);
  and and_2 (and_2_out, in_1[0], not_2_out, not_3_out, not_4_out, not_5_out, not_6_out, not_7_out, not_8_out);
  not not_6 (not_6_out, in_1[5]);
  not not_7 (not_7_out, in_1[6]);
  not not_8 (not_8_out, in_1[7]);
  not not_9 (not_9_out, in_1[0]);
  not not_10 (not_10_out, in_1[2]);
  not not_11 (not_11_out, in_1[3]);
  and and_3 (and_3_out, not_9_out, in_1[1], not_10_out, not_11_out, not_12_out, not_13_out, not_14_out, not_15_out);
  not not_12 (not_12_out, in_1[4]);
  not not_13 (not_13_out, in_1[5]);
  not not_14 (not_14_out, in_1[6]);
  not not_15 (not_15_out, in_1[7]);
  not not_16 (not_16_out, in_1[2]);
  not not_17 (not_17_out, in_1[3]);
  not not_18 (not_18_out, in_1[4]);
  and and_4 (and_4_out, in_1[0], in_1[1], not_16_out, not_17_out, not_18_out, not_19_out, not_20_out, not_21_out);
  not not_19 (not_19_out, in_1[5]);
  not not_20 (not_20_out, in_1[6]);
  not not_21 (not_21_out, in_1[7]);
  not not_22 (not_22_out, in_1[0]);
  not not_23 (not_23_out, in_1[1]);
  not not_24 (not_24_out, in_1[3]);
  and and_5 (and_5_out, not_22_out, not_23_out, in_1[2], not_24_out, not_25_out, not_26_out, not_27_out, not_28_out);
  not not_25 (not_25_out, in_1[4]);
  not not_26 (not_26_out, in_1[5]);
  not not_27 (not_27_out, in_1[6]);
  not not_28 (not_28_out, in_1[7]);
  not not_29 (not_29_out, in_1[1]);
  and and_6 (and_6_out, in_1[0], not_29_out, in_1[2], not_30_out, not_31_out, not_32_out, not_33_out, not_34_out);
  not not_30 (not_30_out, in_1[3]);
  not not_31 (not_31_out, in_1[4]);
  not not_32 (not_32_out, in_1[5]);
  not not_33 (not_33_out, in_1[6]);
  not not_34 (not_34_out, in_1[7]);
  not not_35 (not_35_out, in_1[0]);
  not not_36 (not_36_out, in_1[3]);
  not not_37 (not_37_out, in_1[4]);
  and and_7 (and_7_out, not_35_out, in_1[1], in_1[2], not_36_out, not_37_out, not_38_out, not_39_out, not_40_out);
  not not_38 (not_38_out, in_1[5]);
  not not_39 (not_39_out, in_1[6]);
  not not_40 (not_40_out, in_1[7]);
  not not_41 (not_41_out, in_1[3]);
  not not_42 (not_42_out, in_1[4]);
  not not_43 (not_43_out, in_1[5]);
  not not_44 (not_44_out, in_1[6]);
  not not_45 (not_45_out, in_1[7]);
  not not_46 (not_46_out, in_1[0]);
  not not_47 (not_47_out, in_1[1]);
  not not_48 (not_48_out, in_1[2]);
  not not_49 (not_49_out, in_1[4]);
  not not_50 (not_50_out, in_1[5]);
  not not_51 (not_51_out, in_1[6]);
  not not_52 (not_52_out, in_1[7]);
  not not_53 (not_53_out, in_1[1]);
  not not_54 (not_54_out, in_1[2]);
  not not_55 (not_55_out, in_1[4]);
  not not_56 (not_56_out, in_1[5]);
  not not_57 (not_57_out, in_1[6]);
  not not_58 (not_58_out, in_1[7]);
  and and_8 (and_8_out, in_1[0], in_1[1], in_1[2], not_41_out, not_42_out, not_43_out, not_44_out, not_45_out);
  and and_9 (and_9_out, not_46_out, not_47_out, not_48_out, in_1[3], not_49_out, not_50_out, not_51_out, not_52_out);
  and and_10 (and_10_out, in_1[0], not_53_out, not_54_out, in_1[3], not_55_out, not_56_out, not_57_out, not_58_out);
  assign controlled_buffer_1_out = and_1_out ? {8{1'b0}} : 8'bz;  // Controlled_Buffer controlled_buffer_1
  assign controlled_buffer_1_out = and_2_out ? 8'ha : 8'bz;  // Controlled_Buffer controlled_buffer_2
  assign controlled_buffer_1_out = and_3_out ? 8'h14 : 8'bz;  // Controlled_Buffer controlled_buffer_3
  assign controlled_buffer_1_out = and_4_out ? 8'h1e : 8'bz;  // Controlled_Buffer controlled_buffer_4
  assign controlled_buffer_1_out = and_5_out ? 8'h28 : 8'bz;  // Controlled_Buffer controlled_buffer_5
  assign controlled_buffer_1_out = and_6_out ? 8'h32 : 8'bz;  // Controlled_Buffer controlled_buffer_6
  assign controlled_buffer_1_out = and_7_out ? 8'h3c : 8'bz;  // Controlled_Buffer controlled_buffer_7
  assign controlled_buffer_1_out = and_8_out ? 8'h46 : 8'bz;  // Controlled_Buffer controlled_buffer_8
  assign controlled_buffer_1_out = and_9_out ? 8'h50 : 8'bz;  // Controlled_Buffer controlled_buffer_9
  assign controlled_buffer_1_out = and_10_out ? 8'h5a : 8'bz;  // Controlled_Buffer controlled_buffer_10
  assign out_3 = in_2 ? controlled_buffer_1_out : 8'bz;  // Controlled_Buffer controlled_buffer_11
endmodule

module Logic3 (
  input  in_1,
  output out_2
);

  wire d_ff_1_qn, d_ff_2_qn, d_ff_3_qn, d_ff_4_qn;

  D_Flip_Flop d_ff_1 (.clk(in_1), .D(d_ff_1_qn), .Qn(d_ff_1_qn));  // open: Q, preset, en, reset
  D_Flip_Flop d_ff_2 (.clk(d_ff_1_qn), .D(d_ff_2_qn), .Qn(d_ff_2_qn));  // open: Q, preset, en, reset
  D_Flip_Flop d_ff_3 (.clk(d_ff_2_qn), .D(d_ff_3_qn), .Qn(d_ff_3_qn));  // open: Q, preset, en, reset
  D_Flip_Flop d_ff_4 (.clk(d_ff_3_qn), .D(d_ff_4_qn), .Q(out_2), .Qn(d_ff_4_qn));  // open: preset, en, reset
endmodule
