// Logisim project MBR.circ as structural Verilog: 1 circuit, main circuit main
module main (
  input  clock,
  input  in_2,
  input  in_3,
  input  in_4,
  input  in_5,
  input  in_6,
  input  in_7,
  input  in_8,
  input  in_9,
  output out_10,
  output out_11,
  output out_12,
  output out_13,
  output out_14,
  output out_15,
  output out_16,
  output out_17
);

  D_Flip_Flop d_ff_1 (.clk(clock), .D(in_2), .Q(out_10));  // open: Qn, preset, en, reset
  D_Flip_Flop d_ff_2 (.clk(clock), .D(in_3), .Q(out_11));  // open: Qn, preset, en, reset
  D_Flip_Flop d_ff_3 (.clk(clock), .D(in_4), .Q(out_12));  // open: Qn, preset, en, reset
  D_Flip_Flop d_ff_4 (.clk(clock), .D(in_5), .Q(out_13));  // open: Qn, preset, en, reset
  D_Flip_Flop d_ff_5 (.clk(clock), .D(in_6), .Q(out_14));  // open: Qn, preset, en, reset
  D_Flip_Flop d_ff_6 (.clk(clock), .D(in_7), .Q(out_15));  // open: Qn, preset, en, reset
  D_Flip_Flop d_ff_7 (.clk(clock), .D(in_8), .Q(out_16));  // open: Qn, preset, en, reset
  D_Flip_Flop d_ff_8 (.clk(clock), .D(in_9), .Q(out_17));  // open: Qn, preset, en, reset
endmodule
