// Logisim project Mult.circ as structural Verilog: 7 circuits, main circuit MULT
module MULT (
  input  [7:0] in_1,
  input  [7:0] in_2,
  output [15:0] out_3,
  output [7:0] out_4,
  output overflow
);

  wire [7:0] n1x8_multiplexer_1_out_3, n1x8_multiplexer_2_out_3, n1x8_multiplexer_3_out_3,
       n1x8_multiplexer_4_out_3, n1x8_multiplexer_5_out_3, n1x8_multiplexer_6_out_3,
       n1x8_multiplexer_7_out_3, n1x8_multiplexer_8_out_3;
  wire [15:0] n16bit_adder_1_out_3, n16bit_adder_2_out_3, n16bit_adder_3_out_3, n16bit_adder_4_out_3,
       n16bit_adder_5_out_3, n16bit_adder_6_out_3;
  wire [15:15] not_1_out, not_2_out, not_3_out, not_4_out, not_5_out, not_6_out, not_7_out, not_8_out;

  _1x8_Multiplexer u_1x8_multiplexer_1 (.in_1(in_1[0]), .in_2(in_2), .out_3(n1x8_multiplexer_1_out_3));
  _1x8_Multiplexer u_1x8_multiplexer_2 (.in_1(in_1[1]), .in_2(in_2), .out_3(n1x8_multiplexer_2_out_3));
  _1x8_Multiplexer u_1x8_multiplexer_3 (.in_1(in_1[2]), .in_2(in_2), .out_3(n1x8_multiplexer_3_out_3));
  _1x8_Multiplexer u_1x8_multiplexer_4 (.in_1(in_1[3]), .in_2(in_2), .out_3(n1x8_multiplexer_4_out_3));
  _1x8_Multiplexer u_1x8_multiplexer_5 (.in_1(in_1[4]), .in_2(in_2), .out_3(n1x8_multiplexer_5_out_3));
  _1x8_Multiplexer u_1x8_multiplexer_6 (.in_1(in_1[5]), .in_2(in_2), .out_3(n1x8_multiplexer_6_out_3));
  _1x8_Multiplexer u_1x8_multiplexer_7 (.in_1(in_1[6]), .in_2(in_2), .out_3(n1x8_multiplexer_7_out_3));
  _1x8_Multiplexer u_1x8_multiplexer_8 (.in_1(in_1[7]), .in_2(in_2), .out_3(n1x8_multiplexer_8_out_3));
  not not_1 (not_1_out[15], 1'b1);
  not not_2 (not_2_out[15], 1'b1);
  not not_3 (not_3_out[15], 1'b1);
  not not_4 (not_4_out[15], 1'b1);
  not not_5 (not_5_out[15], 1'b1);
  not not_6 (not_6_out[15], 1'b1);
  not not_7 (not_7_out[15], 1'b1);
  not not_8 (not_8_out[15], 1'b1);
  _16bit_Adder u_16bit_adder_1 (
    .in_1({{8{not_1_out[15]}}, n1x8_multiplexer_1_out_3}),
    .in_2({{7{not_2_out[15]}}, n1x8_multiplexer_2_out_3, not_2_out[15]}), .out_3(n16bit_adder_1_out_3));  // open: out_4
  _16bit_Adder u_16bit_adder_2 (
    .in_1({{4{not_5_out[15]}}, n1x8_multiplexer_5_out_3, {4{not_5_out[15]}}}),
    .in_2({{3{not_6_out[15]}}, n1x8_multiplexer_6_out_3, {5{not_6_out[15]}}}), .out_3(n16bit_adder_2_out_3));  // open: out_4
  _16bit_Adder u_16bit_adder_3 (
    .in_1({{6{not_3_out[15]}}, n1x8_multiplexer_3_out_3, {2{not_3_out[15]}}}),
    .in_2({{5{not_4_out[15]}}, n1x8_multiplexer_4_out_3, {3{not_4_out[15]}}}), .out_3(n16bit_adder_3_out_3));  // open: out_4
  _16bit_Adder u_16bit_adder_4 (
    .in_1({{2{not_7_out[15]}}, n1x8_multiplexer_7_out_3, {6{not_7_out[15]}}}),
    .in_2({not_8_out[15], n1x8_multiplexer_8_out_3, {7{not_8_out[15]}}}), .out_3(n16bit_adder_4_out_3));  // open: out_4
  _16bit_Adder u_16bit_adder_5 (
    .in_1(n16bit_adder_1_out_3), .in_2(n16bit_adder_3_out_3), .out_3(n16bit_adder_5_out_3));  // open: out_4
  _16bit_Adder u_16bit_adder_6 (
    .in_1(n16bit_adder_2_out_3), .in_2(n16bit_adder_4_out_3), .out_3(n16bit_adder_6_out_3));  // open: out_4
  _16bit_Adder u_16bit_adder_7 (
    .in_1(n16bit_adder_5_out_3), .in_2(n16bit_adder_6_out_3), .out_3(out_3));  // open: out_4
  or or_1 (overflow, out_3[8], out_3[9], out_3[10], out_3[11], out_3[12], out_3[13], out_3[14], out_3[15]);

  assign out_4 = out_3[7:0];

  // Notes on the sheet:
  //   Input 1
  //   Input 2
  //   Output
endmodule

module _1bit_Adder (
  input  in_1,
  input  in_2,
  output out_3,
  output out_4
);

  xor xor_1 (out_3, in_1, in_2);
  and and_1 (out_4, in_1, in_2);

  // Notes on the sheet:
  //   Sum
  //   C
endmodule

module _2bit_Adder (
  input  [1:0] in_1,
  input  [1:0] in_2,
  output [1:0] out_3,
  output out_4
);

  wire n1bit_adder_1_out_4, n1bit_adder_2_out_3, n1bit_adder_2_out_4, n1bit_adder_3_out_4;

  _1bit_Adder u_1bit_adder_1 (.in_1(in_1[0]), .in_2(in_2[0]), .out_3(out_3[0]), .out_4(n1bit_adder_1_out_4));
  _1bit_Adder u_1bit_adder_2 (.in_1(in_1[1]), .in_2(in_2[1]), .out_3(n1bit_adder_2_out_3), .out_4(n1bit_adder_2_out_4));
  _1bit_Adder u_1bit_adder_3 (
    .in_1(n1bit_adder_1_out_4), .in_2(n1bit_adder_2_out_3), .out_3(out_3[1]), .out_4(n1bit_adder_3_out_4));
  or or_1 (out_4, n1bit_adder_3_out_4, n1bit_adder_2_out_4);
endmodule

module _4bit_Adder (
  input  [3:0] in_1,
  input  [3:0] in_2,
  output [3:0] out_3,
  output C
);

  wire n2bit_adder_2_out_4, n2bit_adder_3_out_4;
  wire [1:0] n2bit_adder_1_out_4, n2bit_adder_2_out_3;

  _2bit_Adder u_2bit_adder_1 (.in_1(in_1[1:0]), .in_2(in_2[1:0]), .out_3(out_3[1:0]), .out_4(n2bit_adder_1_out_4[0]));
  _2bit_Adder u_2bit_adder_2 (
    .in_1(in_1[3:2]), .in_2(in_2[3:2]), .out_3(n2bit_adder_2_out_3), .out_4(n2bit_adder_2_out_4));
  not not_1 (n2bit_adder_1_out_4[1], 1'b1);
  _2bit_Adder u_2bit_adder_3 (
    .in_1(n2bit_adder_1_out_4), .in_2(n2bit_adder_2_out_3), .out_3(out_3[3:2]), .out_4(n2bit_adder_3_out_4));
  or or_1 (C, n2bit_adder_3_out_4, n2bit_adder_2_out_4);
endmodule

module _8bit_Adder (
  input  [7:0] in_1,
  input  [7:0] in_2,
  output [7:0] out_3,
  output out_4
);

  wire n4bit_adder_2_c, n4bit_adder_3_c;
  wire [3:0] n4bit_adder_1_c, n4bit_adder_2_out_3;

  _4bit_Adder u_4bit_adder_1 (.in_1(in_1[3:0]), .in_2(in_2[3:0]), .out_3(out_3[3:0]), .C(n4bit_adder_1_c[0]));
  _4bit_Adder u_4bit_adder_2 (.in_1(in_1[7:4]), .in_2(in_2[7:4]), .out_3(n4bit_adder_2_out_3), .C(n4bit_adder_2_c));
  not not_1 (n4bit_adder_1_c[3], 1'b1);
  _4bit_Adder u_4bit_adder_3 (
    .in_1(n4bit_adder_2_out_3), .in_2({{3{n4bit_adder_1_c[3]}}, n4bit_adder_1_c[0]}), .out_3(out_3[7:4]),
    .C(n4bit_adder_3_c));
  or or_1 (out_4, n4bit_adder_3_c, n4bit_adder_2_c);
endmodule

module _16bit_Adder (
  input  [15:0] in_1,
  input  [15:0] in_2,
  output [15:0] out_3,
  output out_4
);

  wire n8bit_adder_2_out_4, n8bit_adder_3_out_4;
  wire [7:0] n8bit_adder_1_out_4, n8bit_adder_2_out_3;

  _8bit_Adder u_8bit_adder_1 (.in_1(in_1[7:0]), .in_2(in_2[7:0]), .out_3(out_3[7:0]), .out_4(n8bit_adder_1_out_4[0]));
  _8bit_Adder u_8bit_adder_2 (
    .in_1(in_1[15:8]), .in_2(in_2[15:8]), .out_3(n8bit_adder_2_out_3), .out_4(n8bit_adder_2_out_4));
  not not_1 (n8bit_adder_1_out_4[7], 1'b1);
  _8bit_Adder u_8bit_adder_3 (
    .in_1({{7{n8bit_adder_1_out_4[7]}}, n8bit_adder_1_out_4[0]}), .in_2(n8bit_adder_2_out_3),
    .out_3(out_3[15:8]), .out_4(n8bit_adder_3_out_4));
  or or_1 (out_4, n8bit_adder_3_out_4, n8bit_adder_2_out_4);
endmodule

module _1x8_Multiplexer (
  input  in_1,
  input  [7:0] in_2,
  output [7:0] out_3
);

  and and_1 (out_3[0], in_1, in_2[0]);
  and and_2 (out_3[1], in_1, in_2[1]);
  and and_3 (out_3[2], in_1, in_2[2]);
  and and_4 (out_3[3], in_1, in_2[3]);
  and and_5 (out_3[4], in_1, in_2[4]);
  and and_6 (out_3[5], in_1, in_2[5]);
  and and_7 (out_3[6], in_1, in_2[6]);
  and and_8 (out_3[7], in_1, in_2[7]);
endmodule
