// Logisim project adder.circ as structural Verilog: 1 circuit, main circuit main
module main (
  input  in_1,
  input  L_Register,
  input  in_3,
  input  in_4,
  input  R_Register,
  input  in_6,
  output out_7,
  output Sum_of_L_and_R,
  output out_9,
  output Overflow___1
);

  wire and_1_out, and_2_out, and_3_out, and_4_out, and_5_out, and_6_out, and_7_out, and_8_out, and_9_out,
       and_10_out, and_11_out, and_12_out, and_13_out, and_14_out, and_15_out, and_16_out, and_17_out,
       clock_1_out, d_ff_1_q, d_ff_2_q, d_ff_3_q, d_ff_4_q, d_ff_5_q, d_ff_6_q, not_1_out, not_2_out,
       not_3_out, not_4_out, not_5_out, not_6_out, not_7_out, not_8_out, not_9_out, not_10_out, not_11_out,
       not_12_out, not_13_out, not_14_out, not_15_out, not_16_out, not_17_out, not_18_out, not_19_out,
       not_20_out, or_1_out, or_2_out, or_3_out, or_4_out, or_5_out, or_6_out, or_7_out;

  Clock clock_1 (.out(clock_1_out));
  not not_1 (not_1_out, in_3);
  not not_2 (not_2_out, in_6);
  not not_3 (not_3_out, L_Register);
  not not_4 (not_4_out, R_Register);
  D_Flip_Flop #(.trigger("low")) d_ff_1 (.clk(not_1_out), .D(in_3), .Q(d_ff_1_q));  // open: Qn, preset, en, reset
  D_Flip_Flop #(.trigger("low")) d_ff_2 (.clk(not_2_out), .D(in_6), .Q(d_ff_2_q));  // open: Qn, preset, en, reset
  D_Flip_Flop #(.trigger("low")) d_ff_3 (.clk(not_3_out), .D(L_Register), .Q(d_ff_3_q));  // open: Qn, preset, en, reset
  D_Flip_Flop #(.trigger("low")) d_ff_4 (.clk(not_4_out), .D(R_Register), .Q(d_ff_4_q));  // open: Qn, preset, en, reset
  not not_5 (not_5_out, in_4);
  not not_6 (not_6_out, in_1);
  D_Flip_Flop #(.trigger("low")) d_ff_5 (.clk(not_5_out), .D(in_4), .Q(d_ff_5_q));  // open: Qn, preset, en, reset
  D_Flip_Flop #(.trigger("low")) d_ff_6 (.clk(not_6_out), .D(in_1), .Q(d_ff_6_q));  // open: Qn, preset, en, reset
  not not_7 (not_7_out, d_ff_2_q);
  not not_8 (not_8_out, d_ff_1_q);
  not not_9 (not_9_out, d_ff_4_q);
  not not_10 (not_10_out, d_ff_3_q);
  not not_11 (not_11_out, d_ff_5_q);
  not not_12 (not_12_out, d_ff_6_q);
  and and_1 (and_1_out, not_7_out, d_ff_1_q);
  and and_2 (and_2_out, not_8_out, d_ff_2_q);
  and and_3 (and_3_out, d_ff_2_q, d_ff_1_q);
  and and_4 (and_4_out, not_9_out, d_ff_3_q);
  and and_5 (and_5_out, not_10_out, d_ff_4_q);
  and and_6 (and_6_out, d_ff_4_q, d_ff_3_q);
  and and_7 (and_7_out, and_3_out, d_ff_4_q);
  and and_8 (and_8_out, and_3_out, d_ff_3_q);
  and and_9 (and_9_out, not_11_out, d_ff_6_q);
  and and_10 (and_10_out, not_12_out, d_ff_5_q);
  and and_11 (and_11_out, d_ff_5_q, d_ff_6_q);
  and and_12 (and_12_out, or_3_out, d_ff_5_q);
  and and_13 (and_13_out, or_3_out, d_ff_6_q);
  or or_1 (or_1_out, and_1_out, and_2_out);
  or or_2 (or_2_out, and_4_out, and_5_out);
  or or_3 (or_3_out, and_6_out, and_7_out, and_8_out);
  or or_4 (or_4_out, and_9_out, and_10_out);
  or or_5 (or_5_out, and_11_out, and_12_out, and_13_out);
  not not_13 (not_13_out, or_5_out);
  not not_14 (not_14_out, or_1_out);
  not not_15 (not_15_out, and_3_out);
  and and_14 (and_14_out, not_15_out, or_2_out);
  not not_16 (not_16_out, or_2_out);
  and and_15 (and_15_out, not_16_out, and_3_out);
  or or_6 (or_6_out, and_14_out, and_15_out);
  not not_17 (not_17_out, or_3_out);
  and and_16 (and_16_out, not_17_out, or_4_out);
  not not_18 (not_18_out, or_4_out);
  and and_17 (and_17_out, not_18_out, or_3_out);
  not not_19 (not_19_out, or_6_out);
  or or_7 (or_7_out, and_16_out, and_17_out);
  not not_20 (not_20_out, or_7_out);
  S_R_Flip_Flop s_r_ff_1 (.S(or_7_out), .clk(clock_1_out), .R(not_20_out), .Q(out_7));  // open: Qn, preset, reset, en
  S_R_Flip_Flop s_r_ff_2 (
    .S(or_6_out), .clk(clock_1_out), .R(not_19_out), .Q(Sum_of_L_and_R));  // open: Qn, preset, reset, en
  S_R_Flip_Flop s_r_ff_3 (.S(or_1_out), .clk(clock_1_out), .R(not_14_out), .Q(out_9));  // open: Qn, preset, reset, en
  S_R_Flip_Flop s_r_ff_4 (
    .S(or_5_out), .clk(clock_1_out), .R(not_13_out), .Q(Overflow___1));  // open: Qn, preset, reset, en

  // Notes on the sheet:
  //   Input Pins
  //   Input Pins
  //   clock
  //   A-Register
  //   status register
endmodule
