// Logisim project adress-register.circ as structural Verilog: 1 circuit, main circuit main
module main (
  input  clock,
  input  in_2,
  input  in_3,
  input  in_4,
  input  in_5,
  input  in_6,
  input  in_7,
  input  in_8,
  input  in_9,
  output out_10,
  output out_11,
  output out_12,
  output out_13,
  output out_14,
  output out_15,
  output out_16,
  output out_17,
  output out_18,
  output out_19,
  output out_20,
  output out_21,
  output out_22,
  output out_23,
  output out_24,
  output out_25
);

  wire d_ff_1_q, d_ff_2_q, d_ff_3_q, d_ff_4_q, d_ff_5_q, d_ff_6_q, d_ff_7_q, d_ff_8_q, not_1_out, not_2_out,
       not_3_out, not_5_out, not_6_out, not_7_out, not_8_out, not_9_out, not_10_out, not_11_out, not_12_out,
       not_13_out, not_14_out, not_15_out, not_16_out, not_17_out, not_18_out, not_19_out, not_20_out,
       not_21_out, not_22_out, not_23_out, not_24_out, not_25_out, not_26_out, not_27_out, not_28_out,
       not_29_out, not_30_out, not_31_out, not_32_out, not_33_out, not_34_out, not_35_out, not_36_out;

  D_Flip_Flop d_ff_1 (.clk(clock), .D(in_2), .Q(d_ff_1_q));  // open: Qn, preset, en, reset
  not not_1 (not_1_out, d_ff_1_q);
  D_Flip_Flop d_ff_2 (.clk(clock), .D(in_3), .Q(d_ff_2_q));  // open: Qn, preset, en, reset
  not not_2 (not_2_out, d_ff_2_q);
  D_Flip_Flop d_ff_3 (.clk(clock), .D(in_4), .Q(d_ff_3_q));  // open: Qn, preset, en, reset
  not not_3 (not_3_out, d_ff_3_q);
  D_Flip_Flop d_ff_4 (.clk(clock), .D(in_5), .Q(d_ff_4_q));  // open: Qn, preset, en, reset
  not not_4 (not_1_out, d_ff_4_q);
  D_Flip_Flop d_ff_5 (.clk(clock), .D(in_6), .Q(d_ff_5_q));  // open: Qn, preset, en, reset
  D_Flip_Flop d_ff_6 (.clk(clock), .D(in_7), .Q(d_ff_6_q));  // open: Qn, preset, en, reset
  not not_5 (not_5_out, d_ff_5_q);
  not not_6 (not_6_out, d_ff_5_q);
  not not_7 (not_7_out, d_ff_5_q);
  not not_8 (not_8_out, d_ff_5_q);
  not not_9 (not_9_out, d_ff_5_q);
  not not_10 (not_10_out, d_ff_5_q);
  not not_11 (not_11_out, d_ff_5_q);
  not not_12 (not_12_out, d_ff_5_q);
  not not_13 (not_13_out, d_ff_6_q);
  not not_14 (not_14_out, d_ff_6_q);
  not not_15 (not_15_out, d_ff_6_q);
  not not_16 (not_16_out, d_ff_6_q);
  not not_17 (not_17_out, d_ff_6_q);
  not not_18 (not_18_out, d_ff_6_q);
  not not_19 (not_19_out, d_ff_6_q);
  not not_20 (not_20_out, d_ff_6_q);
  D_Flip_Flop d_ff_7 (.clk(clock), .D(in_8), .Q(d_ff_7_q));  // open: Qn, preset, en, reset
  not not_21 (not_21_out, d_ff_7_q);
  not not_22 (not_22_out, d_ff_7_q);
  not not_23 (not_23_out, d_ff_7_q);
  not not_24 (not_24_out, d_ff_7_q);
  not not_25 (not_25_out, d_ff_7_q);
  not not_26 (not_26_out, d_ff_7_q);
  not not_27 (not_27_out, d_ff_7_q);
  not not_28 (not_28_out, d_ff_7_q);
  D_Flip_Flop d_ff_8 (.clk(clock), .D(in_9), .Q(d_ff_8_q));  // open: Qn, preset, en, reset
  not not_29 (not_29_out, d_ff_8_q);
  not not_30 (not_30_out, d_ff_8_q);
  not not_31 (not_31_out, d_ff_8_q);
  not not_32 (not_32_out, d_ff_8_q);
  not not_33 (not_33_out, d_ff_8_q);
  not not_34 (not_34_out, d_ff_8_q);
  not not_35 (not_35_out, d_ff_8_q);
  not not_36 (not_36_out, d_ff_8_q);
  and and_1 (out_10, not_29_out, not_21_out, not_13_out, not_5_out, not_1_out, not_2_out, not_3_out, not_1_out);
  and and_2 (out_11, d_ff_8_q, not_22_out, not_14_out, not_6_out, not_1_out, not_2_out, not_3_out, not_1_out);
  and and_3 (out_12, not_30_out, d_ff_7_q, not_15_out, not_7_out, not_1_out, not_2_out, not_3_out, not_1_out);
  and and_4 (out_13, d_ff_8_q, d_ff_7_q, not_16_out, not_8_out, not_1_out, not_2_out, not_3_out, not_1_out);
  and and_5 (out_14, not_31_out, not_23_out, d_ff_6_q, not_9_out, not_1_out, not_2_out, not_3_out, not_1_out);
  and and_6 (out_15, d_ff_8_q, not_24_out, d_ff_6_q, not_10_out, not_1_out, not_2_out, not_3_out, not_1_out);
  and and_7 (out_16, not_32_out, d_ff_7_q, d_ff_6_q, not_11_out, not_1_out, not_2_out, not_3_out, not_1_out);
  and and_8 (out_17, d_ff_8_q, d_ff_7_q, d_ff_6_q, not_12_out, not_1_out, not_2_out, not_3_out, not_1_out);
  and and_9 (out_18, not_33_out, not_25_out, not_17_out, d_ff_5_q, not_1_out, not_2_out, not_3_out, not_1_out);
  and and_10 (out_19, d_ff_8_q, not_26_out, not_18_out, d_ff_5_q, not_1_out, not_2_out, not_3_out, not_1_out);
  and and_11 (out_20, not_34_out, d_ff_7_q, not_19_out, d_ff_5_q, not_1_out, not_2_out, not_3_out, not_1_out);
  and and_12 (out_21, d_ff_8_q, d_ff_7_q, not_20_out, d_ff_5_q, not_1_out, not_2_out, not_3_out, not_1_out);
  and and_13 (out_22, not_35_out, not_27_out, d_ff_6_q, d_ff_5_q, not_1_out, not_2_out, not_3_out, not_1_out);
  and and_14 (out_23, d_ff_8_q, not_28_out, d_ff_6_q, d_ff_5_q, not_1_out, not_2_out, not_3_out, not_1_out);
  and and_15 (out_24, not_36_out, d_ff_7_q, d_ff_6_q, d_ff_5_q, not_1_out, not_2_out, not_3_out, not_1_out);
  and and_16 (out_25, d_ff_8_q, d_ff_7_q, d_ff_6_q, d_ff_5_q, not_1_out, not_2_out, not_3_out, not_1_out);

  // Notes on the sheet:
  //   adress register
endmodule
