// Logisim project alu.circ as structural Verilog: 25 circuits, main circuit ALU
module Half_adder (
  input  A,
  input  B,
  output Sum,
  output Carry
);

  wire not_1_out, or_1_out;

  or or_1 (or_1_out, A, B);
  and and_1 (Carry, A, B);
  not not_1 (not_1_out, Carry);
  and and_2 (Sum, or_1_out, not_1_out);
endmodule

module Full_Adder (
  input  Carry,
  input  A,
  input  B,
  output Sum,
  output Carry_2
);

  wire half_adder_1_carry, half_adder_1_sum, half_adder_2_carry;

  Half_adder half_adder_1 (.A(A), .B(B), .Sum(half_adder_1_sum), .Carry(half_adder_1_carry));
  Half_adder half_adder_2 (.A(Carry), .B(half_adder_1_sum), .Sum(Sum), .Carry(half_adder_2_carry));
  or or_1 (Carry_2, half_adder_2_carry, half_adder_1_carry);
endmodule

module Adder (
  input  A0,
  input  B0,
  input  A1,
  input  B1,
  input  A2,
  input  B2,
  input  A3,
  input  B3,
  output R0,
  output R1,
  output R2,
  output R3,
  output OVERFLOW
);

  wire full_adder_1_carry_2, full_adder_2_carry_2, half_adder_1_carry;

  Half_adder half_adder_1 (.A(A0), .B(B0), .Sum(R0), .Carry(half_adder_1_carry));
  Full_Adder full_adder_1 (.Carry(half_adder_1_carry), .A(A1), .B(B1), .Sum(R1), .Carry_2(full_adder_1_carry_2));
  Full_Adder full_adder_2 (.Carry(full_adder_1_carry_2), .A(A2), .B(B2), .Sum(R2), .Carry_2(full_adder_2_carry_2));
  Full_Adder full_adder_3 (.Carry(full_adder_2_carry_2), .A(A3), .B(B3), .Sum(R3), .Carry_2(OVERFLOW));
endmodule

module Subtractor (
  input  in_1,
  input  A0,
  input  B0,
  input  A1,
  input  B1,
  input  A2,
  input  B2,
  input  A3,
  input  B3,
  output R0,
  output R1,
  output R2,
  output R3,
  output OVERFLOW
);

  wire full_adder_1_carry_2, full_adder_2_carry_2, full_adder_3_carry_2, not_1_out, not_2_out, not_3_out,
       not_4_out, not_5_out, or_1_out;

  not not_1 (not_1_out, in_1);
  or or_1 (or_1_out, in_1, not_1_out);
  Full_Adder full_adder_1 (.Carry(or_1_out), .A(A0), .B(not_2_out), .Sum(R0), .Carry_2(full_adder_1_carry_2));
  not not_2 (not_2_out, B0);
  Full_Adder full_adder_2 (
    .Carry(full_adder_1_carry_2), .A(A1), .B(not_3_out), .Sum(R1), .Carry_2(full_adder_2_carry_2));
  not not_3 (not_3_out, B1);
  Full_Adder full_adder_3 (
    .Carry(full_adder_2_carry_2), .A(A2), .B(not_4_out), .Sum(R2), .Carry_2(full_adder_3_carry_2));
  not not_4 (not_4_out, B2);
  Full_Adder full_adder_4 (.Carry(full_adder_3_carry_2), .A(A3), .B(not_5_out), .Sum(R3), .Carry_2(OVERFLOW));
  not not_5 (not_5_out, B3);
endmodule

module SetLessThan (
  input  A0,
  input  B0,
  input  A1,
  input  B1,
  input  A2,
  input  _1,
  input  B2,
  input  A3,
  input  B3,
  output R0,
  output R1,
  output R2,
  output R3,
  output SLT
);

  wire subtractor_1_overflow;

  Subtractor subtractor_1 (
    .A0(A0), .B0(B0), .A1(A1), .B1(B1), .A2(A2), .B2(B2), .A3(A3), .B3(B3), .R0(R0), .R1(R1), .R2(R2),
    .R3(R3), .OVERFLOW(subtractor_1_overflow), .in_1(_1));
  not not_1 (SLT, subtractor_1_overflow);
endmodule

module Bitwise_And (
  input  A0,
  input  B0,
  input  A1,
  input  B1,
  input  A2,
  input  B2,
  input  A3,
  input  B3,
  output R0,
  output R1,
  output R2,
  output R3
);

  and and_1 (R0, A0, B0);
  and and_2 (R1, A1, B1);
  and and_3 (R2, A2, B2);
  and and_4 (R3, A3, B3);
endmodule

module Bitwise_Or (
  input  A0,
  input  B0,
  input  A1,
  input  B1,
  input  A2,
  input  B2,
  input  A3,
  input  B3,
  output R0,
  output R1,
  output R2,
  output R3
);

  or or_1 (R0, A0, B0);
  or or_2 (R1, A1, B1);
  or or_3 (R2, A2, B2);
  or or_4 (R3, A3, B3);
endmodule

module Bitwise_Nor (
  input  in_1,
  input  A0,
  input  B0,
  input  A1,
  input  B1,
  input  A2,
  input  B2,
  input  A3,
  input  B3,
  output R0,
  output R1,
  output R2,
  output R3
);

  wire not_1_out, not_2_out, not_3_out, not_4_out, not_5_out, not_6_out, not_7_out, not_8_out;

  not not_1 (not_1_out, A0);
  not not_2 (not_2_out, B0);
  not not_3 (not_3_out, A1);
  not not_4 (not_4_out, B1);
  not not_5 (not_5_out, A2);
  not not_6 (not_6_out, B2);
  not not_7 (not_7_out, A3);
  not not_8 (not_8_out, B3);
  and and_1 (R0, not_1_out, in_1, not_2_out);
  and and_2 (R1, not_3_out, in_1, not_4_out);
  and and_3 (R2, not_5_out, in_1, not_6_out);
  and and_4 (R3, not_7_out, in_1, not_8_out);
endmodule

module Decoder (
  input  C0,
  input  C1,
  input  C2,
  input  C3,
  output AND,
  output OR,
  output ADD,
  output SUB,
  output SLT,
  output NOR
);

  wire not_1_out, not_2_out, not_3_out, not_4_out, not_5_out, not_6_out, not_7_out, not_8_out, not_9_out,
       not_10_out, not_11_out, not_12_out, not_13_out, not_14_out, not_15_out;

  not not_1 (not_1_out, C0);
  not not_2 (not_2_out, C1);
  not not_3 (not_3_out, C2);
  not not_4 (not_4_out, C3);
  not not_5 (not_5_out, C1);
  not not_6 (not_6_out, C2);
  not not_7 (not_7_out, C3);
  not not_8 (not_8_out, C0);
  not not_9 (not_9_out, C2);
  not not_10 (not_10_out, C3);
  not not_11 (not_11_out, C0);
  not not_12 (not_12_out, C3);
  not not_13 (not_13_out, C3);
  not not_14 (not_14_out, C0);
  not not_15 (not_15_out, C1);
  and and_1 (AND, not_1_out, not_2_out, not_3_out, not_4_out);
  and and_2 (OR, C0, not_5_out, not_6_out, not_7_out);
  and and_3 (ADD, not_8_out, C1, not_9_out, not_10_out);
  and and_4 (SUB, not_11_out, C1, C2, not_12_out);
  and and_5 (SLT, C0, C1, C2, not_13_out);
  and and_6 (NOR, not_14_out, not_15_out, C2, C3);
endmodule

module ZERO (
  input  R0,
  input  R1,
  input  R2,
  input  R3,
  output Zer0
);

  wire not_1_out, not_2_out, not_3_out, not_4_out;

  not not_1 (not_1_out, R0);
  not not_2 (not_2_out, R1);
  not not_3 (not_3_out, R2);
  not not_4 (not_4_out, R3);
  and and_1 (Zer0, not_1_out, not_2_out, not_3_out, not_4_out);
endmodule

module AND (
  input  C,
  input  A0,
  input  B0,
  input  A1,
  input  B1,
  input  A2,
  input  B2,
  input  A3,
  input  B3,
  output R0,
  output R1,
  output R2,
  output R3
);

  wire and_1_out, and_2_out, and_3_out, and_4_out, and_5_out, and_6_out, and_7_out, and_8_out;

  and and_1 (and_1_out, C, A0);
  and and_2 (and_2_out, C, B0);
  and and_3 (and_3_out, C, A1);
  and and_4 (and_4_out, C, B1);
  and and_5 (and_5_out, C, A2);
  and and_6 (and_6_out, C, B2);
  and and_7 (and_7_out, C, A3);
  and and_8 (and_8_out, C, B3);
  Bitwise_And bitwise_and_1 (
    .A0(and_1_out), .B0(and_2_out), .A1(and_3_out), .B1(and_4_out), .A2(and_5_out), .B2(and_6_out),
    .A3(and_7_out), .B3(and_8_out), .R0(R0), .R1(R1), .R2(R2), .R3(R3));
endmodule

module OR (
  input  C,
  input  A0,
  input  B0,
  input  A1,
  input  B1,
  input  A2,
  input  B2,
  input  A3,
  input  B3,
  output R0,
  output R1,
  output R2,
  output R3
);

  wire and_1_out, and_2_out, and_3_out, and_4_out, and_5_out, and_6_out, and_7_out, and_8_out;

  and and_1 (and_1_out, C, A0);
  and and_2 (and_2_out, C, B0);
  and and_3 (and_3_out, C, A1);
  and and_4 (and_4_out, C, B1);
  and and_5 (and_5_out, C, A2);
  and and_6 (and_6_out, C, B2);
  and and_7 (and_7_out, C, A3);
  and and_8 (and_8_out, C, B3);
  Bitwise_Or bitwise_or_1 (
    .A0(and_1_out), .B0(and_2_out), .A1(and_3_out), .B1(and_4_out), .A2(and_5_out), .B2(and_6_out),
    .A3(and_7_out), .B3(and_8_out), .R0(R0), .R1(R1), .R2(R2), .R3(R3));
endmodule

module ADD (
  input  C,
  input  A0,
  input  B0,
  input  A1,
  input  B1,
  input  A2,
  input  B2,
  input  A3,
  input  B3,
  output R0,
  output R1,
  output R2,
  output R3,
  output Overflow
);

  wire and_1_out, and_2_out, and_3_out, and_4_out, and_5_out, and_6_out, and_7_out, and_8_out;

  and and_1 (and_1_out, C, A0);
  and and_2 (and_2_out, C, B0);
  and and_3 (and_3_out, C, A1);
  and and_4 (and_4_out, C, B1);
  and and_5 (and_5_out, C, A2);
  and and_6 (and_6_out, C, B2);
  and and_7 (and_7_out, C, A3);
  and and_8 (and_8_out, C, B3);
  Adder adder_1 (
    .A0(and_1_out), .B0(and_2_out), .A1(and_3_out), .B1(and_4_out), .A2(and_5_out), .B2(and_6_out),
    .A3(and_7_out), .B3(and_8_out), .R0(R0), .R1(R1), .R2(R2), .R3(R3), .OVERFLOW(Overflow));
endmodule

module SUB (
  input  C,
  input  A0,
  input  B0,
  input  A1,
  input  in_5,
  input  B1,
  input  A2,
  input  B2,
  input  A3,
  input  B3,
  output R0,
  output R1,
  output R2,
  output R3,
  output Overflow
);

  wire and_1_out, and_2_out, and_3_out, and_4_out, and_5_out, and_6_out, and_7_out, and_8_out;

  and and_1 (and_1_out, C, A0);
  and and_2 (and_2_out, C, B0);
  and and_3 (and_3_out, C, A1);
  and and_4 (and_4_out, C, B1);
  and and_5 (and_5_out, C, A2);
  and and_6 (and_6_out, C, B2);
  and and_7 (and_7_out, C, A3);
  and and_8 (and_8_out, C, B3);
  Subtractor subtractor_1 (
    .A0(and_1_out), .B0(and_2_out), .A1(and_3_out), .B1(and_4_out), .A2(and_5_out), .B2(and_6_out),
    .A3(and_7_out), .B3(and_8_out), .R0(R0), .R1(R1), .R2(R2), .R3(R3), .OVERFLOW(Overflow), .in_1(in_5));
endmodule

module SLT (
  input  C,
  input  in_2,
  input  A0,
  input  B0,
  input  A1,
  input  B1,
  input  A2,
  input  B2,
  input  A3,
  input  B3,
  output R0,
  output R1,
  output R2,
  output R3
);

  wire and_1_out, and_2_out, and_3_out, and_4_out, and_5_out, and_6_out, and_7_out, and_8_out;

  and and_1 (and_1_out, C, A0);
  and and_2 (and_2_out, C, B0);
  and and_3 (and_3_out, C, A1);
  and and_4 (and_4_out, C, B1);
  and and_5 (and_5_out, C, A2);
  and and_6 (and_6_out, C, B2);
  and and_7 (and_7_out, C, A3);
  and and_8 (and_8_out, C, B3);
  SetLessThan setlessthan_1 (
    ._1(in_2), .A0(and_1_out), .B0(and_2_out), .A1(and_3_out), .B1(and_4_out), .A2(and_5_out),
    .B2(and_6_out), .A3(and_7_out), .B3(and_8_out), .SLT(R0));  // open: R0, R1, R2, R3

  assign R1 = R0;
  assign R2 = R0;
  assign R3 = R0;
endmodule

module NOR (
  input  C,
  input  A0,
  input  B0,
  input  A1,
  input  B1,
  input  A2,
  input  B2,
  input  A3,
  input  B3,
  output R0,
  output R1,
  output R2,
  output R3
);

  wire and_1_out, and_2_out, and_3_out, and_4_out, and_5_out, and_6_out, and_7_out, and_8_out;

  and and_1 (and_1_out, C, A0);
  and and_2 (and_2_out, C, B0);
  and and_3 (and_3_out, C, A1);
  and and_4 (and_4_out, C, B1);
  and and_5 (and_5_out, C, A2);
  and and_6 (and_6_out, C, B2);
  and and_7 (and_7_out, C, A3);
  and and_8 (and_8_out, C, B3);
  Bitwise_Nor bitwise_nor_1 (
    .A0(and_1_out), .B0(and_2_out), .A1(and_3_out), .B1(and_4_out), .A2(and_5_out), .B2(and_6_out),
    .A3(and_7_out), .B3(and_8_out), .R0(R0), .R1(R1), .R2(R2), .R3(R3), .in_1(C));
endmodule

module ALU (
  input  C0,
  input  C1,
  input  C2,
  input  C3,
  input  A0,
  input  B0,
  input  A1,
  input  B1,
  input  A2,
  input  B2,
  input  A3,
  input  B3,
  input  in_13,
  input  cOR,
  input  C0_2,
  input  C1_2,
  input  C2_2,
  input  cAND,
  input  C3_2,
  input  cADD,
  input  A0_2,
  input  A1_2,
  input  A2_2,
  input  A3_2,
  input  A4,
  input  A5,
  input  A6,
  input  A7,
  input  B0_2,
  input  B1_2,
  input  B2_2,
  input  B3_2,
  input  B4,
  input  B5,
  input  B6,
  input  B7,
  input  cSUB,
  input  in_38,
  output ZERO,
  output R0,
  output R1,
  output R2,
  output R3,
  output OVERFLOW,
  output NEGATIVE,
  output R0_to_R7,
  output out_47,
  output out_48,
  output out_49,
  output Zero_2,
  output out_51,
  output out_52,
  output out_53,
  output out_54,
  output Overflow_2,
  output Negative_2
);

  wire add_1_r0, add_1_r1, add_1_r2, add_1_r3, and_1_r0, and_1_r1, and_1_r2, and_1_r3, decoder_1_add,
       decoder_1_and, decoder_1_nor, decoder_1_or, decoder_1_slt, decoder_1_sub, n8bitadd_1_r0,
       n8bitadd_1_r1, n8bitadd_1_r2, n8bitadd_1_r3, n8bitadd_1_r4, n8bitadd_1_r5, n8bitadd_1_r6,
       n8bitadd_1_r7, n8bitand_1_r0, n8bitand_1_r1, n8bitand_1_r2, n8bitand_1_r3, n8bitand_1_r4,
       n8bitand_1_r5, n8bitand_1_r6, n8bitand_1_r7, n8bitor_1_r0, n8bitor_1_r1, n8bitor_1_r2, n8bitor_1_r3,
       n8bitor_1_r4, n8bitor_1_r5, n8bitor_1_r6, n8bitor_1_r7, n8bitsub_1_negative, n8bitsub_1_r0,
       n8bitsub_1_r1, n8bitsub_1_r2, n8bitsub_1_r3, n8bitsub_1_r4, n8bitsub_1_r5, n8bitsub_1_r6,
       n8bitsub_1_r7, nor_1_r0, nor_1_r1, nor_1_r2, nor_1_r3, not_1_out, not_3_out, not_4_out, not_5_out,
       not_6_out, not_7_out, not_8_out, not_9_out, not_10_out, or_1_r0, or_1_r1, or_1_r2, or_1_r3, or_6_out,
       slt_1_r0, sub_1_overflow, sub_1_r0, sub_1_r1, sub_1_r2, sub_1_r3;

  Decoder decoder_1 (
    .C0(C0), .C1(C1), .C2(C2), .C3(C3), .AND(decoder_1_and), .OR(decoder_1_or), .ADD(decoder_1_add),
    .SUB(decoder_1_sub), .SLT(decoder_1_slt), .NOR(decoder_1_nor));
  AND and_1 (
    .C(decoder_1_and), .A0(A0), .B0(B0), .A1(A1), .B1(B1), .A2(A2), .B2(B2), .A3(A3), .B3(B3), .R0(and_1_r0),
    .R1(and_1_r1), .R2(and_1_r2), .R3(and_1_r3));
  OR or_1 (
    .C(decoder_1_or), .A0(A0), .B0(B0), .A1(A1), .B1(B1), .A2(A2), .B2(B2), .A3(A3), .B3(B3), .R0(or_1_r0),
    .R1(or_1_r1), .R2(or_1_r2), .R3(or_1_r3));
  ADD add_1 (
    .C(decoder_1_add), .A0(A0), .B0(B0), .A1(A1), .B1(B1), .A2(A2), .B2(B2), .A3(A3), .B3(B3), .R0(add_1_r0),
    .R1(add_1_r1), .R2(add_1_r2), .R3(add_1_r3), .Overflow(OVERFLOW));
  SUB sub_1 (
    .C(decoder_1_sub), .A0(A0), .B0(B0), .A1(A1), .in_5(in_13), .B1(B1), .A2(A2), .B2(B2), .A3(A3), .B3(B3),
    .R0(sub_1_r0), .R1(sub_1_r1), .R2(sub_1_r2), .R3(sub_1_r3), .Overflow(sub_1_overflow));
  SLT slt_1 (
    .C(decoder_1_slt), .in_2(in_13), .A0(A0), .B0(B0), .A1(A1), .B1(B1), .A2(A2), .B2(B2), .A3(A3), .B3(B3),
    .R0(slt_1_r0));  // open: R1, R2, R3
  NOR nor_1 (
    .C(decoder_1_nor), .A0(A0), .B0(B0), .A1(A1), .B1(B1), .A2(A2), .B2(B2), .A3(A3), .B3(B3), .R0(nor_1_r0),
    .R1(nor_1_r1), .R2(nor_1_r2), .R3(nor_1_r3));
  or or_2 (R0, and_1_r0, or_1_r0, add_1_r0, sub_1_r0, or_6_out);
  or or_3 (R1, and_1_r1, or_1_r1, add_1_r1, sub_1_r1, nor_1_r1);
  or or_4 (R2, and_1_r2, or_1_r2, add_1_r2, sub_1_r2, nor_1_r2);
  not not_1 (not_1_out, sub_1_overflow);
  or or_5 (R3, and_1_r3, or_1_r3, add_1_r3, sub_1_r3, nor_1_r3);
  or or_6 (or_6_out, slt_1_r0, nor_1_r0);
  ZERO zero_1 (.R0(R0), .R1(R1), .R2(R2), .R3(R3), .Zer0(ZERO));
  and and_2 (NEGATIVE, not_1_out, decoder_1_sub);
  _8bitOR u_8bitor_1 (
    .C(cOR), .A0(A0_2), .A1(A1_2), .A2(A2_2), .A3(A3_2), .A4(A4), .A5(A5), .A6(A6), .A7(A7), .B0(B0_2),
    .B1(B1_2), .B2(B2_2), .B3(B3_2), .B4(B4), .B5(B5), .B6(B6), .B7(B7), .R0(n8bitor_1_r0),
    .R1(n8bitor_1_r1), .R2(n8bitor_1_r2), .R3(n8bitor_1_r3), .R4(n8bitor_1_r4), .R5(n8bitor_1_r5),
    .R6(n8bitor_1_r6), .R7(n8bitor_1_r7));
  _8bitAND u_8bitand_1 (
    .C(cAND), .A0(A0_2), .A1(A1_2), .A2(A2_2), .A3(A3_2), .A4(A4), .A5(A5), .A6(A6), .A7(A7), .B0(B0_2),
    .B1(B1_2), .B2(B2_2), .B3(B3_2), .B4(B4), .B5(B5), .B6(B6), .B7(B7), .R0(n8bitand_1_r0),
    .R1(n8bitand_1_r1), .R2(n8bitand_1_r2), .R3(n8bitand_1_r3), .R4(n8bitand_1_r4), .R5(n8bitand_1_r5),
    .R6(n8bitand_1_r6), .R7(n8bitand_1_r7));
  _8bitADD u_8bitadd_1 (
    .C(cADD), .A0(A0_2), .A1(A1_2), .A2(A2_2), .A3(A3_2), .A4(A4), .A5(A5), .A6(A6), .A7(A7), .B0(B0_2),
    .B1(B1_2), .B2(B2_2), .B3(B3_2), .B4(B4), .B5(B5), .B6(B6), .B7(B7), .R0(n8bitadd_1_r0),
    .R1(n8bitadd_1_r1), .R2(n8bitadd_1_r2), .R3(n8bitadd_1_r3), .R4(n8bitadd_1_r4), .R5(n8bitadd_1_r5),
    .R6(n8bitadd_1_r6), .R7(n8bitadd_1_r7), .Overflow(Overflow_2));
  _8bitSUB u_8bitsub_1 (
    .C(cSUB), .A0(A0_2), .A1(A1_2), .A2(A2_2), .A3(A3_2), .A4(A4), .A5(A5), .A6(A6), .A7(A7), .B0(B0_2),
    .B1(B1_2), .B2(B2_2), .B3(B3_2), .B4(B4), .B5(B5), .B6(B6), .B7(B7), .useless_shitter(in_38),
    .R0(n8bitsub_1_r0), .R1(n8bitsub_1_r1), .R2(n8bitsub_1_r2), .R3(n8bitsub_1_r3), .R4(n8bitsub_1_r4),
    .R5(n8bitsub_1_r5), .R6(n8bitsub_1_r6), .R7(n8bitsub_1_r7), .Negative(n8bitsub_1_negative));
  not not_2 (Negative_2, n8bitsub_1_negative);
  or or_7 (R0_to_R7, n8bitor_1_r0, n8bitand_1_r0, n8bitadd_1_r0, n8bitsub_1_r0);
  or or_8 (out_47, n8bitor_1_r1, n8bitand_1_r1, n8bitadd_1_r1, n8bitsub_1_r1);
  or or_9 (out_48, n8bitor_1_r2, n8bitand_1_r2, n8bitadd_1_r2, n8bitsub_1_r2);
  or or_10 (out_49, n8bitor_1_r3, n8bitand_1_r3, n8bitadd_1_r3, n8bitsub_1_r3);
  or or_11 (out_51, n8bitor_1_r4, n8bitand_1_r4, n8bitadd_1_r4, n8bitsub_1_r4);
  or or_12 (out_52, n8bitor_1_r5, n8bitand_1_r5, n8bitadd_1_r5, n8bitsub_1_r5);
  or or_13 (out_53, n8bitor_1_r6, n8bitand_1_r6, n8bitadd_1_r6, n8bitsub_1_r6);
  or or_14 (out_54, n8bitor_1_r7, n8bitand_1_r7, n8bitadd_1_r7, n8bitsub_1_r7);
  not not_3 (not_3_out, R0_to_R7);
  not not_4 (not_4_out, out_47);
  not not_5 (not_5_out, out_48);
  not not_6 (not_6_out, out_49);
  not not_7 (not_7_out, out_51);
  not not_8 (not_8_out, out_52);
  not not_9 (not_9_out, out_53);
  not not_10 (not_10_out, out_54);
  and and_3 (Zero_2, not_3_out, not_4_out, not_5_out, not_6_out, not_7_out, not_8_out, not_9_out, not_10_out);

  // Notes on the sheet:
  //   decoder
  //   AND, OR, ADD, NOR all have 9
  //   useless shit for subtraction
endmodule

module _8bitOR (
  input  C,
  input  A0,
  input  A1,
  input  A2,
  input  A3,
  input  A4,
  input  A5,
  input  A6,
  input  A7,
  input  B0,
  input  B1,
  input  B2,
  input  B3,
  input  B4,
  input  B5,
  input  B6,
  input  B7,
  output R0,
  output R1,
  output R2,
  output R3,
  output R4,
  output R5,
  output R6,
  output R7
);

  wire and_1_out, and_2_out, and_3_out, and_4_out, and_5_out, and_6_out, and_7_out, and_8_out, and_9_out,
       and_10_out, and_11_out, and_12_out, and_13_out, and_14_out, and_15_out, and_16_out;

  and and_1 (and_1_out, C, A0);
  and and_2 (and_2_out, C, A1);
  and and_3 (and_3_out, C, A2);
  and and_4 (and_4_out, C, A3);
  and and_5 (and_5_out, C, A4);
  and and_6 (and_6_out, C, A5);
  and and_7 (and_7_out, C, A6);
  and and_8 (and_8_out, C, A7);
  and and_9 (and_9_out, C, B0);
  and and_10 (and_10_out, C, B1);
  and and_11 (and_11_out, C, B2);
  and and_12 (and_12_out, C, B3);
  and and_13 (and_13_out, C, B4);
  and and_14 (and_14_out, C, B5);
  and and_15 (and_15_out, C, B6);
  and and_16 (and_16_out, C, B7);
  Bitwise_OR bitwise_or_1 (
    .A0(and_1_out), .A1(and_2_out), .A2(and_3_out), .A3(and_4_out), .A4(and_5_out), .A5(and_6_out),
    .A6(and_7_out), .A7(and_8_out), .B0(and_9_out), .B1(and_10_out), .B2(and_11_out), .B3(and_12_out),
    .B4(and_13_out), .B5(and_14_out), .B6(and_15_out), .B7(and_16_out), .R0(R0), .R1(R1), .R2(R2), .R3(R3),
    .R4(R4), .R5(R5), .R6(R6), .R7(R7));
endmodule

module Bitwise_OR (
  input  A0,
  input  A1,
  input  A2,
  input  A3,
  input  A4,
  input  A5,
  input  A6,
  input  A7,
  input  B0,
  input  B1,
  input  B2,
  input  B3,
  input  B4,
  input  B5,
  input  B6,
  input  B7,
  output R0,
  output R1,
  output R2,
  output R3,
  output R4,
  output R5,
  output R6,
  output R7
);

  or or_1 (R0, A0, B0);
  or or_2 (R1, A1, B1);
  or or_3 (R2, A2, B2);
  or or_4 (R3, A3, B3);
  or or_5 (R4, A4, B4);
  or or_6 (R5, A5, B5);
  or or_7 (R6, A6, B6);
  or or_8 (R7, A7, B7);
endmodule

module _8bitAND (
  input  C,
  input  A0,
  input  A1,
  input  A2,
  input  A3,
  input  A4,
  input  A5,
  input  A6,
  input  A7,
  input  B0,
  input  B1,
  input  B2,
  input  B3,
  input  B4,
  input  B5,
  input  B6,
  input  B7,
  output R0,
  output R1,
  output R2,
  output R3,
  output R4,
  output R5,
  output R6,
  output R7
);

  wire and_1_out, and_2_out, and_3_out, and_4_out, and_5_out, and_6_out, and_7_out, and_8_out, and_9_out,
       and_10_out, and_11_out, and_12_out, and_13_out, and_14_out, and_15_out, and_16_out;

  and and_1 (and_1_out, C, A0);
  and and_2 (and_2_out, C, A1);
  and and_3 (and_3_out, C, A2);
  and and_4 (and_4_out, C, A3);
  and and_5 (and_5_out, C, A4);
  and and_6 (and_6_out, C, A5);
  and and_7 (and_7_out, C, A6);
  and and_8 (and_8_out, C, A7);
  and and_9 (and_9_out, C, B0);
  and and_10 (and_10_out, C, B1);
  and and_11 (and_11_out, C, B2);
  and and_12 (and_12_out, C, B3);
  and and_13 (and_13_out, C, B4);
  and and_14 (and_14_out, C, B5);
  and and_15 (and_15_out, C, B6);
  and and_16 (and_16_out, C, B7);
  Bitwise_AND bitwise_and_1 (
    .A0(and_1_out), .A1(and_2_out), .A2(and_3_out), .A3(and_4_out), .A4(and_5_out), .A5(and_6_out),
    .A6(and_7_out), .A7(and_8_out), .B0(and_9_out), .B1(and_10_out), .B2(and_11_out), .B3(and_12_out),
    .B4(and_13_out), .B5(and_14_out), .B6(and_15_out), .B7(and_16_out), .R0(R0), .R1(R1), .R2(R2), .R3(R3),
    .R4(R4), .R5(R5), .R6(R6), .R7(R7));
endmodule

module Bitwise_AND (
  input  A0,
  input  A1,
  input  A2,
  input  A3,
  input  A4,
  input  A5,
  input  A6,
  input  A7,
  input  B0,
  input  B1,
  input  B2,
  input  B3,
  input  B4,
  input  B5,
  input  B6,
  input  B7,
  output R0,
  output R1,
  output R2,
  output R3,
  output R4,
  output R5,
  output R6,
  output R7
);

  and and_1 (R0, A0, B0);
  and and_2 (R1, A1, B1);
  and and_3 (R2, A2, B2);
  and and_4 (R3, A3, B3);
  and and_5 (R4, A4, B4);
  and and_6 (R5, A5, B5);
  and and_7 (R6, A6, B6);
  and and_8 (R7, A7, B7);
endmodule

module _8bitADD (
  input  C,
  input  A0,
  input  A1,
  input  A2,
  input  A3,
  input  A4,
  input  A5,
  input  A6,
  input  A7,
  input  B0,
  input  B1,
  input  B2,
  input  B3,
  input  B4,
  input  B5,
  input  B6,
  input  B7,
  output R0,
  output R1,
  output R2,
  output R3,
  output R4,
  output R5,
  output R6,
  output R7,
  output Overflow
);

  wire and_1_out, and_2_out, and_3_out, and_4_out, and_5_out, and_6_out, and_7_out, and_8_out, and_9_out,
       and_10_out, and_11_out, and_12_out, and_13_out, and_14_out, and_15_out, and_16_out;

  and and_1 (and_1_out, C, A0);
  and and_2 (and_2_out, C, A1);
  and and_3 (and_3_out, C, A2);
  and and_4 (and_4_out, C, A3);
  and and_5 (and_5_out, C, A4);
  and and_6 (and_6_out, C, A5);
  and and_7 (and_7_out, C, A6);
  and and_8 (and_8_out, C, A7);
  and and_9 (and_9_out, C, B0);
  and and_10 (and_10_out, C, B1);
  and and_11 (and_11_out, C, B2);
  and and_12 (and_12_out, C, B3);
  and and_13 (and_13_out, C, B4);
  and and_14 (and_14_out, C, B5);
  and and_15 (and_15_out, C, B6);
  and and_16 (and_16_out, C, B7);
  _8bitAdder u_8bitadder_1 (
    .A0(and_1_out), .A1(and_2_out), .A2(and_3_out), .A3(and_4_out), .A4(and_5_out), .A5(and_6_out),
    .A6(and_7_out), .A7(and_8_out), .B0(and_9_out), .B1(and_10_out), .B2(and_11_out), .B3(and_12_out),
    .B4(and_13_out), .B5(and_14_out), .B6(and_15_out), .B7(and_16_out), .R0(R0), .R1(R1), .R2(R2), .R3(R3),
    .R4(R4), .R5(R5), .R6(R6), .R7(R7), .Overflow(Overflow));
endmodule

module _8bitAdder (
  input  A0,
  input  A1,
  input  A2,
  input  A3,
  input  A4,
  input  A5,
  input  A6,
  input  A7,
  input  B0,
  input  B1,
  input  B2,
  input  B3,
  input  B4,
  input  B5,
  input  B6,
  input  B7,
  output R0,
  output R1,
  output R2,
  output R3,
  output R4,
  output R5,
  output R6,
  output R7,
  output Overflow
);

  wire full_adder_1_carry_2, full_adder_2_carry_2, full_adder_3_carry_2, full_adder_4_carry_2,
       full_adder_5_carry_2, full_adder_6_carry_2, half_adder_1_carry;

  Half_adder half_adder_1 (.A(A0), .B(B0), .Sum(R0), .Carry(half_adder_1_carry));
  Full_Adder full_adder_1 (.Carry(half_adder_1_carry), .A(A1), .B(B1), .Sum(R1), .Carry_2(full_adder_1_carry_2));
  Full_Adder full_adder_2 (.Carry(full_adder_1_carry_2), .A(A2), .B(B2), .Sum(R2), .Carry_2(full_adder_2_carry_2));
  Full_Adder full_adder_3 (.Carry(full_adder_2_carry_2), .A(A3), .B(B3), .Sum(R3), .Carry_2(full_adder_3_carry_2));
  Full_Adder full_adder_4 (.Carry(full_adder_3_carry_2), .A(A4), .B(B4), .Sum(R4), .Carry_2(full_adder_4_carry_2));
  Full_Adder full_adder_5 (.Carry(full_adder_4_carry_2), .A(A5), .B(B5), .Sum(R5), .Carry_2(full_adder_5_carry_2));
  Full_Adder full_adder_6 (.Carry(full_adder_5_carry_2), .A(A6), .B(B6), .Sum(R6), .Carry_2(full_adder_6_carry_2));
  Full_Adder full_adder_7 (.Carry(full_adder_6_carry_2), .A(A7), .B(B7), .Sum(R7), .Carry_2(Overflow));
endmodule

module _8bitSUB (
  input  C,
  input  A0,
  input  A1,
  input  A2,
  input  A3,
  input  A4,
  input  A5,
  input  A6,
  input  A7,
  input  B0,
  input  B1,
  input  B2,
  input  B3,
  input  B4,
  input  B5,
  input  B6,
  input  B7,
  input  useless_shitter,
  output R0,
  output R1,
  output R2,
  output R3,
  output R4,
  output R5,
  output R6,
  output R7,
  output Negative
);

  wire and_1_out, and_2_out, and_3_out, and_4_out, and_5_out, and_6_out, and_7_out, and_8_out, and_9_out,
       and_10_out, and_11_out, and_12_out, and_13_out, and_14_out, and_15_out, and_16_out;

  and and_1 (and_1_out, C, A0);
  and and_2 (and_2_out, C, A1);
  and and_3 (and_3_out, C, A2);
  and and_4 (and_4_out, C, A3);
  and and_5 (and_5_out, C, A4);
  and and_6 (and_6_out, C, A5);
  and and_7 (and_7_out, C, A6);
  and and_8 (and_8_out, C, A7);
  and and_9 (and_9_out, C, B0);
  and and_10 (and_10_out, C, B1);
  and and_11 (and_11_out, C, B2);
  and and_12 (and_12_out, C, B3);
  and and_13 (and_13_out, C, B4);
  and and_14 (and_14_out, C, B5);
  and and_15 (and_15_out, C, B6);
  and and_16 (and_16_out, C, B7);
  _8bitSubtractor u_8bitsubtractor_1 (
    .usless_shit(useless_shitter), .A0(and_1_out), .A1(and_2_out), .A2(and_3_out), .A3(and_4_out),
    .A4(and_5_out), .A5(and_6_out), .A6(and_7_out), .A7(and_8_out), .B0(and_9_out), .B1(and_10_out),
    .B2(and_11_out), .B3(and_12_out), .B4(and_13_out), .B5(and_14_out), .B6(and_15_out), .B7(and_16_out),
    .out_18(R0), .out_19(R1), .out_20(R2), .out_21(R3), .out_22(R4), .out_23(R5), .out_24(R6), .out_25(R7),
    .Negative(Negative));
endmodule

module _8bitSubtractor (
  input  usless_shit,
  input  A0,
  input  A1,
  input  A2,
  input  A3,
  input  A4,
  input  A5,
  input  A6,
  input  A7,
  input  B0,
  input  B1,
  input  B2,
  input  B3,
  input  B4,
  input  B5,
  input  B6,
  input  B7,
  output out_18,
  output out_19,
  output out_20,
  output out_21,
  output out_22,
  output out_23,
  output out_24,
  output out_25,
  output Negative
);

  wire full_adder_1_carry_2, full_adder_2_carry_2, full_adder_3_carry_2, full_adder_4_carry_2,
       full_adder_6_carry_2, full_adder_7_carry_2, full_adder_8_carry_2, not_1_out, not_2_out, not_3_out,
       not_4_out, not_5_out, not_6_out, not_7_out, not_8_out, not_9_out, or_1_out;

  not not_1 (not_1_out, B0);
  not not_2 (not_2_out, B1);
  not not_3 (not_3_out, B2);
  not not_4 (not_4_out, B3);
  not not_5 (not_5_out, B4);
  not not_6 (not_6_out, B5);
  not not_7 (not_7_out, B6);
  not not_8 (not_8_out, B7);
  not not_9 (not_9_out, usless_shit);
  or or_1 (or_1_out, usless_shit, not_9_out);
  Full_Adder full_adder_1 (.Carry(or_1_out), .A(A0), .B(not_1_out), .Sum(out_18), .Carry_2(full_adder_1_carry_2));
  Full_Adder full_adder_2 (
    .Carry(full_adder_8_carry_2), .A(A4), .B(not_5_out), .Sum(out_22), .Carry_2(full_adder_2_carry_2));
  Full_Adder full_adder_3 (
    .Carry(full_adder_2_carry_2), .A(A5), .B(not_6_out), .Sum(out_23), .Carry_2(full_adder_3_carry_2));
  Full_Adder full_adder_4 (
    .Carry(full_adder_3_carry_2), .A(A6), .B(not_7_out), .Sum(out_24), .Carry_2(full_adder_4_carry_2));
  Full_Adder full_adder_5 (.Carry(full_adder_4_carry_2), .A(A7), .B(not_8_out), .Sum(out_25), .Carry_2(Negative));
  Full_Adder full_adder_6 (
    .Carry(full_adder_1_carry_2), .A(A1), .B(not_2_out), .Sum(out_19), .Carry_2(full_adder_6_carry_2));
  Full_Adder full_adder_7 (
    .Carry(full_adder_6_carry_2), .A(A2), .B(not_3_out), .Sum(out_20), .Carry_2(full_adder_7_carry_2));
  Full_Adder full_adder_8 (
    .Carry(full_adder_7_carry_2), .A(A3), .B(not_4_out), .Sum(out_21), .Carry_2(full_adder_8_carry_2));
endmodule
