// Logisim project cpu-ram-project.circ as structural Verilog: 3 circuits, main circuit main
module main (
  input  in_1,
  input  _1for_write_mode,
  input  in_3,
  input  in_4,
  input  in_5,
  input  in_6,
  input  in_7,
  input  in_8,
  input  in_9,
  input  in_10,
  input  in_11,
  input  in_12,
  input  in_13,
  input  in_14,
  input  in_15,
  input  in_16,
  input  in_17,
  input  in_18,
  input  in_19,
  input  in_20,
  input  in_21,
  input  in_22,
  input  in_23,
  input  in_24,
  input  in_25,
  input  in_26,
  output out_27,
  output out_28,
  output out_29,
  output out_30,
  output out_31,
  output out_32,
  output out_33,
  output out_34,
  output out_35,
  output out_36,
  output out_37,
  output out_38,
  output out_39,
  output out_40,
  output out_41,
  output out_42,
  output out_43,
  output out_44,
  output out_45,
  output out_46,
  output out_47,
  output out_48,
  output out_49,
  output out_50,
  output out_51,
  output out_52,
  output out_53,
  output out_54,
  output out_55,
  output out_56,
  output out_57,
  output out_58,
  output out_59,
  output out_60,
  output out_61,
  output out_62,
  output out_63,
  output out_64,
  output out_65,
  output out_66,
  output out_67,
  output out_68,
  output out_69,
  output out_70,
  output out_71,
  output out_72,
  output out_73,
  output out_74,
  output out_75,
  output out_76,
  output out_77,
  output out_78,
  output out_79,
  output out_80,
  output out_81,
  output out_82,
  output out_83,
  output out_84,
  output out_85,
  output out_86,
  output out_87,
  output out_88,
  output out_89,
  output out_90,
  output out_91,
  output out_92,
  output out_93,
  output out_94,
  output out_95,
  output out_96,
  output out_97,
  output out_98,
  output out_99,
  output out_100,
  output out_101,
  output out_102,
  output out_103,
  output out_104,
  output out_105,
  output out_106,
  output out_107,
  output out_108,
  output out_109,
  output out_110,
  output out_111,
  output out_112,
  output out_113,
  output out_114,
  output out_115,
  output out_116,
  output out_117,
  output out_118,
  output out_119,
  output out_120,
  output out_121,
  output out_122,
  output out_123,
  output out_124,
  output out_125,
  output out_126,
  output out_127,
  output out_128,
  output out_129,
  output out_130,
  output out_131,
  output out_132,
  output out_133,
  output out_134,
  output out_135,
  output out_136,
  output out_137,
  output out_138,
  output out_139,
  output out_140,
  output out_141,
  output out_142,
  output out_143,
  output out_144,
  output out_145,
  output out_146,
  output out_147,
  output out_148,
  output out_149,
  output out_150,
  output out_151,
  output out_152,
  output out_153,
  output out_154,
  output out_155,
  output out_156,
  output out_157,
  output out_158,
  output out_159,
  output out_160,
  output out_161,
  output out_162
);

  wire and_1_out, and_2_out, and_3_out, and_4_out, and_5_out, and_6_out, and_7_out, and_8_out, and_9_out,
       and_10_out, and_11_out, and_12_out, and_13_out, and_14_out, and_15_out, and_16_out, and_17_out,
       and_18_out, and_19_out, and_20_out, and_21_out, and_22_out, and_23_out, and_24_out, and_25_out,
       and_26_out, and_27_out, and_28_out, and_29_out, and_30_out, and_31_out, and_32_out, byte_1_out_11,
       byte_1_out_13, byte_1_out_15, byte_1_out_17, byte_1_out_19, byte_1_out_21, byte_1_out_23,
       byte_1_out_25, byte_2_out_11, byte_2_out_13, byte_2_out_15, byte_2_out_17, byte_2_out_19,
       byte_2_out_21, byte_2_out_23, byte_2_out_25, byte_3_out_11, byte_3_out_13, byte_3_out_15,
       byte_3_out_17, byte_3_out_19, byte_3_out_21, byte_3_out_23, byte_3_out_25, byte_4_out_11,
       byte_4_out_13, byte_4_out_15, byte_4_out_17, byte_4_out_19, byte_4_out_21, byte_4_out_23,
       byte_4_out_25, byte_5_out_11, byte_5_out_13, byte_5_out_15, byte_5_out_17, byte_5_out_19,
       byte_5_out_21, byte_5_out_23, byte_5_out_25, byte_6_out_11, byte_6_out_13, byte_6_out_15,
       byte_6_out_17, byte_6_out_19, byte_6_out_21, byte_6_out_23, byte_6_out_25, byte_7_out_11,
       byte_7_out_13, byte_7_out_15, byte_7_out_17, byte_7_out_19, byte_7_out_21, byte_7_out_23,
       byte_7_out_25, byte_8_out_11, byte_8_out_13, byte_8_out_15, byte_8_out_17, byte_8_out_19,
       byte_8_out_21, byte_8_out_23, byte_8_out_25, byte_9_out_11, byte_9_out_13, byte_9_out_15,
       byte_9_out_17, byte_9_out_19, byte_9_out_21, byte_9_out_23, byte_9_out_25, byte_10_out_11,
       byte_10_out_13, byte_10_out_15, byte_10_out_17, byte_10_out_19, byte_10_out_21, byte_10_out_23,
       byte_10_out_25, byte_11_out_11, byte_11_out_13, byte_11_out_15, byte_11_out_17, byte_11_out_19,
       byte_11_out_21, byte_11_out_23, byte_11_out_25, byte_12_out_11, byte_12_out_13, byte_12_out_15,
       byte_12_out_17, byte_12_out_19, byte_12_out_21, byte_12_out_23, byte_12_out_25, byte_13_out_11,
       byte_13_out_13, byte_13_out_15, byte_13_out_17, byte_13_out_19, byte_13_out_21, byte_13_out_23,
       byte_13_out_25, byte_14_out_11, byte_14_out_13, byte_14_out_15, byte_14_out_17, byte_14_out_19,
       byte_14_out_21, byte_14_out_23, byte_14_out_25, byte_15_out_11, byte_15_out_13, byte_15_out_15,
       byte_15_out_17, byte_15_out_19, byte_15_out_21, byte_15_out_23, byte_15_out_25, byte_16_out_11,
       byte_16_out_13, byte_16_out_15, byte_16_out_17, byte_16_out_19, byte_16_out_21, byte_16_out_23,
       byte_16_out_25, n8_bit_condition_gate_1_out_10, n8_bit_condition_gate_1_out_11,
       n8_bit_condition_gate_1_out_12, n8_bit_condition_gate_1_out_13, n8_bit_condition_gate_1_out_14,
       n8_bit_condition_gate_1_out_15, n8_bit_condition_gate_1_out_16, n8_bit_condition_gate_1_out_17,
       n8_bit_condition_gate_2_out_10, n8_bit_condition_gate_2_out_11, n8_bit_condition_gate_2_out_12,
       n8_bit_condition_gate_2_out_13, n8_bit_condition_gate_2_out_14, n8_bit_condition_gate_2_out_15,
       n8_bit_condition_gate_2_out_16, n8_bit_condition_gate_2_out_17, n8_bit_condition_gate_3_out_10,
       n8_bit_condition_gate_3_out_11, n8_bit_condition_gate_3_out_12, n8_bit_condition_gate_3_out_13,
       n8_bit_condition_gate_3_out_14, n8_bit_condition_gate_3_out_15, n8_bit_condition_gate_3_out_16,
       n8_bit_condition_gate_3_out_17, n8_bit_condition_gate_4_out_10, n8_bit_condition_gate_4_out_11,
       n8_bit_condition_gate_4_out_12, n8_bit_condition_gate_4_out_13, n8_bit_condition_gate_4_out_14,
       n8_bit_condition_gate_4_out_15, n8_bit_condition_gate_4_out_16, n8_bit_condition_gate_4_out_17,
       n8_bit_condition_gate_5_out_10, n8_bit_condition_gate_5_out_11, n8_bit_condition_gate_5_out_12,
       n8_bit_condition_gate_5_out_13, n8_bit_condition_gate_5_out_14, n8_bit_condition_gate_5_out_15,
       n8_bit_condition_gate_5_out_16, n8_bit_condition_gate_5_out_17, n8_bit_condition_gate_6_out_10,
       n8_bit_condition_gate_6_out_11, n8_bit_condition_gate_6_out_12, n8_bit_condition_gate_6_out_13,
       n8_bit_condition_gate_6_out_14, n8_bit_condition_gate_6_out_15, n8_bit_condition_gate_6_out_16,
       n8_bit_condition_gate_6_out_17, n8_bit_condition_gate_7_out_10, n8_bit_condition_gate_7_out_11,
       n8_bit_condition_gate_7_out_12, n8_bit_condition_gate_7_out_13, n8_bit_condition_gate_7_out_14,
       n8_bit_condition_gate_7_out_15, n8_bit_condition_gate_7_out_16, n8_bit_condition_gate_7_out_17,
       n8_bit_condition_gate_8_out_10, n8_bit_condition_gate_8_out_11, n8_bit_condition_gate_8_out_12,
       n8_bit_condition_gate_8_out_13, n8_bit_condition_gate_8_out_14, n8_bit_condition_gate_8_out_15,
       n8_bit_condition_gate_8_out_16, n8_bit_condition_gate_8_out_17, n8_bit_condition_gate_9_out_10,
       n8_bit_condition_gate_9_out_11, n8_bit_condition_gate_9_out_12, n8_bit_condition_gate_9_out_13,
       n8_bit_condition_gate_9_out_14, n8_bit_condition_gate_9_out_15, n8_bit_condition_gate_9_out_16,
       n8_bit_condition_gate_9_out_17, n8_bit_condition_gate_10_out_10, n8_bit_condition_gate_10_out_11,
       n8_bit_condition_gate_10_out_12, n8_bit_condition_gate_10_out_13, n8_bit_condition_gate_10_out_14,
       n8_bit_condition_gate_10_out_15, n8_bit_condition_gate_10_out_16, n8_bit_condition_gate_10_out_17,
       n8_bit_condition_gate_11_out_10, n8_bit_condition_gate_11_out_11, n8_bit_condition_gate_11_out_12,
       n8_bit_condition_gate_11_out_13, n8_bit_condition_gate_11_out_14, n8_bit_condition_gate_11_out_15,
       n8_bit_condition_gate_11_out_16, n8_bit_condition_gate_11_out_17, n8_bit_condition_gate_12_out_10,
       n8_bit_condition_gate_12_out_11, n8_bit_condition_gate_12_out_12, n8_bit_condition_gate_12_out_13,
       n8_bit_condition_gate_12_out_14, n8_bit_condition_gate_12_out_15, n8_bit_condition_gate_12_out_16,
       n8_bit_condition_gate_12_out_17, n8_bit_condition_gate_13_out_10, n8_bit_condition_gate_13_out_11,
       n8_bit_condition_gate_13_out_12, n8_bit_condition_gate_13_out_13, n8_bit_condition_gate_13_out_14,
       n8_bit_condition_gate_13_out_15, n8_bit_condition_gate_13_out_16, n8_bit_condition_gate_13_out_17,
       n8_bit_condition_gate_14_out_10, n8_bit_condition_gate_14_out_11, n8_bit_condition_gate_14_out_12,
       n8_bit_condition_gate_14_out_13, n8_bit_condition_gate_14_out_14, n8_bit_condition_gate_14_out_15,
       n8_bit_condition_gate_14_out_16, n8_bit_condition_gate_14_out_17, n8_bit_condition_gate_15_out_10,
       n8_bit_condition_gate_15_out_11, n8_bit_condition_gate_15_out_12, n8_bit_condition_gate_15_out_13,
       n8_bit_condition_gate_15_out_14, n8_bit_condition_gate_15_out_15, n8_bit_condition_gate_15_out_16,
       n8_bit_condition_gate_15_out_17, n8_bit_condition_gate_16_out_10, n8_bit_condition_gate_16_out_11,
       n8_bit_condition_gate_16_out_12, n8_bit_condition_gate_16_out_13, n8_bit_condition_gate_16_out_14,
       n8_bit_condition_gate_16_out_15, n8_bit_condition_gate_16_out_16, n8_bit_condition_gate_16_out_17,
       n8_bit_condition_gate_17_out_10, n8_bit_condition_gate_17_out_11, n8_bit_condition_gate_17_out_12,
       n8_bit_condition_gate_17_out_13, n8_bit_condition_gate_17_out_14, n8_bit_condition_gate_17_out_15,
       n8_bit_condition_gate_17_out_16, n8_bit_condition_gate_17_out_17, n8_bit_condition_gate_18_out_10,
       n8_bit_condition_gate_18_out_11, n8_bit_condition_gate_18_out_12, n8_bit_condition_gate_18_out_13,
       n8_bit_condition_gate_18_out_14, n8_bit_condition_gate_18_out_15, n8_bit_condition_gate_18_out_16,
       n8_bit_condition_gate_18_out_17, n8_bit_condition_gate_19_out_10, n8_bit_condition_gate_19_out_11,
       n8_bit_condition_gate_19_out_12, n8_bit_condition_gate_19_out_13, n8_bit_condition_gate_19_out_14,
       n8_bit_condition_gate_19_out_15, n8_bit_condition_gate_19_out_16, n8_bit_condition_gate_19_out_17,
       n8_bit_condition_gate_20_out_10, n8_bit_condition_gate_20_out_11, n8_bit_condition_gate_20_out_12,
       n8_bit_condition_gate_20_out_13, n8_bit_condition_gate_20_out_14, n8_bit_condition_gate_20_out_15,
       n8_bit_condition_gate_20_out_16, n8_bit_condition_gate_20_out_17, n8_bit_condition_gate_21_out_10,
       n8_bit_condition_gate_21_out_11, n8_bit_condition_gate_21_out_12, n8_bit_condition_gate_21_out_13,
       n8_bit_condition_gate_21_out_14, n8_bit_condition_gate_21_out_15, n8_bit_condition_gate_21_out_16,
       n8_bit_condition_gate_21_out_17, n8_bit_condition_gate_22_out_10, n8_bit_condition_gate_22_out_11,
       n8_bit_condition_gate_22_out_12, n8_bit_condition_gate_22_out_13, n8_bit_condition_gate_22_out_14,
       n8_bit_condition_gate_22_out_15, n8_bit_condition_gate_22_out_16, n8_bit_condition_gate_22_out_17,
       n8_bit_condition_gate_23_out_10, n8_bit_condition_gate_23_out_11, n8_bit_condition_gate_23_out_12,
       n8_bit_condition_gate_23_out_13, n8_bit_condition_gate_23_out_14, n8_bit_condition_gate_23_out_15,
       n8_bit_condition_gate_23_out_16, n8_bit_condition_gate_23_out_17, n8_bit_condition_gate_24_out_10,
       n8_bit_condition_gate_24_out_11, n8_bit_condition_gate_24_out_12, n8_bit_condition_gate_24_out_13,
       n8_bit_condition_gate_24_out_14, n8_bit_condition_gate_24_out_15, n8_bit_condition_gate_24_out_16,
       n8_bit_condition_gate_24_out_17, n8_bit_condition_gate_25_out_10, n8_bit_condition_gate_25_out_11,
       n8_bit_condition_gate_25_out_12, n8_bit_condition_gate_25_out_13, n8_bit_condition_gate_25_out_14,
       n8_bit_condition_gate_25_out_15, n8_bit_condition_gate_25_out_16, n8_bit_condition_gate_25_out_17,
       n8_bit_condition_gate_26_out_10, n8_bit_condition_gate_26_out_11, n8_bit_condition_gate_26_out_12,
       n8_bit_condition_gate_26_out_13, n8_bit_condition_gate_26_out_14, n8_bit_condition_gate_26_out_15,
       n8_bit_condition_gate_26_out_16, n8_bit_condition_gate_26_out_17, n8_bit_condition_gate_27_out_10,
       n8_bit_condition_gate_27_out_11, n8_bit_condition_gate_27_out_12, n8_bit_condition_gate_27_out_13,
       n8_bit_condition_gate_27_out_14, n8_bit_condition_gate_27_out_15, n8_bit_condition_gate_27_out_16,
       n8_bit_condition_gate_27_out_17, n8_bit_condition_gate_28_out_10, n8_bit_condition_gate_28_out_11,
       n8_bit_condition_gate_28_out_12, n8_bit_condition_gate_28_out_13, n8_bit_condition_gate_28_out_14,
       n8_bit_condition_gate_28_out_15, n8_bit_condition_gate_28_out_16, n8_bit_condition_gate_28_out_17,
       n8_bit_condition_gate_29_out_10, n8_bit_condition_gate_29_out_11, n8_bit_condition_gate_29_out_12,
       n8_bit_condition_gate_29_out_13, n8_bit_condition_gate_29_out_14, n8_bit_condition_gate_29_out_15,
       n8_bit_condition_gate_29_out_16, n8_bit_condition_gate_29_out_17, n8_bit_condition_gate_30_out_10,
       n8_bit_condition_gate_30_out_11, n8_bit_condition_gate_30_out_12, n8_bit_condition_gate_30_out_13,
       n8_bit_condition_gate_30_out_14, n8_bit_condition_gate_30_out_15, n8_bit_condition_gate_30_out_16,
       n8_bit_condition_gate_30_out_17, n8_bit_condition_gate_31_out_10, n8_bit_condition_gate_31_out_11,
       n8_bit_condition_gate_31_out_12, n8_bit_condition_gate_31_out_13, n8_bit_condition_gate_31_out_14,
       n8_bit_condition_gate_31_out_15, n8_bit_condition_gate_31_out_16, n8_bit_condition_gate_31_out_17,
       n8_bit_condition_gate_32_out_10, n8_bit_condition_gate_32_out_11, n8_bit_condition_gate_32_out_12,
       n8_bit_condition_gate_32_out_13, n8_bit_condition_gate_32_out_14, n8_bit_condition_gate_32_out_15,
       n8_bit_condition_gate_32_out_16, n8_bit_condition_gate_32_out_17, not_1_out, not_2_out, not_3_out,
       not_4_out, not_5_out, not_6_out, not_7_out, not_8_out, not_9_out, not_10_out, not_11_out, not_12_out,
       not_13_out, not_14_out, not_15_out, not_16_out, or_2_out, or_3_out, or_4_out, or_5_out, or_6_out,
       or_7_out, or_8_out, or_9_out, or_10_out, or_11_out, or_12_out, or_13_out, or_14_out, or_15_out,
       or_16_out, or_19_out, or_20_out, or_21_out, or_22_out, or_23_out, or_24_out, or_25_out, or_26_out,
       or_27_out, or_28_out, or_29_out, or_30_out, or_31_out, or_32_out, or_34_out, or_35_out, or_36_out,
       or_37_out, or_38_out, or_39_out, or_40_out, or_41_out, or_42_out, or_43_out, or_44_out, or_45_out,
       or_46_out, or_47_out, or_48_out, or_51_out, or_52_out, or_53_out, or_54_out, or_55_out, or_56_out,
       or_57_out, or_58_out, or_59_out, or_60_out, or_61_out, or_62_out, or_63_out, or_64_out, or_65_out,
       or_66_out, or_67_out, or_68_out, or_69_out, or_70_out, or_71_out, or_72_out, or_73_out, or_74_out,
       or_75_out, or_76_out, or_77_out, or_78_out, or_79_out, or_80_out, or_83_out, or_84_out, or_85_out,
       or_86_out, or_87_out, or_88_out, or_89_out, or_90_out, or_91_out, or_92_out, or_93_out, or_94_out,
       or_95_out, or_96_out, or_97_out, or_98_out, or_99_out, or_100_out, or_101_out, or_102_out, or_103_out,
       or_104_out, or_105_out, or_106_out, or_107_out, or_108_out, or_109_out, or_110_out, or_111_out,
       or_112_out, or_114_out, or_115_out, or_116_out, or_117_out, or_118_out, or_119_out, or_120_out,
       or_121_out, or_122_out, or_123_out, or_124_out, or_125_out, or_126_out, or_127_out, or_128_out;

  not not_1 (not_1_out, _1for_write_mode);
  and and_1 (and_1_out, not_1_out, in_11);
  and and_2 (and_2_out, in_11, _1for_write_mode);
  not not_2 (not_2_out, _1for_write_mode);
  and and_3 (and_3_out, not_2_out, in_12);
  and and_4 (and_4_out, in_12, _1for_write_mode);
  not not_3 (not_3_out, _1for_write_mode);
  and and_5 (and_5_out, not_3_out, in_13);
  and and_6 (and_6_out, in_13, _1for_write_mode);
  not not_4 (not_4_out, _1for_write_mode);
  and and_7 (and_7_out, not_4_out, in_14);
  and and_8 (and_8_out, in_14, _1for_write_mode);
  not not_5 (not_5_out, _1for_write_mode);
  and and_9 (and_9_out, not_5_out, in_15);
  and and_10 (and_10_out, in_15, _1for_write_mode);
  not not_6 (not_6_out, _1for_write_mode);
  and and_11 (and_11_out, not_6_out, in_16);
  and and_12 (and_12_out, in_16, _1for_write_mode);
  not not_7 (not_7_out, _1for_write_mode);
  and and_13 (and_13_out, not_7_out, in_17);
  and and_14 (and_14_out, in_17, _1for_write_mode);
  not not_8 (not_8_out, _1for_write_mode);
  and and_15 (and_15_out, not_8_out, in_18);
  and and_16 (and_16_out, in_18, _1for_write_mode);
  not not_9 (not_9_out, _1for_write_mode);
  and and_17 (and_17_out, not_9_out, in_19);
  and and_18 (and_18_out, in_19, _1for_write_mode);
  not not_10 (not_10_out, _1for_write_mode);
  and and_19 (and_19_out, not_10_out, in_20);
  and and_20 (and_20_out, in_20, _1for_write_mode);
  not not_11 (not_11_out, _1for_write_mode);
  and and_21 (and_21_out, not_11_out, in_21);
  and and_22 (and_22_out, in_21, _1for_write_mode);
  not not_12 (not_12_out, _1for_write_mode);
  and and_23 (and_23_out, not_12_out, in_22);
  and and_24 (and_24_out, in_22, _1for_write_mode);
  not not_13 (not_13_out, _1for_write_mode);
  and and_25 (and_25_out, not_13_out, in_23);
  and and_26 (and_26_out, in_23, _1for_write_mode);
  not not_14 (not_14_out, _1for_write_mode);
  and and_27 (and_27_out, not_14_out, in_24);
  and and_28 (and_28_out, in_24, _1for_write_mode);
  not not_15 (not_15_out, _1for_write_mode);
  and and_29 (and_29_out, not_15_out, in_25);
  and and_30 (and_30_out, in_25, _1for_write_mode);
  not not_16 (not_16_out, _1for_write_mode);
  and and_31 (and_31_out, not_16_out, in_26);
  and and_32 (and_32_out, in_26, _1for_write_mode);
  _8_bit_condition_gate u_8_bit_condition_gate_1 (
    .Bit_7(in_3), .Bit_6(in_4), .Bit_5(in_5), .Bit_4(in_6), .Bit_3(in_7), .Bit_2(in_8), .Bit_1(in_9),
    .Bit_0(in_9), .out_10(n8_bit_condition_gate_1_out_10), .out_11(n8_bit_condition_gate_1_out_11),
    .out_12(n8_bit_condition_gate_1_out_12), .out_13(n8_bit_condition_gate_1_out_13),
    .out_14(n8_bit_condition_gate_1_out_14), .out_15(n8_bit_condition_gate_1_out_15),
    .out_16(n8_bit_condition_gate_1_out_16), .out_17(n8_bit_condition_gate_1_out_17), .Condition(and_2_out));
  _8_bit_condition_gate u_8_bit_condition_gate_2 (
    .Bit_7(in_3), .Bit_6(in_4), .Bit_5(in_5), .Bit_4(in_6), .Bit_3(in_7), .Bit_2(in_8), .Bit_1(in_9),
    .Bit_0(in_10), .out_10(n8_bit_condition_gate_2_out_10), .out_11(n8_bit_condition_gate_2_out_11),
    .out_12(n8_bit_condition_gate_2_out_12), .out_13(n8_bit_condition_gate_2_out_13),
    .out_14(n8_bit_condition_gate_2_out_14), .out_15(n8_bit_condition_gate_2_out_15),
    .out_16(n8_bit_condition_gate_2_out_16), .out_17(n8_bit_condition_gate_2_out_17), .Condition(and_4_out));
  _8_bit_condition_gate u_8_bit_condition_gate_3 (
    .Bit_7(in_3), .Bit_6(in_4), .Bit_5(in_5), .Bit_4(in_6), .Bit_3(in_7), .Bit_2(in_8), .Bit_1(in_9),
    .Bit_0(in_10), .out_10(n8_bit_condition_gate_3_out_10), .out_11(n8_bit_condition_gate_3_out_11),
    .out_12(n8_bit_condition_gate_3_out_12), .out_13(n8_bit_condition_gate_3_out_13),
    .out_14(n8_bit_condition_gate_3_out_14), .out_15(n8_bit_condition_gate_3_out_15),
    .out_16(n8_bit_condition_gate_3_out_16), .out_17(n8_bit_condition_gate_3_out_17), .Condition(and_6_out));
  _8_bit_condition_gate u_8_bit_condition_gate_4 (
    .Bit_7(in_3), .Bit_6(in_4), .Bit_5(in_5), .Bit_4(in_6), .Bit_3(in_7), .Bit_2(in_8), .Bit_1(in_9),
    .Bit_0(in_10), .out_10(n8_bit_condition_gate_4_out_10), .out_11(n8_bit_condition_gate_4_out_11),
    .out_12(n8_bit_condition_gate_4_out_12), .out_13(n8_bit_condition_gate_4_out_13),
    .out_14(n8_bit_condition_gate_4_out_14), .out_15(n8_bit_condition_gate_4_out_15),
    .out_16(n8_bit_condition_gate_4_out_16), .out_17(n8_bit_condition_gate_4_out_17), .Condition(and_8_out));
  _8_bit_condition_gate u_8_bit_condition_gate_5 (
    .Bit_7(in_3), .Bit_6(in_4), .Bit_5(in_5), .Bit_4(in_6), .Bit_3(in_7), .Bit_2(in_8), .Bit_1(in_9),
    .Bit_0(in_10), .out_10(n8_bit_condition_gate_5_out_10), .out_11(n8_bit_condition_gate_5_out_11),
    .out_12(n8_bit_condition_gate_5_out_12), .out_13(n8_bit_condition_gate_5_out_13),
    .out_14(n8_bit_condition_gate_5_out_14), .out_15(n8_bit_condition_gate_5_out_15),
    .out_16(n8_bit_condition_gate_5_out_16), .out_17(n8_bit_condition_gate_5_out_17), .Condition(and_10_out));
  _8_bit_condition_gate u_8_bit_condition_gate_6 (
    .Bit_7(in_3), .Bit_6(in_4), .Bit_5(in_5), .Bit_4(in_6), .Bit_3(in_7), .Bit_2(in_8), .Bit_1(in_9),
    .Bit_0(in_10), .out_10(n8_bit_condition_gate_6_out_10), .out_11(n8_bit_condition_gate_6_out_11),
    .out_12(n8_bit_condition_gate_6_out_12), .out_13(n8_bit_condition_gate_6_out_13),
    .out_14(n8_bit_condition_gate_6_out_14), .out_15(n8_bit_condition_gate_6_out_15),
    .out_16(n8_bit_condition_gate_6_out_16), .out_17(n8_bit_condition_gate_6_out_17), .Condition(and_12_out));
  _8_bit_condition_gate u_8_bit_condition_gate_7 (
    .Bit_7(in_3), .Bit_6(in_4), .Bit_5(in_5), .Bit_4(in_6), .Bit_3(in_7), .Bit_2(in_8), .Bit_1(in_9),
    .Bit_0(in_10), .out_10(n8_bit_condition_gate_7_out_10), .out_11(n8_bit_condition_gate_7_out_11),
    .out_12(n8_bit_condition_gate_7_out_12), .out_13(n8_bit_condition_gate_7_out_13),
    .out_14(n8_bit_condition_gate_7_out_14), .out_15(n8_bit_condition_gate_7_out_15),
    .out_16(n8_bit_condition_gate_7_out_16), .out_17(n8_bit_condition_gate_7_out_17), .Condition(and_14_out));
  _8_bit_condition_gate u_8_bit_condition_gate_8 (
    .Bit_7(in_3), .Bit_6(in_4), .Bit_5(in_5), .Bit_4(in_6), .Bit_3(in_7), .Bit_2(in_8), .Bit_1(in_9),
    .Bit_0(in_10), .out_10(n8_bit_condition_gate_8_out_10), .out_11(n8_bit_condition_gate_8_out_11),
    .out_12(n8_bit_condition_gate_8_out_12), .out_13(n8_bit_condition_gate_8_out_13),
    .out_14(n8_bit_condition_gate_8_out_14), .out_15(n8_bit_condition_gate_8_out_15),
    .out_16(n8_bit_condition_gate_8_out_16), .out_17(n8_bit_condition_gate_8_out_17), .Condition(and_16_out));
  _8_bit_condition_gate u_8_bit_condition_gate_9 (
    .Bit_7(in_3), .Bit_6(in_4), .Bit_5(in_5), .Bit_4(in_6), .Bit_3(in_7), .Bit_2(in_8), .Bit_1(in_9),
    .Bit_0(in_10), .out_10(n8_bit_condition_gate_9_out_10), .out_11(n8_bit_condition_gate_9_out_11),
    .out_12(n8_bit_condition_gate_9_out_12), .out_13(n8_bit_condition_gate_9_out_13),
    .out_14(n8_bit_condition_gate_9_out_14), .out_15(n8_bit_condition_gate_9_out_15),
    .out_16(n8_bit_condition_gate_9_out_16), .out_17(n8_bit_condition_gate_9_out_17), .Condition(and_18_out));
  _8_bit_condition_gate u_8_bit_condition_gate_10 (
    .Bit_7(in_3), .Bit_6(in_4), .Bit_5(in_5), .Bit_4(in_6), .Bit_3(in_7), .Bit_2(in_8), .Bit_1(in_9),
    .Bit_0(in_10), .out_10(n8_bit_condition_gate_10_out_10), .out_11(n8_bit_condition_gate_10_out_11),
    .out_12(n8_bit_condition_gate_10_out_12), .out_13(n8_bit_condition_gate_10_out_13),
    .out_14(n8_bit_condition_gate_10_out_14), .out_15(n8_bit_condition_gate_10_out_15),
    .out_16(n8_bit_condition_gate_10_out_16), .out_17(n8_bit_condition_gate_10_out_17), .Condition(and_20_out));
  _8_bit_condition_gate u_8_bit_condition_gate_11 (
    .Bit_7(in_3), .Bit_6(in_4), .Bit_5(in_5), .Bit_4(in_6), .Bit_3(in_7), .Bit_2(in_8), .Bit_1(in_9),
    .Bit_0(in_10), .out_10(n8_bit_condition_gate_11_out_10), .out_11(n8_bit_condition_gate_11_out_11),
    .out_12(n8_bit_condition_gate_11_out_12), .out_13(n8_bit_condition_gate_11_out_13),
    .out_14(n8_bit_condition_gate_11_out_14), .out_15(n8_bit_condition_gate_11_out_15),
    .out_16(n8_bit_condition_gate_11_out_16), .out_17(n8_bit_condition_gate_11_out_17), .Condition(and_22_out));
  _8_bit_condition_gate u_8_bit_condition_gate_12 (
    .Bit_7(in_3), .Bit_6(in_4), .Bit_5(in_5), .Bit_4(in_6), .Bit_3(in_7), .Bit_2(in_8), .Bit_1(in_9),
    .Bit_0(in_10), .out_10(n8_bit_condition_gate_12_out_10), .out_11(n8_bit_condition_gate_12_out_11),
    .out_12(n8_bit_condition_gate_12_out_12), .out_13(n8_bit_condition_gate_12_out_13),
    .out_14(n8_bit_condition_gate_12_out_14), .out_15(n8_bit_condition_gate_12_out_15),
    .out_16(n8_bit_condition_gate_12_out_16), .out_17(n8_bit_condition_gate_12_out_17), .Condition(and_24_out));
  _8_bit_condition_gate u_8_bit_condition_gate_13 (
    .Bit_7(in_3), .Bit_6(in_4), .Bit_5(in_5), .Bit_4(in_6), .Bit_3(in_7), .Bit_2(in_8), .Bit_1(in_9),
    .Bit_0(in_10), .out_10(n8_bit_condition_gate_13_out_10), .out_11(n8_bit_condition_gate_13_out_11),
    .out_12(n8_bit_condition_gate_13_out_12), .out_13(n8_bit_condition_gate_13_out_13),
    .out_14(n8_bit_condition_gate_13_out_14), .out_15(n8_bit_condition_gate_13_out_15),
    .out_16(n8_bit_condition_gate_13_out_16), .out_17(n8_bit_condition_gate_13_out_17), .Condition(and_26_out));
  _8_bit_condition_gate u_8_bit_condition_gate_14 (
    .Bit_7(in_3), .Bit_6(in_4), .Bit_5(in_5), .Bit_4(in_6), .Bit_3(in_7), .Bit_2(in_8), .Bit_1(in_9),
    .Bit_0(in_10), .out_10(n8_bit_condition_gate_14_out_10), .out_11(n8_bit_condition_gate_14_out_11),
    .out_12(n8_bit_condition_gate_14_out_12), .out_13(n8_bit_condition_gate_14_out_13),
    .out_14(n8_bit_condition_gate_14_out_14), .out_15(n8_bit_condition_gate_14_out_15),
    .out_16(n8_bit_condition_gate_14_out_16), .out_17(n8_bit_condition_gate_14_out_17), .Condition(and_28_out));
  _8_bit_condition_gate u_8_bit_condition_gate_15 (
    .Bit_7(in_3), .Bit_6(in_4), .Bit_5(in_5), .Bit_4(in_6), .Bit_3(in_7), .Bit_2(in_8), .Bit_1(in_9),
    .Bit_0(in_10), .out_10(n8_bit_condition_gate_15_out_10), .out_11(n8_bit_condition_gate_15_out_11),
    .out_12(n8_bit_condition_gate_15_out_12), .out_13(n8_bit_condition_gate_15_out_13),
    .out_14(n8_bit_condition_gate_15_out_14), .out_15(n8_bit_condition_gate_15_out_15),
    .out_16(n8_bit_condition_gate_15_out_16), .out_17(n8_bit_condition_gate_15_out_17), .Condition(and_30_out));
  _8_bit_condition_gate u_8_bit_condition_gate_16 (
    .Bit_7(in_3), .Bit_6(in_4), .Bit_5(in_5), .Bit_4(in_6), .Bit_3(in_7), .Bit_2(in_8), .Bit_1(in_9),
    .Bit_0(in_10), .out_10(n8_bit_condition_gate_16_out_10), .out_11(n8_bit_condition_gate_16_out_11),
    .out_12(n8_bit_condition_gate_16_out_12), .out_13(n8_bit_condition_gate_16_out_13),
    .out_14(n8_bit_condition_gate_16_out_14), .out_15(n8_bit_condition_gate_16_out_15),
    .out_16(n8_bit_condition_gate_16_out_16), .out_17(n8_bit_condition_gate_16_out_17), .Condition(and_32_out));
  \byte  byte_1 (
    .in_3(n8_bit_condition_gate_1_out_10), .in_4(n8_bit_condition_gate_1_out_11),
    .in_5(n8_bit_condition_gate_1_out_12), .in_6(n8_bit_condition_gate_1_out_13),
    .in_7(n8_bit_condition_gate_1_out_14), .in_8(n8_bit_condition_gate_1_out_15),
    .in_9(n8_bit_condition_gate_1_out_16), .in_10(n8_bit_condition_gate_1_out_17), .out_11(byte_1_out_11),
    .out_13(byte_1_out_13), .out_15(byte_1_out_15), .out_17(byte_1_out_17), .out_19(byte_1_out_19),
    .out_21(byte_1_out_21), .out_23(byte_1_out_23), .out_25(byte_1_out_25), .R_W(and_2_out), .Clock(in_1),
    .out_12(out_35), .out_14(out_36), .out_16(out_37), .out_18(out_38), .out_20(out_39), .out_22(out_40),
    .out_24(out_41), .out_26(out_42));
  \byte  byte_2 (
    .in_3(n8_bit_condition_gate_2_out_10), .in_4(n8_bit_condition_gate_2_out_11),
    .in_5(n8_bit_condition_gate_2_out_12), .in_6(n8_bit_condition_gate_2_out_13),
    .in_7(n8_bit_condition_gate_2_out_14), .in_8(n8_bit_condition_gate_2_out_15),
    .in_9(n8_bit_condition_gate_2_out_16), .in_10(n8_bit_condition_gate_2_out_17), .out_11(byte_2_out_11),
    .out_13(byte_2_out_13), .out_15(byte_2_out_15), .out_17(byte_2_out_17), .out_19(byte_2_out_19),
    .out_21(byte_2_out_21), .out_23(byte_2_out_23), .out_25(byte_2_out_25), .R_W(and_4_out), .Clock(in_1),
    .out_12(out_43), .out_14(out_44), .out_16(out_45), .out_18(out_46), .out_20(out_47), .out_22(out_48),
    .out_24(out_49), .out_26(out_50));
  \byte  byte_3 (
    .in_3(n8_bit_condition_gate_3_out_10), .in_4(n8_bit_condition_gate_3_out_11),
    .in_5(n8_bit_condition_gate_3_out_12), .in_6(n8_bit_condition_gate_3_out_13),
    .in_7(n8_bit_condition_gate_3_out_14), .in_8(n8_bit_condition_gate_3_out_15),
    .in_9(n8_bit_condition_gate_3_out_16), .in_10(n8_bit_condition_gate_3_out_17), .out_11(byte_3_out_11),
    .out_13(byte_3_out_13), .out_15(byte_3_out_15), .out_17(byte_3_out_17), .out_19(byte_3_out_19),
    .out_21(byte_3_out_21), .out_23(byte_3_out_23), .out_25(byte_3_out_25), .R_W(and_6_out), .Clock(in_1),
    .out_12(out_51), .out_14(out_52), .out_16(out_53), .out_18(out_54), .out_20(out_55), .out_22(out_56),
    .out_24(out_57), .out_26(out_58));
  \byte  byte_4 (
    .in_3(n8_bit_condition_gate_4_out_10), .in_4(n8_bit_condition_gate_4_out_11),
    .in_5(n8_bit_condition_gate_4_out_12), .in_6(n8_bit_condition_gate_4_out_13),
    .in_7(n8_bit_condition_gate_4_out_14), .in_8(n8_bit_condition_gate_4_out_15),
    .in_9(n8_bit_condition_gate_4_out_16), .in_10(n8_bit_condition_gate_4_out_17), .out_11(byte_4_out_11),
    .out_13(byte_4_out_13), .out_15(byte_4_out_15), .out_17(byte_4_out_17), .out_19(byte_4_out_19),
    .out_21(byte_4_out_21), .out_23(byte_4_out_23), .out_25(byte_4_out_25), .R_W(and_8_out), .Clock(in_1),
    .out_12(out_59), .out_14(out_60), .out_16(out_61), .out_18(out_62), .out_20(out_63), .out_22(out_64),
    .out_24(out_65), .out_26(out_66));
  \byte  byte_5 (
    .in_3(n8_bit_condition_gate_5_out_10), .in_4(n8_bit_condition_gate_5_out_11),
    .in_5(n8_bit_condition_gate_5_out_12), .in_6(n8_bit_condition_gate_5_out_13),
    .in_7(n8_bit_condition_gate_5_out_14), .in_8(n8_bit_condition_gate_5_out_15),
    .in_9(n8_bit_condition_gate_5_out_16), .in_10(n8_bit_condition_gate_5_out_17), .out_11(byte_5_out_11),
    .out_13(byte_5_out_13), .out_15(byte_5_out_15), .out_17(byte_5_out_17), .out_19(byte_5_out_19),
    .out_21(byte_5_out_21), .out_23(byte_5_out_23), .out_25(byte_5_out_25), .R_W(and_10_out), .Clock(in_1),
    .out_12(out_67), .out_14(out_68), .out_16(out_69), .out_18(out_70), .out_20(out_71), .out_22(out_72),
    .out_24(out_73), .out_26(out_74));
  \byte  byte_6 (
    .in_3(n8_bit_condition_gate_6_out_10), .in_4(n8_bit_condition_gate_6_out_11),
    .in_5(n8_bit_condition_gate_6_out_12), .in_6(n8_bit_condition_gate_6_out_13),
    .in_7(n8_bit_condition_gate_6_out_14), .in_8(n8_bit_condition_gate_6_out_15),
    .in_9(n8_bit_condition_gate_6_out_16), .in_10(n8_bit_condition_gate_6_out_17), .out_11(byte_6_out_11),
    .out_13(byte_6_out_13), .out_15(byte_6_out_15), .out_17(byte_6_out_17), .out_19(byte_6_out_19),
    .out_21(byte_6_out_21), .out_23(byte_6_out_23), .out_25(byte_6_out_25), .R_W(and_12_out), .Clock(in_1),
    .out_12(out_75), .out_14(out_76), .out_16(out_77), .out_18(out_78), .out_20(out_79), .out_22(out_80),
    .out_24(out_81), .out_26(out_82));
  \byte  byte_7 (
    .in_3(n8_bit_condition_gate_7_out_10), .in_4(n8_bit_condition_gate_7_out_11),
    .in_5(n8_bit_condition_gate_7_out_12), .in_6(n8_bit_condition_gate_7_out_13),
    .in_7(n8_bit_condition_gate_7_out_14), .in_8(n8_bit_condition_gate_7_out_15),
    .in_9(n8_bit_condition_gate_7_out_16), .in_10(n8_bit_condition_gate_7_out_17), .out_11(byte_7_out_11),
    .out_13(byte_7_out_13), .out_15(byte_7_out_15), .out_17(byte_7_out_17), .out_19(byte_7_out_19),
    .out_21(byte_7_out_21), .out_23(byte_7_out_23), .out_25(byte_7_out_25), .R_W(and_14_out), .Clock(in_1),
    .out_12(out_83), .out_14(out_84), .out_16(out_85), .out_18(out_86), .out_20(out_87), .out_22(out_88),
    .out_24(out_89), .out_26(out_90));
  \byte  byte_8 (
    .in_3(n8_bit_condition_gate_8_out_10), .in_4(n8_bit_condition_gate_8_out_11),
    .in_5(n8_bit_condition_gate_8_out_12), .in_6(n8_bit_condition_gate_8_out_13),
    .in_7(n8_bit_condition_gate_8_out_14), .in_8(n8_bit_condition_gate_8_out_15),
    .in_9(n8_bit_condition_gate_8_out_16), .in_10(n8_bit_condition_gate_8_out_17), .out_11(byte_8_out_11),
    .out_13(byte_8_out_13), .out_15(byte_8_out_15), .out_17(byte_8_out_17), .out_19(byte_8_out_19),
    .out_21(byte_8_out_21), .out_23(byte_8_out_23), .out_25(byte_8_out_25), .R_W(and_16_out), .Clock(in_1),
    .out_12(out_91), .out_14(out_92), .out_16(out_93), .out_18(out_94), .out_20(out_95), .out_22(out_96),
    .out_24(out_97), .out_26(out_98));
  \byte  byte_9 (
    .in_3(n8_bit_condition_gate_9_out_10), .in_4(n8_bit_condition_gate_9_out_11),
    .in_5(n8_bit_condition_gate_9_out_12), .in_6(n8_bit_condition_gate_9_out_13),
    .in_7(n8_bit_condition_gate_9_out_14), .in_8(n8_bit_condition_gate_9_out_15),
    .in_9(n8_bit_condition_gate_9_out_16), .in_10(n8_bit_condition_gate_9_out_17), .out_11(byte_9_out_11),
    .out_13(byte_9_out_13), .out_15(byte_9_out_15), .out_17(byte_9_out_17), .out_19(byte_9_out_19),
    .out_21(byte_9_out_21), .out_23(byte_9_out_23), .out_25(byte_9_out_25), .R_W(and_18_out), .Clock(in_1),
    .out_12(out_99), .out_14(out_100), .out_16(out_101), .out_18(out_102), .out_20(out_103),
    .out_22(out_104), .out_24(out_105), .out_26(out_106));
  \byte  byte_10 (
    .in_3(n8_bit_condition_gate_10_out_10), .in_4(n8_bit_condition_gate_10_out_11),
    .in_5(n8_bit_condition_gate_10_out_12), .in_6(n8_bit_condition_gate_10_out_13),
    .in_7(n8_bit_condition_gate_10_out_14), .in_8(n8_bit_condition_gate_10_out_15),
    .in_9(n8_bit_condition_gate_10_out_16), .in_10(n8_bit_condition_gate_10_out_17), .out_11(byte_10_out_11),
    .out_13(byte_10_out_13), .out_15(byte_10_out_15), .out_17(byte_10_out_17), .out_19(byte_10_out_19),
    .out_21(byte_10_out_21), .out_23(byte_10_out_23), .out_25(byte_10_out_25), .R_W(and_20_out),
    .Clock(in_1), .out_12(out_107), .out_14(out_108), .out_16(out_109), .out_18(out_110), .out_20(out_111),
    .out_22(out_112), .out_24(out_113), .out_26(out_114));
  \byte  byte_11 (
    .in_3(n8_bit_condition_gate_11_out_10), .in_4(n8_bit_condition_gate_11_out_11),
    .in_5(n8_bit_condition_gate_11_out_12), .in_6(n8_bit_condition_gate_11_out_13),
    .in_7(n8_bit_condition_gate_11_out_14), .in_8(n8_bit_condition_gate_11_out_15),
    .in_9(n8_bit_condition_gate_11_out_16), .in_10(n8_bit_condition_gate_11_out_17), .out_11(byte_11_out_11),
    .out_13(byte_11_out_13), .out_15(byte_11_out_15), .out_17(byte_11_out_17), .out_19(byte_11_out_19),
    .out_21(byte_11_out_21), .out_23(byte_11_out_23), .out_25(byte_11_out_25), .R_W(and_22_out),
    .Clock(in_1), .out_12(out_115), .out_14(out_116), .out_16(out_117), .out_18(out_118), .out_20(out_119),
    .out_22(out_120), .out_24(out_121), .out_26(out_122));
  \byte  byte_12 (
    .in_3(n8_bit_condition_gate_12_out_10), .in_4(n8_bit_condition_gate_12_out_11),
    .in_5(n8_bit_condition_gate_12_out_12), .in_6(n8_bit_condition_gate_12_out_13),
    .in_7(n8_bit_condition_gate_12_out_14), .in_8(n8_bit_condition_gate_12_out_15),
    .in_9(n8_bit_condition_gate_12_out_16), .in_10(n8_bit_condition_gate_12_out_17), .out_11(byte_12_out_11),
    .out_13(byte_12_out_13), .out_15(byte_12_out_15), .out_17(byte_12_out_17), .out_19(byte_12_out_19),
    .out_21(byte_12_out_21), .out_23(byte_12_out_23), .out_25(byte_12_out_25), .R_W(and_24_out),
    .Clock(in_1), .out_12(out_123), .out_14(out_124), .out_16(out_125), .out_18(out_126), .out_20(out_127),
    .out_22(out_128), .out_24(out_129), .out_26(out_130));
  \byte  byte_13 (
    .in_3(n8_bit_condition_gate_13_out_10), .in_4(n8_bit_condition_gate_13_out_11),
    .in_5(n8_bit_condition_gate_13_out_12), .in_6(n8_bit_condition_gate_13_out_13),
    .in_7(n8_bit_condition_gate_13_out_14), .in_8(n8_bit_condition_gate_13_out_15),
    .in_9(n8_bit_condition_gate_13_out_16), .in_10(n8_bit_condition_gate_13_out_17), .out_11(byte_13_out_11),
    .out_13(byte_13_out_13), .out_15(byte_13_out_15), .out_17(byte_13_out_17), .out_19(byte_13_out_19),
    .out_21(byte_13_out_21), .out_23(byte_13_out_23), .out_25(byte_13_out_25), .R_W(and_26_out),
    .Clock(in_1), .out_12(out_131), .out_14(out_132), .out_16(out_133), .out_18(out_134), .out_20(out_135),
    .out_22(out_136), .out_24(out_137), .out_26(out_138));
  \byte  byte_14 (
    .in_3(n8_bit_condition_gate_14_out_10), .in_4(n8_bit_condition_gate_14_out_11),
    .in_5(n8_bit_condition_gate_14_out_12), .in_6(n8_bit_condition_gate_14_out_13),
    .in_7(n8_bit_condition_gate_14_out_14), .in_8(n8_bit_condition_gate_14_out_15),
    .in_9(n8_bit_condition_gate_14_out_16), .in_10(n8_bit_condition_gate_14_out_17), .out_11(byte_14_out_11),
    .out_13(byte_14_out_13), .out_15(byte_14_out_15), .out_17(byte_14_out_17), .out_19(byte_14_out_19),
    .out_21(byte_14_out_21), .out_23(byte_14_out_23), .out_25(byte_14_out_25), .R_W(and_28_out),
    .Clock(in_1), .out_12(out_139), .out_14(out_140), .out_16(out_141), .out_18(out_142), .out_20(out_143),
    .out_22(out_144), .out_24(out_145), .out_26(out_146));
  \byte  byte_15 (
    .in_3(n8_bit_condition_gate_15_out_10), .in_4(n8_bit_condition_gate_15_out_11),
    .in_5(n8_bit_condition_gate_15_out_12), .in_6(n8_bit_condition_gate_15_out_13),
    .in_7(n8_bit_condition_gate_15_out_14), .in_8(n8_bit_condition_gate_15_out_15),
    .in_9(n8_bit_condition_gate_15_out_16), .in_10(n8_bit_condition_gate_15_out_17), .out_11(byte_15_out_11),
    .out_13(byte_15_out_13), .out_15(byte_15_out_15), .out_17(byte_15_out_17), .out_19(byte_15_out_19),
    .out_21(byte_15_out_21), .out_23(byte_15_out_23), .out_25(byte_15_out_25), .R_W(and_30_out),
    .Clock(in_1), .out_12(out_147), .out_14(out_148), .out_16(out_149), .out_18(out_150), .out_20(out_151),
    .out_22(out_152), .out_24(out_153), .out_26(out_154));
  \byte  byte_16 (
    .in_3(n8_bit_condition_gate_16_out_10), .in_4(n8_bit_condition_gate_16_out_11),
    .in_5(n8_bit_condition_gate_16_out_12), .in_6(n8_bit_condition_gate_16_out_13),
    .in_7(n8_bit_condition_gate_16_out_14), .in_8(n8_bit_condition_gate_16_out_15),
    .in_9(n8_bit_condition_gate_16_out_16), .in_10(n8_bit_condition_gate_16_out_17), .out_11(byte_16_out_11),
    .out_13(byte_16_out_13), .out_15(byte_16_out_15), .out_17(byte_16_out_17), .out_19(byte_16_out_19),
    .out_21(byte_16_out_21), .out_23(byte_16_out_23), .out_25(byte_16_out_25), .R_W(and_32_out),
    .Clock(in_1), .out_12(out_155), .out_14(out_156), .out_16(out_157), .out_18(out_158), .out_20(out_159),
    .out_22(out_160), .out_24(out_161), .out_26(out_162));
  or or_1 (out_27, n8_bit_condition_gate_17_out_10, or_2_out);
  _8_bit_condition_gate u_8_bit_condition_gate_17 (
    .Bit_7(byte_1_out_11), .Bit_6(byte_1_out_13), .Bit_5(byte_1_out_15), .Bit_4(byte_1_out_17),
    .Bit_3(byte_1_out_19), .Bit_2(byte_1_out_21), .Bit_1(byte_1_out_23), .Bit_0(byte_1_out_25),
    .out_10(n8_bit_condition_gate_17_out_10), .out_11(n8_bit_condition_gate_17_out_11),
    .out_12(n8_bit_condition_gate_17_out_12), .out_13(n8_bit_condition_gate_17_out_13),
    .out_14(n8_bit_condition_gate_17_out_14), .out_15(n8_bit_condition_gate_17_out_15),
    .out_16(n8_bit_condition_gate_17_out_16), .out_17(n8_bit_condition_gate_17_out_17), .Condition(and_1_out));
  or or_2 (or_2_out, n8_bit_condition_gate_18_out_10, or_3_out);
  _8_bit_condition_gate u_8_bit_condition_gate_18 (
    .Bit_7(byte_2_out_11), .Bit_6(byte_2_out_13), .Bit_5(byte_2_out_15), .Bit_4(byte_2_out_17),
    .Bit_3(byte_2_out_19), .Bit_2(byte_2_out_21), .Bit_1(byte_2_out_23), .Bit_0(byte_2_out_25),
    .out_10(n8_bit_condition_gate_18_out_10), .out_11(n8_bit_condition_gate_18_out_11),
    .out_12(n8_bit_condition_gate_18_out_12), .out_13(n8_bit_condition_gate_18_out_13),
    .out_14(n8_bit_condition_gate_18_out_14), .out_15(n8_bit_condition_gate_18_out_15),
    .out_16(n8_bit_condition_gate_18_out_16), .out_17(n8_bit_condition_gate_18_out_17), .Condition(and_3_out));
  or or_3 (or_3_out, n8_bit_condition_gate_19_out_10, or_4_out);
  _8_bit_condition_gate u_8_bit_condition_gate_19 (
    .Bit_7(byte_3_out_11), .Bit_6(byte_3_out_13), .Bit_5(byte_3_out_15), .Bit_4(byte_3_out_17),
    .Bit_3(byte_3_out_19), .Bit_2(byte_3_out_21), .Bit_1(byte_3_out_23), .Bit_0(byte_3_out_25),
    .out_10(n8_bit_condition_gate_19_out_10), .out_11(n8_bit_condition_gate_19_out_11),
    .out_12(n8_bit_condition_gate_19_out_12), .out_13(n8_bit_condition_gate_19_out_13),
    .out_14(n8_bit_condition_gate_19_out_14), .out_15(n8_bit_condition_gate_19_out_15),
    .out_16(n8_bit_condition_gate_19_out_16), .out_17(n8_bit_condition_gate_19_out_17), .Condition(and_5_out));
  or or_4 (or_4_out, n8_bit_condition_gate_20_out_10, or_5_out);
  _8_bit_condition_gate u_8_bit_condition_gate_20 (
    .Bit_7(byte_4_out_11), .Bit_6(byte_4_out_13), .Bit_5(byte_4_out_15), .Bit_4(byte_4_out_17),
    .Bit_3(byte_4_out_19), .Bit_2(byte_4_out_21), .Bit_1(byte_4_out_23), .Bit_0(byte_4_out_25),
    .out_10(n8_bit_condition_gate_20_out_10), .out_11(n8_bit_condition_gate_20_out_11),
    .out_12(n8_bit_condition_gate_20_out_12), .out_13(n8_bit_condition_gate_20_out_13),
    .out_14(n8_bit_condition_gate_20_out_14), .out_15(n8_bit_condition_gate_20_out_15),
    .out_16(n8_bit_condition_gate_20_out_16), .out_17(n8_bit_condition_gate_20_out_17), .Condition(and_7_out));
  or or_5 (or_5_out, n8_bit_condition_gate_21_out_10, or_6_out);
  _8_bit_condition_gate u_8_bit_condition_gate_21 (
    .Bit_7(byte_5_out_11), .Bit_6(byte_5_out_13), .Bit_5(byte_5_out_15), .Bit_4(byte_5_out_17),
    .Bit_3(byte_5_out_19), .Bit_2(byte_5_out_21), .Bit_1(byte_5_out_23), .Bit_0(byte_5_out_25),
    .out_10(n8_bit_condition_gate_21_out_10), .out_11(n8_bit_condition_gate_21_out_11),
    .out_12(n8_bit_condition_gate_21_out_12), .out_13(n8_bit_condition_gate_21_out_13),
    .out_14(n8_bit_condition_gate_21_out_14), .out_15(n8_bit_condition_gate_21_out_15),
    .out_16(n8_bit_condition_gate_21_out_16), .out_17(n8_bit_condition_gate_21_out_17), .Condition(and_9_out));
  or or_6 (or_6_out, n8_bit_condition_gate_22_out_10, or_7_out);
  _8_bit_condition_gate u_8_bit_condition_gate_22 (
    .Bit_7(byte_6_out_11), .Bit_6(byte_6_out_13), .Bit_5(byte_6_out_15), .Bit_4(byte_6_out_17),
    .Bit_3(byte_6_out_19), .Bit_2(byte_6_out_21), .Bit_1(byte_6_out_23), .Bit_0(byte_6_out_25),
    .out_10(n8_bit_condition_gate_22_out_10), .out_11(n8_bit_condition_gate_22_out_11),
    .out_12(n8_bit_condition_gate_22_out_12), .out_13(n8_bit_condition_gate_22_out_13),
    .out_14(n8_bit_condition_gate_22_out_14), .out_15(n8_bit_condition_gate_22_out_15),
    .out_16(n8_bit_condition_gate_22_out_16), .out_17(n8_bit_condition_gate_22_out_17), .Condition(and_11_out));
  or or_7 (or_7_out, n8_bit_condition_gate_23_out_10, or_8_out);
  _8_bit_condition_gate u_8_bit_condition_gate_23 (
    .Bit_7(byte_7_out_11), .Bit_6(byte_7_out_13), .Bit_5(byte_7_out_15), .Bit_4(byte_7_out_17),
    .Bit_3(byte_7_out_19), .Bit_2(byte_7_out_21), .Bit_1(byte_7_out_23), .Bit_0(byte_7_out_25),
    .out_10(n8_bit_condition_gate_23_out_10), .out_11(n8_bit_condition_gate_23_out_11),
    .out_12(n8_bit_condition_gate_23_out_12), .out_13(n8_bit_condition_gate_23_out_13),
    .out_14(n8_bit_condition_gate_23_out_14), .out_15(n8_bit_condition_gate_23_out_15),
    .out_16(n8_bit_condition_gate_23_out_16), .out_17(n8_bit_condition_gate_23_out_17), .Condition(and_13_out));
  or or_8 (or_8_out, n8_bit_condition_gate_24_out_10, or_9_out);
  _8_bit_condition_gate u_8_bit_condition_gate_24 (
    .Bit_7(byte_8_out_11), .Bit_6(byte_8_out_13), .Bit_5(byte_8_out_15), .Bit_4(byte_8_out_17),
    .Bit_3(byte_8_out_19), .Bit_2(byte_8_out_21), .Bit_1(byte_8_out_23), .Bit_0(byte_8_out_25),
    .out_10(n8_bit_condition_gate_24_out_10), .out_11(n8_bit_condition_gate_24_out_11),
    .out_12(n8_bit_condition_gate_24_out_12), .out_13(n8_bit_condition_gate_24_out_13),
    .out_14(n8_bit_condition_gate_24_out_14), .out_15(n8_bit_condition_gate_24_out_15),
    .out_16(n8_bit_condition_gate_24_out_16), .out_17(n8_bit_condition_gate_24_out_17), .Condition(and_15_out));
  or or_9 (or_9_out, n8_bit_condition_gate_25_out_10, or_10_out);
  _8_bit_condition_gate u_8_bit_condition_gate_25 (
    .Bit_7(byte_9_out_11), .Bit_6(byte_9_out_13), .Bit_5(byte_9_out_15), .Bit_4(byte_9_out_17),
    .Bit_3(byte_9_out_19), .Bit_2(byte_9_out_21), .Bit_1(byte_9_out_23), .Bit_0(byte_9_out_25),
    .out_10(n8_bit_condition_gate_25_out_10), .out_11(n8_bit_condition_gate_25_out_11),
    .out_12(n8_bit_condition_gate_25_out_12), .out_13(n8_bit_condition_gate_25_out_13),
    .out_14(n8_bit_condition_gate_25_out_14), .out_15(n8_bit_condition_gate_25_out_15),
    .out_16(n8_bit_condition_gate_25_out_16), .out_17(n8_bit_condition_gate_25_out_17), .Condition(and_17_out));
  or or_10 (or_10_out, n8_bit_condition_gate_26_out_10, or_11_out);
  _8_bit_condition_gate u_8_bit_condition_gate_26 (
    .Bit_7(byte_10_out_11), .Bit_6(byte_10_out_13), .Bit_5(byte_10_out_15), .Bit_4(byte_10_out_17),
    .Bit_3(byte_10_out_19), .Bit_2(byte_10_out_21), .Bit_1(byte_10_out_23), .Bit_0(byte_10_out_25),
    .out_10(n8_bit_condition_gate_26_out_10), .out_11(n8_bit_condition_gate_26_out_11),
    .out_12(n8_bit_condition_gate_26_out_12), .out_13(n8_bit_condition_gate_26_out_13),
    .out_14(n8_bit_condition_gate_26_out_14), .out_15(n8_bit_condition_gate_26_out_15),
    .out_16(n8_bit_condition_gate_26_out_16), .out_17(n8_bit_condition_gate_26_out_17), .Condition(and_19_out));
  or or_11 (or_11_out, n8_bit_condition_gate_27_out_10, or_12_out);
  _8_bit_condition_gate u_8_bit_condition_gate_27 (
    .Bit_7(byte_11_out_11), .Bit_6(byte_11_out_13), .Bit_5(byte_11_out_15), .Bit_4(byte_11_out_17),
    .Bit_3(byte_11_out_19), .Bit_2(byte_11_out_21), .Bit_1(byte_11_out_23), .Bit_0(byte_11_out_25),
    .out_10(n8_bit_condition_gate_27_out_10), .out_11(n8_bit_condition_gate_27_out_11),
    .out_12(n8_bit_condition_gate_27_out_12), .out_13(n8_bit_condition_gate_27_out_13),
    .out_14(n8_bit_condition_gate_27_out_14), .out_15(n8_bit_condition_gate_27_out_15),
    .out_16(n8_bit_condition_gate_27_out_16), .out_17(n8_bit_condition_gate_27_out_17), .Condition(and_21_out));
  or or_12 (or_12_out, n8_bit_condition_gate_28_out_10, or_13_out);
  _8_bit_condition_gate u_8_bit_condition_gate_28 (
    .Bit_7(byte_12_out_11), .Bit_6(byte_12_out_13), .Bit_5(byte_12_out_15), .Bit_4(byte_12_out_17),
    .Bit_3(byte_12_out_19), .Bit_2(byte_12_out_21), .Bit_1(byte_12_out_23), .Bit_0(byte_12_out_25),
    .out_10(n8_bit_condition_gate_28_out_10), .out_11(n8_bit_condition_gate_28_out_11),
    .out_12(n8_bit_condition_gate_28_out_12), .out_13(n8_bit_condition_gate_28_out_13),
    .out_14(n8_bit_condition_gate_28_out_14), .out_15(n8_bit_condition_gate_28_out_15),
    .out_16(n8_bit_condition_gate_28_out_16), .out_17(n8_bit_condition_gate_28_out_17), .Condition(and_23_out));
  or or_13 (or_13_out, n8_bit_condition_gate_29_out_10, or_14_out);
  _8_bit_condition_gate u_8_bit_condition_gate_29 (
    .Bit_7(byte_13_out_11), .Bit_6(byte_13_out_13), .Bit_5(byte_13_out_15), .Bit_4(byte_13_out_17),
    .Bit_3(byte_13_out_19), .Bit_2(byte_13_out_21), .Bit_1(byte_13_out_23), .Bit_0(byte_13_out_25),
    .out_10(n8_bit_condition_gate_29_out_10), .out_11(n8_bit_condition_gate_29_out_11),
    .out_12(n8_bit_condition_gate_29_out_12), .out_13(n8_bit_condition_gate_29_out_13),
    .out_14(n8_bit_condition_gate_29_out_14), .out_15(n8_bit_condition_gate_29_out_15),
    .out_16(n8_bit_condition_gate_29_out_16), .out_17(n8_bit_condition_gate_29_out_17), .Condition(and_25_out));
  or or_14 (or_14_out, n8_bit_condition_gate_30_out_10, or_15_out);
  _8_bit_condition_gate u_8_bit_condition_gate_30 (
    .Bit_7(byte_14_out_11), .Bit_6(byte_14_out_13), .Bit_5(byte_14_out_15), .Bit_4(byte_14_out_17),
    .Bit_3(byte_14_out_19), .Bit_2(byte_14_out_21), .Bit_1(byte_14_out_23), .Bit_0(byte_14_out_25),
    .out_10(n8_bit_condition_gate_30_out_10), .out_11(n8_bit_condition_gate_30_out_11),
    .out_12(n8_bit_condition_gate_30_out_12), .out_13(n8_bit_condition_gate_30_out_13),
    .out_14(n8_bit_condition_gate_30_out_14), .out_15(n8_bit_condition_gate_30_out_15),
    .out_16(n8_bit_condition_gate_30_out_16), .out_17(n8_bit_condition_gate_30_out_17), .Condition(and_27_out));
  or or_15 (or_15_out, n8_bit_condition_gate_31_out_10, or_16_out);
  _8_bit_condition_gate u_8_bit_condition_gate_31 (
    .Bit_7(byte_15_out_11), .Bit_6(byte_15_out_13), .Bit_5(byte_15_out_15), .Bit_4(byte_15_out_17),
    .Bit_3(byte_15_out_19), .Bit_2(byte_15_out_21), .Bit_1(byte_15_out_23), .Bit_0(byte_15_out_25),
    .out_10(n8_bit_condition_gate_31_out_10), .out_11(n8_bit_condition_gate_31_out_11),
    .out_12(n8_bit_condition_gate_31_out_12), .out_13(n8_bit_condition_gate_31_out_13),
    .out_14(n8_bit_condition_gate_31_out_14), .out_15(n8_bit_condition_gate_31_out_15),
    .out_16(n8_bit_condition_gate_31_out_16), .out_17(n8_bit_condition_gate_31_out_17), .Condition(and_29_out));
  buf or_16 (or_16_out, n8_bit_condition_gate_32_out_10);  // OR_Gate
  _8_bit_condition_gate u_8_bit_condition_gate_32 (
    .Bit_7(byte_16_out_11), .Bit_6(byte_16_out_13), .Bit_5(byte_16_out_15), .Bit_4(byte_16_out_17),
    .Bit_3(byte_16_out_19), .Bit_2(byte_16_out_21), .Bit_1(byte_16_out_23), .Bit_0(byte_16_out_25),
    .out_10(n8_bit_condition_gate_32_out_10), .out_11(n8_bit_condition_gate_32_out_11),
    .out_12(n8_bit_condition_gate_32_out_12), .out_13(n8_bit_condition_gate_32_out_13),
    .out_14(n8_bit_condition_gate_32_out_14), .out_15(n8_bit_condition_gate_32_out_15),
    .out_16(n8_bit_condition_gate_32_out_16), .out_17(n8_bit_condition_gate_32_out_17), .Condition(and_31_out));
  or or_17 (out_28, n8_bit_condition_gate_17_out_11, or_19_out);
  or or_18 (out_29, n8_bit_condition_gate_17_out_12, or_20_out);
  or or_19 (or_19_out, n8_bit_condition_gate_18_out_11, or_21_out);
  or or_20 (or_20_out, n8_bit_condition_gate_18_out_12, or_22_out);
  or or_21 (or_21_out, n8_bit_condition_gate_19_out_11, or_23_out);
  or or_22 (or_22_out, n8_bit_condition_gate_19_out_12, or_24_out);
  or or_23 (or_23_out, n8_bit_condition_gate_20_out_11, or_25_out);
  or or_24 (or_24_out, n8_bit_condition_gate_20_out_12, or_26_out);
  or or_25 (or_25_out, n8_bit_condition_gate_21_out_11, or_27_out);
  or or_26 (or_26_out, n8_bit_condition_gate_21_out_12, or_28_out);
  or or_27 (or_27_out, n8_bit_condition_gate_22_out_11, or_29_out);
  or or_28 (or_28_out, n8_bit_condition_gate_22_out_12, or_30_out);
  or or_29 (or_29_out, n8_bit_condition_gate_23_out_11, or_31_out);
  or or_30 (or_30_out, n8_bit_condition_gate_23_out_12, or_32_out);
  or or_31 (or_31_out, n8_bit_condition_gate_24_out_11, n8_bit_condition_gate_24_out_13);
  or or_32 (or_32_out, n8_bit_condition_gate_24_out_12, or_34_out);
  or or_33 (n8_bit_condition_gate_24_out_13, n8_bit_condition_gate_25_out_11, or_35_out);
  or or_34 (or_34_out, n8_bit_condition_gate_25_out_12, or_36_out);
  or or_35 (or_35_out, n8_bit_condition_gate_26_out_11, or_37_out);
  or or_36 (or_36_out, n8_bit_condition_gate_26_out_12, or_38_out);
  or or_37 (or_37_out, n8_bit_condition_gate_27_out_11, or_39_out);
  or or_38 (or_38_out, n8_bit_condition_gate_27_out_12, or_40_out);
  or or_39 (or_39_out, n8_bit_condition_gate_28_out_11, or_41_out);
  or or_40 (or_40_out, n8_bit_condition_gate_28_out_12, or_42_out);
  or or_41 (or_41_out, n8_bit_condition_gate_29_out_11, or_43_out);
  or or_42 (or_42_out, n8_bit_condition_gate_29_out_12, or_44_out);
  or or_43 (or_43_out, n8_bit_condition_gate_30_out_11, or_45_out);
  or or_44 (or_44_out, n8_bit_condition_gate_30_out_12, or_46_out);
  or or_45 (or_45_out, n8_bit_condition_gate_31_out_11, or_47_out);
  or or_46 (or_46_out, n8_bit_condition_gate_31_out_12, or_48_out);
  buf or_47 (or_47_out, n8_bit_condition_gate_32_out_11);  // OR_Gate
  buf or_48 (or_48_out, n8_bit_condition_gate_32_out_12);  // OR_Gate
  or or_49 (out_30, n8_bit_condition_gate_17_out_13, or_51_out);
  or or_50 (out_31, n8_bit_condition_gate_17_out_14, or_52_out);
  or or_51 (or_51_out, n8_bit_condition_gate_18_out_13, or_53_out);
  or or_52 (or_52_out, n8_bit_condition_gate_18_out_14, or_54_out);
  or or_53 (or_53_out, n8_bit_condition_gate_19_out_13, or_55_out);
  or or_54 (or_54_out, n8_bit_condition_gate_19_out_14, or_56_out);
  or or_55 (or_55_out, n8_bit_condition_gate_20_out_13, or_57_out);
  or or_56 (or_56_out, n8_bit_condition_gate_20_out_14, or_58_out);
  or or_57 (or_57_out, n8_bit_condition_gate_21_out_13, or_59_out);
  or or_58 (or_58_out, n8_bit_condition_gate_21_out_14, or_60_out);
  or or_59 (or_59_out, n8_bit_condition_gate_22_out_13, or_61_out);
  or or_60 (or_60_out, n8_bit_condition_gate_22_out_14, or_62_out);
  or or_61 (or_61_out, n8_bit_condition_gate_23_out_13, or_63_out);
  or or_62 (or_62_out, n8_bit_condition_gate_23_out_14, or_64_out);
  or or_63 (or_63_out, n8_bit_condition_gate_24_out_13, or_65_out);
  or or_64 (or_64_out, n8_bit_condition_gate_24_out_14, or_66_out);
  or or_65 (or_65_out, n8_bit_condition_gate_25_out_13, or_67_out);
  or or_66 (or_66_out, n8_bit_condition_gate_25_out_14, or_68_out);
  or or_67 (or_67_out, n8_bit_condition_gate_26_out_13, or_69_out);
  or or_68 (or_68_out, n8_bit_condition_gate_26_out_14, or_70_out);
  or or_69 (or_69_out, n8_bit_condition_gate_27_out_13, or_71_out);
  or or_70 (or_70_out, n8_bit_condition_gate_27_out_14, or_72_out);
  or or_71 (or_71_out, n8_bit_condition_gate_28_out_13, or_73_out);
  or or_72 (or_72_out, n8_bit_condition_gate_28_out_14, or_74_out);
  or or_73 (or_73_out, n8_bit_condition_gate_29_out_13, or_75_out);
  or or_74 (or_74_out, n8_bit_condition_gate_29_out_14, or_76_out);
  or or_75 (or_75_out, n8_bit_condition_gate_30_out_13, or_77_out);
  or or_76 (or_76_out, n8_bit_condition_gate_30_out_14, or_78_out);
  or or_77 (or_77_out, n8_bit_condition_gate_31_out_13, or_79_out);
  or or_78 (or_78_out, n8_bit_condition_gate_31_out_14, or_80_out);
  buf or_79 (or_79_out, n8_bit_condition_gate_32_out_13);  // OR_Gate
  buf or_80 (or_80_out, n8_bit_condition_gate_32_out_14);  // OR_Gate
  or or_81 (out_32, n8_bit_condition_gate_17_out_15, or_83_out);
  or or_82 (out_33, n8_bit_condition_gate_17_out_16, or_84_out);
  or or_83 (or_83_out, n8_bit_condition_gate_18_out_15, or_85_out);
  or or_84 (or_84_out, n8_bit_condition_gate_18_out_16, or_86_out);
  or or_85 (or_85_out, n8_bit_condition_gate_19_out_15, or_87_out);
  or or_86 (or_86_out, n8_bit_condition_gate_19_out_16, or_88_out);
  or or_87 (or_87_out, n8_bit_condition_gate_20_out_15, or_89_out);
  or or_88 (or_88_out, n8_bit_condition_gate_20_out_16, or_90_out);
  or or_89 (or_89_out, n8_bit_condition_gate_21_out_15, or_91_out);
  or or_90 (or_90_out, n8_bit_condition_gate_21_out_16, or_92_out);
  or or_91 (or_91_out, n8_bit_condition_gate_22_out_15, or_93_out);
  or or_92 (or_92_out, n8_bit_condition_gate_22_out_16, or_94_out);
  or or_93 (or_93_out, n8_bit_condition_gate_23_out_15, or_95_out);
  or or_94 (or_94_out, n8_bit_condition_gate_23_out_16, or_96_out);
  or or_95 (or_95_out, n8_bit_condition_gate_24_out_15, or_97_out);
  or or_96 (or_96_out, n8_bit_condition_gate_24_out_16, or_98_out);
  or or_97 (or_97_out, n8_bit_condition_gate_25_out_15, or_99_out);
  or or_98 (or_98_out, n8_bit_condition_gate_25_out_16, or_100_out);
  or or_99 (or_99_out, n8_bit_condition_gate_26_out_15, or_101_out);
  or or_100 (or_100_out, n8_bit_condition_gate_26_out_16, or_102_out);
  or or_101 (or_101_out, n8_bit_condition_gate_27_out_15, or_103_out);
  or or_102 (or_102_out, n8_bit_condition_gate_27_out_16, or_104_out);
  or or_103 (or_103_out, n8_bit_condition_gate_28_out_15, or_105_out);
  or or_104 (or_104_out, n8_bit_condition_gate_28_out_16, or_106_out);
  or or_105 (or_105_out, n8_bit_condition_gate_29_out_15, or_107_out);
  or or_106 (or_106_out, n8_bit_condition_gate_29_out_16, or_108_out);
  or or_107 (or_107_out, n8_bit_condition_gate_30_out_15, or_109_out);
  or or_108 (or_108_out, n8_bit_condition_gate_30_out_16, or_110_out);
  or or_109 (or_109_out, n8_bit_condition_gate_31_out_15, or_111_out);
  or or_110 (or_110_out, n8_bit_condition_gate_31_out_16, or_112_out);
  buf or_111 (or_111_out, n8_bit_condition_gate_32_out_15);  // OR_Gate
  buf or_112 (or_112_out, n8_bit_condition_gate_32_out_16);  // OR_Gate
  or or_113 (out_34, n8_bit_condition_gate_17_out_17, or_114_out);
  or or_114 (or_114_out, n8_bit_condition_gate_18_out_17, or_115_out);
  or or_115 (or_115_out, n8_bit_condition_gate_19_out_17, or_116_out);
  or or_116 (or_116_out, n8_bit_condition_gate_20_out_17, or_117_out);
  or or_117 (or_117_out, n8_bit_condition_gate_21_out_17, or_118_out);
  or or_118 (or_118_out, n8_bit_condition_gate_22_out_17, or_119_out);
  or or_119 (or_119_out, n8_bit_condition_gate_23_out_17, or_120_out);
  or or_120 (or_120_out, n8_bit_condition_gate_24_out_17, or_121_out);
  or or_121 (or_121_out, n8_bit_condition_gate_25_out_17, or_122_out);
  or or_122 (or_122_out, n8_bit_condition_gate_26_out_17, or_123_out);
  or or_123 (or_123_out, n8_bit_condition_gate_27_out_17, or_124_out);
  or or_124 (or_124_out, n8_bit_condition_gate_28_out_17, or_125_out);
  or or_125 (or_125_out, n8_bit_condition_gate_29_out_17, or_126_out);
  or or_126 (or_126_out, n8_bit_condition_gate_30_out_17, or_127_out);
  or or_127 (or_127_out, n8_bit_condition_gate_31_out_17, or_128_out);
  buf or_128 (or_128_out, n8_bit_condition_gate_32_out_17);  // OR_Gate
endmodule

module \byte  (
  input  R_W,
  input  Clock,
  input  in_3,
  input  in_4,
  input  in_5,
  input  in_6,
  input  in_7,
  input  in_8,
  input  in_9,
  input  in_10,
  output out_11,
  output out_12,
  output out_13,
  output out_14,
  output out_15,
  output out_16,
  output out_17,
  output out_18,
  output out_19,
  output out_20,
  output out_21,
  output out_22,
  output out_23,
  output out_24,
  output out_25,
  output out_26
);

  wire and_1_out, and_2_out, and_3_out, and_4_out, and_5_out, and_6_out, and_7_out, and_8_out, and_9_out,
       and_10_out, and_11_out, and_12_out, and_13_out, and_14_out, and_15_out, and_16_out, not_1_out,
       or_1_out, or_2_out, or_3_out, or_4_out, or_5_out, or_6_out, or_7_out, or_8_out;

  not not_1 (not_1_out, R_W);
  and and_1 (and_1_out, out_12, not_1_out);
  or or_1 (or_1_out, and_1_out, and_2_out);
  and and_2 (and_2_out, R_W, in_3);
  and and_3 (and_3_out, out_14, not_1_out);
  or or_2 (or_2_out, and_3_out, and_4_out);
  and and_4 (and_4_out, R_W, in_4);
  and and_5 (and_5_out, out_16, not_1_out);
  or or_3 (or_3_out, and_5_out, and_6_out);
  and and_6 (and_6_out, R_W, in_5);
  and and_7 (and_7_out, out_18, not_1_out);
  or or_4 (or_4_out, and_7_out, and_8_out);
  and and_8 (and_8_out, R_W, in_6);
  and and_9 (and_9_out, out_20, not_1_out);
  or or_5 (or_5_out, and_9_out, and_10_out);
  and and_10 (and_10_out, R_W, in_7);
  and and_11 (and_11_out, out_22, not_1_out);
  or or_6 (or_6_out, and_11_out, and_12_out);
  and and_12 (and_12_out, R_W, in_8);
  and and_13 (and_13_out, out_24, not_1_out);
  or or_7 (or_7_out, and_13_out, and_14_out);
  and and_14 (and_14_out, R_W, in_9);
  and and_15 (and_15_out, out_26, not_1_out);
  or or_8 (or_8_out, and_15_out, and_16_out);
  and and_16 (and_16_out, R_W, in_10);
  D_Flip_Flop d_ff_1 (.clk(Clock), .D(or_1_out), .Q(out_12));  // open: Qn, preset, en, reset
  D_Flip_Flop d_ff_2 (.clk(Clock), .D(or_2_out), .Q(out_14));  // open: Qn, preset, en, reset
  D_Flip_Flop d_ff_3 (.clk(Clock), .D(or_3_out), .Q(out_16));  // open: Qn, preset, en, reset
  D_Flip_Flop d_ff_4 (.clk(Clock), .D(or_4_out), .Q(out_18));  // open: Qn, preset, en, reset
  D_Flip_Flop d_ff_5 (.clk(Clock), .D(or_5_out), .Q(out_20));  // open: Qn, preset, en, reset
  D_Flip_Flop d_ff_6 (.clk(Clock), .D(or_6_out), .Q(out_22));  // open: Qn, preset, en, reset
  D_Flip_Flop d_ff_7 (.clk(Clock), .D(or_7_out), .Q(out_24));  // open: Qn, preset, en, reset
  D_Flip_Flop d_ff_8 (.clk(Clock), .D(or_8_out), .Q(out_26));  // open: Qn, preset, en, reset
  and and_17 (out_11, not_1_out, out_12);
  and and_18 (out_13, not_1_out, out_14);
  and and_19 (out_15, not_1_out, out_16);
  and and_20 (out_17, not_1_out, out_18);
  and and_21 (out_19, not_1_out, out_20);
  and and_22 (out_21, not_1_out, out_22);
  and and_23 (out_23, not_1_out, out_24);
  and and_24 (out_25, not_1_out, out_26);
endmodule

module _8_bit_condition_gate (
  input  Condition,
  input  Bit_7,
  input  Bit_6,
  input  Bit_5,
  input  Bit_4,
  input  Bit_3,
  input  Bit_2,
  input  Bit_1,
  input  Bit_0,
  output out_10,
  output out_11,
  output out_12,
  output out_13,
  output out_14,
  output out_15,
  output out_16,
  output out_17
);

  and and_1 (out_10, Condition, Bit_7);
  and and_2 (out_11, Condition, Bit_6);
  and and_3 (out_12, Condition, Bit_5);
  and and_4 (out_13, Condition, Bit_4);
  and and_5 (out_14, Condition, Bit_3);
  and and_6 (out_15, Condition, Bit_2);
  and and_7 (out_16, Condition, Bit_1);
  and and_8 (out_17, Condition, Bit_0);
endmodule
