// Logisim project data-register.circ as structural Verilog: 1 circuit, main circuit main
module main (
  input  Clock,
  input  R_W,
  input  in_3,
  input  in_4,
  input  in_5,
  input  in_6,
  input  in_7,
  input  in_8,
  input  in_9,
  input  in_10,
  input  in_11,
  input  in_12,
  input  in_13,
  input  in_14,
  input  in_15,
  input  in_16,
  input  in_17,
  input  in_18,
  output out_19,
  output out_20,
  output out_21,
  output out_22,
  output out_23,
  output out_24,
  output out_25,
  output out_26
);

  wire and_1_out, and_2_out, and_3_out, and_4_out, and_5_out, and_6_out, and_7_out, and_8_out, and_9_out,
       and_10_out, and_11_out, and_12_out, and_13_out, and_14_out, and_15_out, and_16_out, not_1_out,
       or_1_out, or_2_out, or_3_out, or_4_out, or_5_out, or_6_out, or_7_out, or_8_out;

  not not_1 (not_1_out, R_W);
  and and_1 (and_1_out, in_3, R_W);
  and and_2 (and_2_out, not_1_out, in_11);
  or or_1 (or_1_out, and_1_out, and_2_out);
  D_Flip_Flop d_ff_1 (.clk(Clock), .D(or_1_out), .Q(out_19));  // open: Qn, preset, en, reset
  and and_3 (and_3_out, not_1_out, in_12);
  and and_4 (and_4_out, in_4, R_W);
  or or_2 (or_2_out, and_4_out, and_3_out);
  and and_5 (and_5_out, not_1_out, in_13);
  and and_6 (and_6_out, in_5, R_W);
  or or_3 (or_3_out, and_6_out, and_5_out);
  D_Flip_Flop d_ff_2 (.clk(Clock), .D(or_2_out), .Q(out_20));  // open: Qn, preset, en, reset
  and and_7 (and_7_out, in_6, R_W);
  and and_8 (and_8_out, not_1_out, in_14);
  or or_4 (or_4_out, and_7_out, and_8_out);
  D_Flip_Flop d_ff_3 (.clk(Clock), .D(or_3_out), .Q(out_21));  // open: Qn, preset, en, reset
  and and_9 (and_9_out, in_7, R_W);
  or or_5 (or_5_out, and_9_out, and_11_out);
  D_Flip_Flop d_ff_4 (.clk(Clock), .D(or_4_out), .Q(out_22));  // open: Qn, preset, en, reset
  and and_10 (and_10_out, in_8, R_W);
  and and_11 (and_11_out, not_1_out, in_15);
  or or_6 (or_6_out, and_10_out, and_12_out);
  D_Flip_Flop d_ff_5 (.clk(Clock), .D(or_5_out), .Q(out_23));  // open: Qn, preset, en, reset
  and and_12 (and_12_out, not_1_out, in_16);
  and and_13 (and_13_out, in_9, R_W);
  D_Flip_Flop d_ff_6 (.clk(Clock), .D(or_6_out), .Q(out_24));  // open: Qn, preset, en, reset
  and and_14 (and_14_out, in_10, R_W);
  and and_15 (and_15_out, not_1_out, in_17);
  or or_7 (or_7_out, and_13_out, and_15_out);
  D_Flip_Flop d_ff_7 (.clk(Clock), .D(or_7_out), .Q(out_25));  // open: Qn, preset, en, reset
  and and_16 (and_16_out, not_1_out, in_18);
  or or_8 (or_8_out, and_14_out, and_16_out);
  D_Flip_Flop d_ff_8 (.clk(Clock), .D(or_8_out), .Q(out_26));  // open: Qn, preset, en, reset

  // Notes on the sheet:
  //   Manual input
endmodule
